// Logisim project 1.circ as structural Verilog: 14 circuits, main circuit main
module main (
  input  C0,
  input  A3,
  input  A2,
  input  A1,
  input  A0,
  input  B3,
  input  B2,
  input  B1,
  input  B0,
  output S3,
  output S2,
  output S1,
  output S0,
  output C4
);

  \先行进位的四位二进制并行加法器  \u_先行进位的四位二进制并行加法器_1  (
    .C0(C0), .A1(B0), .B1(A0), .A2(B1), .B2(A1), .A3(B2), .B3(A2), .A4(B3), .B4(A3), .S0(S0), .S1(S1),
    .S2(S2), .S3(S3), .S4(C4));
endmodule

module \半加器  (
  input  A,
  input  B,
  output S,
  output C
);

  wire nand_1_out, nand_2_out, nand_3_out;

  nand nand_1 (nand_1_out, A, B);
  nand nand_2 (nand_2_out, A, nand_1_out);
  nand nand_3 (nand_3_out, nand_1_out, B);
  not not_1 (C, nand_1_out);
  nand nand_4 (S, nand_2_out, nand_3_out);
endmodule

module \全加器  (
  input  A,
  input  B,
  input  Ci,
  output S,
  output C
);

  wire nand_1_out, nand_2_out, xor_1_out;

  xor xor_1 (xor_1_out, A, B);
  nand nand_1 (nand_1_out, xor_1_out, Ci);
  nand nand_2 (nand_2_out, B, A);
  xor xor_2 (S, xor_1_out, Ci);
  nand nand_3 (C, nand_1_out, nand_2_out);
endmodule

module \串行进位的四位二进制并行加法器  (
  input  C0,
  input  A3,
  input  B3,
  input  A2,
  input  B2,
  input  A1,
  input  B1,
  input  A0,
  input  B0,
  output S3,
  output S2,
  output S1,
  output S0,
  output C
);

  wire \全加器_2_c , \全加器_3_c , \全加器_4_c ;

  \全加器  \u_全加器_1  (.A(A3), .B(B3), .Ci(\全加器_2_c ), .S(S3), .C(C));
  \全加器  \u_全加器_2  (.A(A2), .B(B2), .Ci(\全加器_3_c ), .S(S2), .C(\全加器_2_c ));
  \全加器  \u_全加器_3  (.A(A1), .B(B1), .Ci(\全加器_4_c ), .S(S1), .C(\全加器_3_c ));
  \全加器  \u_全加器_4  (.A(A0), .B(B0), .Ci(C0), .S(S0), .C(\全加器_4_c ));
endmodule

module \先行进位的四位二进制并行加法器  (
  input  C0,
  input  A1,
  input  B1,
  input  A2,
  input  B2,
  input  A3,
  input  B3,
  input  A4,
  input  B4,
  output S0,
  output S1,
  output S2,
  output S3,
  output S4
);

  wire C1_out, C2_out, C3_out, G1_out, G2_out, G3_out, G4_out, P1_out, P1C0_out, P1P2P3C0_out, P2_out,
       P2G1_out, P2P1C0_out, P3_out, P3G2_out, P3P2G1_out, P4_out, P4G3_out, P4P3G2_out, P4P3P2G1_out,
       P4P3P2P1C0_out, xor_1_out, xor_2_out, xor_3_out, xor_4_out;

  xor P3 (P3_out, A3, B3);
  and G3 (G3_out, A3, B3);
  xor P4 (P4_out, A4, B4);
  and G4 (G4_out, A4, B4);
  xor P1 (P1_out, A1, B1);
  and G1 (G1_out, A1, B1);
  xor P2 (P2_out, A2, B2);
  and G2 (G2_out, A2, B2);
  and P1C0 (P1C0_out, C0, P1_out);
  and P2P1C0 (P2P1C0_out, C0, P1_out, P2_out);
  and P2G1 (P2G1_out, G1_out, P2_out);
  and P1P2P3C0 (P1P2P3C0_out, C0, P1_out, P3_out, P2_out);
  and P3P2G1 (P3P2G1_out, G1_out, P3_out, P2_out);
  and P3G2 (P3G2_out, P3_out, G2_out);
  and P4P3P2P1C0 (P4P3P2P1C0_out, C0, P1_out, P2_out, P3_out, P4_out);
  and P4P3P2G1 (P4P3P2G1_out, G1_out, P2_out, P4_out, P3_out);
  and P4P3G2 (P4P3G2_out, G2_out, P4_out, P3_out);
  and P4G3 (P4G3_out, P4_out, G3_out);
  or C1 (C1_out, P1C0_out, G1_out);
  or C2 (C2_out, P2P1C0_out, P2G1_out, G2_out);
  or C3 (C3_out, P1P2P3C0_out, P3P2G1_out, P3G2_out, G3_out);
  xor xor_1 (xor_1_out, B1, A1);
  xor xor_2 (xor_2_out, C1_out, B2);
  xor xor_3 (xor_3_out, C2_out, A3);
  xor xor_4 (xor_4_out, C3_out, A4);
  or C4 (S4, P4P3P2P1C0_out, P4P3P2G1_out, P4P3G2_out, P4G3_out, G4_out);
  xor xor_5 (S0, xor_1_out, C0);
  xor xor_6 (S1, xor_2_out, A2);
  xor xor_7 (S2, xor_3_out, B3);
  xor xor_8 (S3, xor_4_out, B4);
endmodule

module \测试电路  (
  input  C0,
  input  A3,
  input  A2,
  input  A1,
  input  A0,
  input  B3,
  input  B2,
  input  B1,
  input  B0,
  output S3,
  output S2,
  output S1,
  output S0,
  output C4
);

  \先行进位的四位二进制并行加法器  \u_先行进位的四位二进制并行加法器_1  (
    .C0(C0), .A1(B0), .B1(A0), .A2(B1), .B2(A1), .A3(B2), .B3(A2), .A4(B3), .B4(A3), .S0(S0), .S1(S1),
    .S2(S2), .S3(S3), .S4(C4));
endmodule

module \四位可逆二进制计数器  (
  input  CPd,
  input  CLR,
  input  CPu,
  output Qa,
  output Qb,
  output Qc,
  output Qd
);

  wire and_1_out, and_2_out, and_3_out, and_4_out, and_5_out, and_6_out, C1_out, not_1_out, not_2_out,
       not_3_out, not_4_out, or_1_out, or_2_out, or_3_out;

  not not_1 (not_1_out, Qa);
  not not_2 (not_2_out, Qb);
  not not_3 (not_3_out, Qc);
  or C1 (C1_out, CPd, CPu);
  and and_1 (and_1_out, Qa, CPu);
  and and_2 (and_2_out, not_1_out, CPd);
  and and_3 (and_3_out, Qa, Qb, CPu);
  and and_4 (and_4_out, not_1_out, not_2_out, CPd);
  and and_5 (and_5_out, Qa, Qb, Qc, CPu);
  and and_6 (and_6_out, not_2_out, not_1_out, not_3_out, CPd);
  or or_1 (or_1_out, and_1_out, and_2_out);
  or or_2 (or_2_out, and_3_out, and_4_out);
  or or_3 (or_3_out, and_5_out, and_6_out);
  D_Flip_Flop #(.trigger("falling")) D1 (.clk(C1_out), .D(not_1_out), .Q(Qa), .reset(CLR));  // open: Qn, preset, en
  D_Flip_Flop #(.trigger("falling")) D2 (.clk(or_1_out), .D(not_2_out), .Q(Qb), .reset(CLR));  // open: Qn, preset, en
  D_Flip_Flop #(.trigger("falling")) D3 (.clk(or_2_out), .D(not_3_out), .Q(Qc), .reset(CLR));  // open: Qn, preset, en
  D_Flip_Flop #(.trigger("falling")) D4 (.clk(or_3_out), .D(not_4_out), .Q(Qd), .reset(CLR));  // open: Qn, preset, en
  not not_4 (not_4_out, Qd);
endmodule

module \二进制转8421BCD码  (
  input  A3,
  input  A2,
  input  A1,
  input  A0,
  output S3,
  output S2,
  output S1,
  output S0,
  output out_9
);

  wire and_1_out, or_1_out;

  and and_1 (and_1_out, A3, or_1_out);
  or or_1 (or_1_out, A1, A2);
  \先行进位的四位二进制并行加法器  \u_先行进位的四位二进制并行加法器_1  (
    .C0(1'b0), .A1(1'b0), .B1(A0), .A2(and_1_out), .B2(A1), .A3(and_1_out), .B3(A2), .A4(1'b0), .B4(A3),
    .S0(S0), .S1(S1), .S2(S2), .S3(S3), .S4(out_9));
endmodule

module \二进制转8421_封装  (
  input  A3,
  input  in_2,
  input  A1,
  input  A0,
  output S3,
  output S2,
  output S1,
  output S0,
  output C4
);

  \二进制转8421BCD码  \u_二进制转8421bcd码_1  (
    .out_9(C4), .S3(S3), .S2(S2), .S1(S1), .S0(S0), .A3(A3), .A2(in_2), .A1(A1), .A0(A0));

  // Notes on the sheet:
  //   A2
endmodule

module \七段译码器  (
  input  A3,
  input  A2,
  input  A1,
  input  A0,
  output a,
  output b,
  output c,
  output d,
  output e,
  output f,
  output g
);

  wire and_1_out, and_2_out, and_3_out, and_4_out, and_5_out, and_6_out, and_7_out, and_8_out, and_9_out,
       and_10_out, and_11_out, and_12_out, and_13_out, and_14_out, and_15_out, and_16_out, and_17_out,
       and_18_out, and_19_out, and_20_out, and_21_out, and_22_out, and_23_out, and_24_out, and_25_out,
       and_26_out, not_1_out, not_2_out, not_3_out, not_4_out, not_5_out, not_6_out, not_7_out, not_8_out,
       not_9_out, not_10_out, not_11_out, not_12_out, not_13_out, not_14_out, not_15_out, not_16_out,
       not_17_out, not_18_out, not_19_out, not_20_out, not_21_out, not_22_out, not_23_out, not_24_out,
       not_25_out, not_26_out, not_27_out, not_28_out, not_29_out, not_30_out, not_31_out, not_32_out,
       not_33_out, not_34_out, not_35_out, not_36_out, not_37_out;

  not not_1 (not_1_out, A3);
  not not_2 (not_2_out, A2);
  and and_1 (and_1_out, not_1_out, not_2_out, not_3_out);
  not not_3 (not_3_out, A0);
  not not_4 (not_4_out, A3);
  and and_2 (and_2_out, not_4_out, not_5_out, A1);
  not not_5 (not_5_out, A2);
  not not_6 (not_6_out, A3);
  and and_3 (and_3_out, not_6_out, A2, A0);
  and and_4 (and_4_out, A3, not_7_out, not_8_out);
  not not_7 (not_7_out, A2);
  not not_8 (not_8_out, A1);
  and and_5 (and_5_out, A3, not_9_out, A0);
  not not_9 (not_9_out, A1);
  not not_10 (not_10_out, A3);
  and and_6 (and_6_out, not_10_out, not_11_out);
  not not_11 (not_11_out, A2);
  not not_12 (not_12_out, A2);
  and and_7 (and_7_out, not_12_out, not_13_out);
  not not_13 (not_13_out, A1);
  not not_14 (not_14_out, A1);
  and and_8 (and_8_out, not_14_out, not_15_out);
  not not_15 (not_15_out, A0);
  not not_16 (not_16_out, A3);
  and and_9 (and_9_out, not_16_out, A1, A0);
  not not_17 (not_17_out, A2);
  and and_10 (and_10_out, not_17_out, not_18_out);
  not not_18 (not_18_out, A1);
  not not_19 (not_19_out, A2);
  and and_11 (and_11_out, not_19_out, A0);
  not not_20 (not_20_out, A3);
  and and_12 (and_12_out, not_20_out, A2);
  not not_21 (not_21_out, A2);
  and and_13 (and_13_out, not_21_out, not_22_out);
  not not_22 (not_22_out, A0);
  not not_23 (not_23_out, A2);
  and and_14 (and_14_out, not_23_out, A1);
  and and_15 (and_15_out, A1, not_24_out);
  not not_24 (not_24_out, A0);
  and and_16 (and_16_out, A2, not_25_out, A0);
  not not_25 (not_25_out, A1);
  not not_26 (not_26_out, A2);
  and and_17 (and_17_out, not_26_out, not_27_out);
  not not_27 (not_27_out, A0);
  and and_18 (and_18_out, A1, not_28_out);
  not not_28 (not_28_out, A0);
  not not_29 (not_29_out, A1);
  and and_19 (and_19_out, not_29_out, not_30_out);
  not not_30 (not_30_out, A0);
  and and_20 (and_20_out, A2, not_31_out);
  not not_31 (not_31_out, A1);
  and and_21 (and_21_out, A2, not_32_out);
  not not_32 (not_32_out, A0);
  and and_22 (and_22_out, A3, not_33_out);
  not not_33 (not_33_out, A1);
  not not_34 (not_34_out, A2);
  and and_23 (and_23_out, not_34_out, A1);
  and and_24 (and_24_out, A2, not_35_out);
  not not_35 (not_35_out, A1);
  and and_25 (and_25_out, A2, not_36_out);
  not not_36 (not_36_out, A0);
  and and_26 (and_26_out, A3, not_37_out);
  not not_37 (not_37_out, A2);
  or or_1 (a, and_1_out, and_2_out, and_3_out, and_4_out, and_5_out);
  or or_2 (b, and_6_out, and_7_out, and_8_out, and_9_out);
  or or_3 (c, and_10_out, and_11_out, and_12_out);
  or or_4 (d, and_13_out, and_14_out, and_15_out, and_16_out);
  or or_5 (e, and_17_out, and_18_out);
  or or_6 (f, and_19_out, and_20_out, and_21_out, and_22_out);
  or or_7 (g, and_23_out, and_24_out, and_25_out, and_26_out);
endmodule

module \七段译码器封装  (
  input  A3,
  input  A2,
  input  in_3,
  input  A0
);

  wire \七段译码器_1_a , \七段译码器_1_b , \七段译码器_1_c , \七段译码器_1_d , \七段译码器_1_e , \七段译码器_1_f , \七段译码器_1_g ,
       \七段译码器_2_a , \七段译码器_2_b , \七段译码器_2_c , \七段译码器_2_d , \七段译码器_2_e , \七段译码器_2_f , \七段译码器_2_g ,
       \二进制转8421bcd码_1_out_9 , \二进制转8421bcd码_1_s0 , \二进制转8421bcd码_1_s1 , \二进制转8421bcd码_1_s2 ,
       \二进制转8421bcd码_1_s3 ;

  _7_Segment_Display u_7_segment_display_1 (
    .g(\七段译码器_1_g ), .f(\七段译码器_1_f ), .a(\七段译码器_1_a ), .b(\七段译码器_1_b ), .e(\七段译码器_1_e ), .d(\七段译码器_1_d ),
    .c(\七段译码器_1_c ), .dp(1'b0));
  \七段译码器  \u_七段译码器_1  (
    .A3(1'b0), .A2(1'b0), .A1(1'b0), .A0(\二进制转8421bcd码_1_out_9 ), .a(\七段译码器_1_a ), .b(\七段译码器_1_b ),
    .c(\七段译码器_1_c ), .d(\七段译码器_1_d ), .e(\七段译码器_1_e ), .f(\七段译码器_1_f ), .g(\七段译码器_1_g ));
  _7_Segment_Display u_7_segment_display_2 (
    .g(\七段译码器_2_g ), .f(\七段译码器_2_f ), .a(\七段译码器_2_a ), .b(\七段译码器_2_b ), .e(\七段译码器_2_e ), .d(\七段译码器_2_d ),
    .c(\七段译码器_2_c ), .dp(1'b0));
  \二进制转8421BCD码  \u_二进制转8421bcd码_1  (
    .out_9(\二进制转8421bcd码_1_out_9 ), .S3(\二进制转8421bcd码_1_s3 ), .S2(\二进制转8421bcd码_1_s2 ),
    .S1(\二进制转8421bcd码_1_s1 ), .S0(\二进制转8421bcd码_1_s0 ), .A3(A3), .A2(A2), .A1(in_3), .A0(A0));
  \七段译码器  \u_七段译码器_2  (
    .A3(\二进制转8421bcd码_1_s3 ), .A2(\二进制转8421bcd码_1_s2 ), .A1(\二进制转8421bcd码_1_s1 ), .A0(\二进制转8421bcd码_1_s0 ),
    .a(\七段译码器_2_a ), .b(\七段译码器_2_b ), .c(\七段译码器_2_c ), .d(\七段译码器_2_d ), .e(\七段译码器_2_e ), .f(\七段译码器_2_f ),
    .g(\七段译码器_2_g ));

  // Notes on the sheet:
  //   A1
endmodule

module \报警电路  (
  input  CPu,
  input  CLR,
  input  CPd,
  output C,
  output Qd,
  output Qc,
  output Qb,
  output Qa
);

  wire and_2_out, and_3_out, and_4_out, not_1_out, or_1_out;

  and and_1 (C, and_2_out, CPu);
  or or_1 (or_1_out, Qd, Qc, Qb, Qa);
  and and_2 (and_2_out, Qd, Qc, Qb, Qa);
  not not_1 (not_1_out, and_2_out);
  and and_3 (and_3_out, or_1_out, CPd);
  and and_4 (and_4_out, not_1_out, CPu);
  \四位可逆二进制计数器  \u_四位可逆二进制计数器_1  (.CPd(and_3_out), .CLR(CLR), .CPu(and_4_out), .Qa(Qa), .Qb(Qb), .Qc(Qc), .Qd(Qd));
endmodule

module \门禁系统  (
  input  CPu,
  input  CLR,
  input  CPd,
  output a,
  output b,
  output c,
  output d,
  output e,
  output f,
  output g,
  output a_2,
  output b_2,
  output c_2,
  output d_2,
  output e_2,
  output f_2,
  output g_2,
  output \报警 
);

  wire \二进制转8421bcd码_1_out_9 , \二进制转8421bcd码_1_s0 , \二进制转8421bcd码_1_s1 , \二进制转8421bcd码_1_s2 ,
       \二进制转8421bcd码_1_s3 , \报警电路_1_qa , \报警电路_1_qb , \报警电路_1_qc , \报警电路_1_qd ;

  \七段译码器  \u_七段译码器_1  (
    .A3(1'b0), .A2(1'b0), .A1(1'b0), .A0(\二进制转8421bcd码_1_out_9 ), .a(a), .b(b), .c(c), .d(d), .e(e), .f(f),
    .g(g));
  \二进制转8421BCD码  \u_二进制转8421bcd码_1  (
    .out_9(\二进制转8421bcd码_1_out_9 ), .S3(\二进制转8421bcd码_1_s3 ), .S2(\二进制转8421bcd码_1_s2 ),
    .S1(\二进制转8421bcd码_1_s1 ), .S0(\二进制转8421bcd码_1_s0 ), .A3(\报警电路_1_qd ), .A2(\报警电路_1_qc ), .A1(\报警电路_1_qb ),
    .A0(\报警电路_1_qa ));
  \七段译码器  \u_七段译码器_2  (
    .A3(\二进制转8421bcd码_1_s3 ), .A2(\二进制转8421bcd码_1_s2 ), .A1(\二进制转8421bcd码_1_s1 ), .A0(\二进制转8421bcd码_1_s0 ),
    .a(a_2), .b(b_2), .c(c_2), .d(d_2), .e(e_2), .f(f_2), .g(g_2));
  \报警电路  \u_报警电路_1  (
    .CPu(CPu), .CLR(CLR), .CPd(CPd), .C(\报警 ), .Qd(\报警电路_1_qd ), .Qc(\报警电路_1_qc ), .Qb(\报警电路_1_qb ),
    .Qa(\报警电路_1_qa ));
endmodule

module \门禁系统测试  (
  input  CPu,
  input  CLR,
  input  CPd
);

  wire \门禁系统_1_a , \门禁系统_1_a_2 , \门禁系统_1_b , \门禁系统_1_b_2 , \门禁系统_1_c , \门禁系统_1_c_2 , \门禁系统_1_d ,
       \门禁系统_1_d_2 , \门禁系统_1_e , \门禁系统_1_e_2 , \门禁系统_1_f , \门禁系统_1_f_2 , \门禁系统_1_g , \门禁系统_1_g_2 ,
       \门禁系统_1_报警 ;

  _7_Segment_Display u_7_segment_display_1 (
    .g(\门禁系统_1_g ), .f(\门禁系统_1_f ), .a(\门禁系统_1_a ), .b(\门禁系统_1_b ), .e(\门禁系统_1_e ), .d(\门禁系统_1_d ),
    .c(\门禁系统_1_c ), .dp(1'b0));
  _7_Segment_Display u_7_segment_display_2 (
    .g(\门禁系统_1_g_2 ), .f(\门禁系统_1_f_2 ), .a(\门禁系统_1_a_2 ), .b(\门禁系统_1_b_2 ), .e(\门禁系统_1_e_2 ),
    .d(\门禁系统_1_d_2 ), .c(\门禁系统_1_c_2 ), .dp(1'b0));
  LED led_1 (.in(\门禁系统_1_报警 ));
  \门禁系统  \u_门禁系统_1  (
    .CPu(CPu), .CLR(CLR), .CPd(CPd), .\报警 (\门禁系统_1_报警 ), .a(\门禁系统_1_a ), .b(\门禁系统_1_b ), .c(\门禁系统_1_c ),
    .d(\门禁系统_1_d ), .e(\门禁系统_1_e ), .f(\门禁系统_1_f ), .g(\门禁系统_1_g ), .a_2(\门禁系统_1_a_2 ), .b_2(\门禁系统_1_b_2 ),
    .c_2(\门禁系统_1_c_2 ), .d_2(\门禁系统_1_d_2 ), .e_2(\门禁系统_1_e_2 ), .f_2(\门禁系统_1_f_2 ), .g_2(\门禁系统_1_g_2 ));
endmodule
