// Logisim project 2_1.circ as structural Verilog: 7 circuits, main circuit 四位乘法器
module \四位乘法器  (
  input  a0,
  input  a1,
  input  a2,
  input  a3,
  input  [7:0] in_5,
  input  [3:0] in_6,
  output [7:0] p
);

  wire [7:0] adder_1_out, adder_2_out, adder_3_out, adder_4_out, bit_extender_1_out, multiplexer_1_out,
       multiplexer_2_out, multiplexer_3_out, shifter_1_out, shifter_2_out, shifter_3_out, shifter_4_out;

  assign bit_extender_1_out = {{4{1'b0}}, in_6};  // Bit_Extender bit_extender_1
  Adder adder_1 (.a(in_5), .b(bit_extender_1_out), .out(adder_1_out), .cin(1'b0));  // open: cout
  Shifter shifter_1 (.in(bit_extender_1_out), .\dist (3'b001), .out(shifter_1_out));
  Multiplexer #(.width(8), .enable("false")) multiplexer_1 (
    .in0(in_5), .in1(adder_1_out), .out(multiplexer_1_out), .sel(a0));
  Adder adder_2 (.a(multiplexer_1_out), .b(shifter_1_out), .out(adder_2_out), .cin(1'b0));  // open: cout
  Multiplexer #(.width(8), .enable("false")) multiplexer_2 (
    .in0(multiplexer_1_out), .in1(adder_2_out), .out(multiplexer_2_out), .sel(a1));
  Shifter shifter_2 (.in(shifter_1_out), .\dist (3'b001), .out(shifter_2_out));
  Adder adder_3 (.a(multiplexer_2_out), .b(shifter_2_out), .out(adder_3_out), .cin(1'b0));  // open: cout
  Shifter shifter_3 (.in(shifter_2_out), .\dist (3'b001), .out(shifter_3_out));
  Multiplexer #(.width(8), .enable("false")) multiplexer_3 (
    .in0(multiplexer_2_out), .in1(adder_3_out), .out(multiplexer_3_out), .sel(a2));
  Adder adder_4 (.a(multiplexer_3_out), .b(shifter_3_out), .out(adder_4_out), .cin(1'b0));  // open: cout
  Shifter shifter_4 (.in(shifter_3_out), .\dist (3'b001), .out(shifter_4_out));
  Multiplexer #(.width(8), .enable("false")) multiplexer_4 (
    .in0(multiplexer_3_out), .in1(adder_4_out), .out(p), .sel(a3));

  // Notes on the sheet:
  //   b(3:0)
endmodule

module \_32x4乘法器  (
  input  in_1,
  input  in_2,
  input  in_3,
  input  in_4,
  input  [31:0] in_5,
  output [31:0] out_6
);

  wire [31:0] adder_1_out, adder_2_out, adder_3_out, adder_4_out, multiplexer_1_out, multiplexer_2_out,
       multiplexer_3_out, shifter_1_out, shifter_2_out, shifter_3_out, shifter_4_out;

  Adder #(.width(32)) adder_1 (.a({32{1'b0}}), .b(in_5), .out(adder_1_out), .cin(1'b0));  // open: cout
  Shifter #(.width(32)) shifter_1 (.in(in_5), .\dist (5'b00001), .out(shifter_1_out));
  Multiplexer #(.width(32), .enable("false")) multiplexer_1 (
    .in0({32{1'b0}}), .in1(adder_1_out), .out(multiplexer_1_out), .sel(in_1));
  Adder #(.width(32)) adder_2 (.a(multiplexer_1_out), .b(shifter_1_out), .out(adder_2_out), .cin(1'b0));  // open: cout
  Multiplexer #(.width(32), .enable("false")) multiplexer_2 (
    .in0(multiplexer_1_out), .in1(adder_2_out), .out(multiplexer_2_out), .sel(in_2));
  Shifter #(.width(32)) shifter_2 (.in(shifter_1_out), .\dist (5'b00001), .out(shifter_2_out));
  Adder #(.width(32)) adder_3 (.a(multiplexer_2_out), .b(shifter_2_out), .out(adder_3_out), .cin(1'b0));  // open: cout
  Shifter #(.width(32)) shifter_3 (.in(shifter_2_out), .\dist (5'b00001), .out(shifter_3_out));
  Multiplexer #(.width(32), .enable("false")) multiplexer_3 (
    .in0(multiplexer_2_out), .in1(adder_3_out), .out(multiplexer_3_out), .sel(in_3));
  Adder #(.width(32)) adder_4 (.a(multiplexer_3_out), .b(shifter_3_out), .out(adder_4_out), .cin(1'b0));  // open: cout
  Shifter #(.width(32)) shifter_4 (.in(shifter_3_out), .\dist (5'b00001), .out(shifter_4_out));
  Multiplexer #(.width(32), .enable("false")) multiplexer_4 (
    .in0(multiplexer_3_out), .in1(adder_4_out), .out(out_6), .sel(in_4));
endmodule

module \_32x32乘法器  (
  input  a0,
  input  a1,
  input  a2,
  input  a3,
  input  a4,
  input  a5,
  input  a6,
  input  a7,
  input  a8,
  input  a9,
  input  a10,
  input  a11,
  input  a12,
  input  a13,
  input  a14,
  input  a15,
  input  a16,
  input  a17,
  input  a18,
  input  a19,
  input  a20,
  input  a21,
  input  a22,
  input  a23,
  input  a24,
  input  a25,
  input  a26,
  input  a27,
  input  a28,
  input  a29,
  input  a30,
  input  a31,
  input  [31:0] in_33,
  output [31:0] out_34
);

  wire [31:0] adder_1_out, adder_2_out, adder_3_out, adder_4_out, adder_5_out, adder_6_out,
       \n32x4乘法器_1_out_6 , \n32x4乘法器_2_out_6 , \n32x4乘法器_3_out_6 , \n32x4乘法器_4_out_6 , \n32x4乘法器_5_out_6 ,
       \n32x4乘法器_6_out_6 , \n32x4乘法器_7_out_6 , \n32x4乘法器_8_out_6 , shifter_1_out, shifter_2_out,
       shifter_3_out, shifter_4_out, shifter_5_out, shifter_6_out, shifter_7_out, shifter_8_out;

  \_32x4乘法器  \u_32x4乘法器_1  (.in_5(in_33), .out_6(\n32x4乘法器_1_out_6 ), .in_1(a0), .in_2(a1), .in_3(a2), .in_4(a3));
  Shifter #(.width(32)) shifter_1 (.in(\n32x4乘法器_1_out_6 ), .\dist ({5{1'b0}}), .out(shifter_1_out));
  \_32x4乘法器  \u_32x4乘法器_2  (.in_5(in_33), .out_6(\n32x4乘法器_2_out_6 ), .in_1(a4), .in_2(a5), .in_3(a6), .in_4(a7));
  Shifter #(.width(32)) shifter_2 (.in(\n32x4乘法器_2_out_6 ), .\dist (5'b00100), .out(shifter_2_out));
  Adder #(.width(32)) adder_1 (.a(shifter_1_out), .b(shifter_2_out), .out(adder_1_out), .cin(1'b0));  // open: cout
  \_32x4乘法器  \u_32x4乘法器_3  (.in_5(in_33), .out_6(\n32x4乘法器_3_out_6 ), .in_1(a8), .in_2(a9), .in_3(a10), .in_4(a11));
  Shifter #(.width(32)) shifter_3 (.in(\n32x4乘法器_3_out_6 ), .\dist (5'b01000), .out(shifter_3_out));
  Adder #(.width(32)) adder_2 (.a(adder_1_out), .b(shifter_3_out), .out(adder_2_out), .cin(1'b0));  // open: cout
  \_32x4乘法器  \u_32x4乘法器_4  (.in_5(in_33), .out_6(\n32x4乘法器_4_out_6 ), .in_1(a12), .in_2(a13), .in_3(a14), .in_4(a15));
  Shifter #(.width(32)) shifter_4 (.in(\n32x4乘法器_4_out_6 ), .\dist (5'b01100), .out(shifter_4_out));
  Adder #(.width(32)) adder_3 (.a(adder_2_out), .b(shifter_4_out), .out(adder_3_out), .cin(1'b0));  // open: cout
  \_32x4乘法器  \u_32x4乘法器_5  (.in_5(in_33), .out_6(\n32x4乘法器_5_out_6 ), .in_1(a16), .in_2(a17), .in_3(a18), .in_4(a19));
  Shifter #(.width(32)) shifter_5 (.in(\n32x4乘法器_5_out_6 ), .\dist (5'b10000), .out(shifter_5_out));
  Adder #(.width(32)) adder_4 (.a(adder_3_out), .b(shifter_5_out), .out(adder_4_out), .cin(1'b0));  // open: cout
  \_32x4乘法器  \u_32x4乘法器_6  (.in_5(in_33), .out_6(\n32x4乘法器_6_out_6 ), .in_1(a20), .in_2(a21), .in_3(a22), .in_4(a23));
  Shifter #(.width(32)) shifter_6 (.in(\n32x4乘法器_6_out_6 ), .\dist (5'b10100), .out(shifter_6_out));
  Adder #(.width(32)) adder_5 (.a(adder_4_out), .b(shifter_6_out), .out(adder_5_out), .cin(1'b0));  // open: cout
  \_32x4乘法器  \u_32x4乘法器_7  (.in_5(in_33), .out_6(\n32x4乘法器_7_out_6 ), .in_1(a24), .in_2(a25), .in_3(a26), .in_4(a27));
  Shifter #(.width(32)) shifter_7 (.in(\n32x4乘法器_7_out_6 ), .\dist (5'b11000), .out(shifter_7_out));
  Adder #(.width(32)) adder_6 (.a(adder_5_out), .b(shifter_7_out), .out(adder_6_out), .cin(1'b0));  // open: cout
  \_32x4乘法器  \u_32x4乘法器_8  (.in_5(in_33), .out_6(\n32x4乘法器_8_out_6 ), .in_1(a28), .in_2(a29), .in_3(a30), .in_4(a31));
  Shifter #(.width(32)) shifter_8 (.in(\n32x4乘法器_8_out_6 ), .\dist (5'b11100), .out(shifter_8_out));
  Adder #(.width(32)) adder_7 (.a(adder_6_out), .b(shifter_8_out), .out(out_34), .cin(1'b0));  // open: cout
endmodule

module test (
  input  in_1,
  input  in_2,
  input  in_3,
  input  in_4,
  input  in_5,
  input  in_6,
  input  in_7,
  input  in_8,
  input  in_9,
  input  in_10,
  input  in_11,
  input  in_12,
  input  in_13,
  input  in_14,
  input  in_15,
  input  in_16,
  input  in_17,
  input  in_18,
  input  in_19,
  input  in_20,
  input  in_21,
  input  in_22,
  input  in_23,
  input  in_24,
  input  in_25,
  input  in_26,
  input  in_27,
  input  in_28,
  input  in_29,
  input  in_30,
  input  in_31,
  input  in_32,
  input  [31:0] in_33,
  output [31:0] out_34
);

  \_32x32乘法器  \u_32x32乘法器_1  (
    .in_33(in_33), .a0(in_1), .a1(in_2), .a2(in_3), .a3(in_4), .a4(in_5), .a5(in_6), .a6(in_7), .a7(in_8),
    .a8(in_9), .a9(in_10), .a10(in_11), .a11(in_12), .a12(in_13), .a13(in_14), .a14(in_15), .a15(in_16),
    .a16(in_17), .a17(in_18), .a18(in_19), .a19(in_20), .a20(in_21), .a21(in_22), .a22(in_23), .a23(in_24),
    .a24(in_25), .a25(in_26), .a26(in_27), .a27(in_28), .a28(in_29), .a29(in_30), .a30(in_31), .a31(in_32),
    .out_34(out_34));
endmodule

module \new  (
  input  [3:0] in_1,
  input  [31:0] in_2,
  output [31:0] out_3
);

  wire bitselector_1_out, bitselector_2_out, bitselector_3_out, bitselector_4_out;
  wire [31:0] adder_1_out, adder_2_out, adder_3_out, adder_4_out, multiplexer_1_out, multiplexer_2_out,
       multiplexer_3_out, shifter_1_out, shifter_2_out, shifter_3_out, shifter_4_out;

  Adder #(.width(32)) adder_1 (.a({32{1'b0}}), .b(in_2), .out(adder_1_out), .cin(1'b0));  // open: cout
  Shifter #(.width(32)) shifter_1 (.in(in_2), .\dist (5'b00001), .out(shifter_1_out));
  BitSelector #(.width(4)) bitselector_1 (.in(in_1), .out(bitselector_1_out), .sel(2'b00));
  Multiplexer #(.width(32), .enable("false")) multiplexer_1 (
    .in0({32{1'b0}}), .in1(adder_1_out), .out(multiplexer_1_out), .sel(bitselector_1_out));
  Adder #(.width(32)) adder_2 (.a(multiplexer_1_out), .b(shifter_1_out), .out(adder_2_out), .cin(1'b0));  // open: cout
  BitSelector #(.width(4)) bitselector_2 (.in(in_1), .out(bitselector_2_out), .sel(2'b01));
  Multiplexer #(.width(32), .enable("false")) multiplexer_2 (
    .in0(multiplexer_1_out), .in1(adder_2_out), .out(multiplexer_2_out), .sel(bitselector_2_out));
  Shifter #(.width(32)) shifter_2 (.in(shifter_1_out), .\dist (5'b00001), .out(shifter_2_out));
  Adder #(.width(32)) adder_3 (.a(multiplexer_2_out), .b(shifter_2_out), .out(adder_3_out), .cin(1'b0));  // open: cout
  Shifter #(.width(32)) shifter_3 (.in(shifter_2_out), .\dist (5'b00001), .out(shifter_3_out));
  BitSelector #(.width(4)) bitselector_3 (.in(in_1), .out(bitselector_3_out), .sel(2'b10));
  Multiplexer #(.width(32), .enable("false")) multiplexer_3 (
    .in0(multiplexer_2_out), .in1(adder_3_out), .out(multiplexer_3_out), .sel(bitselector_3_out));
  Adder #(.width(32)) adder_4 (.a(multiplexer_3_out), .b(shifter_3_out), .out(adder_4_out), .cin(1'b0));  // open: cout
  Shifter #(.width(32)) shifter_4 (.in(shifter_3_out), .\dist (5'b00001), .out(shifter_4_out));
  BitSelector #(.width(4)) bitselector_4 (.in(in_1), .out(bitselector_4_out), .sel(2'b11));
  Multiplexer #(.width(32), .enable("false")) multiplexer_4 (
    .in0(multiplexer_3_out), .in1(adder_4_out), .out(out_3), .sel(bitselector_4_out));
endmodule

module new32_32 (
  input  [31:0] in_1,
  input  [31:0] in_2,
  output [31:0] out_3
);

  wire [3:0] bitselector_1_out, bitselector_2_out, bitselector_3_out, bitselector_4_out, bitselector_5_out,
       bitselector_6_out, bitselector_7_out, bitselector_8_out;
  wire [31:0] adder_1_out, adder_2_out, adder_3_out, adder_4_out, adder_5_out, adder_6_out, new_1_out_3,
       new_2_out_3, new_3_out_3, new_4_out_3, new_5_out_3, new_6_out_3, new_7_out_3, new_8_out_3,
       shifter_1_out, shifter_2_out, shifter_3_out, shifter_4_out, shifter_5_out, shifter_6_out,
       shifter_7_out, shifter_8_out;

  BitSelector #(.width(32), .group(4)) bitselector_1 (.in(in_1), .out(bitselector_1_out), .sel(3'b000));
  \new  new_1 (.in_1(bitselector_1_out), .in_2(in_2), .out_3(new_1_out_3));
  Shifter #(.width(32)) shifter_1 (.in(new_1_out_3), .\dist ({5{1'b0}}), .out(shifter_1_out));
  BitSelector #(.width(32), .group(4)) bitselector_2 (.in(in_1), .out(bitselector_2_out), .sel(3'b001));
  \new  new_2 (.in_1(bitselector_2_out), .in_2(in_2), .out_3(new_2_out_3));
  Shifter #(.width(32)) shifter_2 (.in(new_2_out_3), .\dist (5'b00100), .out(shifter_2_out));
  BitSelector #(.width(32), .group(4)) bitselector_3 (.in(in_1), .out(bitselector_3_out), .sel(3'b010));
  Adder #(.width(32)) adder_1 (.a(shifter_2_out), .b(shifter_1_out), .out(adder_1_out), .cin(1'b0));  // open: cout
  \new  new_3 (.in_1(bitselector_3_out), .in_2(in_2), .out_3(new_3_out_3));
  Shifter #(.width(32)) shifter_3 (.in(new_3_out_3), .\dist (5'b01000), .out(shifter_3_out));
  BitSelector #(.width(32), .group(4)) bitselector_4 (.in(in_1), .out(bitselector_4_out), .sel(3'b011));
  Adder #(.width(32)) adder_2 (.a(shifter_3_out), .b(adder_1_out), .out(adder_2_out), .cin(1'b0));  // open: cout
  \new  new_4 (.in_1(bitselector_4_out), .in_2(in_2), .out_3(new_4_out_3));
  Shifter #(.width(32)) shifter_4 (.in(new_4_out_3), .\dist (5'b01100), .out(shifter_4_out));
  BitSelector #(.width(32), .group(4)) bitselector_5 (.in(in_1), .out(bitselector_5_out), .sel(3'b100));
  \new  new_5 (.in_1(bitselector_5_out), .in_2(in_2), .out_3(new_5_out_3));
  Adder #(.width(32)) adder_3 (.a(shifter_4_out), .b(adder_2_out), .out(adder_3_out), .cin(1'b0));  // open: cout
  Shifter #(.width(32)) shifter_5 (.in(new_5_out_3), .\dist (5'b10000), .out(shifter_5_out));
  BitSelector #(.width(32), .group(4)) bitselector_6 (.in(in_1), .out(bitselector_6_out), .sel(3'b101));
  \new  new_6 (.in_1(bitselector_6_out), .in_2(in_2), .out_3(new_6_out_3));
  Adder #(.width(32)) adder_4 (.a(shifter_5_out), .b(adder_3_out), .out(adder_4_out), .cin(1'b0));  // open: cout
  BitSelector #(.width(32), .group(4)) bitselector_7 (.in(in_1), .out(bitselector_7_out), .sel(3'b110));
  Shifter #(.width(32)) shifter_6 (.in(new_6_out_3), .\dist (5'b10100), .out(shifter_6_out));
  \new  new_7 (.in_1(bitselector_7_out), .in_2(in_2), .out_3(new_7_out_3));
  Adder #(.width(32)) adder_5 (.a(shifter_6_out), .b(adder_4_out), .out(adder_5_out), .cin(1'b0));  // open: cout
  BitSelector #(.width(32), .group(4)) bitselector_8 (.in(in_1), .out(bitselector_8_out), .sel(3'b111));
  Shifter #(.width(32)) shifter_7 (.in(new_7_out_3), .\dist (5'b11000), .out(shifter_7_out));
  \new  new_8 (.in_1(bitselector_8_out), .in_2(in_2), .out_3(new_8_out_3));
  Shifter #(.width(32)) shifter_8 (.in(new_8_out_3), .\dist (5'b11100), .out(shifter_8_out));
  Adder #(.width(32)) adder_6 (.a(shifter_7_out), .b(adder_5_out), .out(adder_6_out), .cin(1'b0));  // open: cout
  Adder #(.width(32)) adder_7 (.a(shifter_8_out), .b(adder_6_out), .out(out_3), .cin(1'b0));  // open: cout
endmodule

module new_test (
  output [31:0] out_1
);

  new32_32 new32_32_1 (.in_1(32'h5462), .in_2(32'h4321), .out_3(out_1));
endmodule
