// Logisim project 2_2.circ as structural Verilog: 5 circuits, main circuit main
module main (
  input  [3:0] n2,
  input  [3:0] d,
  output [3:0] \余数 ,
  output [3:0] \商 
);

  wire [7:0] bit_extender_1_out, \基本单元_1_output , \基本单元_2_output , \基本单元_3_output , \基本单元_4_output ;

  assign bit_extender_1_out = {{4{1'b0}}, n2};  // Bit_Extender bit_extender_1
  \基本单元  \u_基本单元_1  (.\input (bit_extender_1_out), .d(d), .\output (\基本单元_1_output ));
  \基本单元  \u_基本单元_2  (.\input (\基本单元_1_output ), .d(d), .\output (\基本单元_2_output ));
  \基本单元  \u_基本单元_3  (.\input (\基本单元_2_output ), .d(d), .\output (\基本单元_3_output ));
  \基本单元  \u_基本单元_4  (.\input (\基本单元_3_output ), .d(d), .\output (\基本单元_4_output ));
  BitSelector #(.group(4)) bitselector_1 (.in(\基本单元_4_output ), .out(\余数 ), .sel(1'b1));
  BitSelector #(.group(4)) bitselector_2 (.in(\基本单元_4_output ), .out(\商 ), .sel(1'b0));
endmodule

module \基本单元  (
  input  [7:0] \input ,
  input  [3:0] d,
  output [7:0] \output 
);

  wire comparator_1_lt;
  wire [3:0] bitselector_1_out, bitselector_2_out, multiplexer_1_out, multiplexer_2_out, or_1_out,
       subtractor_1_out;
  wire [7:0] bit_extender_1_out, bit_extender_2_out, shifter_1_out, shifter_2_out;

  Shifter shifter_1 (.in(\input ), .\dist (3'b001), .out(shifter_1_out));
  BitSelector #(.group(4)) bitselector_1 (.in(shifter_1_out), .out(bitselector_1_out), .sel(1'b0));
  BitSelector #(.group(4)) bitselector_2 (.in(shifter_1_out), .out(bitselector_2_out), .sel(1'b1));
  Comparator #(.width(4), .mode("unsigned")) comparator_1 (
    .a(bitselector_2_out), .b(d), .lt(comparator_1_lt));  // open: gt, eq
  Multiplexer #(.width(4), .enable("false")) multiplexer_1 (
    .in0(d), .in1(4'b0000), .out(multiplexer_1_out), .sel(comparator_1_lt));
  Multiplexer #(.width(4), .enable("false")) multiplexer_2 (
    .in0(4'b0001), .in1(4'b0000), .out(multiplexer_2_out), .sel(comparator_1_lt));
  Subtractor #(.width(4)) subtractor_1 (
    .a(bitselector_2_out), .b(multiplexer_1_out), .out(subtractor_1_out), .bin(1'b0));  // open: bout
  assign bit_extender_1_out = {{4{1'b0}}, subtractor_1_out};  // Bit_Extender bit_extender_1
  assign or_1_out = bitselector_1_out | multiplexer_2_out;  // OR_Gate or_1, 4 bits wide
  Shifter shifter_2 (.in(bit_extender_1_out), .\dist (3'b100), .out(shifter_2_out));
  assign bit_extender_2_out = {{4{1'b0}}, or_1_out};  // Bit_Extender bit_extender_2
  assign \output  = shifter_2_out | bit_extender_2_out;  // OR_Gate or_2, 8 bits wide
endmodule

module \基本单元x32  (
  input  [31:0] \n2_被除数 ,
  input  [31:0] in_2,
  input  [31:0] \d_除数 ,
  output [31:0] n2,
  output [31:0] n1
);

  wire bitselector_1_out, comparator_1_lt;
  wire [31:0] bit_extender_1_out, multiplexer_1_out, multiplexer_2_out, or_1_out, shifter_1_out,
       shifter_2_out;

  BitSelector #(.width(32)) bitselector_1 (.in(\n2_被除数 ), .out(bitselector_1_out), .sel({5{1'b1}}));
  assign bit_extender_1_out = {{31{1'b0}}, bitselector_1_out};  // Bit_Extender bit_extender_1
  Shifter #(.width(32)) shifter_1 (.in(in_2), .\dist (5'b00001), .out(shifter_1_out));
  Shifter #(.width(32)) shifter_2 (.in(\n2_被除数 ), .\dist (5'b00001), .out(shifter_2_out));
  assign or_1_out = bit_extender_1_out | shifter_1_out;  // OR_Gate or_1, 32 bits wide
  Comparator #(.width(32), .mode("unsigned")) comparator_1 (
    .a(or_1_out), .b(\d_除数 ), .lt(comparator_1_lt));  // open: gt, eq
  Multiplexer #(.width(32), .enable("false")) multiplexer_1 (
    .in0(32'h1), .in1({32{1'b0}}), .out(multiplexer_1_out), .sel(comparator_1_lt));
  Multiplexer #(.width(32), .enable("false")) multiplexer_2 (
    .in0(\d_除数 ), .in1({32{1'b0}}), .out(multiplexer_2_out), .sel(comparator_1_lt));
  assign n2 = shifter_2_out | multiplexer_1_out;  // OR_Gate or_2, 32 bits wide
  Subtractor #(.width(32)) subtractor_1 (.a(or_1_out), .b(multiplexer_2_out), .out(n1), .bin(1'b0));  // open: bout
endmodule

module \_32位除法器  (
  input  [31:0] \n2_被除数 ,
  input  [31:0] \d_除数 ,
  output [31:0] \余数 ,
  output [31:0] \商 
);

  wire [31:0] \基本单元x32_1_n1 , \基本单元x32_1_n2 , \基本单元x32_2_n1 , \基本单元x32_2_n2 , \基本单元x32_3_n1 , \基本单元x32_3_n2 ,
       \基本单元x32_4_n1 , \基本单元x32_4_n2 , \基本单元x32_5_n1 , \基本单元x32_5_n2 , \基本单元x32_6_n1 , \基本单元x32_6_n2 ,
       \基本单元x32_7_n1 , \基本单元x32_7_n2 , \基本单元x32_8_n1 , \基本单元x32_8_n2 , \基本单元x32_9_n1 , \基本单元x32_9_n2 ,
       \基本单元x32_10_n1 , \基本单元x32_10_n2 , \基本单元x32_11_n1 , \基本单元x32_11_n2 , \基本单元x32_12_n1 , \基本单元x32_12_n2 ,
       \基本单元x32_13_n1 , \基本单元x32_13_n2 , \基本单元x32_14_n1 , \基本单元x32_14_n2 , \基本单元x32_15_n1 , \基本单元x32_15_n2 ,
       \基本单元x32_16_n1 , \基本单元x32_16_n2 , \基本单元x32_17_n1 , \基本单元x32_17_n2 , \基本单元x32_18_n1 , \基本单元x32_18_n2 ,
       \基本单元x32_19_n1 , \基本单元x32_19_n2 , \基本单元x32_20_n1 , \基本单元x32_20_n2 , \基本单元x32_21_n1 , \基本单元x32_21_n2 ,
       \基本单元x32_22_n1 , \基本单元x32_22_n2 , \基本单元x32_23_n1 , \基本单元x32_23_n2 , \基本单元x32_24_n1 , \基本单元x32_24_n2 ,
       \基本单元x32_25_n1 , \基本单元x32_25_n2 , \基本单元x32_26_n1 , \基本单元x32_26_n2 , \基本单元x32_27_n1 , \基本单元x32_27_n2 ,
       \基本单元x32_28_n1 , \基本单元x32_28_n2 , \基本单元x32_29_n1 , \基本单元x32_29_n2 , \基本单元x32_30_n1 , \基本单元x32_30_n2 ,
       \基本单元x32_31_n1 , \基本单元x32_31_n2 ;

  \基本单元x32  \u_基本单元x32_1  (
    .\n2_被除数 (\n2_被除数 ), .in_2({32{1'b0}}), .\d_除数 (\d_除数 ), .n2(\基本单元x32_1_n2 ), .n1(\基本单元x32_1_n1 ));
  \基本单元x32  \u_基本单元x32_2  (
    .\n2_被除数 (\基本单元x32_1_n2 ), .in_2(\基本单元x32_1_n1 ), .\d_除数 (\d_除数 ), .n2(\基本单元x32_2_n2 ),
    .n1(\基本单元x32_2_n1 ));
  \基本单元x32  \u_基本单元x32_3  (
    .\n2_被除数 (\基本单元x32_2_n2 ), .in_2(\基本单元x32_2_n1 ), .\d_除数 (\d_除数 ), .n2(\基本单元x32_3_n2 ),
    .n1(\基本单元x32_3_n1 ));
  \基本单元x32  \u_基本单元x32_4  (
    .\n2_被除数 (\基本单元x32_3_n2 ), .in_2(\基本单元x32_3_n1 ), .\d_除数 (\d_除数 ), .n2(\基本单元x32_4_n2 ),
    .n1(\基本单元x32_4_n1 ));
  \基本单元x32  \u_基本单元x32_5  (
    .\n2_被除数 (\基本单元x32_4_n2 ), .in_2(\基本单元x32_4_n1 ), .\d_除数 (\d_除数 ), .n2(\基本单元x32_5_n2 ),
    .n1(\基本单元x32_5_n1 ));
  \基本单元x32  \u_基本单元x32_6  (
    .\n2_被除数 (\基本单元x32_5_n2 ), .in_2(\基本单元x32_5_n1 ), .\d_除数 (\d_除数 ), .n2(\基本单元x32_6_n2 ),
    .n1(\基本单元x32_6_n1 ));
  \基本单元x32  \u_基本单元x32_7  (
    .\n2_被除数 (\基本单元x32_6_n2 ), .in_2(\基本单元x32_6_n1 ), .\d_除数 (\d_除数 ), .n2(\基本单元x32_7_n2 ),
    .n1(\基本单元x32_7_n1 ));
  \基本单元x32  \u_基本单元x32_8  (
    .\n2_被除数 (\基本单元x32_9_n2 ), .in_2(\基本单元x32_9_n1 ), .\d_除数 (\d_除数 ), .n2(\基本单元x32_8_n2 ),
    .n1(\基本单元x32_8_n1 ));
  \基本单元x32  \u_基本单元x32_9  (
    .\n2_被除数 (\基本单元x32_7_n2 ), .in_2(\基本单元x32_7_n1 ), .\d_除数 (\d_除数 ), .n2(\基本单元x32_9_n2 ),
    .n1(\基本单元x32_9_n1 ));
  \基本单元x32  \u_基本单元x32_10  (
    .\n2_被除数 (\基本单元x32_8_n2 ), .in_2(\基本单元x32_8_n1 ), .\d_除数 (\d_除数 ), .n2(\基本单元x32_10_n2 ),
    .n1(\基本单元x32_10_n1 ));
  \基本单元x32  \u_基本单元x32_11  (
    .\n2_被除数 (\基本单元x32_12_n2 ), .in_2(\基本单元x32_12_n1 ), .\d_除数 (\d_除数 ), .n2(\基本单元x32_11_n2 ),
    .n1(\基本单元x32_11_n1 ));
  \基本单元x32  \u_基本单元x32_12  (
    .\n2_被除数 (\基本单元x32_10_n2 ), .in_2(\基本单元x32_10_n1 ), .\d_除数 (\d_除数 ), .n2(\基本单元x32_12_n2 ),
    .n1(\基本单元x32_12_n1 ));
  \基本单元x32  \u_基本单元x32_13  (
    .\n2_被除数 (\基本单元x32_11_n2 ), .in_2(\基本单元x32_11_n1 ), .\d_除数 (\d_除数 ), .n2(\基本单元x32_13_n2 ),
    .n1(\基本单元x32_13_n1 ));
  \基本单元x32  \u_基本单元x32_14  (
    .\n2_被除数 (\基本单元x32_13_n2 ), .in_2(\基本单元x32_13_n1 ), .\d_除数 (\d_除数 ), .n2(\基本单元x32_14_n2 ),
    .n1(\基本单元x32_14_n1 ));
  \基本单元x32  \u_基本单元x32_15  (
    .\n2_被除数 (\基本单元x32_14_n2 ), .in_2(\基本单元x32_14_n1 ), .\d_除数 (\d_除数 ), .n2(\基本单元x32_15_n2 ),
    .n1(\基本单元x32_15_n1 ));
  \基本单元x32  \u_基本单元x32_16  (
    .\n2_被除数 (\基本单元x32_17_n2 ), .in_2(\基本单元x32_17_n1 ), .\d_除数 (\d_除数 ), .n2(\基本单元x32_16_n2 ),
    .n1(\基本单元x32_16_n1 ));
  \基本单元x32  \u_基本单元x32_17  (
    .\n2_被除数 (\基本单元x32_15_n2 ), .in_2(\基本单元x32_15_n1 ), .\d_除数 (\d_除数 ), .n2(\基本单元x32_17_n2 ),
    .n1(\基本单元x32_17_n1 ));
  \基本单元x32  \u_基本单元x32_18  (
    .\n2_被除数 (\基本单元x32_16_n2 ), .in_2(\基本单元x32_16_n1 ), .\d_除数 (\d_除数 ), .n2(\基本单元x32_18_n2 ),
    .n1(\基本单元x32_18_n1 ));
  \基本单元x32  \u_基本单元x32_19  (
    .\n2_被除数 (\基本单元x32_20_n2 ), .in_2(\基本单元x32_20_n1 ), .\d_除数 (\d_除数 ), .n2(\基本单元x32_19_n2 ),
    .n1(\基本单元x32_19_n1 ));
  \基本单元x32  \u_基本单元x32_20  (
    .\n2_被除数 (\基本单元x32_18_n2 ), .in_2(\基本单元x32_18_n1 ), .\d_除数 (\d_除数 ), .n2(\基本单元x32_20_n2 ),
    .n1(\基本单元x32_20_n1 ));
  \基本单元x32  \u_基本单元x32_21  (
    .\n2_被除数 (\基本单元x32_19_n2 ), .in_2(\基本单元x32_19_n1 ), .\d_除数 (\d_除数 ), .n2(\基本单元x32_21_n2 ),
    .n1(\基本单元x32_21_n1 ));
  \基本单元x32  \u_基本单元x32_22  (
    .\n2_被除数 (\基本单元x32_21_n2 ), .in_2(\基本单元x32_21_n1 ), .\d_除数 (\d_除数 ), .n2(\基本单元x32_22_n2 ),
    .n1(\基本单元x32_22_n1 ));
  \基本单元x32  \u_基本单元x32_23  (
    .\n2_被除数 (\基本单元x32_22_n2 ), .in_2(\基本单元x32_22_n1 ), .\d_除数 (\d_除数 ), .n2(\基本单元x32_23_n2 ),
    .n1(\基本单元x32_23_n1 ));
  \基本单元x32  \u_基本单元x32_24  (
    .\n2_被除数 (\基本单元x32_25_n2 ), .in_2(\基本单元x32_25_n1 ), .\d_除数 (\d_除数 ), .n2(\基本单元x32_24_n2 ),
    .n1(\基本单元x32_24_n1 ));
  \基本单元x32  \u_基本单元x32_25  (
    .\n2_被除数 (\基本单元x32_23_n2 ), .in_2(\基本单元x32_23_n1 ), .\d_除数 (\d_除数 ), .n2(\基本单元x32_25_n2 ),
    .n1(\基本单元x32_25_n1 ));
  \基本单元x32  \u_基本单元x32_26  (
    .\n2_被除数 (\基本单元x32_24_n2 ), .in_2(\基本单元x32_24_n1 ), .\d_除数 (\d_除数 ), .n2(\基本单元x32_26_n2 ),
    .n1(\基本单元x32_26_n1 ));
  \基本单元x32  \u_基本单元x32_27  (
    .\n2_被除数 (\基本单元x32_26_n2 ), .in_2(\基本单元x32_26_n1 ), .\d_除数 (\d_除数 ), .n2(\基本单元x32_27_n2 ),
    .n1(\基本单元x32_27_n1 ));
  \基本单元x32  \u_基本单元x32_28  (
    .\n2_被除数 (\基本单元x32_27_n2 ), .in_2(\基本单元x32_27_n1 ), .\d_除数 (\d_除数 ), .n2(\基本单元x32_28_n2 ),
    .n1(\基本单元x32_28_n1 ));
  \基本单元x32  \u_基本单元x32_29  (
    .\n2_被除数 (\基本单元x32_28_n2 ), .in_2(\基本单元x32_28_n1 ), .\d_除数 (\d_除数 ), .n2(\基本单元x32_29_n2 ),
    .n1(\基本单元x32_29_n1 ));
  \基本单元x32  \u_基本单元x32_30  (
    .\n2_被除数 (\基本单元x32_29_n2 ), .in_2(\基本单元x32_29_n1 ), .\d_除数 (\d_除数 ), .n2(\基本单元x32_30_n2 ),
    .n1(\基本单元x32_30_n1 ));
  \基本单元x32  \u_基本单元x32_31  (
    .\n2_被除数 (\基本单元x32_30_n2 ), .in_2(\基本单元x32_30_n1 ), .\d_除数 (\d_除数 ), .n2(\基本单元x32_31_n2 ),
    .n1(\基本单元x32_31_n1 ));
  \基本单元x32  \u_基本单元x32_32  (.\n2_被除数 (\基本单元x32_31_n2 ), .in_2(\基本单元x32_31_n1 ), .\d_除数 (\d_除数 ), .n2(\商 ), .n1(\余数 ));
endmodule

module test (
  output [31:0] \余数 ,
  output [31:0] \商 
);

  \_32位除法器  \u_32位除法器_1  (.\n2_被除数 ({32{1'b1}}), .\d_除数 ({32{1'b1}}), .\余数 (\余数 ), .\商 (\商 ));

  // Notes on the sheet:
  //   被除数
  //   除数
endmodule
