// Logisim project 3.circ as structural Verilog: 13 circuits, main circuit 模60计数器(new2)
module \模60计数器_new2  (
  input  in_1,
  input  in_2,
  input  in_3,
  input  in_4,
  output out_5,
  output out_6,
  output out_7,
  output out_8,
  output out_9,
  output out_10,
  output out_11,
  output out_12,
  output out_13
);

  wire and_1_out, or_1_out, or_2_out, \模10计数器_1_out_8 , \模10计数器_1_out_9 ;

  or or_1 (or_1_out, out_13, in_2);
  and and_1 (and_1_out, in_3, or_2_out, in_4);
  \模10计数器  \u_模10计数器_1  (
    .CPd(and_1_out), .CLR(or_1_out), .CPu(in_1), .Qa(out_8), .Qb(out_7), .Qc(out_6), .Qd(out_5),
    .out_9(\模10计数器_1_out_9 ), .out_8(\模10计数器_1_out_8 ));
  or or_2 (or_2_out, out_8, out_7, out_6, out_5, out_9, out_10, out_11, out_12);
  and and_2 (out_13, out_11, out_10);
  \模10计数器  \u_模10计数器_2  (
    .CPd(\模10计数器_1_out_8 ), .CLR(or_1_out), .CPu(\模10计数器_1_out_9 ), .Qa(out_12), .Qb(out_11), .Qc(out_10),
    .Qd(out_9));  // open: out_9, out_8
endmodule

module \模10计数器  (
  input  CPd,
  input  CLR,
  input  CPu,
  output Qa,
  output Qb,
  output Qc,
  output Qd,
  output out_8,
  output out_9
);

  wire and_1_out, and_2_out, and_3_out, and_4_out, and_5_out, and_6_out, C1_out, not_1_out, not_2_out,
       not_3_out, not_4_out, not_5_out, not_6_out, or_1_out, or_2_out, or_3_out, or_4_out, or_5_out, or_6_out;

  or or_1 (or_1_out, CLR, out_9);
  not not_1 (not_1_out, Qa);
  not not_2 (not_2_out, Qb);
  not not_3 (not_3_out, Qc);
  or C1 (C1_out, CPd, CPu);
  and and_1 (and_1_out, Qa, CPu);
  and and_2 (and_2_out, not_1_out, CPd);
  and and_3 (and_3_out, Qa, Qb, CPu);
  and and_4 (and_4_out, not_1_out, not_2_out, CPd);
  and and_5 (and_5_out, Qa, Qb, Qc, CPu);
  and and_6 (and_6_out, not_2_out, not_1_out, not_3_out, CPd);
  or or_2 (or_2_out, and_1_out, and_2_out);
  or or_3 (or_3_out, and_3_out, and_4_out);
  or or_4 (or_4_out, and_5_out, and_6_out);
  D_Flip_Flop #(.trigger("falling")) D1 (
    .clk(C1_out), .D(not_1_out), .Q(Qa), .preset(out_8), .reset(or_1_out));  // open: Qn, en
  D_Flip_Flop #(.trigger("falling")) D2 (
    .clk(or_2_out), .D(not_2_out), .Q(Qb), .reset(or_5_out));  // open: Qn, preset, en
  D_Flip_Flop #(.trigger("falling")) D3 (
    .clk(or_3_out), .D(not_3_out), .Q(Qc), .reset(or_6_out));  // open: Qn, preset, en
  D_Flip_Flop #(.trigger("falling")) D4 (
    .clk(or_4_out), .D(not_4_out), .Q(Qd), .preset(out_8), .reset(or_1_out));  // open: Qn, en
  not not_4 (not_4_out, Qd);
  or or_5 (or_5_out, or_1_out, out_8);
  or or_6 (or_6_out, or_1_out, out_8);
  and and_7 (out_8, Qb, Qc, Qd, Qa);
  not not_5 (not_5_out, Qa);
  not not_6 (not_6_out, Qc);
  and and_8 (out_9, not_5_out, Qb, not_6_out, Qd);
endmodule

module \上午下午显示  (
  input  AM_FM,
  input  TT,
  output [4:0] out_3,
  output [4:0] out_4,
  output [4:0] out_5,
  output [4:0] out_6
);

  wire [4:0] and_1_out, and_2_out, and_3_out, and_4_out, and_5_out, and_6_out, and_7_out, and_8_out,
       multiplexer_1_out, multiplexer_2_out, not_1_out, not_2_out, not_3_out, not_4_out;

  Multiplexer #(.width(5), .enable("false")) multiplexer_1 (
    .in0({5{1'b0}}), .in1({5{1'b1}}), .out(multiplexer_1_out), .sel(AM_FM));
  Multiplexer #(.width(5), .enable("false")) multiplexer_2 (
    .in0({5{1'b0}}), .in1({5{1'b1}}), .out(multiplexer_2_out), .sel(TT));
  assign and_1_out = multiplexer_1_out & 5'b10000 & multiplexer_2_out;  // AND_Gate and_1, 5 bits wide
  assign and_2_out = multiplexer_1_out & {5{1'b1}} & multiplexer_2_out;  // AND_Gate and_2, 5 bits wide
  assign and_3_out = multiplexer_1_out & 5'b10100 & multiplexer_2_out;  // AND_Gate and_3, 5 bits wide
  assign and_4_out = multiplexer_1_out & 5'b10000 & multiplexer_2_out;  // AND_Gate and_4, 5 bits wide
  assign and_5_out = 5'b00001 & not_1_out & multiplexer_2_out;  // AND_Gate and_5, 5 bits wide
  assign not_1_out = ~multiplexer_1_out;  // NOT_Gate not_1, 5 bits wide
  assign not_2_out = ~multiplexer_1_out;  // NOT_Gate not_2, 5 bits wide
  assign and_6_out = {5{1'b1}} & not_2_out & multiplexer_2_out;  // AND_Gate and_6, 5 bits wide
  assign not_3_out = ~multiplexer_1_out;  // NOT_Gate not_3, 5 bits wide
  assign and_7_out = 5'b00101 & not_3_out & multiplexer_2_out;  // AND_Gate and_7, 5 bits wide
  assign not_4_out = ~multiplexer_1_out;  // NOT_Gate not_4, 5 bits wide
  assign and_8_out = 5'b00001 & not_4_out & multiplexer_2_out;  // AND_Gate and_8, 5 bits wide
  assign out_3 = and_5_out | and_1_out;  // OR_Gate or_1, 5 bits wide
  assign out_4 = and_6_out | and_2_out;  // OR_Gate or_2, 5 bits wide
  assign out_5 = and_7_out | and_3_out;  // OR_Gate or_3, 5 bits wide
  assign out_6 = and_8_out | and_4_out;  // OR_Gate or_4, 5 bits wide
endmodule

module \_12_24计数器  (
  input  Set,
  input  in_2,
  input  in_3,
  input  in_4,
  input  in_5,
  output \进位 ,
  output out_7,
  output out_8,
  output out_9,
  output out_10,
  output out_11,
  output out_12,
  output out_13,
  output out_14
);

  wire and_1_out, and_2_out, and_3_out, and_4_out, not_1_out, not_2_out, not_3_out, or_1_out;

  or or_1 (or_1_out, \进位 , in_3);
  and and_1 (and_1_out, not_1_out, and_2_out);
  not not_1 (not_1_out, Set);
  and and_2 (and_2_out, out_9, not_3_out, out_14);
  or or_2 (\进位 , and_1_out, and_3_out);
  and and_3 (and_3_out, Set, and_4_out);
  and and_4 (and_4_out, not_3_out, out_8, not_2_out, out_13);
  not not_2 (not_2_out, out_9);
  not not_3 (not_3_out, out_10);
  \模60计数器_new2  \u_模60计数器_new2_1  (
    .in_1(in_2), .in_2(or_1_out), .in_3(in_4), .in_4(in_5), .out_5(out_7), .out_6(out_8), .out_7(out_9),
    .out_8(out_10), .out_9(out_11), .out_10(out_12), .out_11(out_13), .out_12(out_14));  // open: out_13
endmodule

module \_12_24测试  (
  input  in_1,
  input  in_2,
  input  in_3,
  input  in_4,
  input  in_5,
  output out_6
);

  wire [3:0] \n12_24计数器_1_out_10 , \n12_24计数器_1_out_14 ;

  Hex_Digit_Display hex_digit_display_1 (.value(\n12_24计数器_1_out_14 ));  // open: dp
  Hex_Digit_Display hex_digit_display_2 (.value(\n12_24计数器_1_out_10 ));  // open: dp
  \_12_24计数器  \u_12_24计数器_1  (
    .in_2(in_1), .in_3(in_2), .in_4(in_3), .in_5(in_4), .\进位 (out_6), .out_7(\n12_24计数器_1_out_10 [3]),
    .out_8(\n12_24计数器_1_out_10 [2]), .out_9(\n12_24计数器_1_out_10 [1]), .out_10(\n12_24计数器_1_out_10 [0]),
    .out_11(\n12_24计数器_1_out_14 [3]), .out_12(\n12_24计数器_1_out_14 [2]), .out_13(\n12_24计数器_1_out_14 [1]),
    .out_14(\n12_24计数器_1_out_14 [0]), .Set(in_5));
endmodule

module \整点报时  (
  input  in_1,
  input  in_2,
  input  in_3,
  input  in_4,
  input  in_5,
  input  in_6,
  input  in_7,
  input  in_8,
  input  in_9,
  input  in_10,
  input  in_11,
  input  in_12,
  input  \time ,
  output out_14
);

  wire and_1_out, and_2_out, and_4_out, not_1_out, not_2_out, not_3_out, not_4_out, not_5_out, not_6_out;

  not not_1 (not_1_out, in_1);
  and and_1 (and_1_out, not_1_out, in_2, not_2_out, in_4);
  not not_2 (not_2_out, in_3);
  and and_2 (and_2_out, in_5, not_3_out, not_4_out, in_8);
  not not_3 (not_3_out, in_6);
  and and_3 (out_14, and_1_out, and_2_out, and_4_out, \time );
  not not_4 (not_4_out, in_7);
  not not_5 (not_5_out, in_9);
  and and_4 (and_4_out, not_5_out, in_10, not_6_out, in_12);
  not not_6 (not_6_out, in_11);

  // Notes on the sheet:
  //   5
  //   9
  //   5
endmodule

module \脉冲电路  (
  input  in_1,
  output out_2
);

  wire not_1_out, not_2_out, not_3_out, \模10计数器_1_qa , \模10计数器_1_qb , \模10计数器_1_qc , \模10计数器_1_qd ;

  and and_1 (out_2, not_1_out, \模10计数器_1_qc , not_2_out, not_3_out);
  not not_1 (not_1_out, \模10计数器_1_qd );
  not not_2 (not_2_out, \模10计数器_1_qb );
  not not_3 (not_3_out, \模10计数器_1_qa );
  \模10计数器  \u_模10计数器_1  (
    .CPd(1'b0), .CLR(out_2), .CPu(in_1), .Qa(\模10计数器_1_qa ), .Qb(\模10计数器_1_qb ), .Qc(\模10计数器_1_qc ),
    .Qd(\模10计数器_1_qd ));  // open: out_9, out_8
endmodule

module \时钟电路  (
  input  [7:0] min,
  input  [7:0] h,
  input  CPu,
  input  CP,
  input  in_5,
  input  CPd,
  input  in_7,
  input  Adj0,
  input  Adj1,
  output [4:0] out_10,
  output [4:0] out_11,
  output [4:0] out_12,
  output [4:0] out_13,
  output \闹钟 ,
  output [3:0] out_15,
  output [3:0] out_16,
  output [3:0] out_17,
  output [3:0] out_18,
  output \报时 ,
  output [3:0] out_20,
  output [3:0] out_21
);

  wire and_1_out, and_2_out, and_3_out, and_4_out, and_5_out, and_7_out, \n12_24计数器_new_1_进位 , not_1_out,
       not_2_out, not_3_out, or_1_out, or_2_out, t_ff_1_q, \模60计数器_new2_1_out_13 , \模60计数器_new2_2_out_13 ,
       \脉冲电路_1_out_2 ;
  wire [3:0] and_6_out, bitselector_1_out, bitselector_2_out, bitselector_3_out, bitselector_4_out,
       nor_1_out, nor_2_out, subtractor_1_out, subtractor_2_out, subtractor_3_out, subtractor_4_out;

  \脉冲电路  \u_脉冲电路_1  (.out_2(\脉冲电路_1_out_2 ), .in_1(CP));
  and and_1 (and_1_out, Adj0, Adj1);
  not not_1 (not_1_out, Adj1);
  and and_2 (and_2_out, not_1_out, Adj0);
  \模60计数器_new2  \u_模60计数器_new2_1  (
    .in_1(\脉冲电路_1_out_2 ), .in_2(in_5), .in_3(CPd), .out_13(\模60计数器_new2_1_out_13 ), .out_5(out_15[3]),
    .out_6(out_15[2]), .out_7(out_15[1]), .out_8(out_15[0]), .out_9(out_16[3]), .out_10(out_16[2]),
    .out_11(out_16[1]), .out_12(out_16[0]));  // open: in_4
  \整点报时  \u_整点报时_1  (
    .out_14(\报时 ), .in_1(out_16[3]), .in_2(out_16[2]), .in_3(out_16[1]), .in_4(out_16[0]), .in_5(out_17[3]),
    .in_6(out_17[2]), .in_7(out_17[1]), .in_8(out_17[0]), .in_9(out_18[3]), .in_10(out_18[2]),
    .in_11(out_18[1]), .in_12(out_18[0]), .\time (CP));
  and and_3 (and_3_out, CPu, and_1_out);
  or or_1 (or_1_out, and_3_out, \模60计数器_new2_1_out_13 );
  and and_4 (and_4_out, and_1_out, CPd);
  BitSelector #(.group(4)) bitselector_1 (.in(min), .out(bitselector_1_out), .sel(1'b1));
  BitSelector #(.group(4)) bitselector_2 (.in(min), .out(bitselector_2_out), .sel(1'b0));
  Subtractor #(.width(4)) subtractor_1 (.a(bitselector_1_out), .b(out_17), .out(subtractor_1_out));  // open: bin, bout
  Subtractor #(.width(4)) subtractor_2 (.a(bitselector_2_out), .b(out_18), .out(subtractor_2_out));  // open: bin, bout
  not not_2 (not_2_out, out_16[0]);
  assign nor_1_out = ~(subtractor_2_out | subtractor_1_out);  // NOR_Gate nor_1, 4 bits wide
  BitSelector #(.group(4)) bitselector_3 (.in(h), .out(bitselector_3_out), .sel(1'b1));
  and and_5 (and_5_out, CPu, and_2_out);
  \模60计数器_new2  \u_模60计数器_new2_2  (
    .in_1(or_1_out), .in_2(in_5), .in_3(and_4_out), .in_4(and_1_out), .out_13(\模60计数器_new2_2_out_13 ),
    .out_5(out_17[3]), .out_6(out_17[2]), .out_7(out_17[1]), .out_8(out_17[0]), .out_9(out_18[3]),
    .out_10(out_18[2]), .out_11(out_18[1]), .out_12(out_18[0]));
  assign and_6_out = nor_1_out & nor_2_out;  // AND_Gate and_6, 4 bits wide
  or or_2 (or_2_out, and_5_out, \模60计数器_new2_2_out_13 );
  and and_7 (and_7_out, and_2_out, CPd);
  BitSelector #(.group(4)) bitselector_4 (.in(h), .out(bitselector_4_out), .sel(1'b0));
  Subtractor #(.width(4)) subtractor_3 (.a(bitselector_3_out), .b(out_20), .out(subtractor_3_out));  // open: bin, bout
  and and_8 (\闹钟 , not_2_out, CP, and_6_out[0], and_6_out[1], and_6_out[2], and_6_out[3]);
  Subtractor #(.width(4)) subtractor_4 (.a(bitselector_4_out), .b(out_21), .out(subtractor_4_out));  // open: bin, bout
  T_Flip_Flop t_ff_1 (.clk(\n12_24计数器_new_1_进位 ), .T(1'b1), .Q(t_ff_1_q), .preset(in_5));  // open: Qn, reset, en
  \_12_24计数器_new  \u_12_24计数器_new_1  (
    .in_2(or_2_out), .in_3(in_5), .in_4(and_7_out), .in_5(and_2_out), .\进位 (\n12_24计数器_new_1_进位 ),
    .out_6(out_20[3]), .out_7(out_20[2]), .out_8(out_20[1]), .out_9(out_20[0]), .out_10(out_21[3]),
    .out_11(out_21[2]), .out_12(out_21[1]), .out_13(out_21[0]), .in_1(in_7));
  \上午下午显示  \u_上午下午显示_1  (
    .AM_FM(t_ff_1_q), .TT(not_3_out), .out_3(out_13), .out_4(out_12), .out_5(out_11), .out_6(out_10));
  assign nor_2_out = ~(subtractor_4_out | subtractor_3_out);  // NOR_Gate nor_2, 4 bits wide
  not not_3 (not_3_out, in_7);
endmodule

module \测试电路  (
  input  in_1,
  input  [7:0] in_2,
  input  in_3,
  input  [7:0] in_4,
  input  in_5,
  input  in_6
);

  wire button_1_out, button_2_out, clock_1_out, \时钟电路_1_报时 , \时钟电路_1_闹钟 ;
  wire [3:0] \时钟电路_1_out_15 , \时钟电路_1_out_16 , \时钟电路_1_out_17 , \时钟电路_1_out_18 , \时钟电路_1_out_20 ,
       \时钟电路_1_out_21 ;
  wire [4:0] \时钟电路_1_out_10 , \时钟电路_1_out_11 , \时钟电路_1_out_12 , \时钟电路_1_out_13 ;

  DotMatrix #(.matrixcols(4), .matrixrows(5)) dotmatrix_1 (
    .col0(\时钟电路_1_out_13 ), .col1(\时钟电路_1_out_12 ), .col2(\时钟电路_1_out_11 ), .col3(\时钟电路_1_out_10 ));
  Clock clock_1 (.out(clock_1_out));
  Hex_Digit_Display hex_digit_display_1 (.value(\时钟电路_1_out_20 ));  // open: dp
  Hex_Digit_Display hex_digit_display_2 (.value(\时钟电路_1_out_21 ));  // open: dp
  Button button_1 (.out(button_1_out));
  Button button_2 (.out(button_2_out));
  Hex_Digit_Display hex_digit_display_3 (.value(\时钟电路_1_out_17 ));  // open: dp
  Hex_Digit_Display hex_digit_display_4 (.value(\时钟电路_1_out_18 ));  // open: dp
  Hex_Digit_Display hex_digit_display_5 (.value(\时钟电路_1_out_16 ));  // open: dp
  Hex_Digit_Display hex_digit_display_6 (.value(\时钟电路_1_out_15 ));  // open: dp
  LED led_1 (.in(\时钟电路_1_闹钟 ));
  LED led_2 (.in(\时钟电路_1_报时 ));
  \时钟电路  \u_时钟电路_1  (
    .out_10(\时钟电路_1_out_10 ), .out_15(\时钟电路_1_out_15 ), .out_16(\时钟电路_1_out_16 ), .out_11(\时钟电路_1_out_11 ),
    .out_12(\时钟电路_1_out_12 ), .out_17(\时钟电路_1_out_17 ), .out_18(\时钟电路_1_out_18 ), .out_13(\时钟电路_1_out_13 ),
    .out_20(\时钟电路_1_out_20 ), .out_21(\时钟电路_1_out_21 ), .CPu(button_2_out), .CP(clock_1_out), .in_5(in_6),
    .CPd(button_1_out), .Adj0(in_1), .Adj1(in_3), .in_7(in_5), .\报时 (\时钟电路_1_报时 ), .\闹钟 (\时钟电路_1_闹钟 ),
    .min(in_2), .h(in_4));
endmodule

module \模60测试  (
  input  in_1
);

  wire button_1_out, button_2_out, button_3_out;
  wire [3:0] \模60计数器_new2_1_out_8 , \模60计数器_new2_1_out_12 ;

  Button button_1 (.out(button_1_out));
  Button button_2 (.out(button_2_out));
  Button button_3 (.out(button_3_out));
  Hex_Digit_Display hex_digit_display_1 (.value(\模60计数器_new2_1_out_12 ));  // open: dp
  Hex_Digit_Display hex_digit_display_2 (.value(\模60计数器_new2_1_out_8 ));  // open: dp
  \模60计数器_new2  \u_模60计数器_new2_1  (
    .in_1(button_1_out), .in_2(button_2_out), .in_3(button_3_out), .in_4(in_1),
    .out_5(\模60计数器_new2_1_out_8 [3]), .out_6(\模60计数器_new2_1_out_8 [2]), .out_7(\模60计数器_new2_1_out_8 [1]),
    .out_8(\模60计数器_new2_1_out_8 [0]), .out_9(\模60计数器_new2_1_out_12 [3]), .out_10(\模60计数器_new2_1_out_12 [2]),
    .out_11(\模60计数器_new2_1_out_12 [1]), .out_12(\模60计数器_new2_1_out_12 [0]));  // open: out_13
endmodule

module \_12_24计数器_new  (
  input  in_1,
  input  in_2,
  input  in_3,
  input  in_4,
  input  in_5,
  output out_6,
  output out_7,
  output out_8,
  output out_9,
  output out_10,
  output out_11,
  output out_12,
  output out_13,
  output \进位 
);

  wire and_4_out, and_5_out, and_6_out, and_7_out, and_8_out, and_9_out, and_10_out, and_11_out, and_12_out,
       and_13_out, and_14_out, and_15_out, and_16_out, and_17_out, and_18_out, and_19_out, and_20_out,
       not_1_out, not_2_out, not_3_out, not_4_out, not_5_out, not_6_out, not_7_out, not_8_out, not_9_out,
       not_10_out, not_11_out, not_12_out, not_13_out, or_1_out, or_10_out, \模60计数器_new2_1_out_5 ,
       \模60计数器_new2_1_out_6 , \模60计数器_new2_1_out_7 , \模60计数器_new2_1_out_8 , \模60计数器_new2_1_out_9 ,
       \模60计数器_new2_1_out_10 , \模60计数器_new2_1_out_11 , \模60计数器_new2_1_out_12 , \模60计数器_new2_2_out_5 ,
       \模60计数器_new2_2_out_6 , \模60计数器_new2_2_out_7 , \模60计数器_new2_2_out_8 , \模60计数器_new2_2_out_9 ,
       \模60计数器_new2_2_out_10 , \模60计数器_new2_2_out_11 , \模60计数器_new2_2_out_12 ;

  not not_1 (not_1_out, \模60计数器_new2_1_out_5 );
  or or_1 (or_1_out, \进位 , in_3);
  not not_2 (not_2_out, \模60计数器_new2_1_out_6 );
  and and_1 (\进位 , not_1_out, not_2_out, \模60计数器_new2_1_out_7 , not_3_out, not_4_out, not_5_out, not_6_out, \模60计数器_new2_1_out_12 );
  not not_3 (not_3_out, \模60计数器_new2_1_out_8 );
  not not_4 (not_4_out, \模60计数器_new2_1_out_9 );
  not not_5 (not_5_out, \模60计数器_new2_1_out_10 );
  not not_6 (not_6_out, \模60计数器_new2_1_out_11 );
  or or_2 (out_6, and_4_out, and_11_out);
  // AND_Gate and_2 has open pins: in0=in_1, in1=and_20_out, out=open
  // AND_Gate and_3 has open pins: in0=\进位 , in1=not_7_out, out=open
  and and_4 (and_4_out, \模60计数器_new2_1_out_5 , not_7_out);
  \模60计数器_new2  \u_模60计数器_new2_1  (
    .in_1(in_2), .in_2(or_1_out), .in_3(in_4), .in_4(in_5), .out_5(\模60计数器_new2_1_out_5 ),
    .out_6(\模60计数器_new2_1_out_6 ), .out_7(\模60计数器_new2_1_out_7 ), .out_8(\模60计数器_new2_1_out_8 ),
    .out_9(\模60计数器_new2_1_out_9 ), .out_10(\模60计数器_new2_1_out_10 ), .out_11(\模60计数器_new2_1_out_11 ),
    .out_12(\模60计数器_new2_1_out_12 ));  // open: out_13
  or or_3 (out_8, and_6_out, and_14_out);
  or or_4 (out_7, and_7_out, and_15_out);
  and and_5 (and_5_out, \模60计数器_new2_1_out_8 , not_7_out);
  and and_6 (and_6_out, \模60计数器_new2_1_out_7 , not_7_out);
  and and_7 (and_7_out, \模60计数器_new2_1_out_6 , not_7_out);
  or or_5 (out_9, and_5_out, and_13_out);
  or or_6 (out_11, and_9_out, and_17_out);
  or or_7 (out_10, and_8_out, and_16_out);
  and and_8 (and_8_out, \模60计数器_new2_1_out_9 , not_7_out);
  and and_9 (and_9_out, \模60计数器_new2_1_out_10 , not_7_out);
  or or_8 (out_12, and_10_out, and_19_out);
  or or_9 (out_13, and_12_out, and_18_out);
  and and_10 (and_10_out, \模60计数器_new2_1_out_11 , not_7_out);
  and and_11 (and_11_out, in_1, \模60计数器_new2_2_out_5 );
  and and_12 (and_12_out, \模60计数器_new2_1_out_12 , not_7_out);
  not not_7 (not_7_out, in_1);
  and and_13 (and_13_out, in_1, \模60计数器_new2_2_out_8 );
  and and_14 (and_14_out, in_1, \模60计数器_new2_2_out_7 );
  and and_15 (and_15_out, in_1, \模60计数器_new2_2_out_6 );
  and and_16 (and_16_out, in_1, \模60计数器_new2_2_out_9 );
  and and_17 (and_17_out, in_1, \模60计数器_new2_2_out_10 );
  and and_18 (and_18_out, in_1, \模60计数器_new2_2_out_12 );
  and and_19 (and_19_out, in_1, \模60计数器_new2_2_out_11 );
  not not_8 (not_8_out, \模60计数器_new2_2_out_5 );
  or or_10 (or_10_out, and_20_out, in_3);
  not not_9 (not_9_out, \模60计数器_new2_2_out_7 );
  and and_20 (and_20_out, not_8_out, \模60计数器_new2_2_out_6 , not_9_out, not_11_out, not_10_out, not_12_out, \模60计数器_new2_2_out_11 , not_13_out);
  not not_10 (not_10_out, \模60计数器_new2_2_out_9 );
  not not_11 (not_11_out, \模60计数器_new2_2_out_8 );
  not not_12 (not_12_out, \模60计数器_new2_2_out_10 );
  not not_13 (not_13_out, \模60计数器_new2_2_out_12 );
  \模60计数器_new2  \u_模60计数器_new2_2  (
    .in_1(in_2), .in_2(or_10_out), .in_3(in_4), .in_4(in_5), .out_5(\模60计数器_new2_2_out_5 ),
    .out_6(\模60计数器_new2_2_out_6 ), .out_7(\模60计数器_new2_2_out_7 ), .out_8(\模60计数器_new2_2_out_8 ),
    .out_9(\模60计数器_new2_2_out_9 ), .out_10(\模60计数器_new2_2_out_10 ), .out_11(\模60计数器_new2_2_out_11 ),
    .out_12(\模60计数器_new2_2_out_12 ));  // open: out_13
endmodule

module \_12_24测试_new  (
  input  in_1,
  input  in_2,
  input  in_3,
  input  in_4,
  input  in_5,
  output out_6
);

  wire [3:0] \n12_24计数器_new_1_out_9 , \n12_24计数器_new_1_out_13 ;

  Hex_Digit_Display hex_digit_display_1 (.value(\n12_24计数器_new_1_out_13 ));  // open: dp
  Hex_Digit_Display hex_digit_display_2 (.value(\n12_24计数器_new_1_out_9 ));  // open: dp
  \_12_24计数器_new  \u_12_24计数器_new_1  (
    .in_2(in_1), .in_3(in_2), .in_4(in_3), .in_5(in_4), .\进位 (out_6), .out_6(\n12_24计数器_new_1_out_9 [3]),
    .out_7(\n12_24计数器_new_1_out_9 [2]), .out_8(\n12_24计数器_new_1_out_9 [1]),
    .out_9(\n12_24计数器_new_1_out_9 [0]), .out_10(\n12_24计数器_new_1_out_13 [3]),
    .out_11(\n12_24计数器_new_1_out_13 [2]), .out_12(\n12_24计数器_new_1_out_13 [1]),
    .out_13(\n12_24计数器_new_1_out_13 [0]), .in_1(in_5));
endmodule

module \上午下午测试  (
  input  in_1,
  input  in_2
);

  wire [4:0] \上午下午显示_1_out_3 , \上午下午显示_1_out_4 , \上午下午显示_1_out_5 , \上午下午显示_1_out_6 ;

  DotMatrix #(.matrixcols(4), .matrixrows(5)) dotmatrix_1 (
    .col0(\上午下午显示_1_out_3 ), .col1(\上午下午显示_1_out_4 ), .col2(\上午下午显示_1_out_5 ), .col3(\上午下午显示_1_out_6 ));
  \上午下午显示  \u_上午下午显示_1  (
    .AM_FM(in_1), .TT(in_2), .out_3(\上午下午显示_1_out_3 ), .out_4(\上午下午显示_1_out_4 ), .out_5(\上午下午显示_1_out_5 ),
    .out_6(\上午下午显示_1_out_6 ));
endmodule
