// Logisim project 4.circ as structural Verilog: 6 circuits, main circuit main
module main (
  input  [5:0] in_1
);

  wire button_1_out, clock_1_out, controler_1_out_4, controler_1_out_5, controler_1_out_6, controler_1_out_7;
  wire [3:0] \显示模块_1_d0 , \显示模块_1_d1 , \显示模块_1_d2 , \显示模块_1_d3 , \显示模块_1_d4 , \显示模块_1_d5 , \显示模块_1_d6 ,
       \显示模块_1_d7 , \显示模块_1_d8 , \显示模块_1_d9 ;
  wire [31:0] fibo_1_fi;

  Button button_1 (.out(button_1_out));
  Clock clock_1 (.out(clock_1_out));
  Controler controler_1 (
    .in_1(button_1_out), .in_2(clock_1_out), .in_3(in_1), .out_4(controler_1_out_4),
    .out_5(controler_1_out_5), .out_6(controler_1_out_6), .out_7(controler_1_out_7));
  fibo fibo_1 (
    .start(controler_1_out_4), .clk(controler_1_out_7), .Fi(fibo_1_fi), .clr(controler_1_out_5),
    .ni_1(controler_1_out_6));
  \显示模块  \u_显示模块_1  (
    .in_1(fibo_1_fi), .D0(\显示模块_1_d0 ), .D1(\显示模块_1_d1 ), .D2(\显示模块_1_d2 ), .D3(\显示模块_1_d3 ),
    .D4(\显示模块_1_d4 ), .D5(\显示模块_1_d5 ), .D6(\显示模块_1_d6 ), .D7(\显示模块_1_d7 ), .D8(\显示模块_1_d8 ), .D9(\显示模块_1_d9 ));
  Hex_Digit_Display hex_digit_display_1 (.value(\显示模块_1_d8 ));  // open: dp
  Hex_Digit_Display hex_digit_display_2 (.value(\显示模块_1_d9 ));  // open: dp
  Hex_Digit_Display hex_digit_display_3 (.value(\显示模块_1_d7 ));  // open: dp
  Hex_Digit_Display hex_digit_display_4 (.value(\显示模块_1_d6 ));  // open: dp
  Hex_Digit_Display hex_digit_display_5 (.value(\显示模块_1_d5 ));  // open: dp
  Hex_Digit_Display hex_digit_display_6 (.value(\显示模块_1_d4 ));  // open: dp
  Hex_Digit_Display hex_digit_display_7 (.value(\显示模块_1_d3 ));  // open: dp
  Hex_Digit_Display hex_digit_display_8 (.value(\显示模块_1_d2 ));  // open: dp
  Hex_Digit_Display hex_digit_display_9 (.value(\显示模块_1_d0 ));  // open: dp
  Hex_Digit_Display hex_digit_display_10 (.value(\显示模块_1_d1 ));  // open: dp
endmodule

module sqrtX (
  input  [31:0] a,
  input  [31:0] b,
  input  [31:0] c,
  input  [31:0] d,
  output [31:0] a_prime,
  output [31:0] b_prime,
  output [31:0] c_prime,
  output [31:0] d_prime
);

  wire [31:0] multiplier_1_out, multiplier_2_out, multiplier_3_out, multiplier_4_out, multiplier_5_out,
       multiplier_6_out, multiplier_7_out, multiplier_8_out;

  Multiplier #(.width(32)) multiplier_1 (.a(a), .b(a), .out(multiplier_1_out));  // open: cin, cout
  Multiplier #(.width(32)) multiplier_2 (.a(b), .b(c), .out(multiplier_2_out));  // open: cin, cout
  Multiplier #(.width(32)) multiplier_3 (.a(a), .b(b), .out(multiplier_3_out));  // open: cin, cout
  Multiplier #(.width(32)) multiplier_4 (.a(b), .b(d), .out(multiplier_4_out));  // open: cin, cout
  Multiplier #(.width(32)) multiplier_5 (.a(a), .b(c), .out(multiplier_5_out));  // open: cin, cout
  Multiplier #(.width(32)) multiplier_6 (.a(c), .b(d), .out(multiplier_6_out));  // open: cin, cout
  Multiplier #(.width(32)) multiplier_7 (.a(b), .b(c), .out(multiplier_7_out));  // open: cin, cout
  Multiplier #(.width(32)) multiplier_8 (.a(d), .b(d), .out(multiplier_8_out));  // open: cin, cout
  Adder #(.width(32)) adder_1 (.a(multiplier_1_out), .b(multiplier_2_out), .out(a_prime));  // open: cin, cout
  Adder #(.width(32)) adder_2 (.a(multiplier_3_out), .b(multiplier_4_out), .out(b_prime));  // open: cin, cout
  Adder #(.width(32)) adder_3 (.a(multiplier_5_out), .b(multiplier_6_out), .out(c_prime));  // open: cin, cout
  Adder #(.width(32)) adder_4 (.a(multiplier_7_out), .b(multiplier_8_out), .out(d_prime));  // open: cin, cout
endmodule

module sqrtX___A (
  input  [31:0] a,
  input  [31:0] b,
  input  [31:0] c,
  input  [31:0] d,
  output [31:0] a_prime_prime,
  output [31:0] b_prime_prime,
  output [31:0] c_prime_prime,
  output [31:0] d_prime_prime
);

  wire [31:0] adder_2_out, adder_3_out, adder_5_out, adder_6_out, multiplier_1_out, multiplier_2_out,
       multiplier_3_out, multiplier_4_out, multiplier_5_out, multiplier_6_out, multiplier_7_out,
       multiplier_8_out, multiplier_9_out, multiplier_10_out, multiplier_11_out, multiplier_12_out;

  Multiplier #(.width(32)) multiplier_1 (.a(a), .b(b), .out(multiplier_1_out));  // open: cin, cout
  Multiplier #(.width(32)) multiplier_2 (.a(b), .b(d), .out(multiplier_2_out));  // open: cin, cout
  Multiplier #(.width(32)) multiplier_3 (.a(a), .b(a), .out(multiplier_3_out));  // open: cin, cout
  Multiplier #(.width(32)) multiplier_4 (.a(b), .b(c), .out(multiplier_4_out));  // open: cin, cout
  Multiplier #(.width(32)) multiplier_5 (.a(a), .b(b), .out(multiplier_5_out));  // open: cin, cout
  Multiplier #(.width(32)) multiplier_6 (.a(b), .b(d), .out(multiplier_6_out));  // open: cin, cout
  Multiplier #(.width(32)) multiplier_7 (.a(b), .b(c), .out(multiplier_7_out));  // open: cin, cout
  Multiplier #(.width(32)) multiplier_8 (.a(d), .b(d), .out(multiplier_8_out));  // open: cin, cout
  Multiplier #(.width(32)) multiplier_9 (.a(a), .b(c), .out(multiplier_9_out));  // open: cin, cout
  Multiplier #(.width(32)) multiplier_10 (.a(c), .b(d), .out(multiplier_10_out));  // open: cin, cout
  Multiplier #(.width(32)) multiplier_11 (.a(b), .b(c), .out(multiplier_11_out));  // open: cin, cout
  Multiplier #(.width(32)) multiplier_12 (.a(d), .b(d), .out(multiplier_12_out));  // open: cin, cout
  Adder #(.width(32)) adder_1 (.a(multiplier_1_out), .b(multiplier_2_out), .out(a_prime_prime));  // open: cin, cout
  Adder #(.width(32)) adder_2 (.a(multiplier_3_out), .b(multiplier_4_out), .out(adder_2_out));  // open: cin, cout
  Adder #(.width(32)) adder_3 (.a(multiplier_5_out), .b(multiplier_6_out), .out(adder_3_out));  // open: cin, cout
  Adder #(.width(32)) adder_4 (.a(multiplier_7_out), .b(multiplier_8_out), .out(c_prime_prime));  // open: cin, cout
  Adder #(.width(32)) adder_5 (.a(multiplier_9_out), .b(multiplier_10_out), .out(adder_5_out));  // open: cin, cout
  Adder #(.width(32)) adder_6 (.a(multiplier_11_out), .b(multiplier_12_out), .out(adder_6_out));  // open: cin, cout
  Adder #(.width(32)) adder_7 (.a(adder_2_out), .b(adder_3_out), .out(b_prime_prime));  // open: cin, cout
  Adder #(.width(32)) adder_8 (.a(adder_5_out), .b(adder_6_out), .out(d_prime_prime));  // open: cin, cout
endmodule

// Fi
module fibo (
  input  start,
  input  clk,
  input  clr,
  input  ni_1,
  output [31:0] Fi
);

  wire and_1_out, not_1_out, not_2_out, or_1_out;
  wire [31:0] multiplexer_1_out, multiplexer_2_out, multiplexer_3_out, multiplexer_4_out, multiplexer_5_out,
       multiplexer_6_out, multiplexer_7_out, multiplexer_8_out, register_1_q, register_3_q, register_4_q,
       sqrtx_1_a_prime, sqrtx_1_b_prime, sqrtx_1_c_prime, sqrtx_1_d_prime, sqrtx_a_1_a_prime_prime,
       sqrtx_a_1_b_prime_prime, sqrtx_a_1_c_prime_prime, sqrtx_a_1_d_prime_prime;

  and and_1 (and_1_out, start, not_1_out);
  not not_1 (not_1_out, clr);
  Multiplexer #(.width(32), .enable("false")) multiplexer_1 (
    .in0({32{1'b0}}), .in1(multiplexer_5_out), .out(multiplexer_1_out), .sel(and_1_out));
  Multiplexer #(.width(32), .enable("false")) multiplexer_2 (
    .in0(32'h1), .in1(multiplexer_6_out), .out(multiplexer_2_out), .sel(and_1_out));
  Multiplexer #(.width(32), .enable("false")) multiplexer_3 (
    .in0(32'h1), .in1(multiplexer_7_out), .out(multiplexer_3_out), .sel(and_1_out));
  Multiplexer #(.width(32), .enable("false")) multiplexer_4 (
    .in0(32'h1), .in1(multiplexer_8_out), .out(multiplexer_4_out), .sel(and_1_out));
  or or_1 (or_1_out, clk, clr);
  Register #(.width(32), .trigger("falling")) register_1 (
    .D(multiplexer_1_out), .en(1'b1), .Q(register_1_q), .clk(or_1_out), .clr(not_2_out));
  not not_2 (not_2_out, 1'b1);
  Register #(.width(32), .trigger("falling")) register_2 (
    .D(multiplexer_2_out), .en(1'b1), .Q(Fi), .clk(or_1_out), .clr(not_2_out));
  Register #(.width(32), .trigger("falling")) register_3 (
    .D(multiplexer_3_out), .en(1'b1), .Q(register_3_q), .clk(or_1_out), .clr(not_2_out));
  Register #(.width(32), .trigger("falling")) register_4 (
    .D(multiplexer_4_out), .en(1'b1), .Q(register_4_q), .clk(or_1_out), .clr(not_2_out));
  sqrtX sqrtx_1 (
    .a(register_1_q), .a_prime(sqrtx_1_a_prime), .b(Fi), .b_prime(sqrtx_1_b_prime), .c(register_3_q),
    .c_prime(sqrtx_1_c_prime), .d(register_4_q), .d_prime(sqrtx_1_d_prime));
  sqrtX___A sqrtx_a_1 (
    .a(register_1_q), .a_prime_prime(sqrtx_a_1_a_prime_prime), .b(Fi),
    .b_prime_prime(sqrtx_a_1_b_prime_prime), .c(register_3_q), .c_prime_prime(sqrtx_a_1_c_prime_prime),
    .d(register_4_q), .d_prime_prime(sqrtx_a_1_d_prime_prime));
  Multiplexer #(.width(32), .enable("false")) multiplexer_5 (
    .in0(sqrtx_1_a_prime), .in1(sqrtx_a_1_a_prime_prime), .out(multiplexer_5_out), .sel(ni_1));
  Multiplexer #(.width(32), .enable("false")) multiplexer_6 (
    .in0(sqrtx_1_b_prime), .in1(sqrtx_a_1_b_prime_prime), .out(multiplexer_6_out), .sel(ni_1));
  Multiplexer #(.width(32), .enable("false")) multiplexer_7 (
    .in0(sqrtx_1_c_prime), .in1(sqrtx_a_1_c_prime_prime), .out(multiplexer_7_out), .sel(ni_1));
  Multiplexer #(.width(32), .enable("false")) multiplexer_8 (
    .in0(sqrtx_1_d_prime), .in1(sqrtx_a_1_d_prime_prime), .out(multiplexer_8_out), .sel(ni_1));
endmodule

module \显示模块  (
  input  [31:0] in_1,
  output [3:0] D0,
  output [3:0] D1,
  output [3:0] D2,
  output [3:0] D3,
  output [3:0] D4,
  output [3:0] D5,
  output [3:0] D6,
  output [3:0] D7,
  output [3:0] D8,
  output [3:0] D9
);

  wire [31:0] divider_1_out, divider_2_out, divider_3_out, divider_4_out, divider_5_out, divider_6_out,
       divider_7_out, divider_8_out;
  wire [31:4] divider_1_rem, divider_2_rem, divider_3_rem, divider_4_rem, divider_5_rem, divider_6_rem,
       divider_7_rem, divider_8_rem, divider_9_out, divider_9_rem;

  Divider #(.width(32)) divider_1 (
    .a(in_1), .b(32'ha), .out(divider_1_out), .upper({32{1'b0}}), .rem({divider_1_rem, D0}));
  Divider #(.width(32)) divider_2 (
    .a(divider_1_out), .b(32'ha), .out(divider_2_out), .upper({32{1'b0}}), .rem({divider_2_rem, D1}));
  Divider #(.width(32)) divider_3 (
    .a(divider_2_out), .b(32'ha), .out(divider_3_out), .upper({32{1'b0}}), .rem({divider_3_rem, D2}));
  Divider #(.width(32)) divider_4 (
    .a(divider_3_out), .b(32'ha), .out(divider_4_out), .upper({32{1'b0}}), .rem({divider_4_rem, D3}));
  Divider #(.width(32)) divider_5 (
    .a(divider_4_out), .b(32'ha), .out(divider_5_out), .upper({32{1'b0}}), .rem({divider_5_rem, D4}));
  Divider #(.width(32)) divider_6 (
    .a(divider_5_out), .b(32'ha), .out(divider_6_out), .upper({32{1'b0}}), .rem({divider_6_rem, D5}));
  Divider #(.width(32)) divider_7 (
    .a(divider_6_out), .b(32'ha), .out(divider_7_out), .upper({32{1'b0}}), .rem({divider_7_rem, D6}));
  Divider #(.width(32)) divider_8 (
    .a(divider_7_out), .b(32'ha), .out(divider_8_out), .upper({32{1'b0}}), .rem({divider_8_rem, D7}));
  Divider #(.width(32)) divider_9 (
    .a(divider_8_out), .b(32'ha), .out({divider_9_out, D9}), .upper({32{1'b0}}), .rem({divider_9_rem, D8}));
endmodule

module Controler (
  input  in_1,
  input  in_2,
  input  [5:0] in_3,
  output out_4,
  output out_5,
  output out_6,
  output out_7
);

  wire comparator_1_lt, d_ff_1_q, ni, not_1_out, or_1_out;
  wire [7:0] counter_1_q;

  D_Flip_Flop #(.trigger("falling")) d_ff_1 (.Q(d_ff_1_q), .preset(ni), .en(1'b1), .reset(in_1));  // open: clk, D, Qn
  Counter counter_1 (.count(1'b1), .Q(counter_1_q), .clk(in_2), .clr(in_1));  // open: load, D, carry
  not not_1 (not_1_out, in_1);
  Shift_Register #(.length(7)) shift_register_1 (
    .shift(not_1_out), .in(1'b0), .clk(or_1_out), .out(ni), .load(in_1), .clr(1'b0), .d0(in_3[0]),
    .d1(in_3[1]), .d2(in_3[2]), .d3(in_3[3]), .d4(in_3[4]), .d5(in_3[5]), .d6(1'b0), .q6(out_6));  // open: q0, q1, q2, q3, q4, q5
  or or_1 (or_1_out, in_1, in_2);
  Register #(.width(1), .trigger("falling")) register_1 (.D(d_ff_1_q), .en(1'b1), .Q(out_4), .clk(in_2), .clr(in_1));
  Comparator #(.mode("unsigned")) comparator_1 (.a(counter_1_q), .b(8'h6), .lt(comparator_1_lt));  // open: gt, eq
  and and_1 (out_7, comparator_1_lt, in_2);

  assign out_5 = in_1;

  // Other names for the same wires on the sheet: clear = in_1; clk = out_7; clock = in_2; n[5:0] = in_3; ni_1 = out_6;
  //   start = out_4
endmodule
