// Logisim project cpu24.circ as structural Verilog: 20 circuits, main circuit ◆单周期硬布线控制器
module \单周期MIPS  (
  input  IR1,
  input  IR2,
  input  IR3,
  output RegWrite,
  output MemWrite,
  output [31:0] PC,
  output [31:0] IR,
  output [31:0] RDin,
  output [31:0] MDin,
  output [31:0] LedData
);

  wire and_1_out, and_2_out, and_3_out, and_4_out, and_5_out, and_6_out, and_7_out, BGEZ, Branch, CLK,
       clock_2_out, comparator_1_eq, comparator_2_eq, comparator_2_lt, d_ff_1_q, Go, Halt, IR1_t, IR2_t,
       IR3_t, IRA, IRB, IRC, JAL, JMP, JR, LBU, mips_alu_1_equal, nand_1_out, nor_1_out, not_1_out,
       not_2_out, not_3_out, not_4_out, or_4_out, SignedExt, SLLV, SRAV, Syscall, W1, W2, W3,
       \单周期硬布线控制器_1_alu_src , \单周期硬布线控制器_1_beq , \单周期硬布线控制器_1_bne , \单周期硬布线控制器_1_memtoreg ,
       \单周期硬布线控制器_1_regdst ;
  wire [3:0] \单周期硬布线控制器_1_alu_op ;
  wire [4:0] multiplexer_1_out, multiplexer_2_out, multiplexer_3_out, multiplexer_4_out, multiplexer_9_out;
  wire [12:0] CNT_num;
  wire [15:0] \总周期数 ;
  wire [31:0] adder_1_out, adder_2_out, bit_extender_1_out, bit_extender_2_out, bit_extender_3_out,
       controlled_buffer_1_out, mips_alu_1_result, multiplexer_6_out, multiplexer_7_out, multiplexer_8_out,
       multiplexer_10_out, multiplexer_11_out, ram_1_data, shifter_1_out, v0;

  Clock #(.highDuration(1), .lowDuration(1)) clock_1 ();  // open: out
  Button _1 (.out(IRA));
  Button _2 (.out(IRB));
  Button _3 (.out(IRC));
  Button \u_继续运行  (.out(Go));
  LED #(.active("true")) led_1 (.in(W1));
  LED #(.active("true")) led_2 (.in(W2));
  LED #(.active("true")) led_3 (.in(W3));
  Hex_Digit_Display hex_digit_display_1 (.value(LedData[31:28]));  // open: dp
  and and_1 (and_1_out, JMP, ~JR);  // AND_Gate
  nor nor_1 (nor_1_out, Branch, JMP);
  Hex_Digit_Display hex_digit_display_2 (.value(LedData[27:24]));  // open: dp
  Hex_Digit_Display hex_digit_display_3 (.value(LedData[23:20]));  // open: dp
  assign controlled_buffer_1_out = JR ? v0 : 32'bz;  // Controlled_Buffer controlled_buffer_1
  assign controlled_buffer_1_out = and_1_out ? {PC[31:28], IR[25:0], 2'b00} : 32'bz;  // Controlled_Buffer controlled_buffer_2
  assign controlled_buffer_1_out = Branch ? adder_2_out : 32'bz;  // Controlled_Buffer controlled_buffer_3
  assign controlled_buffer_1_out = nor_1_out ? adder_1_out : 32'bz;  // Controlled_Buffer controlled_buffer_4
  not not_1 (not_1_out, Halt);
  Hex_Digit_Display hex_digit_display_4 (.value(LedData[19:16]));  // open: dp
  Hex_Digit_Display hex_digit_display_5 (.value(LedData[15:12]));  // open: dp
  Register #(.width(32), .trigger("rising"), .Select("low")) u_PC (
    .D(controlled_buffer_1_out), .en(not_1_out), .Q(PC), .clk(CLK));  // open: clr
  Hex_Digit_Display hex_digit_display_6 (.value(LedData[7:4]));  // open: dp
  Hex_Digit_Display hex_digit_display_7 (.value(LedData[11:8]));  // open: dp
  // Probe on \总周期数 
  Counter #(.width(16), .max('hffff), .ongoal("wrap"), .trigger("rising"), .behavior("new")) counter_1 (
    .Q(\总周期数 ), .clk(and_2_out));  // open: load, D, count, carry, clr, preset, down
  and and_2 (and_2_out, ~Halt, CLK);  // AND_Gate
  Hex_Digit_Display hex_digit_display_8 (.value(LedData[3:0]));  // open: dp
  Adder #(.width(32)) adder_1 (.a(PC), .b(32'h4), .out(adder_1_out));  // open: cin, cout
  // Mips_Probe mips_probe_1: pin names not known; wires that end beside it: IR
  ROM #(.addrWidth(10), .dataWidth(32), .Select("high")) rom_1 (.addr(PC[11:2]), .data(IR));
  or or_1 (IR1_t, IR1, IRA);
  or or_2 (IR2_t, IR2, IRB);
  \单周期硬布线控制器  \u_单周期硬布线控制器_1  (
    .Func(IR[5:0]), .OP(IR[31:26]), .ALU_OP(\单周期硬布线控制器_1_alu_op ), .MemToReg(\单周期硬布线控制器_1_memtoreg ),
    .MemWrite(MemWrite), .ALU_SRC(\单周期硬布线控制器_1_alu_src ), .RegWrite(RegWrite), .SysCALL(Syscall),
    .SignedExt(SignedExt), .RegDst(\单周期硬布线控制器_1_regdst ), .JR(JR), .JMP(JMP), .Beq(\单周期硬布线控制器_1_beq ),
    .JAL(JAL), .Bne(\单周期硬布线控制器_1_bne ), .SLLV(SLLV), .SRAV(SRAV), .BGEZ(BGEZ), .LBU(LBU));  // open: ERET, MFC0, MTC0, in_3
  Multiplexer #(.select(1), .width(5), .disabled("Z"), .enable("false")) multiplexer_1 (
    .in0(IR[20:16]), .in1(IR[15:11]), .out(multiplexer_1_out), .sel(\单周期硬布线控制器_1_regdst ));
  assign bit_extender_1_out = {{16{1'b0}}, IR[15:0]};  // Bit_Extender bit_extender_1
  assign bit_extender_2_out = {{16{IR[15]}}, IR[15:0]};  // Bit_Extender bit_extender_2
  Multiplexer #(.select(1), .width(5), .disabled("Z"), .enable("false")) multiplexer_2 (
    .in0(multiplexer_1_out), .in1({5{1'b1}}), .out(multiplexer_2_out), .sel(JAL));
  not not_2 (not_2_out, JAL);
  or or_3 (IR3_t, IR3, IRC);
  Multiplexer #(.select(1), .width(5), .disabled("Z"), .enable("false")) multiplexer_3 (
    .in0(IR[25:21]), .in1(5'b00010), .out(multiplexer_3_out), .sel(Syscall));
  Multiplexer #(.select(1), .width(5), .disabled("Z"), .enable("false")) multiplexer_4 (
    .in0(IR[20:16]), .in1(5'b00100), .out(multiplexer_4_out), .sel(Syscall));
  Multiplexer #(.select(1), .width(32), .disabled("Z"), .enable("false")) multiplexer_5 (
    .in0(adder_1_out), .in1(multiplexer_10_out), .out(RDin), .sel(not_2_out));
  MIPS_Regifile mips_regifile_1 (
    .Din(RDin), .Clk(CLK), .R1(v0), .R2(MDin), .WE(RegWrite), .W_num(multiplexer_2_out),
    .R1_num(multiplexer_3_out), .R2_num(multiplexer_4_out));
  Multiplexer #(.select(1), .width(32), .disabled("Z"), .enable("false")) multiplexer_6 (
    .in0(bit_extender_1_out), .in1(bit_extender_2_out), .out(multiplexer_6_out), .sel(SignedExt));
  Multiplexer #(.select(1), .width(32), .disabled("Z"), .enable("false")) multiplexer_7 (
    .in0(MDin), .in1(multiplexer_6_out), .out(multiplexer_7_out), .sel(\单周期硬布线控制器_1_alu_src ));
  Multiplexer #(.select(1), .width(32), .disabled("Z"), .enable("false")) multiplexer_8 (
    .in0(multiplexer_7_out), .in1({32{1'b0}}), .out(multiplexer_8_out), .sel(BGEZ));
  Shifter #(.width(32), .shift("ll")) shifter_1 (.in(multiplexer_6_out), .\dist (5'b00010), .out(shifter_1_out));
  MIPS_ALU mips_alu_1 (
    .X(v0), .Y(multiplexer_8_out), .AluOP(\单周期硬布线控制器_1_alu_op ), .Equal(mips_alu_1_equal),
    .Result(mips_alu_1_result), .shamt(multiplexer_9_out));  // open: Result_2
  Multiplexer #(.select(1), .width(5), .disabled("Z"), .enable("false")) multiplexer_9 (
    .in0(IR[10:6]), .in1(v0[4:0]), .out(multiplexer_9_out), .sel(or_4_out));
  Adder #(.width(32)) adder_2 (.a(shifter_1_out), .b(adder_1_out), .out(adder_2_out));  // open: cin, cout
  and and_3 (and_3_out, BGEZ, ~mips_alu_1_result[0]);  // AND_Gate
  and and_4 (and_4_out, mips_alu_1_equal, \单周期硬布线控制器_1_beq );
  and and_5 (and_5_out, ~mips_alu_1_equal, \单周期硬布线控制器_1_bne );  // AND_Gate
  or or_4 (or_4_out, SRAV, SLLV);
  or or_5 (Branch, and_3_out, and_4_out, and_5_out);
  not not_3 (not_3_out, Halt);
  Comparator #(.width(32), .mode("twosComplement")) comparator_1 (
    .a(v0), .b(32'h22), .eq(comparator_1_eq));  // open: gt, lt
  not not_4 (not_4_out, comparator_1_eq);
  RAM #(.addrWidth(10), .dataWidth(32), .bus("separate"), .Select("high")) ram_1 (
    .addr(mips_alu_1_result[11:2]), .din(MDin), .data(ram_1_data), .str(MemWrite), .sel(not_3_out), .clk(CLK));  // open: ld, clr
  Multiplexer #(.select(1), .width(32), .disabled("Z"), .enable("false")) multiplexer_10 (
    .in0(multiplexer_11_out), .in1(bit_extender_3_out), .out(multiplexer_10_out), .sel(LBU));
  and and_6 (and_6_out, comparator_1_eq, Syscall);
  and and_7 (and_7_out, Syscall, not_4_out);
  D_Flip_Flop #(.trigger("high"), .Pre_Clr_Positions("LEGACY"), .NegatePresetClear("false"), .enable("true"), .NewFFLayout("false")) d_ff_1 (.Q(d_ff_1_q));  // open: clk, D, Qn, preset, en, reset
  // Probe on 13'ha
  Multiplexer #(.select(1), .width(32), .disabled("Z"), .enable("false")) multiplexer_11 (
    .in0(mips_alu_1_result), .in1(ram_1_data), .out(multiplexer_11_out), .sel(\单周期硬布线控制器_1_memtoreg ));
  Register #(.width(32), .trigger("falling"), .Select("low")) register_1 (
    .D(MDin), .Q(LedData), .clk(and_6_out));  // open: en, clr
  Register #(.width(1), .trigger("rising"), .Select("low")) register_2 (
    .D(and_7_out), .en(and_7_out), .Q(Halt), .clk(CLK), .clr(Go));
  Comparator #(.width(13), .mode("twosComplement")) comparator_2 (
    .a(CNT_num), .b(13'ha), .eq(comparator_2_eq), .lt(comparator_2_lt));  // open: gt
  Clock #(.highDuration(1), .lowDuration(1)) clock_2 (.out(clock_2_out));
  assign bit_extender_3_out = {{24{1'b0}}, multiplexer_11_out[7:0]};  // Bit_Extender bit_extender_3
  nand nand_1 (nand_1_out, d_ff_1_q, comparator_2_eq);
  Counter #(.width(13), .max('h1fff), .ongoal("stay"), .trigger("rising"), .behavior("old")) counter_2 (
    .count(comparator_2_lt), .Q(CNT_num), .clk(clock_2_out));  // open: load, D, carry, clr, preset
  assign CLK = nand_1_out ? clock_2_out : 1'bz;  // Controlled_Buffer controlled_buffer_5
  Pull_Resistor #(.pull(1)) pull_resistor_1 (.node(CLK));

  // Other names for the same wires on the sheet: a0[31:0] = MDin

  // Notes on the sheet:
  //   中断源
  //   中断等待指示
  //   总复位信号应将除ROM以外所有存储组件全部清零
  //   数码管输出
  //   数码管输出应该用寄存器锁存，否则显示数据只能一闪而过
  //   指令存储器
  //   指令字
  //   contents of rom_1 (hex, n*v repeats v):
  //   20110001 8000c05 20110001 20120002 20130003 8000c09 20110001 20120002 20130003 8000c0d 20110001
  //   20120002 20130003 8000c11 20110001 20120002 20130003 c000cb8 20100001 20110001 118fc0 112020
  //   20020022 c 118882 12200001 8000c15 112020 20020022 c 20110001 118880 112020 20020022 c 12200001
  //   8000c1f 20110001 118fc0 112020 20020022 c 1188c3 112020 20020022 c 118903 112020 20020022 c 118903
  //   112020 20020022 c 118903 112020 20020022 c 118903 112020 20020022 c 118903 112020 20020022 c 118903
  //   112020 20020022 c 118903 112020 20020022 c 20100001 109fc0 139fc3 8021 2012000c 24160003 26100001
  //   3210000f 20080008 20090001 139900 2709825 132020 20020022 c 1094022 1500fff9 22100001 2018000f
  //   2188024 108700 20080008 20090001 139902 2709825 132021 20020022 c 1094022 1500fff9 108702 2c9b022
  //   12c00001 8000c50 4020 1084027 84400 3508ffff 82021 20020022 c 2010ffff 20110000 ae300000 22100001
  //   22310004 ae300000 22100001 22310004 ae300000 22100001 22310004 ae300000 22100001 22310004 ae300000
  //   22100001 22310004 ae300000 22100001 22310004 ae300000 22100001 22310004 ae300000 22100001 22310004
  //   ae300000 22100001 22310004 ae300000 22100001 22310004 ae300000 22100001 22310004 ae300000 22100001
  //   22310004 ae300000 22100001 22310004 ae300000 22100001 22310004 ae300000 22100001 22310004 ae300000
  //   22100001 22310004 22100001 8020 2011003c 8e130000 8e340000 274402a 11000002 ae330000 ae140000
  //   2231fffc 1611fff8 102020 20020022 c 22100004 2011003c 1611fff2 20020032 c 20100000 22100001 102020
  //   20020022 c 22100002 102020 20020022 c 22100003 102020 20020022 c 22100004 102020 20020022 c 22100005
  //   102020 20020022 c 22100006 102020 20020022 c 22100007 102020 20020022 c 22100008 102020 20020022
  //   20020022 c 3e00008
  //   JMP
  //   JR
  //   OP
  //   OP
  //   Func
  //   Func
  //   rs
  //   rt
  //   rd
  //   Beq
  //   Bne
  //   MemToReg
  //   MemWrite
  //   AluOP
  //   AluSrcB
  //   RegWrite
  //   JAL
  //   RegDst
  //   Syscall
  //   为方便自动评测，需要输出PC，IR，寄存器堆写如数据RDin
  //   RAM写使能MemWrite、RAM写入数据MDin等信号
  //   控制位
  //   暂停节拍，不能为0
  //   戳工具置1进入计数暂停模式，ctrl+k时钟自动运行到对应节拍暂停
  //   ctrl+k关闭时钟连续运行，将控制位置零，进入单步调试模式调试
  //   用这个时钟源需要去掉电路中的其他时钟源
  //   可计数暂停的时钟源
endmodule

// 单周期硬布线控制器
module \单周期硬布线控制器  (
  input  [5:0] OP,
  input  [5:0] Func,
  input  [4:0] in_3,
  output [3:0] ALU_OP,
  output MemToReg,
  output LBU,
  output MemWrite,
  output SLLV,
  output SRAV,
  output BGEZ,
  output ALU_SRC,
  output RegWrite,
  output SysCALL,
  output SignedExt,
  output RegDst,
  output Beq,
  output Bne,
  output JR,
  output JMP,
  output JAL,
  output ERET,
  output MFC0,
  output MTC0
);

  \运算控制器自动生成  \u_运算控制器自动生成_1  (
    .OP0(OP[0]), .OP1(OP[1]), .OP2(OP[2]), .OP3(OP[3]), .OP4(OP[4]), .OP5(OP[5]), .F0(Func[0]), .F1(Func[1]),
    .F2(Func[2]), .F3(Func[3]), .F4(Func[4]), .F5(Func[5]), .S0(ALU_OP[0]), .S1(ALU_OP[1]), .S2(ALU_OP[2]),
    .S3(ALU_OP[3]));
  \控制信号自动生成  \u_控制信号自动生成_1  (
    .OP0(OP[0]), .OP1(OP[1]), .OP2(OP[2]), .OP3(OP[3]), .OP4(OP[4]), .OP5(OP[5]), .F0(Func[0]), .F1(Func[1]),
    .F2(Func[2]), .F3(Func[3]), .F4(Func[4]), .F5(Func[5]), .MemToReg(MemToReg), .LBU(LBU),
    .MemWrite(MemWrite), .SLLV(SLLV), .SRAV(SRAV), .BGEZ(BGEZ), .ALU_SRC(ALU_SRC), .RegWrite(RegWrite),
    .SysCALL(SysCALL), .SignedExt(SignedExt), .RegDst(RegDst), .BEQ(Beq), .BNE(Bne), .JR(JR), .JUMP(JMP),
    .JAL(JAL));
  and and_1 (ERET, ~OP[0], ~OP[1], ~OP[2], ~OP[3], OP[4], ~OP[5], ~Func[0], ~Func[1], ~Func[2], Func[3], Func[4], ~Func[5]);  // AND_Gate
  and and_2 (MFC0, ~OP[0], ~OP[1], ~OP[2], ~OP[3], OP[4], ~OP[5], ~in_3[0], ~in_3[1], ~in_3[2], ~in_3[3], ~in_3[4]);  // AND_Gate
  and and_3 (MTC0, ~OP[0], ~OP[1], ~OP[2], ~OP[3], OP[4], ~OP[5], ~in_3[0], ~in_3[1], in_3[2], ~in_3[3], ~in_3[4]);  // AND_Gate

  // Other names for the same wires on the sheet: MF[4:0] = in_3; OP_CODE[5:0] = OP

  // Notes on the sheet:
  //   运算器控制器，根据指令生成运算器功能选择信号
  //   控制信号生成，产生数据通路需要的其他控制信号
endmodule

// 运算器控制器
module \运算控制器自动生成  (
  input  OP0,
  input  OP1,
  input  OP2,
  input  OP3,
  input  OP4,
  input  OP5,
  input  F0,
  input  F1,
  input  F2,
  input  F3,
  input  F4,
  input  F5,
  output S0,
  output S1,
  output S2,
  output S3
);

  wire and_1_out, and_2_out, and_3_out, and_4_out, and_5_out, and_6_out, and_7_out, and_8_out, and_9_out,
       and_10_out, and_11_out, and_12_out, and_13_out, and_14_out, and_15_out, and_16_out, and_17_out,
       and_18_out, and_19_out, and_20_out, and_21_out, and_22_out, and_23_out, and_24_out, and_25_out,
       and_26_out, and_27_out, and_28_out, and_29_out, and_30_out, and_31_out, and_32_out, and_33_out,
       and_34_out, and_35_out, and_36_out, and_37_out, and_38_out, and_39_out, and_40_out, not_1_out,
       not_2_out, not_3_out, not_4_out, not_5_out, not_6_out, not_7_out, not_8_out, not_9_out, not_10_out,
       not_11_out, not_12_out, not_13_out, not_14_out, not_15_out, not_16_out, not_17_out, not_18_out,
       not_19_out, not_20_out, not_21_out, not_22_out, not_23_out, not_24_out, not_25_out, not_26_out,
       not_27_out, not_28_out, not_29_out, not_30_out, not_31_out, not_32_out, not_33_out, not_34_out,
       not_35_out, not_36_out, not_37_out, not_38_out, not_39_out, not_40_out, not_41_out, not_42_out,
       not_43_out, not_44_out, not_45_out, not_46_out, not_47_out, not_48_out, not_49_out, not_50_out,
       not_51_out, not_52_out, not_53_out, not_54_out, not_55_out, not_56_out, not_57_out, not_58_out,
       not_59_out, not_60_out, not_61_out, not_62_out, not_63_out, not_64_out, not_65_out, not_66_out,
       not_67_out, not_68_out, not_69_out, not_70_out, not_71_out, not_72_out, not_73_out, not_74_out,
       not_75_out, not_76_out, not_77_out, not_78_out, not_79_out, not_80_out, not_81_out, not_82_out,
       not_83_out, not_84_out, not_85_out, not_86_out, not_87_out, not_88_out, not_89_out, not_90_out,
       not_91_out, not_92_out, not_93_out, not_94_out, not_95_out, not_96_out, not_97_out, not_98_out,
       not_99_out, not_100_out, not_101_out, not_102_out, not_103_out, not_104_out, not_105_out, not_106_out,
       not_107_out, not_108_out, not_109_out, not_110_out, not_111_out, not_112_out, not_113_out,
       not_114_out, not_115_out, not_116_out, not_117_out, not_118_out, not_119_out, not_120_out,
       not_121_out, not_122_out, not_123_out, not_124_out, not_125_out, not_126_out, not_127_out,
       not_128_out, not_129_out, not_130_out, not_131_out, not_132_out, not_133_out, not_134_out,
       not_135_out, not_136_out, not_137_out, not_138_out, not_139_out, not_140_out, not_141_out,
       not_142_out, not_143_out, not_144_out, not_145_out, not_146_out, not_147_out, not_148_out,
       not_149_out, not_150_out, not_151_out, not_152_out, not_153_out, not_154_out, not_155_out,
       not_156_out, not_157_out, not_158_out, not_159_out, not_160_out, not_161_out, not_162_out,
       not_163_out, not_164_out, not_165_out, not_166_out, not_167_out, not_168_out, not_169_out,
       not_170_out, not_171_out, not_172_out, not_173_out, not_174_out, not_175_out, not_176_out,
       not_177_out, not_178_out, not_179_out, not_180_out, not_181_out, not_182_out, not_183_out,
       not_184_out, not_185_out, not_186_out, not_187_out, not_188_out, not_189_out, not_190_out,
       not_191_out, not_192_out, not_193_out, not_194_out, not_195_out, not_196_out, not_197_out,
       not_198_out, not_199_out, not_200_out, not_201_out, not_202_out, not_203_out, not_204_out,
       not_205_out, not_206_out, not_207_out, not_208_out, not_209_out, not_210_out, not_211_out,
       not_212_out, not_213_out, not_214_out, not_215_out, not_216_out, not_217_out, not_218_out,
       not_219_out, not_220_out, not_221_out, not_222_out, not_223_out, not_224_out, not_225_out,
       not_226_out, not_227_out, not_228_out, not_229_out, not_230_out, not_231_out, not_232_out,
       not_233_out, not_234_out, not_235_out, not_236_out, not_237_out, not_238_out, not_239_out,
       not_240_out, not_241_out, not_242_out, not_243_out, not_244_out, not_245_out, not_246_out,
       not_247_out, not_248_out, not_249_out, not_250_out, not_251_out, not_252_out, not_253_out,
       not_254_out, not_255_out, not_256_out, not_257_out, not_258_out, not_259_out, not_260_out,
       not_261_out, not_262_out, not_263_out, not_264_out, not_265_out, not_266_out, not_267_out, not_268_out;

  not not_1 (not_1_out, OP5);
  not not_2 (not_2_out, OP4);
  not not_3 (not_3_out, OP3);
  not not_4 (not_4_out, OP2);
  not not_5 (not_5_out, OP1);
  not not_6 (not_6_out, OP0);
  not not_7 (not_7_out, F5);
  not not_8 (not_8_out, F4);
  not not_9 (not_9_out, F3);
  not not_10 (not_10_out, F2);
  not not_11 (not_11_out, OP5);
  not not_12 (not_12_out, OP4);
  not not_13 (not_13_out, OP3);
  not not_14 (not_14_out, OP2);
  not not_15 (not_15_out, OP1);
  not not_16 (not_16_out, OP0);
  not not_17 (not_17_out, F4);
  not not_18 (not_18_out, F3);
  not not_19 (not_19_out, F2);
  not not_20 (not_20_out, F1);
  not not_21 (not_21_out, F0);
  not not_22 (not_22_out, OP5);
  not not_23 (not_23_out, OP4);
  not not_24 (not_24_out, OP3);
  not not_25 (not_25_out, OP2);
  not not_26 (not_26_out, OP1);
  not not_27 (not_27_out, OP0);
  not not_28 (not_28_out, F4);
  not not_29 (not_29_out, F3);
  not not_30 (not_30_out, F2);
  not not_31 (not_31_out, F1);
  not not_32 (not_32_out, OP5);
  not not_33 (not_33_out, OP4);
  not not_34 (not_34_out, OP3);
  not not_35 (not_35_out, OP2);
  not not_36 (not_36_out, OP1);
  not not_37 (not_37_out, OP0);
  not not_38 (not_38_out, F4);
  not not_39 (not_39_out, F3);
  not not_40 (not_40_out, F1);
  not not_41 (not_41_out, F0);
  not not_42 (not_42_out, OP5);
  not not_43 (not_43_out, OP4);
  not not_44 (not_44_out, OP3);
  not not_45 (not_45_out, OP2);
  not not_46 (not_46_out, OP1);
  not not_47 (not_47_out, OP0);
  not not_48 (not_48_out, F4);
  not not_49 (not_49_out, F2);
  not not_50 (not_50_out, F0);
  not not_51 (not_51_out, OP5);
  not not_52 (not_52_out, OP4);
  not not_53 (not_53_out, OP2);
  not not_54 (not_54_out, OP1);
  not not_55 (not_55_out, OP0);
  not not_56 (not_56_out, OP5);
  not not_57 (not_57_out, OP4);
  not not_58 (not_58_out, OP1);
  not not_59 (not_59_out, OP0);
  not not_60 (not_60_out, OP5);
  not not_61 (not_61_out, OP4);
  not not_62 (not_62_out, OP2);
  not not_63 (not_63_out, OP1);
  not not_64 (not_64_out, OP5);
  not not_65 (not_65_out, OP4);
  not not_66 (not_66_out, OP2);
  not not_67 (not_67_out, OP0);
  not not_68 (not_68_out, OP4);
  not not_69 (not_69_out, OP3);
  not not_70 (not_70_out, OP2);
  not not_71 (not_71_out, OP4);
  not not_72 (not_72_out, OP2);
  not not_73 (not_73_out, OP5);
  not not_74 (not_74_out, OP4);
  not not_75 (not_75_out, OP3);
  not not_76 (not_76_out, OP2);
  not not_77 (not_77_out, OP1);
  not not_78 (not_78_out, OP0);
  not not_79 (not_79_out, F5);
  not not_80 (not_80_out, F4);
  not not_81 (not_81_out, F3);
  not not_82 (not_82_out, OP4);
  not not_83 (not_83_out, OP3);
  not not_84 (not_84_out, OP1);
  not not_85 (not_85_out, OP0);
  not not_86 (not_86_out, OP5);
  not not_87 (not_87_out, OP4);
  not not_88 (not_88_out, OP3);
  not not_89 (not_89_out, OP2);
  not not_90 (not_90_out, OP1);
  not not_91 (not_91_out, OP5);
  not not_92 (not_92_out, OP4);
  not not_93 (not_93_out, OP3);
  not not_94 (not_94_out, OP2);
  not not_95 (not_95_out, OP1);
  not not_96 (not_96_out, OP0);
  not not_97 (not_97_out, F5);
  not not_98 (not_98_out, F4);
  not not_99 (not_99_out, F3);
  not not_100 (not_100_out, F2);
  not not_101 (not_101_out, F0);
  not not_102 (not_102_out, OP5);
  not not_103 (not_103_out, OP4);
  not not_104 (not_104_out, OP3);
  not not_105 (not_105_out, OP2);
  not not_106 (not_106_out, OP1);
  not not_107 (not_107_out, OP0);
  not not_108 (not_108_out, F4);
  not not_109 (not_109_out, F3);
  not not_110 (not_110_out, F2);
  not not_111 (not_111_out, F0);
  not not_112 (not_112_out, OP5);
  not not_113 (not_113_out, OP4);
  not not_114 (not_114_out, OP3);
  not not_115 (not_115_out, OP2);
  not not_116 (not_116_out, OP1);
  not not_117 (not_117_out, OP0);
  not not_118 (not_118_out, F4);
  not not_119 (not_119_out, F3);
  not not_120 (not_120_out, F1);
  not not_121 (not_121_out, F0);
  not not_122 (not_122_out, OP5);
  not not_123 (not_123_out, OP4);
  not not_124 (not_124_out, OP3);
  not not_125 (not_125_out, OP2);
  not not_126 (not_126_out, OP1);
  not not_127 (not_127_out, OP0);
  not not_128 (not_128_out, F4);
  not not_129 (not_129_out, F3);
  not not_130 (not_130_out, OP5);
  not not_131 (not_131_out, OP4);
  not not_132 (not_132_out, OP3);
  not not_133 (not_133_out, OP2);
  not not_134 (not_134_out, OP1);
  not not_135 (not_135_out, OP0);
  not not_136 (not_136_out, F4);
  not not_137 (not_137_out, F2);
  not not_138 (not_138_out, F0);
  not not_139 (not_139_out, OP5);
  not not_140 (not_140_out, OP4);
  not not_141 (not_141_out, OP1);
  not not_142 (not_142_out, OP0);
  not not_143 (not_143_out, OP5);
  not not_144 (not_144_out, OP4);
  not not_145 (not_145_out, OP2);
  not not_146 (not_146_out, OP0);
  not not_147 (not_147_out, OP5);
  not not_148 (not_148_out, OP4);
  not not_149 (not_149_out, OP3);
  not not_150 (not_150_out, OP2);
  not not_151 (not_151_out, OP1);
  not not_152 (not_152_out, OP5);
  not not_153 (not_153_out, OP4);
  not not_154 (not_154_out, OP3);
  not not_155 (not_155_out, OP2);
  not not_156 (not_156_out, OP1);
  not not_157 (not_157_out, OP0);
  not not_158 (not_158_out, F4);
  not not_159 (not_159_out, F3);
  not not_160 (not_160_out, F2);
  not not_161 (not_161_out, F1);
  not not_162 (not_162_out, F0);
  not not_163 (not_163_out, OP5);
  not not_164 (not_164_out, OP4);
  not not_165 (not_165_out, OP3);
  not not_166 (not_166_out, OP2);
  not not_167 (not_167_out, OP1);
  not not_168 (not_168_out, OP0);
  not not_169 (not_169_out, F4);
  not not_170 (not_170_out, F3);
  not not_171 (not_171_out, F2);
  not not_172 (not_172_out, F1);
  not not_173 (not_173_out, OP5);
  not not_174 (not_174_out, OP4);
  not not_175 (not_175_out, OP3);
  not not_176 (not_176_out, OP2);
  not not_177 (not_177_out, OP1);
  not not_178 (not_178_out, OP0);
  not not_179 (not_179_out, F4);
  not not_180 (not_180_out, F3);
  not not_181 (not_181_out, F2);
  not not_182 (not_182_out, F0);
  not not_183 (not_183_out, OP5);
  not not_184 (not_184_out, OP4);
  not not_185 (not_185_out, OP3);
  not not_186 (not_186_out, OP2);
  not not_187 (not_187_out, OP1);
  not not_188 (not_188_out, OP0);
  not not_189 (not_189_out, F4);
  not not_190 (not_190_out, F3);
  not not_191 (not_191_out, F1);
  not not_192 (not_192_out, F0);
  not not_193 (not_193_out, OP5);
  not not_194 (not_194_out, OP4);
  not not_195 (not_195_out, OP3);
  not not_196 (not_196_out, OP2);
  not not_197 (not_197_out, OP1);
  not not_198 (not_198_out, OP0);
  not not_199 (not_199_out, F4);
  not not_200 (not_200_out, F2);
  not not_201 (not_201_out, OP5);
  not not_202 (not_202_out, OP4);
  not not_203 (not_203_out, OP2);
  not not_204 (not_204_out, OP1);
  not not_205 (not_205_out, OP0);
  not not_206 (not_206_out, OP5);
  not not_207 (not_207_out, OP4);
  not not_208 (not_208_out, OP1);
  not not_209 (not_209_out, OP0);
  not not_210 (not_210_out, OP5);
  not not_211 (not_211_out, OP4);
  not not_212 (not_212_out, OP2);
  not not_213 (not_213_out, OP1);
  not not_214 (not_214_out, OP4);
  not not_215 (not_215_out, OP3);
  not not_216 (not_216_out, OP2);
  not not_217 (not_217_out, OP4);
  not not_218 (not_218_out, OP2);
  not not_219 (not_219_out, OP4);
  not not_220 (not_220_out, OP3);
  not not_221 (not_221_out, OP1);
  not not_222 (not_222_out, OP0);
  not not_223 (not_223_out, OP5);
  not not_224 (not_224_out, OP4);
  not not_225 (not_225_out, OP3);
  not not_226 (not_226_out, OP2);
  not not_227 (not_227_out, OP1);
  not not_228 (not_228_out, OP0);
  not not_229 (not_229_out, F4);
  not not_230 (not_230_out, F3);
  not not_231 (not_231_out, F1);
  not not_232 (not_232_out, OP5);
  not not_233 (not_233_out, OP4);
  not not_234 (not_234_out, OP3);
  not not_235 (not_235_out, OP2);
  not not_236 (not_236_out, OP1);
  not not_237 (not_237_out, OP0);
  not not_238 (not_238_out, F4);
  not not_239 (not_239_out, F3);
  not not_240 (not_240_out, OP5);
  not not_241 (not_241_out, OP4);
  not not_242 (not_242_out, OP3);
  not not_243 (not_243_out, OP2);
  not not_244 (not_244_out, OP1);
  not not_245 (not_245_out, OP0);
  not not_246 (not_246_out, F4);
  not not_247 (not_247_out, F2);
  not not_248 (not_248_out, F0);
  not not_249 (not_249_out, OP5);
  not not_250 (not_250_out, OP4);
  not not_251 (not_251_out, OP3);
  not not_252 (not_252_out, OP2);
  not not_253 (not_253_out, OP1);
  not not_254 (not_254_out, OP0);
  not not_255 (not_255_out, F4);
  not not_256 (not_256_out, F2);
  not not_257 (not_257_out, OP5);
  not not_258 (not_258_out, OP4);
  not not_259 (not_259_out, OP2);
  not not_260 (not_260_out, OP0);
  not not_261 (not_261_out, OP5);
  not not_262 (not_262_out, OP4);
  not not_263 (not_263_out, OP1);
  not not_264 (not_264_out, OP5);
  not not_265 (not_265_out, OP4);
  not not_266 (not_266_out, OP3);
  not not_267 (not_267_out, OP2);
  not not_268 (not_268_out, OP1);
  and and_1 (and_1_out, not_1_out, not_2_out, not_3_out, not_4_out, not_5_out, not_6_out, not_7_out, not_8_out, not_9_out, not_10_out, F1, F0);
  and and_2 (and_2_out, not_11_out, not_12_out, not_13_out, not_14_out, not_15_out, not_16_out, F5, not_17_out, not_18_out, not_19_out, not_20_out, not_21_out);
  and and_3 (and_3_out, not_22_out, not_23_out, not_24_out, not_25_out, not_26_out, not_27_out, F5, not_28_out, not_29_out, not_30_out, not_31_out, F0);
  and and_4 (and_4_out, not_32_out, not_33_out, not_34_out, not_35_out, not_36_out, not_37_out, F5, not_38_out, not_39_out, F2, not_40_out, not_41_out);
  and and_5 (and_5_out, not_42_out, not_43_out, not_44_out, not_45_out, not_46_out, not_47_out, F5, not_48_out, F3, not_49_out, F1, not_50_out);
  and and_6 (and_6_out, not_51_out, not_52_out, OP3, not_53_out, not_54_out, not_55_out);
  and and_7 (and_7_out, not_56_out, not_57_out, OP3, OP2, not_58_out, not_59_out);
  and and_8 (and_8_out, not_60_out, not_61_out, OP3, not_62_out, not_63_out, OP0);
  and and_9 (and_9_out, not_64_out, not_65_out, OP3, not_66_out, OP1, not_67_out);
  and and_10 (and_10_out, OP5, not_68_out, not_69_out, not_70_out, OP1, OP0);
  and and_11 (and_11_out, OP5, not_71_out, OP3, not_72_out, OP1, OP0);
  and and_12 (and_12_out, not_73_out, not_74_out, not_75_out, not_76_out, not_77_out, not_78_out, not_79_out, not_80_out, not_81_out, F2, F1, F0);
  and and_13 (and_13_out, OP5, not_82_out, not_83_out, OP2, not_84_out, not_85_out);
  and and_14 (and_14_out, not_86_out, not_87_out, not_88_out, not_89_out, not_90_out, OP0);
  and and_15 (and_15_out, not_91_out, not_92_out, not_93_out, not_94_out, not_95_out, not_96_out, not_97_out, not_98_out, not_99_out, not_100_out, F1, not_101_out);
  and and_16 (and_16_out, not_102_out, not_103_out, not_104_out, not_105_out, not_106_out, not_107_out, F5, not_108_out, not_109_out, not_110_out, F1, not_111_out);
  and and_17 (and_17_out, not_112_out, not_113_out, not_114_out, not_115_out, not_116_out, not_117_out, F5, not_118_out, not_119_out, F2, not_120_out, not_121_out);
  and and_18 (and_18_out, not_122_out, not_123_out, not_124_out, not_125_out, not_126_out, not_127_out, F5, not_128_out, not_129_out, F2, F1, F0);
  and and_19 (and_19_out, not_130_out, not_131_out, not_132_out, not_133_out, not_134_out, not_135_out, F5, not_136_out, F3, not_137_out, F1, not_138_out);
  and and_20 (and_20_out, not_139_out, not_140_out, OP3, OP2, not_141_out, not_142_out);
  and and_21 (and_21_out, not_143_out, not_144_out, OP3, not_145_out, OP1, not_146_out);
  and and_22 (and_22_out, not_147_out, not_148_out, not_149_out, not_150_out, not_151_out, OP0);
  and and_23 (and_23_out, not_152_out, not_153_out, not_154_out, not_155_out, not_156_out, not_157_out, F5, not_158_out, not_159_out, not_160_out, not_161_out, not_162_out);
  and and_24 (and_24_out, not_163_out, not_164_out, not_165_out, not_166_out, not_167_out, not_168_out, F5, not_169_out, not_170_out, not_171_out, not_172_out, F0);
  and and_25 (and_25_out, not_173_out, not_174_out, not_175_out, not_176_out, not_177_out, not_178_out, F5, not_179_out, not_180_out, not_181_out, F1, not_182_out);
  and and_26 (and_26_out, not_183_out, not_184_out, not_185_out, not_186_out, not_187_out, not_188_out, F5, not_189_out, not_190_out, F2, not_191_out, not_192_out);
  and and_27 (and_27_out, not_193_out, not_194_out, not_195_out, not_196_out, not_197_out, not_198_out, F5, not_199_out, F3, not_200_out, F1, F0);
  and and_28 (and_28_out, not_201_out, not_202_out, OP3, not_203_out, not_204_out, not_205_out);
  and and_29 (and_29_out, not_206_out, not_207_out, OP3, OP2, not_208_out, not_209_out);
  and and_30 (and_30_out, not_210_out, not_211_out, OP3, not_212_out, not_213_out, OP0);
  and and_31 (and_31_out, OP5, not_214_out, not_215_out, not_216_out, OP1, OP0);
  and and_32 (and_32_out, OP5, not_217_out, OP3, not_218_out, OP1, OP0);
  and and_33 (and_33_out, OP5, not_219_out, not_220_out, OP2, not_221_out, not_222_out);
  and and_34 (and_34_out, not_223_out, not_224_out, not_225_out, not_226_out, not_227_out, not_228_out, F5, not_229_out, not_230_out, F2, not_231_out, F0);
  and and_35 (and_35_out, not_232_out, not_233_out, not_234_out, not_235_out, not_236_out, not_237_out, F5, not_238_out, not_239_out, F2, F1, F0);
  and and_36 (and_36_out, not_240_out, not_241_out, not_242_out, not_243_out, not_244_out, not_245_out, F5, not_246_out, F3, not_247_out, F1, not_248_out);
  and and_37 (and_37_out, not_249_out, not_250_out, not_251_out, not_252_out, not_253_out, not_254_out, F5, not_255_out, F3, not_256_out, F1, F0);
  and and_38 (and_38_out, not_257_out, not_258_out, OP3, not_259_out, OP1, not_260_out);
  and and_39 (and_39_out, not_261_out, not_262_out, OP3, OP2, not_263_out, OP0);
  and and_40 (and_40_out, not_264_out, not_265_out, not_266_out, not_267_out, not_268_out, OP0);
  or or_1 (S1, and_15_out, and_16_out, and_17_out, and_18_out, and_19_out, and_20_out, and_21_out, and_22_out);
  or or_2 (S2, and_23_out, and_24_out, and_25_out, and_26_out, and_27_out, and_28_out, and_29_out, and_30_out, and_31_out, and_32_out, and_33_out);
  or or_3 (S3, and_34_out, and_35_out, and_36_out, and_37_out, and_38_out, and_39_out, and_40_out);
  or or_4 (S0, and_1_out, and_2_out, and_3_out, and_4_out, and_5_out, and_6_out, and_7_out, and_8_out, and_9_out, and_10_out, and_11_out, and_12_out, and_13_out, and_14_out);
endmodule

// 控制信号生成
module \控制信号自动生成  (
  input  OP0,
  input  OP1,
  input  OP2,
  input  OP3,
  input  OP4,
  input  OP5,
  input  F0,
  input  F1,
  input  F2,
  input  F3,
  input  F4,
  input  F5,
  output MemToReg,
  output LBU,
  output MemWrite,
  output SLLV,
  output SRAV,
  output BGEZ,
  output ALU_SRC,
  output RegWrite,
  output SysCALL,
  output SignedExt,
  output RegDst,
  output BEQ,
  output BNE,
  output JR,
  output JUMP,
  output JAL
);

  wire and_1_out, and_2_out, and_8_out, and_9_out, and_10_out, and_11_out, and_12_out, and_13_out,
       and_14_out, and_15_out, and_16_out, and_17_out, and_18_out, and_19_out, and_20_out, and_21_out,
       and_22_out, and_23_out, and_24_out, and_25_out, and_26_out, and_27_out, and_28_out, and_29_out,
       and_30_out, and_31_out, and_32_out, and_33_out, and_34_out, and_35_out, and_36_out, and_38_out,
       and_39_out, and_40_out, and_41_out, and_42_out, and_43_out, and_44_out, and_45_out, and_46_out,
       and_47_out, and_48_out, and_49_out, and_50_out, and_51_out, and_52_out, and_53_out, and_54_out,
       and_55_out, and_56_out, and_57_out, and_58_out, and_59_out, and_63_out, and_64_out, and_65_out,
       not_1_out, not_2_out, not_3_out, not_4_out, not_5_out, not_6_out, not_7_out, not_8_out, not_9_out,
       not_10_out, not_11_out, not_12_out, not_13_out, not_14_out, not_15_out, not_16_out, not_17_out,
       not_18_out, not_19_out, not_20_out, not_21_out, not_22_out, not_23_out, not_24_out, not_25_out,
       not_26_out, not_27_out, not_28_out, not_29_out, not_30_out, not_31_out, not_32_out, not_33_out,
       not_34_out, not_35_out, not_36_out, not_37_out, not_38_out, not_39_out, not_40_out, not_41_out,
       not_42_out, not_43_out, not_44_out, not_45_out, not_46_out, not_47_out, not_48_out, not_49_out,
       not_50_out, not_51_out, not_52_out, not_53_out, not_54_out, not_55_out, not_56_out, not_57_out,
       not_58_out, not_59_out, not_60_out, not_61_out, not_62_out, not_63_out, not_64_out, not_65_out,
       not_66_out, not_67_out, not_68_out, not_69_out, not_70_out, not_71_out, not_72_out, not_73_out,
       not_74_out, not_75_out, not_76_out, not_77_out, not_78_out, not_79_out, not_80_out, not_81_out,
       not_82_out, not_83_out, not_84_out, not_85_out, not_86_out, not_87_out, not_88_out, not_89_out,
       not_90_out, not_91_out, not_92_out, not_93_out, not_94_out, not_95_out, not_96_out, not_97_out,
       not_98_out, not_99_out, not_100_out, not_101_out, not_102_out, not_103_out, not_104_out, not_105_out,
       not_106_out, not_107_out, not_108_out, not_109_out, not_110_out, not_111_out, not_112_out,
       not_113_out, not_114_out, not_115_out, not_116_out, not_117_out, not_118_out, not_119_out,
       not_120_out, not_121_out, not_122_out, not_123_out, not_124_out, not_125_out, not_126_out,
       not_127_out, not_128_out, not_129_out, not_130_out, not_131_out, not_132_out, not_133_out,
       not_134_out, not_135_out, not_136_out, not_137_out, not_138_out, not_139_out, not_140_out,
       not_141_out, not_142_out, not_143_out, not_144_out, not_145_out, not_146_out, not_147_out,
       not_148_out, not_149_out, not_150_out, not_151_out, not_152_out, not_153_out, not_154_out,
       not_155_out, not_156_out, not_157_out, not_158_out, not_159_out, not_160_out, not_161_out,
       not_162_out, not_163_out, not_164_out, not_165_out, not_166_out, not_167_out, not_168_out,
       not_169_out, not_170_out, not_171_out, not_172_out, not_173_out, not_174_out, not_175_out,
       not_176_out, not_177_out, not_178_out, not_179_out, not_180_out, not_181_out, not_182_out,
       not_183_out, not_184_out, not_185_out, not_186_out, not_187_out, not_188_out, not_189_out,
       not_190_out, not_191_out, not_192_out, not_193_out, not_194_out, not_195_out, not_196_out,
       not_197_out, not_198_out, not_199_out, not_200_out, not_201_out, not_202_out, not_203_out,
       not_204_out, not_205_out, not_206_out, not_207_out, not_208_out, not_209_out, not_210_out,
       not_211_out, not_212_out, not_213_out, not_214_out, not_215_out, not_216_out, not_217_out,
       not_218_out, not_219_out, not_220_out, not_221_out, not_222_out, not_223_out, not_224_out,
       not_225_out, not_226_out, not_227_out, not_228_out, not_229_out, not_230_out, not_231_out,
       not_232_out, not_233_out, not_234_out, not_235_out, not_236_out, not_237_out, not_238_out,
       not_239_out, not_240_out, not_241_out, not_242_out, not_243_out, not_244_out, not_245_out,
       not_246_out, not_247_out, not_248_out, not_249_out, not_250_out, not_251_out, not_252_out,
       not_253_out, not_254_out, not_255_out, not_256_out, not_257_out, not_258_out, not_259_out,
       not_260_out, not_261_out, not_262_out, not_263_out, not_264_out, not_265_out, not_266_out,
       not_267_out, not_268_out, not_269_out, not_270_out, not_271_out, not_272_out, not_273_out,
       not_274_out, not_275_out, not_276_out, not_277_out, not_278_out, not_279_out, not_280_out,
       not_281_out, not_282_out, not_283_out, not_284_out, not_285_out, not_286_out, not_287_out,
       not_288_out, not_289_out, not_290_out, not_291_out, not_292_out, not_293_out, not_294_out,
       not_295_out, not_296_out, not_297_out, not_298_out, not_299_out, not_300_out, not_301_out,
       not_302_out, not_303_out, not_304_out, not_305_out, not_306_out, not_307_out, not_308_out,
       not_309_out, not_310_out, not_311_out, not_312_out, not_313_out, not_314_out, not_315_out,
       not_316_out, not_317_out, not_318_out, not_319_out, not_320_out, not_321_out, not_322_out,
       not_323_out, not_324_out, not_325_out, not_326_out, not_327_out, not_328_out, not_329_out,
       not_330_out, not_331_out, not_332_out, not_333_out, not_334_out, not_335_out, not_336_out,
       not_337_out, not_338_out, not_339_out, not_340_out, not_341_out, not_342_out, not_343_out,
       not_344_out, not_345_out, not_346_out, not_347_out, not_348_out, not_349_out, not_350_out,
       not_351_out, not_352_out, not_353_out, not_354_out, not_355_out, not_356_out, not_357_out,
       not_358_out, not_359_out, not_360_out, not_361_out, not_362_out, not_363_out, not_364_out,
       not_365_out, not_366_out, not_367_out, not_368_out, not_369_out, not_370_out, not_371_out,
       not_372_out, not_373_out, not_374_out, not_375_out, not_376_out, not_377_out, not_378_out,
       not_379_out, not_380_out, not_381_out, not_382_out, not_383_out, not_384_out, not_385_out,
       not_386_out, not_387_out, not_388_out, not_389_out, not_390_out, not_391_out, not_392_out,
       not_393_out, not_394_out, not_395_out, not_396_out, not_397_out, not_398_out, not_399_out,
       not_400_out, not_401_out, not_402_out, not_403_out, not_404_out, not_405_out, not_406_out,
       not_407_out, not_408_out, not_409_out, not_410_out, not_411_out, not_412_out, not_413_out,
       not_414_out, not_415_out, not_416_out, not_417_out, not_418_out, not_419_out, not_420_out,
       not_421_out, not_422_out, not_423_out, not_424_out, not_425_out, not_426_out, not_427_out,
       not_428_out, not_429_out, not_430_out, not_431_out, not_432_out, not_433_out, not_434_out,
       not_435_out, not_436_out, not_437_out, not_438_out, not_439_out, not_440_out, not_441_out,
       not_442_out, not_443_out, not_444_out;

  not not_1 (not_1_out, OP4);
  not not_2 (not_2_out, OP3);
  not not_3 (not_3_out, OP2);
  not not_4 (not_4_out, OP4);
  not not_5 (not_5_out, OP3);
  not not_6 (not_6_out, OP1);
  not not_7 (not_7_out, OP0);
  not not_8 (not_8_out, OP4);
  not not_9 (not_9_out, OP3);
  not not_10 (not_10_out, OP1);
  not not_11 (not_11_out, OP0);
  not not_12 (not_12_out, OP4);
  not not_13 (not_13_out, OP2);
  not not_14 (not_14_out, OP5);
  not not_15 (not_15_out, OP4);
  not not_16 (not_16_out, OP3);
  not not_17 (not_17_out, OP2);
  not not_18 (not_18_out, OP1);
  not not_19 (not_19_out, OP0);
  not not_20 (not_20_out, F5);
  not not_21 (not_21_out, F4);
  not not_22 (not_22_out, F3);
  not not_23 (not_23_out, F1);
  not not_24 (not_24_out, F0);
  not not_25 (not_25_out, OP5);
  not not_26 (not_26_out, OP4);
  not not_27 (not_27_out, OP3);
  not not_28 (not_28_out, OP2);
  not not_29 (not_29_out, OP1);
  not not_30 (not_30_out, OP0);
  not not_31 (not_31_out, F5);
  not not_32 (not_32_out, F4);
  not not_33 (not_33_out, F3);
  not not_34 (not_34_out, OP5);
  not not_35 (not_35_out, OP4);
  not not_36 (not_36_out, OP3);
  not not_37 (not_37_out, OP2);
  not not_38 (not_38_out, OP1);
  not not_39 (not_39_out, OP5);
  not not_40 (not_40_out, OP4);
  not not_41 (not_41_out, OP2);
  not not_42 (not_42_out, OP1);
  not not_43 (not_43_out, OP0);
  not not_44 (not_44_out, OP5);
  not not_45 (not_45_out, OP4);
  not not_46 (not_46_out, OP1);
  not not_47 (not_47_out, OP0);
  not not_48 (not_48_out, OP5);
  not not_49 (not_49_out, OP4);
  not not_50 (not_50_out, OP2);
  not not_51 (not_51_out, OP1);
  not not_52 (not_52_out, OP5);
  not not_53 (not_53_out, OP4);
  not not_54 (not_54_out, OP2);
  not not_55 (not_55_out, OP0);
  not not_56 (not_56_out, OP5);
  not not_57 (not_57_out, OP4);
  not not_58 (not_58_out, OP1);
  not not_59 (not_59_out, OP4);
  not not_60 (not_60_out, OP3);
  not not_61 (not_61_out, OP2);
  not not_62 (not_62_out, OP4);
  not not_63 (not_63_out, OP2);
  not not_64 (not_64_out, OP4);
  not not_65 (not_65_out, OP3);
  not not_66 (not_66_out, OP1);
  not not_67 (not_67_out, OP0);
  not not_68 (not_68_out, OP5);
  not not_69 (not_69_out, OP4);
  not not_70 (not_70_out, OP3);
  not not_71 (not_71_out, OP2);
  not not_72 (not_72_out, OP1);
  not not_73 (not_73_out, OP0);
  not not_74 (not_74_out, F5);
  not not_75 (not_75_out, F4);
  not not_76 (not_76_out, F3);
  not not_77 (not_77_out, F2);
  not not_78 (not_78_out, F1);
  not not_79 (not_79_out, F0);
  not not_80 (not_80_out, OP5);
  not not_81 (not_81_out, OP4);
  not not_82 (not_82_out, OP3);
  not not_83 (not_83_out, OP2);
  not not_84 (not_84_out, OP1);
  not not_85 (not_85_out, OP0);
  not not_86 (not_86_out, F5);
  not not_87 (not_87_out, F4);
  not not_88 (not_88_out, F3);
  not not_89 (not_89_out, F2);
  not not_90 (not_90_out, OP5);
  not not_91 (not_91_out, OP4);
  not not_92 (not_92_out, OP3);
  not not_93 (not_93_out, OP2);
  not not_94 (not_94_out, OP1);
  not not_95 (not_95_out, OP0);
  not not_96 (not_96_out, F5);
  not not_97 (not_97_out, F4);
  not not_98 (not_98_out, F3);
  not not_99 (not_99_out, F2);
  not not_100 (not_100_out, F0);
  not not_101 (not_101_out, OP5);
  not not_102 (not_102_out, OP4);
  not not_103 (not_103_out, OP3);
  not not_104 (not_104_out, OP2);
  not not_105 (not_105_out, OP1);
  not not_106 (not_106_out, OP0);
  not not_107 (not_107_out, F4);
  not not_108 (not_108_out, F3);
  not not_109 (not_109_out, F2);
  not not_110 (not_110_out, F1);
  not not_111 (not_111_out, F0);
  not not_112 (not_112_out, OP5);
  not not_113 (not_113_out, OP4);
  not not_114 (not_114_out, OP3);
  not not_115 (not_115_out, OP2);
  not not_116 (not_116_out, OP1);
  not not_117 (not_117_out, OP0);
  not not_118 (not_118_out, F4);
  not not_119 (not_119_out, F3);
  not not_120 (not_120_out, F2);
  not not_121 (not_121_out, F1);
  not not_122 (not_122_out, OP5);
  not not_123 (not_123_out, OP4);
  not not_124 (not_124_out, OP3);
  not not_125 (not_125_out, OP2);
  not not_126 (not_126_out, OP1);
  not not_127 (not_127_out, OP0);
  not not_128 (not_128_out, F4);
  not not_129 (not_129_out, F3);
  not not_130 (not_130_out, F2);
  not not_131 (not_131_out, F0);
  not not_132 (not_132_out, OP5);
  not not_133 (not_133_out, OP4);
  not not_134 (not_134_out, OP3);
  not not_135 (not_135_out, OP2);
  not not_136 (not_136_out, OP1);
  not not_137 (not_137_out, OP0);
  not not_138 (not_138_out, F4);
  not not_139 (not_139_out, F3);
  not not_140 (not_140_out, F1);
  not not_141 (not_141_out, F0);
  not not_142 (not_142_out, OP5);
  not not_143 (not_143_out, OP4);
  not not_144 (not_144_out, OP3);
  not not_145 (not_145_out, OP2);
  not not_146 (not_146_out, OP1);
  not not_147 (not_147_out, OP0);
  not not_148 (not_148_out, F4);
  not not_149 (not_149_out, F3);
  not not_150 (not_150_out, F1);
  not not_151 (not_151_out, OP5);
  not not_152 (not_152_out, OP4);
  not not_153 (not_153_out, OP3);
  not not_154 (not_154_out, OP2);
  not not_155 (not_155_out, OP1);
  not not_156 (not_156_out, OP0);
  not not_157 (not_157_out, F4);
  not not_158 (not_158_out, F3);
  not not_159 (not_159_out, OP5);
  not not_160 (not_160_out, OP4);
  not not_161 (not_161_out, OP3);
  not not_162 (not_162_out, OP2);
  not not_163 (not_163_out, OP1);
  not not_164 (not_164_out, OP0);
  not not_165 (not_165_out, F4);
  not not_166 (not_166_out, F2);
  not not_167 (not_167_out, F0);
  not not_168 (not_168_out, OP5);
  not not_169 (not_169_out, OP4);
  not not_170 (not_170_out, OP3);
  not not_171 (not_171_out, OP2);
  not not_172 (not_172_out, OP1);
  not not_173 (not_173_out, OP0);
  not not_174 (not_174_out, F4);
  not not_175 (not_175_out, F2);
  not not_176 (not_176_out, OP5);
  not not_177 (not_177_out, OP4);
  not not_178 (not_178_out, OP3);
  not not_179 (not_179_out, OP2);
  not not_180 (not_180_out, OP5);
  not not_181 (not_181_out, OP4);
  not not_182 (not_182_out, OP2);
  not not_183 (not_183_out, OP1);
  not not_184 (not_184_out, OP0);
  not not_185 (not_185_out, OP5);
  not not_186 (not_186_out, OP4);
  not not_187 (not_187_out, OP1);
  not not_188 (not_188_out, OP0);
  not not_189 (not_189_out, OP5);
  not not_190 (not_190_out, OP4);
  not not_191 (not_191_out, OP2);
  not not_192 (not_192_out, OP1);
  not not_193 (not_193_out, OP5);
  not not_194 (not_194_out, OP4);
  not not_195 (not_195_out, OP2);
  not not_196 (not_196_out, OP0);
  not not_197 (not_197_out, OP5);
  not not_198 (not_198_out, OP4);
  not not_199 (not_199_out, OP1);
  not not_200 (not_200_out, OP4);
  not not_201 (not_201_out, OP3);
  not not_202 (not_202_out, OP2);
  not not_203 (not_203_out, OP5);
  not not_204 (not_204_out, OP4);
  not not_205 (not_205_out, OP3);
  not not_206 (not_206_out, OP2);
  not not_207 (not_207_out, OP1);
  not not_208 (not_208_out, OP0);
  not not_209 (not_209_out, F5);
  not not_210 (not_210_out, F4);
  not not_211 (not_211_out, F3);
  not not_212 (not_212_out, F1);
  not not_213 (not_213_out, F0);
  not not_214 (not_214_out, OP5);
  not not_215 (not_215_out, OP4);
  not not_216 (not_216_out, OP3);
  not not_217 (not_217_out, OP2);
  not not_218 (not_218_out, OP1);
  not not_219 (not_219_out, OP0);
  not not_220 (not_220_out, F5);
  not not_221 (not_221_out, F4);
  not not_222 (not_222_out, F3);
  not not_223 (not_223_out, OP4);
  not not_224 (not_224_out, OP3);
  not not_225 (not_225_out, OP1);
  not not_226 (not_226_out, OP0);
  not not_227 (not_227_out, OP5);
  not not_228 (not_228_out, OP4);
  not not_229 (not_229_out, OP3);
  not not_230 (not_230_out, OP2);
  not not_231 (not_231_out, OP1);
  not not_232 (not_232_out, OP0);
  not not_233 (not_233_out, F5);
  not not_234 (not_234_out, F4);
  not not_235 (not_235_out, F1);
  not not_236 (not_236_out, F0);
  not not_237 (not_237_out, OP5);
  not not_238 (not_238_out, OP4);
  not not_239 (not_239_out, OP3);
  not not_240 (not_240_out, OP1);
  not not_241 (not_241_out, OP0);
  not not_242 (not_242_out, OP5);
  not not_243 (not_243_out, OP4);
  not not_244 (not_244_out, OP3);
  not not_245 (not_245_out, OP1);
  not not_246 (not_246_out, OP5);
  not not_247 (not_247_out, OP4);
  not not_248 (not_248_out, OP2);
  not not_249 (not_249_out, OP1);
  not not_250 (not_250_out, OP0);
  not not_251 (not_251_out, OP5);
  not not_252 (not_252_out, OP4);
  not not_253 (not_253_out, OP2);
  not not_254 (not_254_out, OP1);
  not not_255 (not_255_out, OP5);
  not not_256 (not_256_out, OP4);
  not not_257 (not_257_out, OP2);
  not not_258 (not_258_out, OP0);
  not not_259 (not_259_out, OP4);
  not not_260 (not_260_out, OP3);
  not not_261 (not_261_out, OP2);
  not not_262 (not_262_out, OP4);
  not not_263 (not_263_out, OP2);
  not not_264 (not_264_out, OP4);
  not not_265 (not_265_out, OP3);
  not not_266 (not_266_out, OP1);
  not not_267 (not_267_out, OP0);
  not not_268 (not_268_out, OP5);
  not not_269 (not_269_out, OP4);
  not not_270 (not_270_out, OP3);
  not not_271 (not_271_out, OP2);
  not not_272 (not_272_out, OP1);
  not not_273 (not_273_out, OP5);
  not not_274 (not_274_out, OP4);
  not not_275 (not_275_out, OP3);
  not not_276 (not_276_out, OP2);
  not not_277 (not_277_out, OP1);
  not not_278 (not_278_out, OP0);
  not not_279 (not_279_out, F5);
  not not_280 (not_280_out, F4);
  not not_281 (not_281_out, F3);
  not not_282 (not_282_out, F2);
  not not_283 (not_283_out, F1);
  not not_284 (not_284_out, F0);
  not not_285 (not_285_out, OP5);
  not not_286 (not_286_out, OP4);
  not not_287 (not_287_out, OP3);
  not not_288 (not_288_out, OP2);
  not not_289 (not_289_out, OP1);
  not not_290 (not_290_out, OP0);
  not not_291 (not_291_out, F5);
  not not_292 (not_292_out, F4);
  not not_293 (not_293_out, F3);
  not not_294 (not_294_out, F2);
  not not_295 (not_295_out, OP5);
  not not_296 (not_296_out, OP4);
  not not_297 (not_297_out, OP3);
  not not_298 (not_298_out, OP2);
  not not_299 (not_299_out, OP1);
  not not_300 (not_300_out, OP0);
  not not_301 (not_301_out, F5);
  not not_302 (not_302_out, F4);
  not not_303 (not_303_out, F3);
  not not_304 (not_304_out, F2);
  not not_305 (not_305_out, F0);
  not not_306 (not_306_out, OP5);
  not not_307 (not_307_out, OP4);
  not not_308 (not_308_out, OP3);
  not not_309 (not_309_out, OP2);
  not not_310 (not_310_out, OP1);
  not not_311 (not_311_out, OP0);
  not not_312 (not_312_out, F4);
  not not_313 (not_313_out, F3);
  not not_314 (not_314_out, F2);
  not not_315 (not_315_out, F1);
  not not_316 (not_316_out, F0);
  not not_317 (not_317_out, OP5);
  not not_318 (not_318_out, OP4);
  not not_319 (not_319_out, OP3);
  not not_320 (not_320_out, OP2);
  not not_321 (not_321_out, OP1);
  not not_322 (not_322_out, OP0);
  not not_323 (not_323_out, F4);
  not not_324 (not_324_out, F3);
  not not_325 (not_325_out, F2);
  not not_326 (not_326_out, F1);
  not not_327 (not_327_out, OP5);
  not not_328 (not_328_out, OP4);
  not not_329 (not_329_out, OP3);
  not not_330 (not_330_out, OP2);
  not not_331 (not_331_out, OP1);
  not not_332 (not_332_out, OP0);
  not not_333 (not_333_out, F4);
  not not_334 (not_334_out, F3);
  not not_335 (not_335_out, F2);
  not not_336 (not_336_out, F0);
  not not_337 (not_337_out, OP5);
  not not_338 (not_338_out, OP4);
  not not_339 (not_339_out, OP3);
  not not_340 (not_340_out, OP2);
  not not_341 (not_341_out, OP1);
  not not_342 (not_342_out, OP0);
  not not_343 (not_343_out, F4);
  not not_344 (not_344_out, F3);
  not not_345 (not_345_out, F1);
  not not_346 (not_346_out, F0);
  not not_347 (not_347_out, OP5);
  not not_348 (not_348_out, OP4);
  not not_349 (not_349_out, OP3);
  not not_350 (not_350_out, OP2);
  not not_351 (not_351_out, OP1);
  not not_352 (not_352_out, OP0);
  not not_353 (not_353_out, F4);
  not not_354 (not_354_out, F3);
  not not_355 (not_355_out, F1);
  not not_356 (not_356_out, OP5);
  not not_357 (not_357_out, OP4);
  not not_358 (not_358_out, OP3);
  not not_359 (not_359_out, OP2);
  not not_360 (not_360_out, OP1);
  not not_361 (not_361_out, OP0);
  not not_362 (not_362_out, F4);
  not not_363 (not_363_out, F3);
  not not_364 (not_364_out, OP5);
  not not_365 (not_365_out, OP4);
  not not_366 (not_366_out, OP3);
  not not_367 (not_367_out, OP2);
  not not_368 (not_368_out, OP1);
  not not_369 (not_369_out, OP0);
  not not_370 (not_370_out, F4);
  not not_371 (not_371_out, F2);
  not not_372 (not_372_out, F0);
  not not_373 (not_373_out, OP5);
  not not_374 (not_374_out, OP4);
  not not_375 (not_375_out, OP3);
  not not_376 (not_376_out, OP2);
  not not_377 (not_377_out, OP1);
  not not_378 (not_378_out, OP0);
  not not_379 (not_379_out, F4);
  not not_380 (not_380_out, F2);
  not not_381 (not_381_out, OP5);
  not not_382 (not_382_out, OP4);
  not not_383 (not_383_out, OP3);
  not not_384 (not_384_out, OP2);
  not not_385 (not_385_out, OP1);
  not not_386 (not_386_out, OP0);
  not not_387 (not_387_out, F5);
  not not_388 (not_388_out, F4);
  not not_389 (not_389_out, F3);
  not not_390 (not_390_out, F1);
  not not_391 (not_391_out, F0);
  not not_392 (not_392_out, OP5);
  not not_393 (not_393_out, OP4);
  not not_394 (not_394_out, OP3);
  not not_395 (not_395_out, OP2);
  not not_396 (not_396_out, OP1);
  not not_397 (not_397_out, OP0);
  not not_398 (not_398_out, F5);
  not not_399 (not_399_out, F4);
  not not_400 (not_400_out, F3);
  not not_401 (not_401_out, OP5);
  not not_402 (not_402_out, OP4);
  not not_403 (not_403_out, OP3);
  not not_404 (not_404_out, OP1);
  not not_405 (not_405_out, OP0);
  not not_406 (not_406_out, OP5);
  not not_407 (not_407_out, OP4);
  not not_408 (not_408_out, OP3);
  not not_409 (not_409_out, OP1);
  not not_410 (not_410_out, OP5);
  not not_411 (not_411_out, OP4);
  not not_412 (not_412_out, OP3);
  not not_413 (not_413_out, OP2);
  not not_414 (not_414_out, OP1);
  not not_415 (not_415_out, OP0);
  not not_416 (not_416_out, F5);
  not not_417 (not_417_out, F4);
  not not_418 (not_418_out, F2);
  not not_419 (not_419_out, F1);
  not not_420 (not_420_out, F0);
  not not_421 (not_421_out, OP5);
  not not_422 (not_422_out, OP4);
  not not_423 (not_423_out, OP3);
  not not_424 (not_424_out, OP2);
  not not_425 (not_425_out, OP1);
  not not_426 (not_426_out, OP0);
  not not_427 (not_427_out, F5);
  not not_428 (not_428_out, F4);
  not not_429 (not_429_out, F2);
  not not_430 (not_430_out, F1);
  not not_431 (not_431_out, F0);
  not not_432 (not_432_out, OP5);
  not not_433 (not_433_out, OP4);
  not not_434 (not_434_out, OP3);
  not not_435 (not_435_out, OP2);
  not not_436 (not_436_out, OP0);
  not not_437 (not_437_out, OP5);
  not not_438 (not_438_out, OP4);
  not not_439 (not_439_out, OP3);
  not not_440 (not_440_out, OP2);
  not not_441 (not_441_out, OP5);
  not not_442 (not_442_out, OP4);
  not not_443 (not_443_out, OP3);
  not not_444 (not_444_out, OP2);
  and and_1 (and_1_out, OP5, not_1_out, not_2_out, not_3_out, OP1, OP0);
  and and_2 (and_2_out, OP5, not_4_out, not_5_out, OP2, not_6_out, not_7_out);
  and and_3 (LBU, OP5, not_8_out, not_9_out, OP2, not_10_out, not_11_out);
  and and_4 (MemWrite, OP5, not_12_out, OP3, not_13_out, OP1, OP0);
  and and_5 (SLLV, not_14_out, not_15_out, not_16_out, not_17_out, not_18_out, not_19_out, not_20_out, not_21_out, not_22_out, F2, not_23_out, not_24_out);
  and and_6 (SRAV, not_25_out, not_26_out, not_27_out, not_28_out, not_29_out, not_30_out, not_31_out, not_32_out, not_33_out, F2, F1, F0);
  and and_7 (BGEZ, not_34_out, not_35_out, not_36_out, not_37_out, not_38_out, OP0);
  and and_8 (and_8_out, not_39_out, not_40_out, OP3, not_41_out, not_42_out, not_43_out);
  and and_9 (and_9_out, not_44_out, not_45_out, OP3, OP2, not_46_out, not_47_out);
  and and_10 (and_10_out, not_48_out, not_49_out, OP3, not_50_out, not_51_out, OP0);
  and and_11 (and_11_out, not_52_out, not_53_out, OP3, not_54_out, OP1, not_55_out);
  and and_12 (and_12_out, not_56_out, not_57_out, OP3, OP2, not_58_out, OP0);
  and and_13 (and_13_out, OP5, not_59_out, not_60_out, not_61_out, OP1, OP0);
  and and_14 (and_14_out, OP5, not_62_out, OP3, not_63_out, OP1, OP0);
  and and_15 (and_15_out, OP5, not_64_out, not_65_out, OP2, not_66_out, not_67_out);
  and and_16 (and_16_out, not_68_out, not_69_out, not_70_out, not_71_out, not_72_out, not_73_out, not_74_out, not_75_out, not_76_out, not_77_out, not_78_out, not_79_out);
  and and_17 (and_17_out, not_80_out, not_81_out, not_82_out, not_83_out, not_84_out, not_85_out, not_86_out, not_87_out, not_88_out, not_89_out, F1, F0);
  and and_18 (and_18_out, not_90_out, not_91_out, not_92_out, not_93_out, not_94_out, not_95_out, not_96_out, not_97_out, not_98_out, not_99_out, F1, not_100_out);
  and and_19 (and_19_out, not_101_out, not_102_out, not_103_out, not_104_out, not_105_out, not_106_out, F5, not_107_out, not_108_out, not_109_out, not_110_out, not_111_out);
  and and_20 (and_20_out, not_112_out, not_113_out, not_114_out, not_115_out, not_116_out, not_117_out, F5, not_118_out, not_119_out, not_120_out, not_121_out, F0);
  and and_21 (and_21_out, not_122_out, not_123_out, not_124_out, not_125_out, not_126_out, not_127_out, F5, not_128_out, not_129_out, not_130_out, F1, not_131_out);
  and and_22 (and_22_out, not_132_out, not_133_out, not_134_out, not_135_out, not_136_out, not_137_out, F5, not_138_out, not_139_out, F2, not_140_out, not_141_out);
  and and_23 (and_23_out, not_142_out, not_143_out, not_144_out, not_145_out, not_146_out, not_147_out, F5, not_148_out, not_149_out, F2, not_150_out, F0);
  and and_24 (and_24_out, not_151_out, not_152_out, not_153_out, not_154_out, not_155_out, not_156_out, F5, not_157_out, not_158_out, F2, F1, F0);
  and and_25 (and_25_out, not_159_out, not_160_out, not_161_out, not_162_out, not_163_out, not_164_out, F5, not_165_out, F3, not_166_out, F1, not_167_out);
  and and_26 (and_26_out, not_168_out, not_169_out, not_170_out, not_171_out, not_172_out, not_173_out, F5, not_174_out, F3, not_175_out, F1, F0);
  and and_27 (and_27_out, not_176_out, not_177_out, not_178_out, not_179_out, OP1, OP0);
  and and_28 (and_28_out, not_180_out, not_181_out, OP3, not_182_out, not_183_out, not_184_out);
  and and_29 (and_29_out, not_185_out, not_186_out, OP3, OP2, not_187_out, not_188_out);
  and and_30 (and_30_out, not_189_out, not_190_out, OP3, not_191_out, not_192_out, OP0);
  and and_31 (and_31_out, not_193_out, not_194_out, OP3, not_195_out, OP1, not_196_out);
  and and_32 (and_32_out, not_197_out, not_198_out, OP3, OP2, not_199_out, OP0);
  and and_33 (and_33_out, OP5, not_200_out, not_201_out, not_202_out, OP1, OP0);
  and and_34 (and_34_out, not_203_out, not_204_out, not_205_out, not_206_out, not_207_out, not_208_out, not_209_out, not_210_out, not_211_out, F2, not_212_out, not_213_out);
  and and_35 (and_35_out, not_214_out, not_215_out, not_216_out, not_217_out, not_218_out, not_219_out, not_220_out, not_221_out, not_222_out, F2, F1, F0);
  and and_36 (and_36_out, OP5, not_223_out, not_224_out, OP2, not_225_out, not_226_out);
  and and_37 (SysCALL, not_227_out, not_228_out, not_229_out, not_230_out, not_231_out, not_232_out, not_233_out, not_234_out, F3, F2, not_235_out, not_236_out);
  and and_38 (and_38_out, not_237_out, not_238_out, not_239_out, OP2, not_240_out, not_241_out);
  and and_39 (and_39_out, not_242_out, not_243_out, not_244_out, OP2, not_245_out, OP0);
  and and_40 (and_40_out, not_246_out, not_247_out, OP3, not_248_out, not_249_out, not_250_out);
  and and_41 (and_41_out, not_251_out, not_252_out, OP3, not_253_out, not_254_out, OP0);
  and and_42 (and_42_out, not_255_out, not_256_out, OP3, not_257_out, OP1, not_258_out);
  and and_43 (and_43_out, OP5, not_259_out, not_260_out, not_261_out, OP1, OP0);
  and and_44 (and_44_out, OP5, not_262_out, OP3, not_263_out, OP1, OP0);
  and and_45 (and_45_out, OP5, not_264_out, not_265_out, OP2, not_266_out, not_267_out);
  and and_46 (and_46_out, not_268_out, not_269_out, not_270_out, not_271_out, not_272_out, OP0);
  and and_47 (and_47_out, not_273_out, not_274_out, not_275_out, not_276_out, not_277_out, not_278_out, not_279_out, not_280_out, not_281_out, not_282_out, not_283_out, not_284_out);
  and and_48 (and_48_out, not_285_out, not_286_out, not_287_out, not_288_out, not_289_out, not_290_out, not_291_out, not_292_out, not_293_out, not_294_out, F1, F0);
  and and_49 (and_49_out, not_295_out, not_296_out, not_297_out, not_298_out, not_299_out, not_300_out, not_301_out, not_302_out, not_303_out, not_304_out, F1, not_305_out);
  and and_50 (and_50_out, not_306_out, not_307_out, not_308_out, not_309_out, not_310_out, not_311_out, F5, not_312_out, not_313_out, not_314_out, not_315_out, not_316_out);
  and and_51 (and_51_out, not_317_out, not_318_out, not_319_out, not_320_out, not_321_out, not_322_out, F5, not_323_out, not_324_out, not_325_out, not_326_out, F0);
  and and_52 (and_52_out, not_327_out, not_328_out, not_329_out, not_330_out, not_331_out, not_332_out, F5, not_333_out, not_334_out, not_335_out, F1, not_336_out);
  and and_53 (and_53_out, not_337_out, not_338_out, not_339_out, not_340_out, not_341_out, not_342_out, F5, not_343_out, not_344_out, F2, not_345_out, not_346_out);
  and and_54 (and_54_out, not_347_out, not_348_out, not_349_out, not_350_out, not_351_out, not_352_out, F5, not_353_out, not_354_out, F2, not_355_out, F0);
  and and_55 (and_55_out, not_356_out, not_357_out, not_358_out, not_359_out, not_360_out, not_361_out, F5, not_362_out, not_363_out, F2, F1, F0);
  and and_56 (and_56_out, not_364_out, not_365_out, not_366_out, not_367_out, not_368_out, not_369_out, F5, not_370_out, F3, not_371_out, F1, not_372_out);
  and and_57 (and_57_out, not_373_out, not_374_out, not_375_out, not_376_out, not_377_out, not_378_out, F5, not_379_out, F3, not_380_out, F1, F0);
  and and_58 (and_58_out, not_381_out, not_382_out, not_383_out, not_384_out, not_385_out, not_386_out, not_387_out, not_388_out, not_389_out, F2, not_390_out, not_391_out);
  and and_59 (and_59_out, not_392_out, not_393_out, not_394_out, not_395_out, not_396_out, not_397_out, not_398_out, not_399_out, not_400_out, F2, F1, F0);
  and and_60 (BEQ, not_401_out, not_402_out, not_403_out, OP2, not_404_out, not_405_out);
  and and_61 (BNE, not_406_out, not_407_out, not_408_out, OP2, not_409_out, OP0);
  and and_62 (JR, not_410_out, not_411_out, not_412_out, not_413_out, not_414_out, not_415_out, not_416_out, not_417_out, F3, not_418_out, not_419_out, not_420_out);
  and and_63 (and_63_out, not_421_out, not_422_out, not_423_out, not_424_out, not_425_out, not_426_out, not_427_out, not_428_out, F3, not_429_out, not_430_out, not_431_out);
  and and_64 (and_64_out, not_432_out, not_433_out, not_434_out, not_435_out, OP1, not_436_out);
  and and_65 (and_65_out, not_437_out, not_438_out, not_439_out, not_440_out, OP1, OP0);
  and and_66 (JAL, not_441_out, not_442_out, not_443_out, not_444_out, OP1, OP0);
  or or_1 (MemToReg, and_1_out, and_2_out);
  or or_2 (ALU_SRC, and_8_out, and_9_out, and_10_out, and_11_out, and_12_out, and_13_out, and_14_out, and_15_out);
  or or_3 (SignedExt, and_38_out, and_39_out, and_40_out, and_41_out, and_42_out, and_43_out, and_44_out, and_45_out, and_46_out);
  or or_4 (JUMP, and_63_out, and_64_out, and_65_out);
  or or_5 (RegWrite, and_16_out, and_17_out, and_18_out, and_19_out, and_20_out, and_21_out, and_22_out, and_23_out, and_24_out, and_25_out, and_26_out, and_27_out, and_28_out, and_29_out, and_30_out, and_31_out, and_32_out, and_33_out, and_34_out, and_35_out, and_36_out);
  or or_6 (RegDst, and_47_out, and_48_out, and_49_out, and_50_out, and_51_out, and_52_out, and_53_out, and_54_out, and_55_out, and_56_out, and_57_out, and_58_out, and_59_out);
endmodule

// ALU
module MIPS_ALU (
  input  [4:0] shamt,
  input  [31:0] X,
  input  [31:0] Y,
  input  [3:0] AluOP,
  output Equal,
  output [31:0] Result,
  output [31:0] Result_2
);

  wire [0:0] comparator_1_lt, comparator_2_lt;
  wire [31:0] adder_1_out, AND_out, divider_1_out, divider_1_rem, multiplier_1_cout, multiplier_1_out,
       NOR_out, OR_out, shifter_1_out, shifter_2_out, shifter_3_out, subtractor_1_out, XOR_out;

  assign AND_out = X & Y;  // AND_Gate AND, 32 bits wide
  assign OR_out = X | Y;  // OR_Gate OR, 32 bits wide
  Shifter #(.width(32), .shift("ll")) shifter_1 (.in(Y), .\dist (shamt), .out(shifter_1_out));
  Shifter #(.width(32), .shift("ar")) shifter_2 (.in(Y), .\dist (shamt), .out(shifter_2_out));
  Shifter #(.width(32), .shift("lr")) shifter_3 (.in(Y), .\dist (shamt), .out(shifter_3_out));
  Multiplier #(.width(32)) multiplier_1 (.a(X), .b(Y), .out(multiplier_1_out), .cout(multiplier_1_cout));  // open: cin
  Divider #(.width(32)) divider_1 (.a(X), .b(Y), .out(divider_1_out), .rem(divider_1_rem));  // open: upper
  Adder #(.width(32)) adder_1 (.a(X), .b(Y), .out(adder_1_out));  // open: cin, cout
  Subtractor #(.width(32)) subtractor_1 (.a(X), .b(Y), .out(subtractor_1_out));  // open: bin, bout
  assign XOR_out = X ^ Y;  // XOR_Gate XOR, 32 bits wide
  assign NOR_out = ~(X | Y);  // NOR_Gate NOR, 32 bits wide
  Comparator #(.width(32), .mode("twosComplement")) comparator_1 (
    .a(X), .b(Y), .eq(Equal), .lt(comparator_1_lt[0]));  // open: gt
  Comparator #(.width(32), .mode("unsigned")) comparator_2 (.a(X), .b(Y), .lt(comparator_2_lt[0]));  // open: gt, eq
  Multiplexer #(.select(4), .width(32), .disabled("Z"), .enable("false")) multiplexer_1 (
    .in0(shifter_1_out), .in1(shifter_2_out), .in2(shifter_3_out), .in3(multiplier_1_out),
    .in4(divider_1_out), .in5(adder_1_out), .in6(subtractor_1_out), .in7(AND_out), .in8(OR_out),
    .in9(XOR_out), .in10(NOR_out), .in11({{31{1'b0}}, comparator_1_lt[0]}),
    .in12({{31{1'b0}}, comparator_2_lt[0]}), .in13({32{1'b0}}), .in14({32{1'b0}}), .in15({32{1'b0}}),
    .out(Result), .sel(AluOP));
  Multiplexer #(.select(4), .width(32), .disabled("Z"), .enable("false")) multiplexer_2 (
    .in0({32{1'b0}}), .in1({32{1'b0}}), .in2({32{1'b0}}), .in3(multiplier_1_cout), .in4(divider_1_rem),
    .in5({32{1'b0}}), .in6({32{1'b0}}), .in7({32{1'b0}}), .in8({32{1'b0}}), .in9({32{1'b0}}),
    .in10({32{1'b0}}), .in11({32{1'b0}}), .in12({32{1'b0}}), .in13({32{1'b0}}), .in14({32{1'b0}}),
    .in15({32{1'b0}}), .out(Result_2), .sel(AluOP));

  // Other names for the same wires on the sheet: Result2[31:0] = Result_2; S[3:0] = AluOP

  // Notes on the sheet:
  //   不要改变此引脚区域内容，也不要改变ALU封装形式
  //   输入引脚
  //   输出引脚
endmodule

module MIPS_Regifile (
  input  [31:0] Din,
  input  Clk,
  input  WE,
  input  [4:0] R1_num,
  input  [4:0] W_num,
  input  [4:0] R2_num,
  output [31:0] R1,
  output [31:0] R2
);

  // RegisterFile registerfile_1: pin names not known; wires that end beside it: Din, Clk, WE, W_num, R1_num, R2_num, R1, R2
endmodule

module \理想流水线  (
  output RegWrite,
  output MemWrite,
  output [31:0] IF_PC,
  output [31:0] ID_PC,
  output [31:0] EX_PC,
  output [31:0] M_PC,
  output [31:0] WB_PC,
  output [31:0] RDin,
  output [31:0] MDin,
  output [31:0] LedData
);

  wire and_1_out, and_2_out, and_3_out, CLK, clock_1_out, clock_2_out, comparator_1_eq, comparator_1_lt,
       comparator_2_eq, d_ff_1_q, Go, Halt, IR1, IR2, IR3, nand_1_out, not_1_out, not_2_out, not_3_out, RST,
       SignedExt, W1, W2, W3, \单周期硬布线控制器_1_alu_src , \单周期硬布线控制器_1_memtoreg , \单周期硬布线控制器_1_memwrite ,
       \单周期硬布线控制器_1_regdst , \单周期硬布线控制器_1_regwrite , \单周期硬布线控制器_1_syscall , \理想ex_mem_1_memtoreg_out ,
       \理想ex_mem_1_regdst_out , \理想ex_mem_1_regwrite_out , \理想ex_mem_1_syscall_out , \理想id_ex_1_alusrcb_out ,
       \理想id_ex_1_memtoreg_out , \理想id_ex_1_memwrite_2 , \理想id_ex_1_regdst_out , \理想id_ex_1_regwrite_out ,
       \理想id_ex_1_syscall_out , \理想mem_wb_1_memtoreg_out , \理想mem_wb_1_regdst_out , \理想mem_wb_1_syscall_out ;
  wire [3:0] \单周期硬布线控制器_1_alu_op , \理想id_ex_1_aluop_out ;
  wire [4:0] multiplexer_1_out, multiplexer_2_out, multiplexer_6_out, \理想id_ex_1_shamt_2 ;
  wire [12:0] CNT_num;
  wire [15:0] \LoadUse次数 , \总周期数 , \插入气泡数 , \无条件分支数 , \条件分支成功数 ;
  wire [31:0] adder_1_out, bit_extender_1_out, bit_extender_2_out, EX_IR, ID_IR, IF_IR, MEM_IR,
       mips_alu_1_result, mips_regifile_1_r1, mips_regifile_1_r2, multiplexer_3_out, multiplexer_4_out,
       ram_1_data, WB_IR, \理想ex_mem_1_a_in_2 , \理想ex_mem_1_alu_2 , \理想id_ex_1_a_out , \理想id_ex_1_b_out ,
       \理想id_ex_1_imm_out , \理想mem_wb_1_a_out , \理想mem_wb_1_alu_2 , \理想mem_wb_1_b_out , \理想mem_wb_1_md_2 ;

  Button \u_总复位  (.out(RST));
  Button _1 (.out(IR1));
  Button _2 (.out(IR2));
  Button _3 (.out(IR3));
  // Probe on \总周期数 
  // Probe on \总周期数 
  and and_1 (and_1_out, ~Halt, CLK);  // AND_Gate
  Button \u_继续运行  (.out(Go));
  LED #(.active("true")) led_1 (.in(W1));
  LED #(.active("true")) led_2 (.in(W2));
  LED #(.active("true")) led_3 (.in(W3));
  Counter #(.width(16), .max('hffff), .ongoal("wrap"), .trigger("rising"), .behavior("new")) counter_1 (
    .Q(\总周期数 ), .clk(and_1_out));  // open: load, D, count, carry, clr, preset, down
  Hex_Digit_Display hex_digit_display_1 (.value(LedData[31:28]));  // open: dp
  // Probe on IF_PC[19:0]
  // Mips_Probe mips_probe_1: pin names not known; wires that end beside it: IF_IR
  Register #(.width(32), .trigger("rising"), .Select("low")) PC (
    .D(adder_1_out), .en(not_1_out), .Q(IF_PC), .clk(CLK));  // open: clr
  not not_1 (not_1_out, Halt);
  Hex_Digit_Display hex_digit_display_2 (.value(LedData[27:24]));  // open: dp
  Hex_Digit_Display hex_digit_display_3 (.value(LedData[23:20]));  // open: dp
  // Probe on ID_PC[19:0]
  // Mips_Probe mips_probe_2: pin names not known; wires that end beside it: ID_IR
  Hex_Digit_Display hex_digit_display_4 (.value(LedData[19:16]));  // open: dp
  Hex_Digit_Display hex_digit_display_5 (.value(LedData[15:12]));  // open: dp
  Adder #(.width(32)) adder_1 (.a(IF_PC), .b(32'h4), .out(adder_1_out));  // open: cin, cout
  Hex_Digit_Display hex_digit_display_6 (.value(LedData[7:4]));  // open: dp
  Hex_Digit_Display hex_digit_display_7 (.value(LedData[11:8]));  // open: dp
  Clock #(.highDuration(1), .lowDuration(1)) clock_1 (.out(clock_1_out));
  // Probe on EX_PC[19:0]
  // Mips_Probe mips_probe_3: pin names not known; wires that end beside it: clock_1_out, EX_IR, CLK
  Hex_Digit_Display hex_digit_display_8 (.value(LedData[3:0]));  // open: dp
  ROM #(.addrWidth(10), .dataWidth(32), .Select("high")) rom_1 (.addr(IF_PC[11:2]), .data(IF_IR));
  // Probe on \总周期数 
  // Probe on M_PC[19:0]
  // Mips_Probe mips_probe_4: pin names not known; wires that end beside it: MEM_IR
  \理想IF_ID  \u_理想if_id_1  (
    .IR_in(IF_IR), .PC_in(IF_PC), .CLK(CLK), .IR_out(ID_IR), .PC_out(ID_PC), .CLR(RST));  // open: RegDst_in, Beq_in, Syscall_in, Bne_in, JMP_in, MemToReg_in, A_in, JR_in, AluOP_in, SignedExt_in, AluSrcB_in, B_in, SLLV_in, RegWrite_in, Imm_in, SRAV_in, JAL_in, LBU_in, Shamt, MemWrite, BGEZ_in, RegDst_out, Beq_out, Syscall_out, Bne_out, JMP_out, MemToReg_out, A_out, JR_out, AluOP_out, SignedExt_out, AluSrcB_out, B_out, SLLV_out, RegWrite_out, Imm_out, SRAV_out, JAL_out, LBU_out, Shamt_2, MemWrite_2, BGEZ_out, Stall
  // Probe on \总周期数 
  // Probe on \无条件分支数 
  // Probe on \条件分支成功数 
  // Probe on \插入气泡数 
  // Probe on \LoadUse次数 
  // Probe on IF_PC[11:0]
  // Probe on WB_PC[19:0]
  // Mips_Probe mips_probe_5: pin names not known; wires that end beside it: WB_IR
  // Probe on ID_PC[11:0]
  // Probe on EX_PC[11:0]
  \单周期硬布线控制器  \u_单周期硬布线控制器_1  (
    .Func(ID_IR[5:0]), .OP(ID_IR[31:26]), .ALU_OP(\单周期硬布线控制器_1_alu_op ), .MemToReg(\单周期硬布线控制器_1_memtoreg ),
    .MemWrite(\单周期硬布线控制器_1_memwrite ), .ALU_SRC(\单周期硬布线控制器_1_alu_src ), .RegWrite(\单周期硬布线控制器_1_regwrite ),
    .SysCALL(\单周期硬布线控制器_1_syscall ), .SignedExt(SignedExt), .RegDst(\单周期硬布线控制器_1_regdst ));  // open: JR, JMP, Beq, JAL, Bne, SLLV, SRAV, BGEZ, LBU, ERET, MFC0, MTC0, in_3
  assign bit_extender_1_out = {{16{1'b0}}, ID_IR[15:0]};  // Bit_Extender bit_extender_1
  assign bit_extender_2_out = {{16{ID_IR[15]}}, ID_IR[15:0]};  // Bit_Extender bit_extender_2
  // Probe on M_PC[11:0]
  D_Flip_Flop #(.trigger("high"), .Pre_Clr_Positions("LEGACY"), .NegatePresetClear("false"), .enable("true"), .NewFFLayout("false")) d_ff_1 (.Q(d_ff_1_q));  // open: clk, D, Qn, preset, en, reset
  // Probe on 13'hc
  // Probe on WB_PC[11:0]
  Comparator #(.width(13), .mode("twosComplement")) comparator_1 (
    .a(CNT_num), .b(13'hc), .eq(comparator_1_eq), .lt(comparator_1_lt));  // open: gt
  Clock #(.highDuration(1), .lowDuration(1)) clock_2 (.out(clock_2_out));
  Multiplexer #(.select(1), .width(5), .disabled("Z"), .enable("false")) multiplexer_1 (
    .in0(ID_IR[25:21]), .in1(5'b00010), .out(multiplexer_1_out), .sel(\单周期硬布线控制器_1_syscall ));
  Multiplexer #(.select(1), .width(5), .disabled("Z"), .enable("false")) multiplexer_2 (
    .in0(ID_IR[20:16]), .in1(5'b00100), .out(multiplexer_2_out), .sel(\单周期硬布线控制器_1_syscall ));
  nand nand_1 (nand_1_out, d_ff_1_q, comparator_1_eq);
  Counter #(.width(13), .max('h1fff), .ongoal("stay"), .trigger("rising"), .behavior("old")) counter_2 (
    .count(comparator_1_lt), .Q(CNT_num), .clk(clock_2_out));  // open: load, D, carry, clr, preset
  Multiplexer #(.select(1), .width(32), .disabled("Z"), .enable("false")) multiplexer_3 (
    .in0(bit_extender_1_out), .in1(bit_extender_2_out), .out(multiplexer_3_out), .sel(SignedExt));
  assign CLK = nand_1_out ? clock_2_out : 1'bz;  // Controlled_Buffer controlled_buffer_1
  MIPS_Regifile mips_regifile_1 (
    .Din(RDin), .Clk(CLK), .R1(mips_regifile_1_r1), .R2(mips_regifile_1_r2), .WE(RegWrite),
    .W_num(multiplexer_6_out), .R1_num(multiplexer_1_out), .R2_num(multiplexer_2_out));
  Pull_Resistor #(.pull(1)) pull_resistor_1 (.node(CLK));
  \理想ID_EX  \u_理想id_ex_1  (
    .RegDst_in(\单周期硬布线控制器_1_regdst ), .IR_in(ID_IR), .Syscall_in(\单周期硬布线控制器_1_syscall ), .PC_in(ID_PC),
    .MemToReg_in(\单周期硬布线控制器_1_memtoreg ), .A_in(mips_regifile_1_r1), .AluOP_in(\单周期硬布线控制器_1_alu_op ),
    .SignedExt_in(SignedExt), .AluSrcB_in(\单周期硬布线控制器_1_alu_src ), .B_in(mips_regifile_1_r2),
    .RegWrite_in(\单周期硬布线控制器_1_regwrite ), .Imm_in(multiplexer_3_out), .CLK(CLK),
    .RegDst_out(\理想id_ex_1_regdst_out ), .IR_out(EX_IR), .Syscall_out(\理想id_ex_1_syscall_out ),
    .PC_out(EX_PC), .MemToReg_out(\理想id_ex_1_memtoreg_out ), .A_out(\理想id_ex_1_a_out ),
    .AluOP_out(\理想id_ex_1_aluop_out ), .AluSrcB_out(\理想id_ex_1_alusrcb_out ), .B_out(\理想id_ex_1_b_out ),
    .RegWrite_out(\理想id_ex_1_regwrite_out ), .Imm_out(\理想id_ex_1_imm_out ), .CLR(RST), .Shamt(ID_IR[10:6]),
    .Shamt_2(\理想id_ex_1_shamt_2 ), .MemWrite(\单周期硬布线控制器_1_memwrite ), .MemWrite_2(\理想id_ex_1_memwrite_2 ));  // open: Beq_in, Bne_in, JMP_in, JR_in, SLLV_in, SRAV_in, JAL_in, LBU_in, BGEZ_in, Beq_out, Bne_out, JMP_out, JR_out, SignedExt_out, SLLV_out, SRAV_out, JAL_out, LBU_out, BGEZ_out, Stall
  Multiplexer #(.select(1), .width(32), .disabled("Z"), .enable("false")) multiplexer_4 (
    .in0(\理想id_ex_1_b_out ), .in1(\理想id_ex_1_imm_out ), .out(multiplexer_4_out), .sel(\理想id_ex_1_alusrcb_out ));
  MIPS_ALU mips_alu_1 (
    .X(\理想id_ex_1_a_out ), .Y(multiplexer_4_out), .AluOP(\理想id_ex_1_aluop_out ), .Result(mips_alu_1_result),
    .shamt(\理想id_ex_1_shamt_2 ));  // open: Equal, Result_2
  \理想EX_MEM  \u_理想ex_mem_1  (
    .RegDst_in(\理想id_ex_1_regdst_out ), .IR_in(EX_IR), .Syscall_in(\理想id_ex_1_syscall_out ), .PC_in(EX_PC),
    .MemToReg_in(\理想id_ex_1_memtoreg_out ), .A_in(\理想id_ex_1_a_out ), .B_in(\理想id_ex_1_b_out ),
    .RegWrite_in(\理想id_ex_1_regwrite_out ), .CLK(CLK), .RegDst_out(\理想ex_mem_1_regdst_out ), .IR_out(MEM_IR),
    .Syscall_out(\理想ex_mem_1_syscall_out ), .PC_out(M_PC), .MemToReg_out(\理想ex_mem_1_memtoreg_out ),
    .A_in_2(\理想ex_mem_1_a_in_2 ), .B_out(MDin), .RegWrite_out(\理想ex_mem_1_regwrite_out ), .CLR(RST),
    .MemWrite(\理想id_ex_1_memwrite_2 ), .MemWrite_2(MemWrite), .ALU(mips_alu_1_result),
    .ALU_2(\理想ex_mem_1_alu_2 ));  // open: Beq_in, Bne_in, JMP_in, JR_in, SignedExt_in, AluSrcB_in, SLLV_in, Imm_in, SRAV_in, JAL_in, LBU_in, Shamt, BGEZ_in, Beq_out, Bne_out, JMP_out, JR_out, SignedExt_out, AluSrcB_out, SLLV_out, Imm_out, SRAV_out, JAL_out, LBU_out, Shamt_2, BGEZ_out, Stall
  not not_2 (not_2_out, Halt);
  RAM #(.addrWidth(10), .dataWidth(32), .bus("separate"), .Select("high")) ram_1 (
    .addr(\理想ex_mem_1_alu_2 [11:2]), .din(MDin), .data(ram_1_data), .str(MemWrite), .sel(not_2_out), .clk(CLK));  // open: ld, clr
  \理想MEM_WB  \u_理想mem_wb_1  (
    .RegDst_in(\理想ex_mem_1_regdst_out ), .RegDst_out(\理想mem_wb_1_regdst_out ), .IR_in(MEM_IR),
    .IR_out(WB_IR), .Syscall_in(\理想ex_mem_1_syscall_out ), .Syscall_out(\理想mem_wb_1_syscall_out ),
    .PC_in(M_PC), .PC_out(WB_PC), .MemToReg_in(\理想ex_mem_1_memtoreg_out ),
    .MemToReg_out(\理想mem_wb_1_memtoreg_out ), .A_in(\理想ex_mem_1_a_in_2 ), .A_out(\理想mem_wb_1_a_out ),
    .ALU(\理想ex_mem_1_alu_2 ), .ALU_2(\理想mem_wb_1_alu_2 ), .B_in(MDin), .B_out(\理想mem_wb_1_b_out ),
    .RegWrite_in(\理想ex_mem_1_regwrite_out ), .RegWrite_out(RegWrite), .MD(ram_1_data),
    .MD_2(\理想mem_wb_1_md_2 ), .CLK(CLK), .CLR(RST));  // open: Beq_in, Beq_out, Bne_in, Bne_out, JMP_in, JMP_out, JR_in, JR_out, SignedExt_in, SignedExt_out, AluSrcB_in, AluSrcB_out, SLLV_in, SLLV_out, Imm_in, Imm_out, SRAV_in, SRAV_out, JAL_in, JAL_out, LBU_in, LBU_out, BGEZ_in, BGEZ_out, Stall, MemWrite, MemWrite_2
  Multiplexer #(.select(1), .width(32), .disabled("Z"), .enable("false")) multiplexer_5 (
    .in0(\理想mem_wb_1_alu_2 ), .in1(\理想mem_wb_1_md_2 ), .out(RDin), .sel(\理想mem_wb_1_memtoreg_out ));
  Comparator #(.width(32), .mode("twosComplement")) comparator_2 (
    .a(\理想mem_wb_1_a_out ), .b(32'h22), .eq(comparator_2_eq));  // open: gt, lt
  not not_3 (not_3_out, comparator_2_eq);
  Register #(.width(32), .trigger("falling"), .Select("low")) register_1 (
    .D(\理想mem_wb_1_b_out ), .Q(LedData), .clk(and_2_out));  // open: en, clr
  and and_2 (and_2_out, comparator_2_eq, \理想mem_wb_1_syscall_out );
  and and_3 (and_3_out, \理想mem_wb_1_syscall_out , not_3_out);
  Register #(.width(1), .trigger("rising"), .Select("low")) register_2 (
    .D(and_3_out), .en(and_3_out), .Q(Halt), .clk(CLK), .clr(Go));
  Multiplexer #(.select(1), .width(5), .disabled("Z"), .enable("false")) multiplexer_6 (
    .in0(WB_IR[20:16]), .in1(WB_IR[15:11]), .out(multiplexer_6_out), .sel(\理想mem_wb_1_regdst_out ));

  // Other names for the same wires on the sheet: MEM_PC[31:0] = M_PC

  // Notes on the sheet:
  //   中断源
  //   时空图监测，可删除
  //   中断等待指示
  //   数码管输出
  //   contents of rom_1 (hex, n*v repeats v):
  //   20100000 20110000 20120000 20130000 36100000 36310001 36520002 36730003 ae100000 ae110004 ae120008
  //   ae13000c 2002000a 20110000 20120000 20130000 c
  //   指令字
  //   JMP
  //   JR
  //   OP
  //   OP
  //   Func
  //   rs
  //   rt
  //   rd
  //   控制位
  //   Beq
  //   Bne
  //   AluOP
  //   AluSrcB
  //   RegWrite
  //   JAL
  //   RegDst
  //   Syscall
  //   流水调试日志用
  //   暂停节拍，不能为0
  //   MemToReg
  //   MemWrite
  //   戳工具置1进入计数暂停模式，ctrl+k时钟自动运行到对应节拍暂停
  //   ctrl+k关闭时钟连续运行，将控制位置零，进入单步调试模式调试
  //   用这个时钟源需要去掉电路中的其他时钟源
  //   可计数暂停的时钟源
  //   Reg_dst
  //   beq
  //   IR
  //   Syscall
  //   Beq
  //   PC
  //   JMP
  //   MemToReg
  //   JR
  //   AluOP
  //   RegWrite
  //   为方便自动评测，需要输出流水线各段保存的PC值，注意是PC不是PC+4，另外ID段寄存器写入信息，Mem段内存写入信息也要输出
  //   rt
  //   rd
endmodule

module \气泡流水线  (
  output RegWrite,
  output MemWrite,
  output [31:0] IF_PC,
  output [31:0] ID_PC,
  output [31:0] EX_PC,
  output [31:0] M_PC,
  output [31:0] WB_PC,
  output [31:0] RDin,
  output [31:0] MDin,
  output [31:0] LedData
);

  wire and_1_out, and_2_out, and_3_out, and_4_out, and_5_out, and_6_out, and_7_out, B_CLR, Branch, CLK,
       clock_1_out, clock_2_out, comparator_1_eq, comparator_1_lt, comparator_2_eq, Correlated, d_ff_1_q,
       EX_JAL, EX_JMP, EX_JR, EX_RegDst, EX_RegWrite, Go, Halt, IR1, IR2, IR3, MEM_JAL, MEM_RegDst,
       MEM_RegWrite, mips_alu_1_equal, nand_1_out, nor_1_out, not_1_out, not_2_out, not_3_out, or_1_out,
       or_2_out, or_3_out, RST, SignedExt, W1, W2, W3, \单周期硬布线控制器_1_alu_src , \单周期硬布线控制器_1_beq ,
       \单周期硬布线控制器_1_bgez , \单周期硬布线控制器_1_bne , \单周期硬布线控制器_1_jal , \单周期硬布线控制器_1_jmp , \单周期硬布线控制器_1_jr ,
       \单周期硬布线控制器_1_lbu , \单周期硬布线控制器_1_memtoreg , \单周期硬布线控制器_1_memwrite , \单周期硬布线控制器_1_regdst ,
       \单周期硬布线控制器_1_regwrite , \单周期硬布线控制器_1_sllv , \单周期硬布线控制器_1_srav , \单周期硬布线控制器_1_syscall ,
       \源寄存器使用情况_1_r1_used , \源寄存器使用情况_1_r2_used , \理想ex_mem_1_lbu_out , \理想ex_mem_1_memtoreg_out ,
       \理想ex_mem_1_syscall_out , \理想id_ex_1_alusrcb_out , \理想id_ex_1_beq_out , \理想id_ex_1_bgez_out ,
       \理想id_ex_1_bne_out , \理想id_ex_1_lbu_out , \理想id_ex_1_memtoreg_out , \理想id_ex_1_memwrite_2 ,
       \理想id_ex_1_sllv_out , \理想id_ex_1_srav_out , \理想id_ex_1_syscall_out , \理想mem_wb_1_jal_out ,
       \理想mem_wb_1_lbu_out , \理想mem_wb_1_memtoreg_out , \理想mem_wb_1_regdst_out , \理想mem_wb_1_syscall_out ;
  wire [3:0] \单周期硬布线控制器_1_alu_op , \理想id_ex_1_aluop_out ;
  wire [4:0] multiplexer_1_out, multiplexer_2_out, multiplexer_3_out, multiplexer_4_out, multiplexer_10_out,
       multiplexer_13_out, multiplexer_15_out, R1_num, R2_num, \理想id_ex_1_a_out , \理想id_ex_1_shamt_2 ;
  wire [5:0] Func;
  wire [12:0] CNT_num;
  wire [15:0] \LoadUse次数 , \总周期数 , \插入气泡数 , \无条件分支数 , \条件分支成功数 ;
  wire [31:0] adder_2_out, adder_3_out, adder_4_out, bit_extender_1_out, bit_extender_2_out,
       bit_extender_3_out, controlled_buffer_2_out, EX_IR, IF_IR, MEM_IR, mips_alu_1_result,
       mips_regifile_1_r1, mips_regifile_1_r2, multiplexer_7_out, multiplexer_8_out, multiplexer_9_out,
       multiplexer_11_out, multiplexer_12_out, PC_4, ram_1_data, shifter_1_out, WB_IR, \理想ex_mem_1_a_in_2 ,
       \理想ex_mem_1_alu_2 , \理想id_ex_1_b_out , \理想id_ex_1_imm_out , \理想mem_wb_1_a_out , \理想mem_wb_1_alu_2 ,
       \理想mem_wb_1_b_out , \理想mem_wb_1_md_2 ;
  wire [31:5] \理想id_ex_1_a_out_2 ;
  wire [31:6] ID_IR;

  Button \u_总复位  (.out(RST));
  Button _1 (.out(IR1));
  Button _2 (.out(IR2));
  Button _3 (.out(IR3));
  // Probe on \总周期数 
  // Probe on \总周期数 
  and and_1 (and_1_out, ~Halt, CLK);  // AND_Gate
  Button \u_继续运行  (.out(Go));
  LED #(.active("true")) led_1 (.in(W1));
  LED #(.active("true")) led_2 (.in(W2));
  LED #(.active("true")) led_3 (.in(W3));
  Counter #(.width(16), .max('hffff), .ongoal("wrap"), .trigger("rising"), .behavior("new")) counter_1 (
    .Q(\总周期数 ), .clk(and_1_out));  // open: load, D, count, carry, clr, preset, down
  Hex_Digit_Display hex_digit_display_1 (.value(LedData[31:28]));  // open: dp
  // Probe on IF_PC[19:0]
  // Mips_Probe mips_probe_1: pin names not known; wires that end beside it: IF_IR
  nor nor_1 (nor_1_out, Correlated, Halt);
  Hex_Digit_Display hex_digit_display_2 (.value(LedData[27:24]));  // open: dp
  Hex_Digit_Display hex_digit_display_3 (.value(LedData[23:20]));  // open: dp
  // Probe on ID_PC[19:0]
  // Mips_Probe mips_probe_2: pin names not known; wires that end beside it: {ID_IR, Func}
  Register #(.width(32), .trigger("rising"), .Select("low")) PC (
    .D(controlled_buffer_2_out), .en(nor_1_out), .Q(IF_PC), .clk(CLK));  // open: clr
  Hex_Digit_Display hex_digit_display_4 (.value(LedData[15:12]));  // open: dp
  Hex_Digit_Display hex_digit_display_5 (.value(LedData[19:16]));  // open: dp
  Hex_Digit_Display hex_digit_display_6 (.value(LedData[11:8]));  // open: dp
  Hex_Digit_Display hex_digit_display_7 (.value(LedData[7:4]));  // open: dp
  Clock #(.highDuration(1), .lowDuration(1)) clock_1 (.out(clock_1_out));
  // Probe on EX_PC[19:0]
  // Mips_Probe mips_probe_3: pin names not known; wires that end beside it: clock_1_out, EX_IR, CLK
  Adder #(.width(32)) adder_1 (.a(IF_PC), .b(32'h4), .out(PC_4));  // open: cin, cout
  Hex_Digit_Display hex_digit_display_8 (.value(LedData[3:0]));  // open: dp
  ROM #(.addrWidth(10), .dataWidth(32), .Select("high")) rom_1 (.addr(IF_PC[11:2]), .data(IF_IR));
  // Probe on \总周期数 
  // Probe on M_PC[19:0]
  // Mips_Probe mips_probe_4: pin names not known; wires that end beside it: MEM_IR
  \理想IF_ID  \u_理想if_id_1  (
    .IR_in(IF_IR), .PC_in(IF_PC), .CLK(CLK), .IR_out({ID_IR, Func}), .PC_out(ID_PC), .CLR(or_1_out),
    .Stall(Correlated));  // open: RegDst_in, Beq_in, Syscall_in, Bne_in, JMP_in, MemToReg_in, A_in, JR_in, AluOP_in, SignedExt_in, AluSrcB_in, B_in, SLLV_in, RegWrite_in, Imm_in, SRAV_in, JAL_in, LBU_in, Shamt, MemWrite, BGEZ_in, RegDst_out, Beq_out, Syscall_out, Bne_out, JMP_out, MemToReg_out, A_out, JR_out, AluOP_out, SignedExt_out, AluSrcB_out, B_out, SLLV_out, RegWrite_out, Imm_out, SRAV_out, JAL_out, LBU_out, Shamt_2, MemWrite_2, BGEZ_out
  or or_1 (or_1_out, B_CLR, RST);
  // Probe on \总周期数 
  // Probe on \无条件分支数 
  // Probe on \条件分支成功数 
  // Probe on \插入气泡数 
  // Probe on \LoadUse次数 
  // Probe on IF_PC[11:0]
  // Probe on WB_PC[19:0]
  // Mips_Probe mips_probe_5: pin names not known; wires that end beside it: WB_IR
  // Probe on EX_PC[11:0]
  // Probe on ID_PC[11:0]
  Multiplexer #(.select(1), .width(5), .disabled("Z"), .enable("false")) multiplexer_1 (
    .in0(MEM_IR[20:16]), .in1(MEM_IR[15:11]), .out(multiplexer_1_out), .sel(MEM_RegDst));
  Multiplexer #(.select(1), .width(5), .disabled("Z"), .enable("false")) multiplexer_2 (
    .in0(EX_IR[20:16]), .in1(EX_IR[15:11]), .out(multiplexer_2_out), .sel(EX_RegDst));
  // Probe on M_PC[11:0]
  D_Flip_Flop #(.trigger("high"), .Pre_Clr_Positions("LEGACY"), .NegatePresetClear("false"), .enable("true"), .NewFFLayout("false")) d_ff_1 (.Q(d_ff_1_q));  // open: clk, D, Qn, preset, en, reset
  // Probe on 13'h12
  \单周期硬布线控制器  \u_单周期硬布线控制器_1  (
    .Func(Func), .OP(ID_IR[31:26]), .ALU_OP(\单周期硬布线控制器_1_alu_op ), .MemToReg(\单周期硬布线控制器_1_memtoreg ),
    .MemWrite(\单周期硬布线控制器_1_memwrite ), .ALU_SRC(\单周期硬布线控制器_1_alu_src ), .RegWrite(\单周期硬布线控制器_1_regwrite ),
    .SysCALL(\单周期硬布线控制器_1_syscall ), .SignedExt(SignedExt), .RegDst(\单周期硬布线控制器_1_regdst ),
    .JR(\单周期硬布线控制器_1_jr ), .JMP(\单周期硬布线控制器_1_jmp ), .Beq(\单周期硬布线控制器_1_beq ), .JAL(\单周期硬布线控制器_1_jal ),
    .Bne(\单周期硬布线控制器_1_bne ), .SLLV(\单周期硬布线控制器_1_sllv ), .SRAV(\单周期硬布线控制器_1_srav ), .BGEZ(\单周期硬布线控制器_1_bgez ),
    .LBU(\单周期硬布线控制器_1_lbu ), .ERET(\单周期硬布线控制器_1_jmp ), .MFC0(\单周期硬布线控制器_1_jmp ), .MTC0(\单周期硬布线控制器_1_jmp ));  // open: in_3
  assign bit_extender_1_out = {{16{1'b0}}, {ID_IR[15:6], Func}};  // Bit_Extender bit_extender_1
  assign bit_extender_2_out = {{16{ID_IR[15]}}, {ID_IR[15:6], Func}};  // Bit_Extender bit_extender_2
  Multiplexer #(.select(1), .width(5), .disabled("Z"), .enable("false")) multiplexer_3 (
    .in0(multiplexer_1_out), .in1({5{1'b1}}), .out(multiplexer_3_out), .sel(MEM_JAL));
  Multiplexer #(.select(1), .width(5), .disabled("Z"), .enable("false")) multiplexer_4 (
    .in0(multiplexer_2_out), .in1({5{1'b1}}), .out(multiplexer_4_out), .sel(EX_JAL));
  // Probe on WB_PC[11:0]
  Comparator #(.width(13), .mode("twosComplement")) comparator_1 (
    .a(CNT_num), .b(13'h12), .eq(comparator_1_eq), .lt(comparator_1_lt));  // open: gt
  Clock #(.highDuration(1), .lowDuration(1)) clock_2 (.out(clock_2_out));
  Multiplexer #(.select(1), .width(5), .disabled("Z"), .enable("false")) multiplexer_5 (
    .in0(ID_IR[25:21]), .in1(5'b00010), .out(R1_num), .sel(\单周期硬布线控制器_1_syscall ));
  Multiplexer #(.select(1), .width(5), .disabled("Z"), .enable("false")) multiplexer_6 (
    .in0(ID_IR[20:16]), .in1(5'b00100), .out(R2_num), .sel(\单周期硬布线控制器_1_syscall ));
  nand nand_1 (nand_1_out, d_ff_1_q, comparator_1_eq);
  Counter #(.width(13), .max('h1fff), .ongoal("stay"), .trigger("rising"), .behavior("old")) counter_2 (
    .count(comparator_1_lt), .Q(CNT_num), .clk(clock_2_out));  // open: load, D, carry, clr, preset
  Multiplexer #(.select(1), .width(32), .disabled("Z"), .enable("false")) multiplexer_7 (
    .in0(bit_extender_1_out), .in1(bit_extender_2_out), .out(multiplexer_7_out), .sel(SignedExt));
  \源寄存器使用情况  \u_源寄存器使用情况_1  (
    .OP(ID_IR[31:26]), .Funct(Func), .R1_Used(\源寄存器使用情况_1_r1_used ), .R2_Used(\源寄存器使用情况_1_r2_used ));
  assign CLK = nand_1_out ? clock_2_out : 1'bz;  // Controlled_Buffer controlled_buffer_1
  MIPS_Regifile mips_regifile_1 (
    .Din(RDin), .Clk(CLK), .R1(mips_regifile_1_r1), .R2(mips_regifile_1_r2), .WE(RegWrite),
    .W_num(multiplexer_15_out), .R1_num(R1_num), .R2_num(R2_num));
  \数据相关检测  \u_数据相关检测_1  (
    .R1_num(R1_num), .MEM_WriteReg_num(multiplexer_3_out), .MEM_RegWrite(MEM_RegWrite),
    .EX_WriteReg_num(multiplexer_4_out), .EX_RegWrite(EX_RegWrite), .R1_Used(\源寄存器使用情况_1_r1_used ),
    .R2_num(R2_num), .R2_Used(\源寄存器使用情况_1_r2_used ), .Correlated(Correlated));
  Pull_Resistor #(.pull(1)) pull_resistor_1 (.node(CLK));
  \理想ID_EX  \u_理想id_ex_1  (
    .RegDst_in(\单周期硬布线控制器_1_regdst ), .Beq_in(\单周期硬布线控制器_1_beq ), .IR_in({ID_IR, Func}),
    .Syscall_in(\单周期硬布线控制器_1_syscall ), .Bne_in(\单周期硬布线控制器_1_bne ), .PC_in(ID_PC),
    .JMP_in(\单周期硬布线控制器_1_jmp ), .MemToReg_in(\单周期硬布线控制器_1_memtoreg ), .A_in(mips_regifile_1_r1),
    .JR_in(\单周期硬布线控制器_1_jr ), .AluOP_in(\单周期硬布线控制器_1_alu_op ), .SignedExt_in(SignedExt),
    .AluSrcB_in(\单周期硬布线控制器_1_alu_src ), .B_in(mips_regifile_1_r2), .SLLV_in(\单周期硬布线控制器_1_sllv ),
    .RegWrite_in(\单周期硬布线控制器_1_regwrite ), .Imm_in(multiplexer_7_out), .SRAV_in(\单周期硬布线控制器_1_srav ),
    .JAL_in(\单周期硬布线控制器_1_jal ), .LBU_in(\单周期硬布线控制器_1_lbu ), .BGEZ_in(\单周期硬布线控制器_1_bgez ), .CLK(CLK),
    .RegDst_out(EX_RegDst), .Beq_out(\理想id_ex_1_beq_out ), .IR_out(EX_IR),
    .Syscall_out(\理想id_ex_1_syscall_out ), .Bne_out(\理想id_ex_1_bne_out ), .PC_out(EX_PC), .JMP_out(EX_JMP),
    .MemToReg_out(\理想id_ex_1_memtoreg_out ), .A_out({\理想id_ex_1_a_out_2 , \理想id_ex_1_a_out }),
    .JR_out(EX_JR), .AluOP_out(\理想id_ex_1_aluop_out ), .AluSrcB_out(\理想id_ex_1_alusrcb_out ),
    .B_out(\理想id_ex_1_b_out ), .SLLV_out(\理想id_ex_1_sllv_out ), .RegWrite_out(EX_RegWrite),
    .Imm_out(\理想id_ex_1_imm_out ), .SRAV_out(\理想id_ex_1_srav_out ), .JAL_out(EX_JAL),
    .LBU_out(\理想id_ex_1_lbu_out ), .BGEZ_out(\理想id_ex_1_bgez_out ), .CLR(or_2_out), .Shamt(ID_IR[10:6]),
    .Shamt_2(\理想id_ex_1_shamt_2 ), .MemWrite(\单周期硬布线控制器_1_memwrite ), .MemWrite_2(\理想id_ex_1_memwrite_2 ));  // open: SignedExt_out, Stall
  or or_2 (or_2_out, B_CLR, Correlated, RST);
  Multiplexer #(.select(1), .width(32), .disabled("Z"), .enable("false")) multiplexer_8 (
    .in0(\理想id_ex_1_b_out ), .in1(\理想id_ex_1_imm_out ), .out(multiplexer_8_out), .sel(\理想id_ex_1_alusrcb_out ));
  Multiplexer #(.select(1), .width(32), .disabled("Z"), .enable("false")) multiplexer_9 (
    .in0(multiplexer_8_out), .in1({32{1'b0}}), .out(multiplexer_9_out), .sel(\理想id_ex_1_bgez_out ));
  or or_3 (or_3_out, \理想id_ex_1_sllv_out , \理想id_ex_1_srav_out );
  Shifter #(.width(32), .shift("ll")) shifter_1 (.in(\理想id_ex_1_imm_out ), .\dist (5'b00010), .out(shifter_1_out));
  Adder #(.width(32)) adder_2 (.a(EX_PC), .b(32'h4), .out(adder_2_out));  // open: cin, cout
  or or_4 (B_CLR, Branch, EX_JMP);
  Multiplexer #(.select(1), .width(5), .disabled("Z"), .enable("false")) multiplexer_10 (
    .in0(\理想id_ex_1_shamt_2 ), .in1(\理想id_ex_1_a_out ), .out(multiplexer_10_out), .sel(or_3_out));
  Adder #(.width(32)) adder_3 (.a(shifter_1_out), .b(adder_2_out), .out(adder_3_out));  // open: cin, cout
  and and_2 (and_2_out, EX_JMP, ~EX_JR);  // AND_Gate
  not not_1 (not_1_out, B_CLR);
  MIPS_ALU mips_alu_1 (
    .X({\理想id_ex_1_a_out_2 , \理想id_ex_1_a_out }), .Y(multiplexer_9_out), .AluOP(\理想id_ex_1_aluop_out ),
    .Equal(mips_alu_1_equal), .Result(mips_alu_1_result), .shamt(multiplexer_10_out));  // open: Result_2
  assign controlled_buffer_2_out = EX_JR ? {\理想id_ex_1_a_out_2 , \理想id_ex_1_a_out } : 32'bz;  // Controlled_Buffer controlled_buffer_2
  assign controlled_buffer_2_out = Branch ? adder_3_out : 32'bz;  // Controlled_Buffer controlled_buffer_3
  assign controlled_buffer_2_out = and_2_out ? {EX_PC[31:28], EX_IR[25:0], 2'b00} : 32'bz;  // Controlled_Buffer controlled_buffer_4
  assign controlled_buffer_2_out = not_1_out ? PC_4 : 32'bz;  // Controlled_Buffer controlled_buffer_5
  and and_3 (and_3_out, \理想id_ex_1_bgez_out , ~mips_alu_1_result[0]);  // AND_Gate
  and and_4 (and_4_out, mips_alu_1_equal, \理想id_ex_1_beq_out );
  and and_5 (and_5_out, ~mips_alu_1_equal, \理想id_ex_1_bne_out );  // AND_Gate
  or or_5 (Branch, and_3_out, and_4_out, and_5_out);
  \理想EX_MEM  \u_理想ex_mem_1  (
    .RegDst_in(EX_RegDst), .IR_in(EX_IR), .Syscall_in(\理想id_ex_1_syscall_out ), .PC_in(EX_PC),
    .MemToReg_in(\理想id_ex_1_memtoreg_out ), .A_in({\理想id_ex_1_a_out_2 , \理想id_ex_1_a_out }),
    .B_in(\理想id_ex_1_b_out ), .RegWrite_in(EX_RegWrite), .JAL_in(EX_JAL), .LBU_in(\理想id_ex_1_lbu_out ),
    .CLK(CLK), .RegDst_out(MEM_RegDst), .IR_out(MEM_IR), .Syscall_out(\理想ex_mem_1_syscall_out ),
    .PC_out(M_PC), .MemToReg_out(\理想ex_mem_1_memtoreg_out ), .A_in_2(\理想ex_mem_1_a_in_2 ), .B_out(MDin),
    .RegWrite_out(MEM_RegWrite), .JAL_out(MEM_JAL), .LBU_out(\理想ex_mem_1_lbu_out ), .CLR(RST),
    .MemWrite(\理想id_ex_1_memwrite_2 ), .MemWrite_2(MemWrite), .ALU(mips_alu_1_result),
    .ALU_2(\理想ex_mem_1_alu_2 ));  // open: Beq_in, Bne_in, JMP_in, JR_in, SignedExt_in, AluSrcB_in, SLLV_in, Imm_in, SRAV_in, Shamt, BGEZ_in, Beq_out, Bne_out, JMP_out, JR_out, SignedExt_out, AluSrcB_out, SLLV_out, Imm_out, SRAV_out, Shamt_2, BGEZ_out, Stall
  not not_2 (not_2_out, Halt);
  RAM #(.addrWidth(10), .dataWidth(32), .bus("separate"), .Select("high")) ram_1 (
    .addr(\理想ex_mem_1_alu_2 [11:2]), .din(MDin), .data(ram_1_data), .str(MemWrite), .sel(not_2_out), .clk(CLK));  // open: ld, clr
  \理想MEM_WB  \u_理想mem_wb_1  (
    .RegDst_in(MEM_RegDst), .RegDst_out(\理想mem_wb_1_regdst_out ), .IR_in(MEM_IR), .IR_out(WB_IR),
    .Syscall_in(\理想ex_mem_1_syscall_out ), .Syscall_out(\理想mem_wb_1_syscall_out ), .PC_in(M_PC),
    .PC_out(WB_PC), .MemToReg_in(\理想ex_mem_1_memtoreg_out ), .MemToReg_out(\理想mem_wb_1_memtoreg_out ),
    .A_in(\理想ex_mem_1_a_in_2 ), .A_out(\理想mem_wb_1_a_out ), .ALU(\理想ex_mem_1_alu_2 ),
    .ALU_2(\理想mem_wb_1_alu_2 ), .B_in(MDin), .B_out(\理想mem_wb_1_b_out ), .RegWrite_in(MEM_RegWrite),
    .RegWrite_out(RegWrite), .JAL_in(MEM_JAL), .JAL_out(\理想mem_wb_1_jal_out ), .LBU_in(\理想ex_mem_1_lbu_out ),
    .MD(ram_1_data), .LBU_out(\理想mem_wb_1_lbu_out ), .MD_2(\理想mem_wb_1_md_2 ), .CLK(CLK), .CLR(RST));  // open: Beq_in, Beq_out, Bne_in, Bne_out, JMP_in, JMP_out, JR_in, JR_out, SignedExt_in, SignedExt_out, AluSrcB_in, AluSrcB_out, SLLV_in, SLLV_out, Imm_in, Imm_out, SRAV_in, SRAV_out, BGEZ_in, BGEZ_out, Stall, MemWrite, MemWrite_2
  Multiplexer #(.select(1), .width(32), .disabled("Z"), .enable("false")) multiplexer_11 (
    .in0(\理想mem_wb_1_alu_2 ), .in1(\理想mem_wb_1_md_2 ), .out(multiplexer_11_out),
    .sel(\理想mem_wb_1_memtoreg_out ));
  Comparator #(.width(32), .mode("twosComplement")) comparator_2 (
    .a(\理想mem_wb_1_a_out ), .b(32'h22), .eq(comparator_2_eq));  // open: gt, lt
  not not_3 (not_3_out, comparator_2_eq);
  assign bit_extender_3_out = {{24{1'b0}}, multiplexer_11_out[7:0]};  // Bit_Extender bit_extender_3
  Adder #(.width(32)) adder_4 (.a(WB_PC), .b(32'h4), .out(adder_4_out));  // open: cin, cout
  and and_6 (and_6_out, comparator_2_eq, \理想mem_wb_1_syscall_out );
  and and_7 (and_7_out, \理想mem_wb_1_syscall_out , not_3_out);
  Multiplexer #(.select(1), .width(32), .disabled("Z"), .enable("false")) multiplexer_12 (
    .in0(multiplexer_11_out), .in1(bit_extender_3_out), .out(multiplexer_12_out), .sel(\理想mem_wb_1_lbu_out ));
  Register #(.width(32), .trigger("rising"), .Select("low")) register_1 (
    .D(\理想mem_wb_1_b_out ), .Q(LedData), .clk(and_6_out));  // open: en, clr
  Register #(.width(1), .trigger("rising"), .Select("low")) register_2 (
    .D(and_7_out), .en(and_7_out), .Q(Halt), .clk(CLK), .clr(Go));
  Multiplexer #(.select(1), .width(5), .disabled("Z"), .enable("false")) multiplexer_13 (
    .in0(WB_IR[20:16]), .in1(WB_IR[15:11]), .out(multiplexer_13_out), .sel(\理想mem_wb_1_regdst_out ));
  Multiplexer #(.select(1), .width(32), .disabled("Z"), .enable("false")) multiplexer_14 (
    .in0(multiplexer_12_out), .in1(adder_4_out), .out(RDin), .sel(\理想mem_wb_1_jal_out ));
  Multiplexer #(.select(1), .width(5), .disabled("Z"), .enable("false")) multiplexer_15 (
    .in0(multiplexer_13_out), .in1({5{1'b1}}), .out(multiplexer_15_out), .sel(\理想mem_wb_1_jal_out ));

  // Other names for the same wires on the sheet: ID_IR[5:0] = Func; OP[5:0] = ID_IR[31:26]; MEM_PC[31:0] = M_PC

  // Notes on the sheet:
  //   中断源
  //   时空图监测，可删除
  //   中断等待指示
  //   数码管输出
  //   contents of rom_1 (hex, n*v repeats v):
  //   20110001 8000c05 20110001 20120002 20130003 8000c09 20110001 20120002 20130003 8000c0d 20110001
  //   20120002 20130003 8000c11 20110001 20120002 20130003 c000cb8 20100001 20110001 118fc0 112020
  //   20020022 c 118882 12200001 8000c15 112020 20020022 c 20110001 118880 112020 20020022 c 12200001
  //   8000c1f 20110001 118fc0 112020 20020022 c 1188c3 112020 20020022 c 118903 112020 20020022 c 118903
  //   112020 20020022 c 118903 112020 20020022 c 118903 112020 20020022 c 118903 112020 20020022 c 118903
  //   112020 20020022 c 118903 112020 20020022 c 20100001 109fc0 139fc3 8021 2012000c 24160003 26100001
  //   3210000f 20080008 20090001 139900 2709825 132020 20020022 c 1094022 1500fff9 22100001 2018000f
  //   2188024 108700 20080008 20090001 139902 2709825 132021 20020022 c 1094022 1500fff9 108702 2c9b022
  //   12c00001 8000c50 4020 1084027 84400 3508ffff 82021 20020022 c 2010ffff 20110000 ae300000 22100001
  //   22310004 ae300000 22100001 22310004 ae300000 22100001 22310004 ae300000 22100001 22310004 ae300000
  //   22100001 22310004 ae300000 22100001 22310004 ae300000 22100001 22310004 ae300000 22100001 22310004
  //   ae300000 22100001 22310004 ae300000 22100001 22310004 ae300000 22100001 22310004 ae300000 22100001
  //   22310004 ae300000 22100001 22310004 ae300000 22100001 22310004 ae300000 22100001 22310004 ae300000
  //   22100001 22310004 22100001 8020 2011003c 8e130000 8e340000 274402a 11000002 ae330000 ae140000
  //   2231fffc 1611fff8 102020 20020022 c 22100004 2011003c 1611fff2 20020032 c 20100000 22100001 102020
  //   20020022 c 22100002 102020 20020022 c 22100003 102020 20020022 c 22100004 102020 20020022 c 22100005
  //   102020 20020022 c 22100006 102020 20020022 c 22100007 102020 20020022 c 22100008 102020 20020022
  //   20020022 c 3e00008
  //   指令字
  //   rd
  //   rd
  //   控制位
  //   JMP
  //   JR
  //   OP
  //   OP
  //   Func
  //   rs
  //   rt
  //   rd
  //   流水调试日志用
  //   暂停节拍，不能为0
  //   Beq
  //   Bne
  //   MemToReg
  //   MemWrite
  //   AluOP
  //   AluSrcB
  //   RegWrite
  //   JAL
  //   RegDst
  //   Syscall
  //   戳工具置1进入计数暂停模式，ctrl+k时钟自动运行到对应节拍暂停
  //   ctrl+k关闭时钟连续运行，将控制位置零，进入单步调试模式调试
  //   用这个时钟源需要去掉电路中的其他时钟源
  //   可计数暂停的时钟源
  //   Reg_dst
  //   beq
  //   IR
  //   Syscall
  //   Bne
  //   PC
  //   JMP
  //   MemToReg
  //   JR
  //   AluOP
  //   RegWrite
  //   为方便自动评测，需要输出流水线各段保存的PC值，注意是PC不是PC+4，另外ID段寄存器写入信息，Mem段内存写入信息也要输出
  //   rt
  //   rd
endmodule
module \重定向流水线  (
  output RegWrite,
  output MemWrite,
  output [31:0] IF_PC,
  output [31:0] ID_PC,
  output [31:0] EX_PC,
  output [31:0] M_PC,
  output [31:0] WB_PC,
  output [31:0] RDin,
  output [31:0] MDin,
  output [31:0] LedData
);

  wire and_1_out, and_2_out, and_3_out, and_4_out, and_5_out, and_6_out, and_7_out, B_CLR, Branch, CLK,
       clock_1_out, clock_2_out, comparator_1_eq, comparator_2_eq, comparator_3_eq, comparator_3_lt,
       comparator_4_eq, d_ff_1_q, EX_JAL, EX_JMP, EX_JR, EX_RegDst, EX_RegWrite, Go, Halt, IR1, IR2, IR3,
       LoadUse, MEM_JAL, MEM_RegDst, MEM_RegWrite, mips_alu_1_equal, nand_1_out, nor_1_out, not_1_out,
       not_2_out, not_3_out, or_1_out, or_2_out, or_3_out, or_4_out, RST, SignedExt, W1, W2, W3,
       \单周期硬布线控制器_1_alu_src , \单周期硬布线控制器_1_beq , \单周期硬布线控制器_1_bgez , \单周期硬布线控制器_1_bne , \单周期硬布线控制器_1_jal ,
       \单周期硬布线控制器_1_jmp , \单周期硬布线控制器_1_jr , \单周期硬布线控制器_1_lbu , \单周期硬布线控制器_1_memtoreg ,
       \单周期硬布线控制器_1_memwrite , \单周期硬布线控制器_1_regdst , \单周期硬布线控制器_1_regwrite , \单周期硬布线控制器_1_sllv ,
       \单周期硬布线控制器_1_srav , \单周期硬布线控制器_1_syscall , \源寄存器使用情况_1_r1_used , \源寄存器使用情况_1_r2_used ,
       \理想ex_mem_1_lbu_out , \理想ex_mem_1_memtoreg_out , \理想ex_mem_1_syscall_out , \理想id_ex_1_alusrcb_out ,
       \理想id_ex_1_beq_out , \理想id_ex_1_bgez_out , \理想id_ex_1_bne_out , \理想id_ex_1_lbu_out ,
       \理想id_ex_1_memtoreg_out , \理想id_ex_1_memwrite_2 , \理想id_ex_1_sllv_out , \理想id_ex_1_srav_out ,
       \理想id_ex_1_syscall_out , \理想mem_wb_1_jal_out , \理想mem_wb_1_lbu_out , \理想mem_wb_1_memtoreg_out ,
       \理想mem_wb_1_regdst_out , \理想mem_wb_1_syscall_out ;
  wire [1:0] R1_Forward, R2_Forward, \重定向数据相关检测_1_r1 , \重定向数据相关检测_1_r2 ;
  wire [3:0] \单周期硬布线控制器_1_alu_op , \理想id_ex_1_aluop_out ;
  wire [4:0] multiplexer_1_out, multiplexer_2_out, multiplexer_3_out, multiplexer_4_out, multiplexer_12_out,
       multiplexer_15_out, multiplexer_17_out, R1_num, R2_num, \理想id_ex_1_shamt_2 ;
  wire [5:0] Func;
  wire [12:0] CNT_num;
  wire [15:0] \LoadUse次数 , \总周期数 , \插入气泡数 , \无条件分支数 , \条件分支成功数 ;
  wire [31:0] adder_2_out, adder_3_out, adder_4_out, bit_extender_1_out, bit_extender_2_out,
       bit_extender_3_out, controlled_buffer_2_out, EX_ALU, EX_IR, IF_IR, MEM_ALU, MEM_IR,
       mips_regifile_1_r1, mips_regifile_1_r2, multiplexer_7_out, multiplexer_8_out, multiplexer_9_out,
       multiplexer_10_out, multiplexer_11_out, multiplexer_13_out, multiplexer_14_out, PC_4, ram_1_data,
       shifter_1_out, WB_IR, \理想ex_mem_1_a_in_2 , \理想id_ex_1_a_out , \理想id_ex_1_b_out , \理想id_ex_1_imm_out ,
       \理想mem_wb_1_a_out , \理想mem_wb_1_alu_2 , \理想mem_wb_1_b_out , \理想mem_wb_1_md_2 ;
  wire [31:6] ID_IR;

  Button \u_总复位  (.out(RST));
  Button _1 (.out(IR1));
  Button _2 (.out(IR2));
  Button _3 (.out(IR3));
  // Probe on \总周期数 
  // Probe on \总周期数 
  Button \u_继续运行  (.out(Go));
  LED #(.active("true")) led_1 (.in(W1));
  LED #(.active("true")) led_2 (.in(W2));
  LED #(.active("true")) led_3 (.in(W3));
  Counter #(.width(16), .max('hffff), .ongoal("wrap"), .trigger("rising"), .behavior("new")) counter_1 (
    .Q(\总周期数 ), .clk(and_1_out));  // open: load, D, count, carry, clr, preset, down
  and and_1 (and_1_out, ~Halt, CLK);  // AND_Gate
  Hex_Digit_Display hex_digit_display_1 (.value(LedData[31:28]));  // open: dp
  // Probe on IF_PC[19:0]
  // Mips_Probe mips_probe_1: pin names not known; wires that end beside it: IF_IR
  nor nor_1 (nor_1_out, LoadUse, Halt);
  Hex_Digit_Display hex_digit_display_2 (.value(LedData[23:20]));  // open: dp
  Hex_Digit_Display hex_digit_display_3 (.value(LedData[27:24]));  // open: dp
  // Probe on ID_PC[19:0]
  // Mips_Probe mips_probe_2: pin names not known; wires that end beside it: {ID_IR, Func}
  Register #(.width(32), .trigger("rising"), .Select("low")) PC (
    .D(controlled_buffer_2_out), .en(nor_1_out), .Q(IF_PC), .clk(CLK));  // open: clr
  Hex_Digit_Display hex_digit_display_4 (.value(LedData[15:12]));  // open: dp
  Hex_Digit_Display hex_digit_display_5 (.value(LedData[19:16]));  // open: dp
  Hex_Digit_Display hex_digit_display_6 (.value(LedData[11:8]));  // open: dp
  Hex_Digit_Display hex_digit_display_7 (.value(LedData[7:4]));  // open: dp
  Clock #(.highDuration(1), .lowDuration(1)) clock_1 (.out(clock_1_out));
  // Probe on EX_PC[19:0]
  // Mips_Probe mips_probe_3: pin names not known; wires that end beside it: clock_1_out, EX_IR, CLK
  Adder #(.width(32)) adder_1 (.a(IF_PC), .b(32'h4), .out(PC_4));  // open: cin, cout
  Hex_Digit_Display hex_digit_display_8 (.value(LedData[3:0]));  // open: dp
  ROM #(.addrWidth(10), .dataWidth(32), .Select("high")) rom_1 (.addr(IF_PC[11:2]), .data(IF_IR));
  // Probe on \总周期数 
  // Probe on M_PC[19:0]
  // Mips_Probe mips_probe_4: pin names not known; wires that end beside it: MEM_IR
  \理想IF_ID  \u_理想if_id_1  (
    .IR_in(IF_IR), .PC_in(IF_PC), .CLK(CLK), .IR_out({ID_IR, Func}), .PC_out(ID_PC), .CLR(or_1_out),
    .Stall(LoadUse));  // open: RegDst_in, Beq_in, Syscall_in, Bne_in, JMP_in, MemToReg_in, A_in, JR_in, AluOP_in, SignedExt_in, AluSrcB_in, B_in, SLLV_in, RegWrite_in, Imm_in, SRAV_in, JAL_in, LBU_in, Shamt, MemWrite, BGEZ_in, RegDst_out, Beq_out, Syscall_out, Bne_out, JMP_out, MemToReg_out, A_out, JR_out, AluOP_out, SignedExt_out, AluSrcB_out, B_out, SLLV_out, RegWrite_out, Imm_out, SRAV_out, JAL_out, LBU_out, Shamt_2, MemWrite_2, BGEZ_out
  or or_1 (or_1_out, B_CLR, RST);
  // Probe on \总周期数 
  // Probe on \无条件分支数 
  // Probe on \条件分支成功数 
  // Probe on \插入气泡数 
  // Probe on \LoadUse次数 
  // Probe on IF_PC[11:0]
  // Probe on WB_PC[19:0]
  // Mips_Probe mips_probe_5: pin names not known; wires that end beside it: WB_IR
  Comparator #(.width(6), .mode("twosComplement")) comparator_1 (
    .a(EX_IR[31:26]), .b(6'b100011), .eq(comparator_1_eq));  // open: gt, lt
  Comparator #(.width(6), .mode("twosComplement")) comparator_2 (
    .a(EX_IR[31:26]), .b(6'b100100), .eq(comparator_2_eq));  // open: gt, lt
  // Probe on EX_PC[11:0]
  // Probe on ID_PC[11:0]
  or or_2 (or_2_out, comparator_1_eq, comparator_2_eq);
  Multiplexer #(.select(1), .width(5), .disabled("Z"), .enable("false")) multiplexer_1 (
    .in0(MEM_IR[20:16]), .in1(MEM_IR[15:11]), .out(multiplexer_1_out), .sel(MEM_RegDst));
  Multiplexer #(.select(1), .width(5), .disabled("Z"), .enable("false")) multiplexer_2 (
    .in0(EX_IR[20:16]), .in1(EX_IR[15:11]), .out(multiplexer_2_out), .sel(EX_RegDst));
  // Probe on M_PC[11:0]
  D_Flip_Flop #(.trigger("high"), .Pre_Clr_Positions("LEGACY"), .NegatePresetClear("false"), .enable("true"), .NewFFLayout("false")) d_ff_1 (.Q(d_ff_1_q));  // open: clk, D, Qn, preset, en, reset
  // Probe on 13'hc
  \单周期硬布线控制器  \u_单周期硬布线控制器_1  (
    .Func(Func), .OP(ID_IR[31:26]), .ALU_OP(\单周期硬布线控制器_1_alu_op ), .MemToReg(\单周期硬布线控制器_1_memtoreg ),
    .MemWrite(\单周期硬布线控制器_1_memwrite ), .ALU_SRC(\单周期硬布线控制器_1_alu_src ), .RegWrite(\单周期硬布线控制器_1_regwrite ),
    .SysCALL(\单周期硬布线控制器_1_syscall ), .SignedExt(SignedExt), .RegDst(\单周期硬布线控制器_1_regdst ),
    .JR(\单周期硬布线控制器_1_jr ), .JMP(\单周期硬布线控制器_1_jmp ), .Beq(\单周期硬布线控制器_1_beq ), .JAL(\单周期硬布线控制器_1_jal ),
    .Bne(\单周期硬布线控制器_1_bne ), .SLLV(\单周期硬布线控制器_1_sllv ), .SRAV(\单周期硬布线控制器_1_srav ), .BGEZ(\单周期硬布线控制器_1_bgez ),
    .LBU(\单周期硬布线控制器_1_lbu ), .ERET(\单周期硬布线控制器_1_jmp ), .MFC0(\单周期硬布线控制器_1_jmp ), .MTC0(\单周期硬布线控制器_1_jmp ));  // open: in_3
  assign bit_extender_1_out = {{16{1'b0}}, {ID_IR[15:6], Func}};  // Bit_Extender bit_extender_1
  assign bit_extender_2_out = {{16{ID_IR[15]}}, {ID_IR[15:6], Func}};  // Bit_Extender bit_extender_2
  Multiplexer #(.select(1), .width(5), .disabled("Z"), .enable("false")) multiplexer_3 (
    .in0(multiplexer_1_out), .in1({5{1'b1}}), .out(multiplexer_3_out), .sel(MEM_JAL));
  Multiplexer #(.select(1), .width(5), .disabled("Z"), .enable("false")) multiplexer_4 (
    .in0(multiplexer_2_out), .in1({5{1'b1}}), .out(multiplexer_4_out), .sel(EX_JAL));
  // Probe on WB_PC[11:0]
  Comparator #(.width(13), .mode("twosComplement")) comparator_3 (
    .a(CNT_num), .b(13'hc), .eq(comparator_3_eq), .lt(comparator_3_lt));  // open: gt
  Clock #(.highDuration(1), .lowDuration(1)) clock_2 (.out(clock_2_out));
  Multiplexer #(.select(1), .width(5), .disabled("Z"), .enable("false")) multiplexer_5 (
    .in0(ID_IR[25:21]), .in1(5'b00010), .out(R1_num), .sel(\单周期硬布线控制器_1_syscall ));
  Multiplexer #(.select(1), .width(5), .disabled("Z"), .enable("false")) multiplexer_6 (
    .in0(ID_IR[20:16]), .in1(5'b00100), .out(R2_num), .sel(\单周期硬布线控制器_1_syscall ));
  nand nand_1 (nand_1_out, d_ff_1_q, comparator_3_eq);
  Counter #(.width(13), .max('h1fff), .ongoal("stay"), .trigger("rising"), .behavior("old")) counter_2 (
    .count(comparator_3_lt), .Q(CNT_num), .clk(clock_2_out));  // open: load, D, carry, clr, preset
  \源寄存器使用情况  \u_源寄存器使用情况_1  (
    .OP(ID_IR[31:26]), .Funct(Func), .R1_Used(\源寄存器使用情况_1_r1_used ), .R2_Used(\源寄存器使用情况_1_r2_used ));
  assign CLK = nand_1_out ? clock_2_out : 1'bz;  // Controlled_Buffer controlled_buffer_1
  MIPS_Regifile mips_regifile_1 (
    .Din(RDin), .Clk(CLK), .R1(mips_regifile_1_r1), .R2(mips_regifile_1_r2), .WE(RegWrite),
    .W_num(multiplexer_17_out), .R1_num(R1_num), .R2_num(R2_num));
  Multiplexer #(.select(1), .width(32), .disabled("Z"), .enable("false")) multiplexer_7 (
    .in0(bit_extender_1_out), .in1(bit_extender_2_out), .out(multiplexer_7_out), .sel(SignedExt));
  \重定向数据相关检测  \u_重定向数据相关检测_1  (
    .R1_num(R1_num), .MEM_WriteReg_num(multiplexer_3_out), .MEM_RegWrite(MEM_RegWrite),
    .R1_Used(\源寄存器使用情况_1_r1_used ), .EX_WriteReg_num(multiplexer_4_out), .EX_RegWrite(EX_RegWrite),
    .R2_num(R2_num), .R2_Used(\源寄存器使用情况_1_r2_used ), .R1(\重定向数据相关检测_1_r1 ), .R2(\重定向数据相关检测_1_r2 ),
    .Load_Use(or_2_out), .LoadUse(LoadUse));
  Pull_Resistor #(.pull(1)) pull_resistor_1 (.node(CLK));
  Register #(.width(2), .trigger("rising"), .Select("low")) register_1 (
    .D(\重定向数据相关检测_1_r1 ), .Q(R1_Forward), .clk(CLK));  // open: en, clr
  Register #(.width(2), .trigger("rising"), .Select("low")) register_2 (
    .D(\重定向数据相关检测_1_r2 ), .Q(R2_Forward), .clk(CLK));  // open: en, clr
  \理想ID_EX  \u_理想id_ex_1  (
    .RegDst_in(\单周期硬布线控制器_1_regdst ), .Beq_in(\单周期硬布线控制器_1_beq ), .IR_in({ID_IR, Func}),
    .Syscall_in(\单周期硬布线控制器_1_syscall ), .Bne_in(\单周期硬布线控制器_1_bne ), .PC_in(ID_PC),
    .JMP_in(\单周期硬布线控制器_1_jmp ), .MemToReg_in(\单周期硬布线控制器_1_memtoreg ), .A_in(mips_regifile_1_r1),
    .JR_in(\单周期硬布线控制器_1_jr ), .AluOP_in(\单周期硬布线控制器_1_alu_op ), .SignedExt_in(SignedExt),
    .AluSrcB_in(\单周期硬布线控制器_1_alu_src ), .B_in(mips_regifile_1_r2), .SLLV_in(\单周期硬布线控制器_1_sllv ),
    .RegWrite_in(\单周期硬布线控制器_1_regwrite ), .Imm_in(multiplexer_7_out), .SRAV_in(\单周期硬布线控制器_1_srav ),
    .JAL_in(\单周期硬布线控制器_1_jal ), .LBU_in(\单周期硬布线控制器_1_lbu ), .BGEZ_in(\单周期硬布线控制器_1_bgez ), .CLK(CLK),
    .RegDst_out(EX_RegDst), .Beq_out(\理想id_ex_1_beq_out ), .IR_out(EX_IR),
    .Syscall_out(\理想id_ex_1_syscall_out ), .Bne_out(\理想id_ex_1_bne_out ), .PC_out(EX_PC), .JMP_out(EX_JMP),
    .MemToReg_out(\理想id_ex_1_memtoreg_out ), .A_out(\理想id_ex_1_a_out ), .JR_out(EX_JR),
    .AluOP_out(\理想id_ex_1_aluop_out ), .AluSrcB_out(\理想id_ex_1_alusrcb_out ), .B_out(\理想id_ex_1_b_out ),
    .SLLV_out(\理想id_ex_1_sllv_out ), .RegWrite_out(EX_RegWrite), .Imm_out(\理想id_ex_1_imm_out ),
    .SRAV_out(\理想id_ex_1_srav_out ), .JAL_out(EX_JAL), .LBU_out(\理想id_ex_1_lbu_out ),
    .BGEZ_out(\理想id_ex_1_bgez_out ), .CLR(or_3_out), .Shamt(ID_IR[10:6]), .Shamt_2(\理想id_ex_1_shamt_2 ),
    .MemWrite(\单周期硬布线控制器_1_memwrite ), .MemWrite_2(\理想id_ex_1_memwrite_2 ));  // open: SignedExt_out, Stall
  or or_3 (or_3_out, B_CLR, LoadUse, RST);
  Multiplexer #(.select(1), .width(32), .disabled("Z"), .enable("false")) multiplexer_8 (
    .in0(multiplexer_9_out), .in1(\理想id_ex_1_imm_out ), .out(multiplexer_8_out), .sel(\理想id_ex_1_alusrcb_out ));
  Multiplexer #(.select(2), .width(32), .disabled("Z"), .enable("false")) multiplexer_9 (
    .in0(\理想id_ex_1_b_out ), .in1(MEM_ALU), .in2(RDin), .in3(MEM_ALU), .out(multiplexer_9_out),
    .sel(R2_Forward));
  Multiplexer #(.select(1), .width(32), .disabled("Z"), .enable("false")) multiplexer_10 (
    .in0(multiplexer_8_out), .in1({32{1'b0}}), .out(multiplexer_10_out), .sel(\理想id_ex_1_bgez_out ));
  or or_4 (or_4_out, \理想id_ex_1_sllv_out , \理想id_ex_1_srav_out );
  Multiplexer #(.select(2), .width(32), .disabled("Z"), .enable("false")) multiplexer_11 (
    .in0(\理想id_ex_1_a_out ), .in1(MEM_ALU), .in2(RDin), .in3(MEM_ALU), .out(multiplexer_11_out),
    .sel(R1_Forward));
  Multiplexer #(.select(1), .width(5), .disabled("Z"), .enable("false")) multiplexer_12 (
    .in0(\理想id_ex_1_shamt_2 ), .in1(multiplexer_11_out[4:0]), .out(multiplexer_12_out), .sel(or_4_out));
  MIPS_ALU mips_alu_1 (
    .X(multiplexer_11_out), .Y(multiplexer_10_out), .AluOP(\理想id_ex_1_aluop_out ), .Equal(mips_alu_1_equal),
    .Result(EX_ALU), .shamt(multiplexer_12_out));  // open: Result_2
  and and_2 (and_2_out, \理想id_ex_1_bgez_out , ~EX_ALU[0]);  // AND_Gate
  and and_3 (and_3_out, mips_alu_1_equal, \理想id_ex_1_beq_out );
  and and_4 (and_4_out, ~mips_alu_1_equal, \理想id_ex_1_bne_out );  // AND_Gate
  Shifter #(.width(32), .shift("ll")) shifter_1 (.in(\理想id_ex_1_imm_out ), .\dist (5'b00010), .out(shifter_1_out));
  Adder #(.width(32)) adder_2 (.a(EX_PC), .b(32'h4), .out(adder_2_out));  // open: cin, cout
  or or_5 (Branch, and_2_out, and_3_out, and_4_out);
  \理想EX_MEM  \u_理想ex_mem_1  (
    .RegDst_in(EX_RegDst), .IR_in(EX_IR), .Syscall_in(\理想id_ex_1_syscall_out ), .PC_in(EX_PC),
    .MemToReg_in(\理想id_ex_1_memtoreg_out ), .A_in(multiplexer_11_out), .B_in(multiplexer_9_out),
    .RegWrite_in(EX_RegWrite), .JAL_in(EX_JAL), .LBU_in(\理想id_ex_1_lbu_out ), .CLK(CLK),
    .RegDst_out(MEM_RegDst), .IR_out(MEM_IR), .Syscall_out(\理想ex_mem_1_syscall_out ), .PC_out(M_PC),
    .MemToReg_out(\理想ex_mem_1_memtoreg_out ), .A_in_2(\理想ex_mem_1_a_in_2 ), .B_out(MDin),
    .RegWrite_out(MEM_RegWrite), .JAL_out(MEM_JAL), .LBU_out(\理想ex_mem_1_lbu_out ), .CLR(RST),
    .MemWrite(\理想id_ex_1_memwrite_2 ), .MemWrite_2(MemWrite), .ALU(EX_ALU), .ALU_2(MEM_ALU));  // open: Beq_in, Bne_in, JMP_in, JR_in, SignedExt_in, AluSrcB_in, SLLV_in, Imm_in, SRAV_in, Shamt, BGEZ_in, Beq_out, Bne_out, JMP_out, JR_out, SignedExt_out, AluSrcB_out, SLLV_out, Imm_out, SRAV_out, Shamt_2, BGEZ_out, Stall
  Adder #(.width(32)) adder_3 (.a(shifter_1_out), .b(adder_2_out), .out(adder_3_out));  // open: cin, cout
  or or_6 (B_CLR, Branch, EX_JMP);
  not not_1 (not_1_out, B_CLR);
  assign controlled_buffer_2_out = EX_JR ? multiplexer_11_out : 32'bz;  // Controlled_Buffer controlled_buffer_2
  assign controlled_buffer_2_out = Branch ? adder_3_out : 32'bz;  // Controlled_Buffer controlled_buffer_3
  assign controlled_buffer_2_out = and_5_out ? {EX_PC[31:28], EX_IR[25:0], 2'b00} : 32'bz;  // Controlled_Buffer controlled_buffer_4
  and and_5 (and_5_out, EX_JMP, ~EX_JR);  // AND_Gate
  assign controlled_buffer_2_out = not_1_out ? PC_4 : 32'bz;  // Controlled_Buffer controlled_buffer_5
  not not_2 (not_2_out, Halt);
  RAM #(.addrWidth(10), .dataWidth(32), .bus("separate"), .Select("high")) ram_1 (
    .addr(MEM_ALU[11:2]), .din(MDin), .data(ram_1_data), .str(MemWrite), .sel(not_2_out), .clk(CLK));  // open: ld, clr
  \理想MEM_WB  \u_理想mem_wb_1  (
    .RegDst_in(MEM_RegDst), .RegDst_out(\理想mem_wb_1_regdst_out ), .IR_in(MEM_IR), .IR_out(WB_IR),
    .Syscall_in(\理想ex_mem_1_syscall_out ), .Syscall_out(\理想mem_wb_1_syscall_out ), .PC_in(M_PC),
    .PC_out(WB_PC), .MemToReg_in(\理想ex_mem_1_memtoreg_out ), .MemToReg_out(\理想mem_wb_1_memtoreg_out ),
    .A_in(\理想ex_mem_1_a_in_2 ), .A_out(\理想mem_wb_1_a_out ), .ALU(MEM_ALU), .ALU_2(\理想mem_wb_1_alu_2 ),
    .B_in(MDin), .B_out(\理想mem_wb_1_b_out ), .RegWrite_in(MEM_RegWrite), .RegWrite_out(RegWrite),
    .JAL_in(MEM_JAL), .JAL_out(\理想mem_wb_1_jal_out ), .LBU_in(\理想ex_mem_1_lbu_out ), .MD(ram_1_data),
    .LBU_out(\理想mem_wb_1_lbu_out ), .MD_2(\理想mem_wb_1_md_2 ), .CLK(CLK), .CLR(RST));  // open: Beq_in, Beq_out, Bne_in, Bne_out, JMP_in, JMP_out, JR_in, JR_out, SignedExt_in, SignedExt_out, AluSrcB_in, AluSrcB_out, SLLV_in, SLLV_out, Imm_in, Imm_out, SRAV_in, SRAV_out, BGEZ_in, BGEZ_out, Stall, MemWrite, MemWrite_2
  Multiplexer #(.select(1), .width(32), .disabled("Z"), .enable("false")) multiplexer_13 (
    .in0(\理想mem_wb_1_alu_2 ), .in1(\理想mem_wb_1_md_2 ), .out(multiplexer_13_out),
    .sel(\理想mem_wb_1_memtoreg_out ));
  Comparator #(.width(32), .mode("twosComplement")) comparator_4 (
    .a(\理想mem_wb_1_a_out ), .b(32'h22), .eq(comparator_4_eq));  // open: gt, lt
  not not_3 (not_3_out, comparator_4_eq);
  assign bit_extender_3_out = {{24{1'b0}}, multiplexer_13_out[7:0]};  // Bit_Extender bit_extender_3
  Adder #(.width(32)) adder_4 (.a(WB_PC), .b(32'h4), .out(adder_4_out));  // open: cin, cout
  and and_6 (and_6_out, comparator_4_eq, \理想mem_wb_1_syscall_out );
  and and_7 (and_7_out, \理想mem_wb_1_syscall_out , not_3_out);
  Multiplexer #(.select(1), .width(32), .disabled("Z"), .enable("false")) multiplexer_14 (
    .in0(multiplexer_13_out), .in1(bit_extender_3_out), .out(multiplexer_14_out), .sel(\理想mem_wb_1_lbu_out ));
  Register #(.width(32), .trigger("rising"), .Select("low")) register_3 (
    .D(\理想mem_wb_1_b_out ), .Q(LedData), .clk(and_6_out));  // open: en, clr
  Register #(.width(1), .trigger("rising"), .Select("low")) register_4 (
    .D(and_7_out), .en(and_7_out), .Q(Halt), .clk(CLK), .clr(Go));
  Multiplexer #(.select(1), .width(5), .disabled("Z"), .enable("false")) multiplexer_15 (
    .in0(WB_IR[20:16]), .in1(WB_IR[15:11]), .out(multiplexer_15_out), .sel(\理想mem_wb_1_regdst_out ));
  Multiplexer #(.select(1), .width(32), .disabled("Z"), .enable("false")) multiplexer_16 (
    .in0(multiplexer_14_out), .in1(adder_4_out), .out(RDin), .sel(\理想mem_wb_1_jal_out ));
  Multiplexer #(.select(1), .width(5), .disabled("Z"), .enable("false")) multiplexer_17 (
    .in0(multiplexer_15_out), .in1({5{1'b1}}), .out(multiplexer_17_out), .sel(\理想mem_wb_1_jal_out ));

  // Other names for the same wires on the sheet: ID_IR[5:0] = Func; OP[5:0] = ID_IR[31:26]; MEM_PC[31:0] = M_PC

  // Notes on the sheet:
  //   中断源
  //   时空图监测，可删除
  //   中断等待指示
  //   数码管输出
  //   contents of rom_1 (hex, n*v repeats v):
  //   20110001 8000c05 20110001 20120002 20130003 8000c09 20110001 20120002 20130003 8000c0d 20110001
  //   20120002 20130003 8000c11 20110001 20120002 20130003 c000cb8 20100001 20110001 118fc0 112020
  //   20020022 c 118882 12200001 8000c15 112020 20020022 c 20110001 118880 112020 20020022 c 12200001
  //   8000c1f 20110001 118fc0 112020 20020022 c 1188c3 112020 20020022 c 118903 112020 20020022 c 118903
  //   112020 20020022 c 118903 112020 20020022 c 118903 112020 20020022 c 118903 112020 20020022 c 118903
  //   112020 20020022 c 118903 112020 20020022 c 20100001 109fc0 139fc3 8021 2012000c 24160003 26100001
  //   3210000f 20080008 20090001 139900 2709825 132020 20020022 c 1094022 1500fff9 22100001 2018000f
  //   2188024 108700 20080008 20090001 139902 2709825 132021 20020022 c 1094022 1500fff9 108702 2c9b022
  //   12c00001 8000c50 4020 1084027 84400 3508ffff 82021 20020022 c 2010ffff 20110000 ae300000 22100001
  //   22310004 ae300000 22100001 22310004 ae300000 22100001 22310004 ae300000 22100001 22310004 ae300000
  //   22100001 22310004 ae300000 22100001 22310004 ae300000 22100001 22310004 ae300000 22100001 22310004
  //   ae300000 22100001 22310004 ae300000 22100001 22310004 ae300000 22100001 22310004 ae300000 22100001
  //   22310004 ae300000 22100001 22310004 ae300000 22100001 22310004 ae300000 22100001 22310004 ae300000
  //   22100001 22310004 22100001 8020 2011003c 8e130000 8e340000 274402a 11000002 ae330000 ae140000
  //   2231fffc 1611fff8 102020 20020022 c 22100004 2011003c 1611fff2 20020032 c 20100000 22100001 102020
  //   20020022 c 22100002 102020 20020022 c 22100003 102020 20020022 c 22100004 102020 20020022 c 22100005
  //   102020 20020022 c 22100006 102020 20020022 c 22100007 102020 20020022 c 22100008 102020 20020022
  //   20020022 c 3e00008
  //   指令字
  //   控制位
  //   JMP
  //   JR
  //   OP
  //   OP
  //   Func
  //   rs
  //   rt
  //   rd
  //   rd
  //   rd
  //   流水调试日志用
  //   暂停节拍，不能为0
  //   Beq
  //   Bne
  //   MemToReg
  //   MemWrite
  //   AluOP
  //   AluSrcB
  //   RegWrite
  //   JAL
  //   RegDst
  //   Syscall
  //   戳工具置1进入计数暂停模式，ctrl+k时钟自动运行到对应节拍暂停
  //   ctrl+k关闭时钟连续运行，将控制位置零，进入单步调试模式调试
  //   用这个时钟源需要去掉电路中的其他时钟源
  //   可计数暂停的时钟源
  //   IR
  //   Syscall
  //   MemToReg
  //   AluOP
  //   RegWrite
  //   Reg_dst
  //   beq
  //   Bne
  //   PC
  //   JMP
  //   JR
  //   为方便自动评测，需要输出流水线各段保存的PC值，注意是PC不是PC+4，另外ID段寄存器写入信息，Mem段内存写入信息也要输出
  //   rt
  //   rd
endmodule

module \中断按键参考电路  (
  input  \同步清零信号 ,
  output \与中断屏蔽位与 
);

  wire \_1号中断_out , and_1_out, clock_1_out, d_ff_1_q, or_1_out, or_2_out;

  Clock #(.highDuration(1), .lowDuration(1)) clock_1 (.out(clock_1_out));
  Button \_1号中断  (.out(\_1号中断_out ));
  LED #(.active("true")) \_1号中断等待指示灯  (.in(or_1_out));
  or or_1 (or_1_out, \与中断屏蔽位与 , d_ff_1_q);
  D_Flip_Flop #(.trigger("rising"), .Pre_Clr_Positions("LEGACY"), .NegatePresetClear("false"), .enable("true"), .NewFFLayout("false")) d_ff_1 (
    .clk(\_1号中断_out ), .D(1'b1), .Q(d_ff_1_q), .reset(\与中断屏蔽位与 ));  // open: Qn, preset, en
  or or_2 (or_2_out, d_ff_1_q, \与中断屏蔽位与 );
  and and_1 (and_1_out, or_2_out, ~\同步清零信号 );  // AND_Gate
  D_Flip_Flop #(.trigger("rising"), .Pre_Clr_Positions("LEGACY"), .NegatePresetClear("false"), .enable("true"), .NewFFLayout("false")) IR1 (
    .clk(clock_1_out), .D(and_1_out), .Q(\与中断屏蔽位与 ));  // open: Qn, preset, en, reset
  \单周期硬布线控制器  \u_单周期硬布线控制器_1  ();  // open: Func, OP, ALU_OP, MemToReg, MemWrite, ALU_SRC, RegWrite, SysCALL, SignedExt, RegDst, JR, JMP, Beq, JAL, Bne, SLLV, SRAV, BGEZ, LBU, ERET, MFC0, MTC0, in_3

  // Notes on the sheet:
  //   中断信号采样参考电路
  //   Reset 
endmodule

module \单周期MIPS_单级中断  (
  input  IR1,
  input  IR2,
  input  IR3,
  output RegWrite,
  output MemWrite,
  output [31:0] PC,
  output [31:0] IR,
  output [31:0] RDin,
  output [31:0] MDin,
  output [31:0] LedData
);

  wire and_1_out, and_2_out, and_3_out, and_4_out, and_5_out, and_10_out, and_11_out, and_12_out, and_13_out,
       and_14_out, BGEZ, Branch, CLK, comparator_1_eq, comparator_2_eq, comparator_3_eq, comparator_4_eq,
       comparator_5_eq, d_ff_1_q, d_ff_2_q, d_ff_3_q, decoder_1_out1, decoder_1_out2, decoder_1_out3, ERET,
       Go, Halt, IE_Ctrl, IE_q, IR1_t, ir1_t_t, IR2_t, ir2_t_t, IR3_t, ir3_t_t, IRA, IRB, IRC, JAL, JMP, JR,
       LBU, mips_alu_1_equal, nor_1_out, not_1_out, not_2_out, not_3_out, not_4_out, or_4_out, or_5_out,
       or_6_out, or_7_out, or_11_out, or_12_out, priority_encoder_1_gs, Rst1, Rst2, Rst3, SignedExt, SLLV,
       SRAV, Syscall, W1, W2, W3, \单周期硬布线控制器_1_alu_src , \单周期硬布线控制器_1_beq , \单周期硬布线控制器_1_bne ,
       \单周期硬布线控制器_1_memtoreg , \单周期硬布线控制器_1_regdst ;
  wire [1:0] priority_encoder_1_out, register_1_q;
  wire [3:0] \单周期硬布线控制器_1_alu_op ;
  wire [4:0] multiplexer_4_out, multiplexer_5_out, multiplexer_6_out, multiplexer_7_out, multiplexer_12_out;
  wire [15:0] \总周期数 ;
  wire [31:0] adder_1_out, adder_2_out, bit_extender_1_out, bit_extender_2_out, bit_extender_3_out, EPC,
       mips_alu_1_result, multiplexer_1_out, multiplexer_2_out, multiplexer_9_out, multiplexer_10_out,
       multiplexer_11_out, multiplexer_13_out, multiplexer_14_out, Prev_PC, ram_1_data, shifter_1_out, v0,
       \中断入口地址 ;

  Clock #(.highDuration(1), .lowDuration(1)) clock_1 (.out(CLK));
  Button _1 ();  // open: out
  Button _2 ();  // open: out
  Button _3 ();  // open: out
  Button \u_继续运行  (.out(Go));
  LED #(.active("true")) led_1 (.in(W1));
  LED #(.active("true")) led_2 (.in(W2));
  LED #(.active("true")) led_3 (.in(W3));
  or or_1 (W1, ir1_t_t, d_ff_1_q);
  or or_2 (W2, ir2_t_t, d_ff_2_q);
  or or_3 (W3, ir3_t_t, d_ff_3_q);
  Hex_Digit_Display hex_digit_display_1 (.value(LedData[31:28]));  // open: dp
  Comparator #(.width(16), .mode("twosComplement")) comparator_1 (
    .a(16'h23b), .b(\总周期数 ), .eq(comparator_1_eq));  // open: gt, lt
  Comparator #(.width(16), .mode("twosComplement")) comparator_2 (
    .a(\总周期数 ), .b(16'h1), .eq(comparator_2_eq));  // open: gt, lt
  Comparator #(.width(16), .mode("twosComplement")) comparator_3 (
    .a(\总周期数 ), .b(16'h4), .eq(comparator_3_eq));  // open: gt, lt
  Comparator #(.width(16), .mode("twosComplement")) comparator_4 (
    .a(\总周期数 ), .b(16'h7), .eq(comparator_4_eq));  // open: gt, lt
  D_Flip_Flop #(.trigger("rising"), .Pre_Clr_Positions("LEGACY"), .NegatePresetClear("false"), .enable("true"), .NewFFLayout("false")) d_ff_1 (
    .clk(IRA), .D(1'b1), .Q(d_ff_1_q), .reset(ir1_t_t));  // open: Qn, preset, en
  D_Flip_Flop #(.trigger("rising"), .Pre_Clr_Positions("LEGACY"), .NegatePresetClear("false"), .enable("true"), .NewFFLayout("false")) d_ff_2 (
    .clk(IRB), .D(1'b1), .Q(d_ff_2_q), .reset(ir2_t_t));  // open: Qn, preset, en
  D_Flip_Flop #(.trigger("rising"), .Pre_Clr_Positions("LEGACY"), .NegatePresetClear("false"), .enable("true"), .NewFFLayout("false")) d_ff_3 (
    .clk(IRC), .D(1'b1), .Q(d_ff_3_q), .reset(ir3_t_t));  // open: Qn, preset, en
  Hex_Digit_Display hex_digit_display_2 (.value(LedData[27:24]));  // open: dp
  Hex_Digit_Display hex_digit_display_3 (.value(LedData[23:20]));  // open: dp
  or or_4 (or_4_out, comparator_1_eq, comparator_2_eq);
  assign IRA = or_4_out ? ~CLK : 1'bz;  // Controlled_Inverter controlled_inverter_1
  assign IRB = comparator_3_eq ? ~CLK : 1'bz;  // Controlled_Inverter controlled_inverter_2
  assign IRC = comparator_4_eq ? ~CLK : 1'bz;  // Controlled_Inverter controlled_inverter_3
  Register #(.width(32), .trigger("rising"), .Select("low")) u_EPC (
    .D(Prev_PC), .en(IE_Ctrl), .Q(EPC), .clk(CLK));  // open: clr
  or or_5 (or_5_out, d_ff_1_q, ir1_t_t);
  or or_6 (or_6_out, d_ff_2_q, ir2_t_t);
  or or_7 (or_7_out, d_ff_3_q, ir3_t_t);
  Hex_Digit_Display hex_digit_display_4 (.value(LedData[15:12]));  // open: dp
  Hex_Digit_Display hex_digit_display_5 (.value(LedData[19:16]));  // open: dp
  Pull_Resistor #(.pull(0)) pull_resistor_1 (.node(IRA));
  Pull_Resistor #(.pull(0)) pull_resistor_2 (.node(IRB));
  Pull_Resistor #(.pull(0)) pull_resistor_3 (.node(IRC));
  and and_1 (and_1_out, or_5_out, ~Rst1);  // AND_Gate
  and and_2 (and_2_out, or_6_out, ~Rst2);  // AND_Gate
  and and_3 (and_3_out, or_7_out, ~Rst3);  // AND_Gate
  Hex_Digit_Display hex_digit_display_6 (.value(LedData[7:4]));  // open: dp
  Hex_Digit_Display hex_digit_display_7 (.value(LedData[11:8]));  // open: dp
  // Probe on \总周期数 
  D_Flip_Flop #(.trigger("rising"), .Pre_Clr_Positions("LEGACY"), .NegatePresetClear("false"), .enable("true"), .NewFFLayout("false")) u_IR1 (
    .clk(CLK), .D(and_1_out), .Q(ir1_t_t));  // open: Qn, preset, en, reset
  D_Flip_Flop #(.trigger("rising"), .Pre_Clr_Positions("LEGACY"), .NegatePresetClear("false"), .enable("true"), .NewFFLayout("false")) u_IR2 (
    .clk(CLK), .D(and_2_out), .Q(ir2_t_t));  // open: Qn, preset, en, reset
  D_Flip_Flop #(.trigger("rising"), .Pre_Clr_Positions("LEGACY"), .NegatePresetClear("false"), .enable("true"), .NewFFLayout("false")) u_IR3 (
    .clk(CLK), .D(and_3_out), .Q(ir3_t_t));  // open: Qn, preset, en, reset
  Hex_Digit_Display hex_digit_display_8 (.value(LedData[3:0]));  // open: dp
  and and_4 (and_4_out, JMP, ~JR);  // AND_Gate
  nor nor_1 (nor_1_out, Branch, JMP);
  or or_8 (IR1_t, IR1, IRA);
  assign Prev_PC = JR ? v0 : 32'bz;  // Controlled_Buffer controlled_buffer_1
  assign Prev_PC = and_4_out ? {PC[31:28], IR[25:0], 2'b00} : 32'bz;  // Controlled_Buffer controlled_buffer_2
  assign Prev_PC = Branch ? adder_2_out : 32'bz;  // Controlled_Buffer controlled_buffer_3
  assign Prev_PC = nor_1_out ? adder_1_out : 32'bz;  // Controlled_Buffer controlled_buffer_4
  or or_9 (IR2_t, IR2, IRB);
  Multiplexer #(.select(1), .width(32), .disabled("Z"), .enable("false")) multiplexer_1 (
    .in0(Prev_PC), .in1(\中断入口地址 ), .out(multiplexer_1_out), .sel(IE_Ctrl));
  Multiplexer #(.select(1), .width(32), .disabled("Z"), .enable("false")) multiplexer_2 (
    .in0(multiplexer_1_out), .in1(EPC), .out(multiplexer_2_out), .sel(ERET));
  not not_1 (not_1_out, Halt);
  Priority_Encoder #(.select(2), .disabled("Z")) priority_encoder_1 (
    .in0(1'b0), .in1(ir1_t_t), .in2(ir2_t_t), .in3(ir3_t_t), .out(priority_encoder_1_out),
    .gs(priority_encoder_1_gs));  // open: en_out, en_in
  or or_10 (IR3_t, IR3, IRC);
  and and_5 (and_5_out, ~Halt, CLK);  // AND_Gate
  Register #(.width(32), .trigger("rising"), .Select("low")) u_PC (
    .D(multiplexer_2_out), .en(not_1_out), .Q(PC), .clk(CLK));  // open: clr
  Multiplexer #(.select(2), .width(32), .disabled("Z"), .enable("false")) multiplexer_3 (
    .in1(32'h30ac), .in2(32'h3150), .in3(32'h31f4), .out(\中断入口地址 ), .sel(priority_encoder_1_out));  // open: in0
  Counter #(.width(16), .max('hffff), .ongoal("wrap"), .trigger("rising"), .behavior("new")) counter_1 (
    .Q(\总周期数 ), .clk(and_5_out));  // open: load, D, count, carry, clr, preset, down
  ROM #(.addrWidth(10), .dataWidth(32), .Select("high")) rom_1 (.addr(PC[11:2]), .data(IR));
  Adder #(.width(32)) adder_1 (.a(PC), .b(32'h4), .out(adder_1_out));  // open: cin, cout
  or or_11 (or_11_out, ERET, IE_Ctrl);
  // Mips_Probe mips_probe_1: pin names not known; wires that end beside it: IR
  Register #(.width(1), .trigger("rising"), .Select("low")) IE (
    .D(IE_Ctrl), .en(or_11_out), .Q(IE_q), .clk(CLK));  // open: clr
  Register #(.width(2), .trigger("rising"), .Select("low")) register_1 (
    .D(priority_encoder_1_out), .en(IE_Ctrl), .Q(register_1_q), .clk(CLK));  // open: clr
  and and_6 (IE_Ctrl, priority_encoder_1_gs, ~IE_q);  // AND_Gate
  \单周期硬布线控制器  \u_单周期硬布线控制器_1  (
    .Func(IR[5:0]), .OP(IR[31:26]), .ALU_OP(\单周期硬布线控制器_1_alu_op ), .MemToReg(\单周期硬布线控制器_1_memtoreg ),
    .MemWrite(MemWrite), .ALU_SRC(\单周期硬布线控制器_1_alu_src ), .RegWrite(RegWrite), .SysCALL(Syscall),
    .SignedExt(SignedExt), .RegDst(\单周期硬布线控制器_1_regdst ), .JR(JR), .JMP(JMP), .Beq(\单周期硬布线控制器_1_beq ),
    .JAL(JAL), .Bne(\单周期硬布线控制器_1_bne ), .SLLV(SLLV), .SRAV(SRAV), .BGEZ(BGEZ), .LBU(LBU), .ERET(ERET));  // open: MFC0, MTC0, in_3
  Multiplexer #(.select(1), .width(5), .disabled("Z"), .enable("false")) multiplexer_4 (
    .in0(IR[20:16]), .in1(IR[15:11]), .out(multiplexer_4_out), .sel(\单周期硬布线控制器_1_regdst ));
  not not_2 (not_2_out, JAL);
  assign bit_extender_1_out = {{16{1'b0}}, IR[15:0]};  // Bit_Extender bit_extender_1
  assign bit_extender_2_out = {{16{IR[15]}}, IR[15:0]};  // Bit_Extender bit_extender_2
  Decoder #(.select(2), .tristate("false"), .disabled("Z"), .enable("false")) decoder_1 (
    .out1(decoder_1_out1), .out2(decoder_1_out2), .out3(decoder_1_out3), .sel(register_1_q));  // open: out0
  Multiplexer #(.select(1), .width(5), .disabled("Z"), .enable("false")) multiplexer_5 (
    .in0(IR[25:21]), .in1(5'b00010), .out(multiplexer_5_out), .sel(Syscall));
  Multiplexer #(.select(1), .width(5), .disabled("Z"), .enable("false")) multiplexer_6 (
    .in0(IR[20:16]), .in1(5'b00100), .out(multiplexer_6_out), .sel(Syscall));
  Multiplexer #(.select(1), .width(5), .disabled("Z"), .enable("false")) multiplexer_7 (
    .in0(multiplexer_4_out), .in1({5{1'b1}}), .out(multiplexer_7_out), .sel(JAL));
  and and_7 (Rst1, decoder_1_out1, ERET);
  and and_8 (Rst2, decoder_1_out2, ERET);
  and and_9 (Rst3, decoder_1_out3, ERET);
  Multiplexer #(.select(1), .width(32), .disabled("Z"), .enable("false")) multiplexer_8 (
    .in0(adder_1_out), .in1(multiplexer_13_out), .out(RDin), .sel(not_2_out));
  Multiplexer #(.select(1), .width(32), .disabled("Z"), .enable("false")) multiplexer_9 (
    .in0(bit_extender_1_out), .in1(bit_extender_2_out), .out(multiplexer_9_out), .sel(SignedExt));
  MIPS_Regifile mips_regifile_1 (
    .Din(RDin), .Clk(CLK), .R1(v0), .R2(MDin), .WE(RegWrite), .W_num(multiplexer_7_out),
    .R1_num(multiplexer_5_out), .R2_num(multiplexer_6_out));
  Multiplexer #(.select(1), .width(32), .disabled("Z"), .enable("false")) multiplexer_10 (
    .in0(MDin), .in1(multiplexer_9_out), .out(multiplexer_10_out), .sel(\单周期硬布线控制器_1_alu_src ));
  Multiplexer #(.select(1), .width(32), .disabled("Z"), .enable("false")) multiplexer_11 (
    .in0(multiplexer_10_out), .in1({32{1'b0}}), .out(multiplexer_11_out), .sel(BGEZ));
  Multiplexer #(.select(1), .width(5), .disabled("Z"), .enable("false")) multiplexer_12 (
    .in0(IR[10:6]), .in1(v0[4:0]), .out(multiplexer_12_out), .sel(or_12_out));
  Shifter #(.width(32), .shift("ll")) shifter_1 (.in(multiplexer_9_out), .\dist (5'b00010), .out(shifter_1_out));
  Comparator #(.width(32), .mode("twosComplement")) comparator_5 (
    .a(v0), .b(32'h22), .eq(comparator_5_eq));  // open: gt, lt
  MIPS_ALU mips_alu_1 (
    .X(v0), .Y(multiplexer_11_out), .AluOP(\单周期硬布线控制器_1_alu_op ), .Equal(mips_alu_1_equal),
    .Result(mips_alu_1_result), .shamt(multiplexer_12_out));  // open: Result_2
  or or_12 (or_12_out, SRAV, SLLV);
  Adder #(.width(32)) adder_2 (.a(shifter_1_out), .b(adder_1_out), .out(adder_2_out));  // open: cin, cout
  not not_3 (not_3_out, comparator_5_eq);
  and and_10 (and_10_out, BGEZ, ~mips_alu_1_result[0]);  // AND_Gate
  and and_11 (and_11_out, mips_alu_1_equal, \单周期硬布线控制器_1_beq );
  and and_12 (and_12_out, ~mips_alu_1_equal, \单周期硬布线控制器_1_bne );  // AND_Gate
  Register #(.width(32), .trigger("falling"), .Select("low")) register_2 (
    .D(MDin), .Q(LedData), .clk(and_13_out));  // open: en, clr
  and and_13 (and_13_out, comparator_5_eq, Syscall);
  and and_14 (and_14_out, Syscall, not_3_out);
  or or_13 (Branch, and_10_out, and_11_out, and_12_out);
  not not_4 (not_4_out, Halt);
  Multiplexer #(.select(1), .width(32), .disabled("Z"), .enable("false")) multiplexer_13 (
    .in0(multiplexer_14_out), .in1(bit_extender_3_out), .out(multiplexer_13_out), .sel(LBU));
  Register #(.width(1), .trigger("rising"), .Select("low")) register_3 (
    .D(and_14_out), .en(and_14_out), .Q(Halt), .clk(CLK), .clr(Go));
  Multiplexer #(.select(1), .width(32), .disabled("Z"), .enable("false")) multiplexer_14 (
    .in0(mips_alu_1_result), .in1(ram_1_data), .out(multiplexer_14_out), .sel(\单周期硬布线控制器_1_memtoreg ));
  RAM #(.addrWidth(10), .dataWidth(32), .bus("separate"), .Select("high")) ram_1 (
    .addr(mips_alu_1_result[11:2]), .din(MDin), .data(ram_1_data), .str(MemWrite), .sel(not_4_out), .clk(CLK));  // open: ld, clr
  assign bit_extender_3_out = {{24{1'b0}}, multiplexer_14_out[7:0]};  // Bit_Extender bit_extender_3

  // Other names for the same wires on the sheet: a0[31:0] = MDin

  // Notes on the sheet:
  //   中断源
  //   中断等待指示
  //   总复位信号应将除ROM以外所有存储组件全部清零
  //   单级中断测试信号模拟器
  //   数码管输出
  //   Reset 
  //   Reset 
  //   Reset 
  //   数码管输出应该用寄存器锁存，否则显示数据只能一闪而过
  //   指令存储器
  //   contents of rom_1 (hex, n*v repeats v):
  //   201d07d0 20100001 109fc0 139fc3 8021 2012000c 24160008 26100001 3210000f 20080008 20090001 139900
  //   2709825 132020 20020022 c 1094022 1500fff9 22100001 2018000f 2188024 108700 20080008 20090001 139902
  //   2709825 132021 20020022 c 1094022 1500fff9 108702 2c9b022 12c00001 8000c07 4020 1084027 84400
  //   3508ffff 82021 20020022 c 8000c01 afa20000 23bd0004 afa40000 23bd0004 afb00000 23bd0004 afb30000
  //   23bd0004 afb40000 23bd0004 afb50000 23bd0004 afb60000 23bd0004 20160001 20140003 20150001 168020
  //   108100 2149825 132020 20020022 c 1600fffa 295a022 1680fff7 23bdfffc 8fb60000 23bdfffc 8fb50000
  //   23bdfffc 8fb40000 23bdfffc 8fb30000 23bdfffc 8fb00000 23bdfffc 8fa40000 23bdfffc 8fa20000 42000018
  //   afa20000 23bd0004 afa40000 23bd0004 afb00000 23bd0004 afb30000 23bd0004 afb40000 23bd0004 afb50000
  //   23bd0004 afb60000 23bd0004 20160002 20140003 20150001 168020 108100 2149825 132020 20020022 c
  //   1600fffa 295a022 1680fff7 23bdfffc 8fb60000 23bdfffc 8fb50000 23bdfffc 8fb40000 23bdfffc 8fb30000
  //   23bdfffc 8fb00000 23bdfffc 8fa40000 23bdfffc 8fa20000 42000018 afa20000 23bd0004 afa40000 23bd0004
  //   afb00000 23bd0004 afb30000 23bd0004 afb40000 23bd0004 afb50000 23bd0004 afb60000 23bd0004 20160003
  //   20140003 20150001 168020 108100 2149825 132020 20020022 c 1600fffa 295a022 1680fff7 23bdfffc
  //   8fb60000 23bdfffc 8fb50000 23bdfffc 8fb40000 23bdfffc 8fb30000 23bdfffc 8fb00000 23bdfffc 8fa40000
  //   23bdfffc 8fa20000 42000018
  //   为方便自动评测，需要输出PC，IR，寄存器堆写如数据RDin
  //   指令字
  //   RAM写使能MemWrite、RAM写入数据MDin等信号
  //   JMP
  //   JR
  //   OP
  //   OP
  //   Func
  //   Func
  //   rs
  //   rt
  //   rd
  //   Beq
  //   Bne
  //   MemToReg
  //   MemWrite
  //   AluOP
  //   AluSrcB
  //   RegWrite
  //   JAL
  //   RegDst
  //   Syscall
  //   清零
endmodule

module \单周期MIPS_多级中断  (
  input  IR1,
  input  IR2,
  input  IR3,
  output RegWrite,
  output MemWrite,
  output [31:0] PC,
  output [31:0] IR,
  output [31:0] RDin,
  output [31:0] MDin,
  output [31:0] LedData
);

  wire and_1_out, and_2_out, and_3_out, and_4_out, and_5_out, and_10_out, and_11_out, and_12_out, and_13_out,
       and_14_out, BGEZ, Branch, CLK, comparator_1_eq, comparator_2_eq, comparator_3_eq, comparator_4_eq,
       comparator_5_eq, comparator_6_gt, comparator_7_eq, d_ff_1_q, d_ff_2_q, d_ff_3_q, decoder_1_out1,
       decoder_1_out2, decoder_1_out3, ERET, Go, Halt, IE_Ctrl, IE_q, IR1_t, ir1_t_t, IR2_t, ir2_t_t, IR3_t,
       ir3_t_t, IRA, IRB, IRC, JAL, JMP, JR, LBU, MFC0, mips_alu_1_equal, MTC0, nor_1_out, not_1_out,
       not_2_out, not_3_out, not_4_out, or_4_out, or_5_out, or_6_out, or_7_out, or_8_out, or_10_out,
       or_12_out, or_13_out, or_15_out, priority_encoder_1_gs, Rst1, Rst2, Rst3, SignedExt, SLLV, SRAV,
       Syscall, W1, W2, W3, \单周期硬布线控制器_1_alu_src , \单周期硬布线控制器_1_beq , \单周期硬布线控制器_1_bne ,
       \单周期硬布线控制器_1_memtoreg , \单周期硬布线控制器_1_regdst ;
  wire [1:0] multiplexer_2_out, multiplexer_6_out, multiplexer_8_out, register_2_q, register_3_q, \当前中断号 ,
       \当前最优中断号 ;
  wire [3:0] \单周期硬布线控制器_1_alu_op ;
  wire [4:0] multiplexer_10_out, multiplexer_11_out, multiplexer_12_out, multiplexer_13_out,
       multiplexer_18_out;
  wire [15:0] \总周期数 ;
  wire [31:0] adder_1_out, adder_2_out, bit_extender_1_out, bit_extender_2_out, bit_extender_3_out, EPC,
       EPC2_q, EPC3_q, mips_alu_1_result, multiplexer_1_out, multiplexer_3_out, multiplexer_4_out,
       multiplexer_7_out, multiplexer_9_out, multiplexer_15_out, multiplexer_16_out, multiplexer_17_out,
       multiplexer_19_out, multiplexer_20_out, Prev_PC, ram_1_data, shifter_1_out, v0, \中断入口地址 ;

  Clock #(.highDuration(1), .lowDuration(1)) clock_1 (.out(CLK));
  Button _1 ();  // open: out
  Button _2 ();  // open: out
  Button _3 ();  // open: out
  Button \u_继续运行  (.out(Go));
  LED #(.active("true")) led_1 (.in(W1));
  LED #(.active("true")) led_2 (.in(W2));
  LED #(.active("true")) led_3 (.in(W3));
  or or_1 (W1, ir1_t_t, d_ff_1_q);
  or or_2 (W2, ir2_t_t, d_ff_2_q);
  or or_3 (W3, ir3_t_t, d_ff_3_q);
  Hex_Digit_Display hex_digit_display_1 (.value(LedData[31:28]));  // open: dp
  Comparator #(.width(16), .mode("twosComplement")) comparator_1 (
    .a(16'h258), .b(\总周期数 ), .eq(comparator_1_eq));  // open: gt, lt
  Comparator #(.width(16), .mode("twosComplement")) comparator_2 (
    .a(\总周期数 ), .b(16'h1), .eq(comparator_2_eq));  // open: gt, lt
  Comparator #(.width(16), .mode("twosComplement")) comparator_3 (
    .a(\总周期数 ), .b(16'h4), .eq(comparator_3_eq));  // open: gt, lt
  Comparator #(.width(16), .mode("twosComplement")) comparator_4 (
    .a(\总周期数 ), .b(16'h7), .eq(comparator_4_eq));  // open: gt, lt
  Comparator #(.width(16), .mode("twosComplement")) comparator_5 (
    .a(\总周期数 ), .b(16'h241), .eq(comparator_5_eq));  // open: gt, lt
  D_Flip_Flop #(.trigger("rising"), .Pre_Clr_Positions("LEGACY"), .NegatePresetClear("false"), .enable("true"), .NewFFLayout("false")) d_ff_1 (
    .clk(IRA), .D(1'b1), .Q(d_ff_1_q), .reset(ir1_t_t));  // open: Qn, preset, en
  D_Flip_Flop #(.trigger("rising"), .Pre_Clr_Positions("LEGACY"), .NegatePresetClear("false"), .enable("true"), .NewFFLayout("false")) d_ff_2 (
    .clk(IRB), .D(1'b1), .Q(d_ff_2_q), .reset(ir2_t_t));  // open: Qn, preset, en
  D_Flip_Flop #(.trigger("rising"), .Pre_Clr_Positions("LEGACY"), .NegatePresetClear("false"), .enable("true"), .NewFFLayout("false")) d_ff_3 (
    .clk(IRC), .D(1'b1), .Q(d_ff_3_q), .reset(ir3_t_t));  // open: Qn, preset, en
  Hex_Digit_Display hex_digit_display_2 (.value(LedData[27:24]));  // open: dp
  Hex_Digit_Display hex_digit_display_3 (.value(LedData[23:20]));  // open: dp
  or or_4 (or_4_out, comparator_1_eq, comparator_2_eq);
  assign IRA = or_4_out ? ~CLK : 1'bz;  // Controlled_Inverter controlled_inverter_1
  assign IRB = comparator_3_eq ? ~CLK : 1'bz;  // Controlled_Inverter controlled_inverter_2
  or or_5 (or_5_out, comparator_4_eq, comparator_5_eq);
  assign IRC = or_5_out ? ~CLK : 1'bz;  // Controlled_Inverter controlled_inverter_3
  or or_6 (or_6_out, d_ff_1_q, ir1_t_t);
  and and_1 (and_1_out, or_6_out, ~Rst1);  // AND_Gate
  or or_7 (or_7_out, d_ff_2_q, ir2_t_t);
  and and_2 (and_2_out, or_7_out, ~Rst2);  // AND_Gate
  or or_8 (or_8_out, d_ff_3_q, ir3_t_t);
  and and_3 (and_3_out, or_8_out, ~Rst3);  // AND_Gate
  Hex_Digit_Display hex_digit_display_4 (.value(LedData[19:16]));  // open: dp
  Hex_Digit_Display hex_digit_display_5 (.value(LedData[15:12]));  // open: dp
  Pull_Resistor #(.pull(0)) pull_resistor_1 (.node(IRA));
  Pull_Resistor #(.pull(0)) pull_resistor_2 (.node(IRB));
  Pull_Resistor #(.pull(0)) pull_resistor_3 (.node(IRC));
  D_Flip_Flop #(.trigger("rising"), .Pre_Clr_Positions("LEGACY"), .NegatePresetClear("false"), .enable("true"), .NewFFLayout("false")) u_IR1 (
    .clk(CLK), .D(and_1_out), .Q(ir1_t_t));  // open: Qn, preset, en, reset
  D_Flip_Flop #(.trigger("rising"), .Pre_Clr_Positions("LEGACY"), .NegatePresetClear("false"), .enable("true"), .NewFFLayout("false")) u_IR2 (
    .clk(CLK), .D(and_2_out), .Q(ir2_t_t));  // open: Qn, preset, en, reset
  D_Flip_Flop #(.trigger("rising"), .Pre_Clr_Positions("LEGACY"), .NegatePresetClear("false"), .enable("true"), .NewFFLayout("false")) u_IR3 (
    .clk(CLK), .D(and_3_out), .Q(ir3_t_t));  // open: Qn, preset, en, reset
  Hex_Digit_Display hex_digit_display_6 (.value(LedData[11:8]));  // open: dp
  Hex_Digit_Display hex_digit_display_7 (.value(LedData[7:4]));  // open: dp
  // Probe on \总周期数 
  Hex_Digit_Display hex_digit_display_8 (.value(LedData[3:0]));  // open: dp
  and and_4 (and_4_out, JMP, ~JR);  // AND_Gate
  nor nor_1 (nor_1_out, Branch, JMP);
  or or_9 (IR1_t, IR1, IRA);
  assign Prev_PC = JR ? v0 : 32'bz;  // Controlled_Buffer controlled_buffer_1
  assign Prev_PC = and_4_out ? {PC[31:28], IR[25:0], 2'b00} : 32'bz;  // Controlled_Buffer controlled_buffer_2
  assign Prev_PC = Branch ? adder_2_out : 32'bz;  // Controlled_Buffer controlled_buffer_3
  assign Prev_PC = nor_1_out ? adder_1_out : 32'bz;  // Controlled_Buffer controlled_buffer_4
  or or_10 (or_10_out, ERET, IE_Ctrl);
  or or_11 (IR2_t, IR2, IRB);
  Multiplexer #(.select(1), .width(32), .disabled("Z"), .enable("false")) multiplexer_1 (
    .in0(Prev_PC), .in1(\中断入口地址 ), .out(multiplexer_1_out), .sel(IE_Ctrl));
  or or_12 (or_12_out, ERET, MFC0, MTC0, IE_Ctrl);
  Multiplexer #(.select(1), .width(2), .disabled("Z"), .enable("false")) multiplexer_2 (
    .in0(\当前最优中断号 ), .in1(register_2_q), .out(multiplexer_2_out), .sel(ERET));
  Multiplexer #(.select(1), .width(32), .disabled("Z"), .enable("false")) multiplexer_3 (
    .in0(Prev_PC), .in1(EPC2_q), .out(multiplexer_3_out), .sel(ERET));
  Multiplexer #(.select(1), .width(32), .disabled("Z"), .enable("false")) multiplexer_4 (
    .in0(multiplexer_1_out), .in1(EPC), .out(multiplexer_4_out), .sel(ERET));
  not not_1 (not_1_out, Halt);
  Priority_Encoder #(.select(2), .disabled("Z")) priority_encoder_1 (
    .in0(1'b1), .in1(ir1_t_t), .in2(ir2_t_t), .in3(ir3_t_t), .out(\当前最优中断号 ), .gs(priority_encoder_1_gs));  // open: en_out, en_in
  Multiplexer #(.select(2), .width(32), .disabled("Z"), .enable("true")) multiplexer_5 (
    .in1(32'h30ac), .in2(32'h3158), .in3(32'h3204), .out(\中断入口地址 ), .sel(\当前最优中断号 ),
    .en(priority_encoder_1_gs));  // open: in0
  or or_13 (or_13_out, MTC0, IE_Ctrl);
  Register #(.width(1), .trigger("rising"), .Select("low")) IE (
    .D(or_13_out), .en(or_12_out), .Q(IE_q), .clk(CLK));  // open: clr
  Comparator #(.width(2), .mode("unsigned")) comparator_6 (
    .a(\当前最优中断号 ), .b(\当前中断号 ), .gt(comparator_6_gt));  // open: eq, lt
  Register #(.width(2), .trigger("rising"), .Select("low")) register_1 (
    .D(multiplexer_2_out), .en(or_10_out), .Q(\当前中断号 ), .clk(CLK));  // open: clr
  Register #(.width(32), .trigger("rising"), .Select("low")) EPC1 (
    .D(multiplexer_3_out), .en(or_10_out), .Q(EPC), .clk(CLK));  // open: clr
  or or_14 (IR3_t, IR3, IRC);
  and and_5 (and_5_out, ~Halt, CLK);  // AND_Gate
  Register #(.width(32), .trigger("rising"), .Select("low")) u_PC (
    .D(multiplexer_4_out), .en(not_1_out), .Q(PC), .clk(CLK));  // open: clr
  and and_6 (IE_Ctrl, ~IE_q, comparator_6_gt);  // AND_Gate
  Multiplexer #(.select(1), .width(2), .disabled("Z"), .enable("false")) multiplexer_6 (
    .in0(\当前中断号 ), .in1(register_3_q), .out(multiplexer_6_out), .sel(ERET));
  Multiplexer #(.select(1), .width(32), .disabled("Z"), .enable("false")) multiplexer_7 (
    .in0(EPC), .in1(EPC3_q), .out(multiplexer_7_out), .sel(ERET));
  Counter #(.width(16), .max('hffff), .ongoal("wrap"), .trigger("rising"), .behavior("new")) counter_1 (
    .Q(\总周期数 ), .clk(and_5_out));  // open: load, D, count, carry, clr, preset, down
  Decoder #(.select(2), .tristate("false"), .disabled("Z"), .enable("false")) decoder_1 (
    .out1(decoder_1_out1), .out2(decoder_1_out2), .out3(decoder_1_out3), .sel(\当前最优中断号 ));  // open: out0
  Register #(.width(2), .trigger("rising"), .Select("low")) register_2 (
    .D(multiplexer_6_out), .en(or_10_out), .Q(register_2_q), .clk(CLK));  // open: clr
  Register #(.width(32), .trigger("rising"), .Select("low")) EPC2 (
    .D(multiplexer_7_out), .en(or_10_out), .Q(EPC2_q), .clk(CLK));  // open: clr
  ROM #(.addrWidth(10), .dataWidth(32), .Select("high")) rom_1 (.addr(PC[11:2]), .data(IR));
  Adder #(.width(32)) adder_1 (.a(PC), .b(32'h4), .out(adder_1_out));  // open: cin, cout
  and and_7 (Rst1, decoder_1_out1, ERET);
  and and_8 (Rst2, decoder_1_out2, ERET);
  and and_9 (Rst3, decoder_1_out3, ERET);
  Multiplexer #(.select(1), .width(2), .disabled("Z"), .enable("false")) multiplexer_8 (
    .in0(register_2_q), .in1(2'b00), .out(multiplexer_8_out), .sel(ERET));
  Multiplexer #(.select(1), .width(32), .disabled("Z"), .enable("false")) multiplexer_9 (
    .in0(EPC2_q), .in1({32{1'b0}}), .out(multiplexer_9_out), .sel(ERET));
  // Mips_Probe mips_probe_1: pin names not known; wires that end beside it: IR
  Register #(.width(2), .trigger("rising"), .Select("low")) register_3 (
    .D(multiplexer_8_out), .en(or_10_out), .Q(register_3_q), .clk(CLK));  // open: clr
  Register #(.width(32), .trigger("rising"), .Select("low")) EPC3 (
    .D(multiplexer_9_out), .en(or_10_out), .Q(EPC3_q), .clk(CLK));  // open: clr
  \单周期硬布线控制器  \u_单周期硬布线控制器_1  (
    .Func(IR[5:0]), .OP(IR[31:26]), .ALU_OP(\单周期硬布线控制器_1_alu_op ), .MemToReg(\单周期硬布线控制器_1_memtoreg ),
    .MemWrite(MemWrite), .ALU_SRC(\单周期硬布线控制器_1_alu_src ), .RegWrite(RegWrite), .SysCALL(Syscall),
    .SignedExt(SignedExt), .RegDst(\单周期硬布线控制器_1_regdst ), .JR(JR), .JMP(JMP), .Beq(\单周期硬布线控制器_1_beq ),
    .JAL(JAL), .Bne(\单周期硬布线控制器_1_bne ), .SLLV(SLLV), .SRAV(SRAV), .BGEZ(BGEZ), .LBU(LBU), .ERET(ERET),
    .MFC0(MFC0), .MTC0(MTC0), .in_3(IR[25:21]));
  Multiplexer #(.select(1), .width(5), .disabled("Z"), .enable("false")) multiplexer_10 (
    .in0(IR[20:16]), .in1(IR[15:11]), .out(multiplexer_10_out), .sel(\单周期硬布线控制器_1_regdst ));
  not not_2 (not_2_out, JAL);
  assign bit_extender_1_out = {{16{1'b0}}, IR[15:0]};  // Bit_Extender bit_extender_1
  assign bit_extender_2_out = {{16{IR[15]}}, IR[15:0]};  // Bit_Extender bit_extender_2
  Comparator #(.width(32), .mode("twosComplement")) comparator_7 (
    .a(v0), .b(32'h22), .eq(comparator_7_eq));  // open: gt, lt
  Multiplexer #(.select(1), .width(5), .disabled("Z"), .enable("false")) multiplexer_11 (
    .in0(IR[25:21]), .in1(5'b00010), .out(multiplexer_11_out), .sel(Syscall));
  Multiplexer #(.select(1), .width(5), .disabled("Z"), .enable("false")) multiplexer_12 (
    .in0(IR[20:16]), .in1(5'b00100), .out(multiplexer_12_out), .sel(Syscall));
  Multiplexer #(.select(1), .width(5), .disabled("Z"), .enable("false")) multiplexer_13 (
    .in0(multiplexer_10_out), .in1({5{1'b1}}), .out(multiplexer_13_out), .sel(JAL));
  and and_10 (and_10_out, comparator_7_eq, Syscall);
  and and_11 (and_11_out, Syscall, not_3_out);
  not not_3 (not_3_out, comparator_7_eq);
  Multiplexer #(.select(1), .width(32), .disabled("Z"), .enable("false")) multiplexer_14 (
    .in0(adder_1_out), .in1(multiplexer_19_out), .out(RDin), .sel(not_2_out));
  Multiplexer #(.select(1), .width(32), .disabled("Z"), .enable("false")) multiplexer_15 (
    .in0(bit_extender_1_out), .in1(bit_extender_2_out), .out(multiplexer_15_out), .sel(SignedExt));
  Register #(.width(32), .trigger("falling"), .Select("low")) register_4 (
    .D(MDin), .Q(LedData), .clk(and_10_out));  // open: en, clr
  MIPS_Regifile mips_regifile_1 (
    .Din(RDin), .Clk(CLK), .R1(v0), .R2(MDin), .WE(RegWrite), .W_num(multiplexer_13_out),
    .R1_num(multiplexer_11_out), .R2_num(multiplexer_12_out));
  Register #(.width(1), .trigger("rising"), .Select("low")) register_5 (
    .D(and_11_out), .en(and_11_out), .Q(Halt), .clk(CLK), .clr(Go));
  Multiplexer #(.select(1), .width(32), .disabled("Z"), .enable("false")) multiplexer_16 (
    .in0(MDin), .in1(multiplexer_15_out), .out(multiplexer_16_out), .sel(\单周期硬布线控制器_1_alu_src ));
  Multiplexer #(.select(1), .width(32), .disabled("Z"), .enable("false")) multiplexer_17 (
    .in0(multiplexer_16_out), .in1({32{1'b0}}), .out(multiplexer_17_out), .sel(BGEZ));
  Multiplexer #(.select(1), .width(5), .disabled("Z"), .enable("false")) multiplexer_18 (
    .in0(IR[10:6]), .in1(v0[4:0]), .out(multiplexer_18_out), .sel(or_15_out));
  Shifter #(.width(32), .shift("ll")) shifter_1 (.in(multiplexer_15_out), .\dist (5'b00010), .out(shifter_1_out));
  MIPS_ALU mips_alu_1 (
    .X(v0), .Y(multiplexer_17_out), .AluOP(\单周期硬布线控制器_1_alu_op ), .Equal(mips_alu_1_equal),
    .Result(mips_alu_1_result), .shamt(multiplexer_18_out));  // open: Result_2
  or or_15 (or_15_out, SRAV, SLLV);
  Adder #(.width(32)) adder_2 (.a(shifter_1_out), .b(adder_1_out), .out(adder_2_out));  // open: cin, cout
  and and_12 (and_12_out, BGEZ, ~mips_alu_1_result[0]);  // AND_Gate
  and and_13 (and_13_out, mips_alu_1_equal, \单周期硬布线控制器_1_beq );
  and and_14 (and_14_out, ~mips_alu_1_equal, \单周期硬布线控制器_1_bne );  // AND_Gate
  or or_16 (Branch, and_12_out, and_13_out, and_14_out);
  not not_4 (not_4_out, Halt);
  Multiplexer #(.select(1), .width(32), .disabled("Z"), .enable("false")) multiplexer_19 (
    .in0(multiplexer_20_out), .in1(bit_extender_3_out), .out(multiplexer_19_out), .sel(LBU));
  Multiplexer #(.select(1), .width(32), .disabled("Z"), .enable("false")) multiplexer_20 (
    .in0(mips_alu_1_result), .in1(ram_1_data), .out(multiplexer_20_out), .sel(\单周期硬布线控制器_1_memtoreg ));
  RAM #(.addrWidth(10), .dataWidth(32), .bus("separate"), .Select("high")) ram_1 (
    .addr(mips_alu_1_result[11:2]), .din(MDin), .data(ram_1_data), .str(MemWrite), .sel(not_4_out), .clk(CLK));  // open: ld, clr
  assign bit_extender_3_out = {{24{1'b0}}, multiplexer_20_out[7:0]};  // Bit_Extender bit_extender_3

  // Other names for the same wires on the sheet: a0[31:0] = MDin

  // Notes on the sheet:
  //   中断源
  //   中断等待指示
  //   总复位信号应将除ROM以外所有存储组件全部清零
  //   多级中断信号产生
  //   数码管输出
  //   Reset 
  //   Reset 
  //   Reset 
  //   数码管输出应该用寄存器锁存，否则显示数据只能一闪而过
  //   指令存储器
  //   contents of rom_1 (hex, n*v repeats v):
  //   201d07d0 20100001 109fc0 139fc3 8021 2012000c 24160008 26100001 3210000f 20080008 20090001 139900
  //   2709825 132020 20020022 c 1094022 1500fff9 22100001 2018000f 2188024 108700 20080008 20090001 139902
  //   2709825 132021 20020022 c 1094022 1500fff9 108702 2c9b022 12c00001 8000c07 4020 1084027 84400
  //   3508ffff 82021 20020022 c 8000c01 afa20000 23bd0004 afa40000 23bd0004 afb00000 23bd0004 afb30000
  //   23bd0004 afb40000 23bd0004 afb50000 23bd0004 afb60000 23bd0004 40000000 20160001 20140003 20150001
  //   168020 108100 2149825 132020 20020022 c 1600fffa 295a022 1680fff7 40800000 23bdfffc 8fb60000
  //   23bdfffc 8fb50000 23bdfffc 8fb40000 23bdfffc 8fb30000 23bdfffc 8fb00000 23bdfffc 8fa40000 23bdfffc
  //   8fa20000 42000018 afa20000 23bd0004 afa40000 23bd0004 afb00000 23bd0004 afb30000 23bd0004 afb40000
  //   23bd0004 afb50000 23bd0004 afb60000 23bd0004 40000000 20160002 20140003 20150001 168020 108100
  //   2149825 132020 20020022 c 1600fffa 295a022 1680fff7 40800000 23bdfffc 8fb60000 23bdfffc 8fb50000
  //   23bdfffc 8fb40000 23bdfffc 8fb30000 23bdfffc 8fb00000 23bdfffc 8fa40000 23bdfffc 8fa20000 42000018
  //   afa20000 23bd0004 afa40000 23bd0004 afb00000 23bd0004 afb30000 23bd0004 afb40000 23bd0004 afb50000
  //   23bd0004 afb60000 23bd0004 40000000 20160003 20140003 20150001 168020 108100 2149825 132020 20020022
  //   c 1600fffa 295a022 1680fff7 40800000 23bdfffc 8fb60000 23bdfffc 8fb50000 23bdfffc 8fb40000 23bdfffc
  //   8fb30000 23bdfffc 8fb00000 23bdfffc 8fa40000 23bdfffc 8fa20000 42000018
  //   为方便自动评测，需要输出PC，IR，寄存器堆写如数据RDin
  //   指令字
  //   RAM写使能MemWrite、RAM写入数据MDin等信号
  //   JMP
  //   JR
  //   OP
  //   OP
  //   Func
  //   Func
  //   rs
  //   rt
  //   rd
  //   Beq
  //   Bne
  //   MemToReg
  //   MemWrite
  //   AluOP
  //   AluSrcB
  //   RegWrite
  //   JAL
  //   RegDst
  //   Syscall
endmodule

module \封装正确性测试  (
);

  wire IR1, IR2, IR3, MemW, RegW;
  wire [31:0] EX_PC, ID_PC, IF_PC, IR, LED, MDin, MDinr, MEM_PC, PC, RDin, RDinr, WB_PC;

  \单周期MIPS  \u_单周期mips_1  (
    .RegWrite(RegW), .MemWrite(MemW), .PC(PC), .IR(IR), .RDin(RDin), .MDin(MDin), .LedData(LED));  // open: IR1, IR2, IR3
  \气泡流水线  \u_气泡流水线_1  (
    .RegWrite(RegW), .MemWrite(MemW), .IF_PC(IF_PC), .ID_PC(ID_PC), .EX_PC(EX_PC), .M_PC(MEM_PC),
    .WB_PC(WB_PC), .RDin(RDinr), .MDin(MDinr), .LedData(LED));
  \单周期MIPS_单级中断  \u_单周期mips_单级中断_1  (
    .IR1(IR1), .IR2(IR2), .IR3(IR3), .RegWrite(RegW), .MemWrite(MemW), .PC(PC), .IR(IR), .RDin(RDin),
    .MDin(MDin), .LedData(LED));
  \理想流水线  \u_理想流水线_1  (
    .RegWrite(RegW), .MemWrite(MemW), .IF_PC(IF_PC), .ID_PC(ID_PC), .EX_PC(EX_PC), .M_PC(MEM_PC),
    .WB_PC(WB_PC), .RDin(RDinr), .MDin(MDinr), .LedData(LED));
  \重定向流水线  \u_重定向流水线_1  (
    .RegWrite(RegW), .MemWrite(MemW), .IF_PC(IF_PC), .ID_PC(ID_PC), .EX_PC(EX_PC), .M_PC(MEM_PC),
    .WB_PC(WB_PC), .RDin(RDinr), .MDin(MDinr), .LedData(LED));
  \单周期MIPS_多级中断  \u_单周期mips_多级中断_1  (
    .IR1(IR1), .IR2(IR2), .IR3(IR3), .RegWrite(RegW), .MemWrite(MemW), .PC(PC), .IR(IR), .RDin(RDin),
    .MDin(MDin), .LedData(LED));

  // Notes on the sheet:
  //   单周期封装测试
  //   气泡流水封装测试
  //   单周期+单级中断封装测试
  //   请检查上面封装有无位宽不匹配，引脚标签是否和连接的标签相对应，否则无法在educoder平台上正确测试
  //   理想流水封装测试
  //   重定向流水封装测试
  //   单周期+多级中断封装测试
endmodule

module \理想ID_EX  (
  input  RegDst_in,
  input  Beq_in,
  input  [31:0] IR_in,
  input  Syscall_in,
  input  Bne_in,
  input  [31:0] PC_in,
  input  JMP_in,
  input  MemToReg_in,
  input  [31:0] A_in,
  input  JR_in,
  input  [3:0] AluOP_in,
  input  SignedExt_in,
  input  AluSrcB_in,
  input  [31:0] B_in,
  input  SLLV_in,
  input  RegWrite_in,
  input  [31:0] Imm_in,
  input  SRAV_in,
  input  JAL_in,
  input  LBU_in,
  input  [4:0] Shamt,
  input  MemWrite,
  input  BGEZ_in,
  input  CLK,
  input  CLR,
  input  Stall,
  output RegDst_out,
  output Beq_out,
  output [31:0] IR_out,
  output Syscall_out,
  output Bne_out,
  output [31:0] PC_out,
  output JMP_out,
  output MemToReg_out,
  output [31:0] A_out,
  output JR_out,
  output [3:0] AluOP_out,
  output SignedExt_out,
  output AluSrcB_out,
  output [31:0] B_out,
  output SLLV_out,
  output RegWrite_out,
  output [31:0] Imm_out,
  output SRAV_out,
  output JAL_out,
  output LBU_out,
  output [4:0] Shamt_2,
  output MemWrite_2,
  output BGEZ_out
);

  wire multiplexer_1_out, multiplexer_2_out, multiplexer_3_out, multiplexer_4_out, multiplexer_5_out,
       multiplexer_6_out, multiplexer_7_out, multiplexer_8_out, multiplexer_9_out, multiplexer_10_out,
       multiplexer_11_out, multiplexer_12_out, multiplexer_14_out, multiplexer_15_out, multiplexer_16_out,
       multiplexer_17_out, pull_resistor_2_node;
  wire [3:0] multiplexer_13_out;
  wire [4:0] multiplexer_23_out;
  wire [31:0] multiplexer_18_out, multiplexer_19_out, multiplexer_20_out, multiplexer_21_out,
       multiplexer_22_out;

  Pull_Resistor #(.pull(0)) pull_resistor_1 (.node(CLR));
  Multiplexer #(.select(1), .width(1), .disabled("Z"), .enable("false")) multiplexer_1 (
    .in0(RegDst_in), .in1(1'b0), .out(multiplexer_1_out), .sel(CLR));
  Multiplexer #(.select(1), .width(1), .disabled("Z"), .enable("false")) multiplexer_2 (
    .in0(Syscall_in), .in1(1'b0), .out(multiplexer_2_out), .sel(CLR));
  Multiplexer #(.select(1), .width(1), .disabled("Z"), .enable("false")) multiplexer_3 (
    .in0(JMP_in), .in1(1'b0), .out(multiplexer_3_out), .sel(CLR));
  Multiplexer #(.select(1), .width(1), .disabled("Z"), .enable("false")) multiplexer_4 (
    .in0(JR_in), .in1(1'b0), .out(multiplexer_4_out), .sel(CLR));
  Multiplexer #(.select(1), .width(1), .disabled("Z"), .enable("false")) multiplexer_5 (
    .in0(SignedExt_in), .in1(1'b0), .out(multiplexer_5_out), .sel(CLR));
  Multiplexer #(.select(1), .width(1), .disabled("Z"), .enable("false")) multiplexer_6 (
    .in0(SLLV_in), .in1(1'b0), .out(multiplexer_6_out), .sel(CLR));
  Multiplexer #(.select(1), .width(1), .disabled("Z"), .enable("false")) multiplexer_7 (
    .in0(SRAV_in), .in1(1'b0), .out(multiplexer_7_out), .sel(CLR));
  Multiplexer #(.select(1), .width(1), .disabled("Z"), .enable("false")) multiplexer_8 (
    .in0(LBU_in), .in1(1'b0), .out(multiplexer_8_out), .sel(CLR));
  Multiplexer #(.select(1), .width(1), .disabled("Z"), .enable("false")) multiplexer_9 (
    .in0(BGEZ_in), .in1(1'b0), .out(multiplexer_9_out), .sel(CLR));
  Register #(.width(1), .trigger("rising"), .Select("low")) register_1 (
    .D(multiplexer_1_out), .en(pull_resistor_2_node), .Q(RegDst_out), .clk(CLK));  // open: clr
  Register #(.width(1), .trigger("rising"), .Select("low")) register_2 (
    .D(multiplexer_2_out), .en(pull_resistor_2_node), .Q(Syscall_out), .clk(CLK));  // open: clr
  Register #(.width(1), .trigger("rising"), .Select("low")) register_3 (
    .D(multiplexer_3_out), .en(pull_resistor_2_node), .Q(JMP_out), .clk(CLK));  // open: clr
  Register #(.width(1), .trigger("rising"), .Select("low")) register_4 (
    .D(multiplexer_4_out), .en(pull_resistor_2_node), .Q(JR_out), .clk(CLK));  // open: clr
  Register #(.width(1), .trigger("rising"), .Select("low")) register_5 (
    .D(multiplexer_5_out), .en(pull_resistor_2_node), .Q(SignedExt_out), .clk(CLK));  // open: clr
  Register #(.width(1), .trigger("rising"), .Select("low")) register_6 (
    .D(multiplexer_6_out), .en(pull_resistor_2_node), .Q(SLLV_out), .clk(CLK));  // open: clr
  Register #(.width(1), .trigger("rising"), .Select("low")) register_7 (
    .D(multiplexer_7_out), .en(pull_resistor_2_node), .Q(SRAV_out), .clk(CLK));  // open: clr
  Register #(.width(1), .trigger("rising"), .Select("low")) register_8 (
    .D(multiplexer_8_out), .en(pull_resistor_2_node), .Q(LBU_out), .clk(CLK));  // open: clr
  Register #(.width(1), .trigger("rising"), .Select("low")) register_9 (
    .D(multiplexer_9_out), .en(pull_resistor_2_node), .Q(BGEZ_out), .clk(CLK));  // open: clr
  Pull_Resistor #(.pull(0)) pull_resistor_2 (.node(pull_resistor_2_node));
  not not_1 (pull_resistor_2_node, Stall);
  Multiplexer #(.select(1), .width(1), .disabled("Z"), .enable("false")) multiplexer_10 (
    .in0(Beq_in), .in1(1'b0), .out(multiplexer_10_out), .sel(CLR));
  Multiplexer #(.select(1), .width(1), .disabled("Z"), .enable("false")) multiplexer_11 (
    .in0(Bne_in), .in1(1'b0), .out(multiplexer_11_out), .sel(CLR));
  Multiplexer #(.select(1), .width(1), .disabled("Z"), .enable("false")) multiplexer_12 (
    .in0(MemToReg_in), .in1(1'b0), .out(multiplexer_12_out), .sel(CLR));
  Multiplexer #(.select(1), .width(4), .disabled("Z"), .enable("false")) multiplexer_13 (
    .in0(AluOP_in), .in1(4'b0000), .out(multiplexer_13_out), .sel(CLR));
  Multiplexer #(.select(1), .width(1), .disabled("Z"), .enable("false")) multiplexer_14 (
    .in0(AluSrcB_in), .in1(1'b0), .out(multiplexer_14_out), .sel(CLR));
  Multiplexer #(.select(1), .width(1), .disabled("Z"), .enable("false")) multiplexer_15 (
    .in0(RegWrite_in), .in1(1'b0), .out(multiplexer_15_out), .sel(CLR));
  Multiplexer #(.select(1), .width(1), .disabled("Z"), .enable("false")) multiplexer_16 (
    .in0(JAL_in), .in1(1'b0), .out(multiplexer_16_out), .sel(CLR));
  Multiplexer #(.select(1), .width(1), .disabled("Z"), .enable("false")) multiplexer_17 (
    .in0(MemWrite), .in1(1'b0), .out(multiplexer_17_out), .sel(CLR));
  Register #(.width(1), .trigger("rising"), .Select("low")) register_10 (
    .D(multiplexer_10_out), .en(pull_resistor_2_node), .Q(Beq_out), .clk(CLK));  // open: clr
  Register #(.width(1), .trigger("rising"), .Select("low")) register_11 (
    .D(multiplexer_11_out), .en(pull_resistor_2_node), .Q(Bne_out), .clk(CLK));  // open: clr
  Register #(.width(1), .trigger("rising"), .Select("low")) register_12 (
    .D(multiplexer_12_out), .en(pull_resistor_2_node), .Q(MemToReg_out), .clk(CLK));  // open: clr
  Register #(.width(4), .trigger("rising"), .Select("low")) register_13 (
    .D(multiplexer_13_out), .en(pull_resistor_2_node), .Q(AluOP_out), .clk(CLK));  // open: clr
  Register #(.width(1), .trigger("rising"), .Select("low")) register_14 (
    .D(multiplexer_14_out), .en(pull_resistor_2_node), .Q(AluSrcB_out), .clk(CLK));  // open: clr
  Register #(.width(1), .trigger("rising"), .Select("low")) register_15 (
    .D(multiplexer_15_out), .en(pull_resistor_2_node), .Q(RegWrite_out), .clk(CLK));  // open: clr
  Register #(.width(1), .trigger("rising"), .Select("low")) register_16 (
    .D(multiplexer_16_out), .en(pull_resistor_2_node), .Q(JAL_out), .clk(CLK));  // open: clr
  Register #(.width(1), .trigger("rising"), .Select("low")) register_17 (
    .D(multiplexer_17_out), .en(pull_resistor_2_node), .Q(MemWrite_2), .clk(CLK));  // open: clr
  Multiplexer #(.select(1), .width(32), .disabled("Z"), .enable("false")) multiplexer_18 (
    .in0(IR_in), .in1({32{1'b0}}), .out(multiplexer_18_out), .sel(CLR));
  Multiplexer #(.select(1), .width(32), .disabled("Z"), .enable("false")) multiplexer_19 (
    .in0(PC_in), .in1({32{1'b0}}), .out(multiplexer_19_out), .sel(CLR));
  Multiplexer #(.select(1), .width(32), .disabled("Z"), .enable("false")) multiplexer_20 (
    .in0(A_in), .in1({32{1'b0}}), .out(multiplexer_20_out), .sel(CLR));
  Multiplexer #(.select(1), .width(32), .disabled("Z"), .enable("false")) multiplexer_21 (
    .in0(B_in), .in1({32{1'b0}}), .out(multiplexer_21_out), .sel(CLR));
  Multiplexer #(.select(1), .width(32), .disabled("Z"), .enable("false")) multiplexer_22 (
    .in0(Imm_in), .in1({32{1'b0}}), .out(multiplexer_22_out), .sel(CLR));
  Multiplexer #(.select(1), .width(5), .disabled("Z"), .enable("false")) multiplexer_23 (
    .in0(Shamt), .in1({5{1'b0}}), .out(multiplexer_23_out), .sel(CLR));
  Register #(.width(32), .trigger("rising"), .Select("low")) register_18 (
    .D(multiplexer_18_out), .en(pull_resistor_2_node), .Q(IR_out), .clk(CLK));  // open: clr
  Register #(.width(32), .trigger("rising"), .Select("low")) register_19 (
    .D(multiplexer_19_out), .en(pull_resistor_2_node), .Q(PC_out), .clk(CLK));  // open: clr
  Register #(.width(32), .trigger("rising"), .Select("low")) register_20 (
    .D(multiplexer_20_out), .en(pull_resistor_2_node), .Q(A_out), .clk(CLK));  // open: clr
  Register #(.width(32), .trigger("rising"), .Select("low")) register_21 (
    .D(multiplexer_21_out), .en(pull_resistor_2_node), .Q(B_out), .clk(CLK));  // open: clr
  Register #(.width(32), .trigger("rising"), .Select("low")) register_22 (
    .D(multiplexer_22_out), .en(pull_resistor_2_node), .Q(Imm_out), .clk(CLK));  // open: clr
  Register #(.width(5), .trigger("rising"), .Select("low")) register_23 (
    .D(multiplexer_23_out), .en(pull_resistor_2_node), .Q(Shamt_2), .clk(CLK));  // open: clr
endmodule

module \理想EX_MEM  (
  input  RegDst_in,
  input  Beq_in,
  input  [31:0] IR_in,
  input  Syscall_in,
  input  Bne_in,
  input  [31:0] PC_in,
  input  JMP_in,
  input  MemToReg_in,
  input  [31:0] A_in,
  input  JR_in,
  input  [31:0] ALU,
  input  SignedExt_in,
  input  AluSrcB_in,
  input  [31:0] B_in,
  input  SLLV_in,
  input  RegWrite_in,
  input  [31:0] Imm_in,
  input  SRAV_in,
  input  JAL_in,
  input  LBU_in,
  input  [4:0] Shamt,
  input  MemWrite,
  input  BGEZ_in,
  input  CLK,
  input  CLR,
  input  Stall,
  output RegDst_out,
  output Beq_out,
  output [31:0] IR_out,
  output Syscall_out,
  output Bne_out,
  output [31:0] PC_out,
  output JMP_out,
  output MemToReg_out,
  output [31:0] A_in_2,
  output JR_out,
  output [31:0] ALU_2,
  output SignedExt_out,
  output AluSrcB_out,
  output [31:0] B_out,
  output SLLV_out,
  output RegWrite_out,
  output [31:0] Imm_out,
  output SRAV_out,
  output JAL_out,
  output LBU_out,
  output [4:0] Shamt_2,
  output MemWrite_2,
  output BGEZ_out
);

  wire multiplexer_1_out, multiplexer_2_out, multiplexer_3_out, multiplexer_4_out, multiplexer_5_out,
       multiplexer_6_out, multiplexer_7_out, multiplexer_8_out, multiplexer_9_out, multiplexer_10_out,
       multiplexer_11_out, multiplexer_12_out, multiplexer_14_out, multiplexer_15_out, multiplexer_16_out,
       multiplexer_17_out, pull_resistor_2_node;
  wire [4:0] multiplexer_23_out;
  wire [31:0] multiplexer_13_out, multiplexer_18_out, multiplexer_19_out, multiplexer_20_out,
       multiplexer_21_out, multiplexer_22_out;

  Pull_Resistor #(.pull(0)) pull_resistor_1 (.node(CLR));
  Multiplexer #(.select(1), .width(1), .disabled("Z"), .enable("false")) multiplexer_1 (
    .in0(RegDst_in), .in1(1'b0), .out(multiplexer_1_out), .sel(CLR));
  Multiplexer #(.select(1), .width(1), .disabled("Z"), .enable("false")) multiplexer_2 (
    .in0(Syscall_in), .in1(1'b0), .out(multiplexer_2_out), .sel(CLR));
  Multiplexer #(.select(1), .width(1), .disabled("Z"), .enable("false")) multiplexer_3 (
    .in0(JMP_in), .in1(1'b0), .out(multiplexer_3_out), .sel(CLR));
  Multiplexer #(.select(1), .width(1), .disabled("Z"), .enable("false")) multiplexer_4 (
    .in0(JR_in), .in1(1'b0), .out(multiplexer_4_out), .sel(CLR));
  Multiplexer #(.select(1), .width(1), .disabled("Z"), .enable("false")) multiplexer_5 (
    .in0(SignedExt_in), .in1(1'b0), .out(multiplexer_5_out), .sel(CLR));
  Multiplexer #(.select(1), .width(1), .disabled("Z"), .enable("false")) multiplexer_6 (
    .in0(SLLV_in), .in1(1'b0), .out(multiplexer_6_out), .sel(CLR));
  Multiplexer #(.select(1), .width(1), .disabled("Z"), .enable("false")) multiplexer_7 (
    .in0(SRAV_in), .in1(1'b0), .out(multiplexer_7_out), .sel(CLR));
  Multiplexer #(.select(1), .width(1), .disabled("Z"), .enable("false")) multiplexer_8 (
    .in0(LBU_in), .in1(1'b0), .out(multiplexer_8_out), .sel(CLR));
  Multiplexer #(.select(1), .width(1), .disabled("Z"), .enable("false")) multiplexer_9 (
    .in0(BGEZ_in), .in1(1'b0), .out(multiplexer_9_out), .sel(CLR));
  Register #(.width(1), .trigger("rising"), .Select("low")) register_1 (
    .D(multiplexer_1_out), .en(pull_resistor_2_node), .Q(RegDst_out), .clk(CLK));  // open: clr
  Register #(.width(1), .trigger("rising"), .Select("low")) register_2 (
    .D(multiplexer_2_out), .en(pull_resistor_2_node), .Q(Syscall_out), .clk(CLK));  // open: clr
  Register #(.width(1), .trigger("rising"), .Select("low")) register_3 (
    .D(multiplexer_3_out), .en(pull_resistor_2_node), .Q(JMP_out), .clk(CLK));  // open: clr
  Register #(.width(1), .trigger("rising"), .Select("low")) register_4 (
    .D(multiplexer_4_out), .en(pull_resistor_2_node), .Q(JR_out), .clk(CLK));  // open: clr
  Register #(.width(1), .trigger("rising"), .Select("low")) register_5 (
    .D(multiplexer_5_out), .en(pull_resistor_2_node), .Q(SignedExt_out), .clk(CLK));  // open: clr
  Register #(.width(1), .trigger("rising"), .Select("low")) register_6 (
    .D(multiplexer_6_out), .en(pull_resistor_2_node), .Q(SLLV_out), .clk(CLK));  // open: clr
  Register #(.width(1), .trigger("rising"), .Select("low")) register_7 (
    .D(multiplexer_7_out), .en(pull_resistor_2_node), .Q(SRAV_out), .clk(CLK));  // open: clr
  Register #(.width(1), .trigger("rising"), .Select("low")) register_8 (
    .D(multiplexer_8_out), .en(pull_resistor_2_node), .Q(LBU_out), .clk(CLK));  // open: clr
  Register #(.width(1), .trigger("rising"), .Select("low")) register_9 (
    .D(multiplexer_9_out), .en(pull_resistor_2_node), .Q(BGEZ_out), .clk(CLK));  // open: clr
  Pull_Resistor #(.pull(0)) pull_resistor_2 (.node(pull_resistor_2_node));
  not not_1 (pull_resistor_2_node, Stall);
  Multiplexer #(.select(1), .width(1), .disabled("Z"), .enable("false")) multiplexer_10 (
    .in0(Beq_in), .in1(1'b0), .out(multiplexer_10_out), .sel(CLR));
  Multiplexer #(.select(1), .width(1), .disabled("Z"), .enable("false")) multiplexer_11 (
    .in0(Bne_in), .in1(1'b0), .out(multiplexer_11_out), .sel(CLR));
  Multiplexer #(.select(1), .width(1), .disabled("Z"), .enable("false")) multiplexer_12 (
    .in0(MemToReg_in), .in1(1'b0), .out(multiplexer_12_out), .sel(CLR));
  Multiplexer #(.select(1), .width(32), .disabled("Z"), .enable("false")) multiplexer_13 (
    .in0(ALU), .in1({32{1'b0}}), .out(multiplexer_13_out), .sel(CLR));
  Multiplexer #(.select(1), .width(1), .disabled("Z"), .enable("false")) multiplexer_14 (
    .in0(AluSrcB_in), .in1(1'b0), .out(multiplexer_14_out), .sel(CLR));
  Multiplexer #(.select(1), .width(1), .disabled("Z"), .enable("false")) multiplexer_15 (
    .in0(RegWrite_in), .in1(1'b0), .out(multiplexer_15_out), .sel(CLR));
  Multiplexer #(.select(1), .width(1), .disabled("Z"), .enable("false")) multiplexer_16 (
    .in0(JAL_in), .in1(1'b0), .out(multiplexer_16_out), .sel(CLR));
  Multiplexer #(.select(1), .width(1), .disabled("Z"), .enable("false")) multiplexer_17 (
    .in0(MemWrite), .in1(1'b0), .out(multiplexer_17_out), .sel(CLR));
  Register #(.width(1), .trigger("rising"), .Select("low")) register_10 (
    .D(multiplexer_10_out), .en(pull_resistor_2_node), .Q(Beq_out), .clk(CLK));  // open: clr
  Register #(.width(1), .trigger("rising"), .Select("low")) register_11 (
    .D(multiplexer_11_out), .en(pull_resistor_2_node), .Q(Bne_out), .clk(CLK));  // open: clr
  Register #(.width(1), .trigger("rising"), .Select("low")) register_12 (
    .D(multiplexer_12_out), .en(pull_resistor_2_node), .Q(MemToReg_out), .clk(CLK));  // open: clr
  Register #(.width(32), .trigger("rising"), .Select("low")) register_13 (
    .D(multiplexer_13_out), .en(pull_resistor_2_node), .Q(ALU_2), .clk(CLK));  // open: clr
  Register #(.width(1), .trigger("rising"), .Select("low")) register_14 (
    .D(multiplexer_14_out), .en(pull_resistor_2_node), .Q(AluSrcB_out), .clk(CLK));  // open: clr
  Register #(.width(1), .trigger("rising"), .Select("low")) register_15 (
    .D(multiplexer_15_out), .en(pull_resistor_2_node), .Q(RegWrite_out), .clk(CLK));  // open: clr
  Register #(.width(1), .trigger("rising"), .Select("low")) register_16 (
    .D(multiplexer_16_out), .en(pull_resistor_2_node), .Q(JAL_out), .clk(CLK));  // open: clr
  Register #(.width(1), .trigger("rising"), .Select("low")) register_17 (
    .D(multiplexer_17_out), .en(pull_resistor_2_node), .Q(MemWrite_2), .clk(CLK));  // open: clr
  Multiplexer #(.select(1), .width(32), .disabled("Z"), .enable("false")) multiplexer_18 (
    .in0(IR_in), .in1({32{1'b0}}), .out(multiplexer_18_out), .sel(CLR));
  Multiplexer #(.select(1), .width(32), .disabled("Z"), .enable("false")) multiplexer_19 (
    .in0(PC_in), .in1({32{1'b0}}), .out(multiplexer_19_out), .sel(CLR));
  Multiplexer #(.select(1), .width(32), .disabled("Z"), .enable("false")) multiplexer_20 (
    .in0(A_in), .in1({32{1'b0}}), .out(multiplexer_20_out), .sel(CLR));
  Multiplexer #(.select(1), .width(32), .disabled("Z"), .enable("false")) multiplexer_21 (
    .in0(B_in), .in1({32{1'b0}}), .out(multiplexer_21_out), .sel(CLR));
  Multiplexer #(.select(1), .width(32), .disabled("Z"), .enable("false")) multiplexer_22 (
    .in0(Imm_in), .in1({32{1'b0}}), .out(multiplexer_22_out), .sel(CLR));
  Multiplexer #(.select(1), .width(5), .disabled("Z"), .enable("false")) multiplexer_23 (
    .in0(Shamt), .in1({5{1'b0}}), .out(multiplexer_23_out), .sel(CLR));
  Register #(.width(32), .trigger("rising"), .Select("low")) register_18 (
    .D(multiplexer_18_out), .en(pull_resistor_2_node), .Q(IR_out), .clk(CLK));  // open: clr
  Register #(.width(32), .trigger("rising"), .Select("low")) register_19 (
    .D(multiplexer_19_out), .en(pull_resistor_2_node), .Q(PC_out), .clk(CLK));  // open: clr
  Register #(.width(32), .trigger("rising"), .Select("low")) register_20 (
    .D(multiplexer_20_out), .en(pull_resistor_2_node), .Q(A_in_2), .clk(CLK));  // open: clr
  Register #(.width(32), .trigger("rising"), .Select("low")) register_21 (
    .D(multiplexer_21_out), .en(pull_resistor_2_node), .Q(B_out), .clk(CLK));  // open: clr
  Register #(.width(32), .trigger("rising"), .Select("low")) register_22 (
    .D(multiplexer_22_out), .en(pull_resistor_2_node), .Q(Imm_out), .clk(CLK));  // open: clr
  Register #(.width(5), .trigger("rising"), .Select("low")) register_23 (
    .D(multiplexer_23_out), .en(pull_resistor_2_node), .Q(Shamt_2), .clk(CLK));  // open: clr
endmodule

module \理想MEM_WB  (
  input  RegDst_in,
  input  Beq_in,
  input  [31:0] IR_in,
  input  Syscall_in,
  input  Bne_in,
  input  [31:0] PC_in,
  input  JMP_in,
  input  MemToReg_in,
  input  [31:0] A_in,
  input  JR_in,
  input  [31:0] ALU,
  input  SignedExt_in,
  input  AluSrcB_in,
  input  [31:0] B_in,
  input  SLLV_in,
  input  RegWrite_in,
  input  [31:0] Imm_in,
  input  SRAV_in,
  input  JAL_in,
  input  LBU_in,
  input  [31:0] MD,
  input  MemWrite,
  input  BGEZ_in,
  input  CLK,
  input  CLR,
  input  Stall,
  output RegDst_out,
  output Beq_out,
  output [31:0] IR_out,
  output Syscall_out,
  output Bne_out,
  output [31:0] PC_out,
  output JMP_out,
  output MemToReg_out,
  output [31:0] A_out,
  output JR_out,
  output [31:0] ALU_2,
  output SignedExt_out,
  output AluSrcB_out,
  output [31:0] B_out,
  output SLLV_out,
  output RegWrite_out,
  output [31:0] Imm_out,
  output SRAV_out,
  output JAL_out,
  output LBU_out,
  output [31:0] MD_2,
  output MemWrite_2,
  output BGEZ_out
);

  wire multiplexer_1_out, multiplexer_2_out, multiplexer_3_out, multiplexer_4_out, multiplexer_5_out,
       multiplexer_6_out, multiplexer_7_out, multiplexer_8_out, multiplexer_9_out, multiplexer_10_out,
       multiplexer_11_out, multiplexer_12_out, multiplexer_14_out, multiplexer_15_out, multiplexer_16_out,
       multiplexer_17_out, pull_resistor_2_node;
  wire [31:0] multiplexer_13_out, multiplexer_18_out, multiplexer_19_out, multiplexer_20_out,
       multiplexer_21_out, multiplexer_22_out, multiplexer_23_out;

  Pull_Resistor #(.pull(0)) pull_resistor_1 (.node(CLR));
  Multiplexer #(.select(1), .width(1), .disabled("Z"), .enable("false")) multiplexer_1 (
    .in0(RegDst_in), .in1(1'b0), .out(multiplexer_1_out), .sel(CLR));
  Multiplexer #(.select(1), .width(1), .disabled("Z"), .enable("false")) multiplexer_2 (
    .in0(Syscall_in), .in1(1'b0), .out(multiplexer_2_out), .sel(CLR));
  Multiplexer #(.select(1), .width(1), .disabled("Z"), .enable("false")) multiplexer_3 (
    .in0(JMP_in), .in1(1'b0), .out(multiplexer_3_out), .sel(CLR));
  Multiplexer #(.select(1), .width(1), .disabled("Z"), .enable("false")) multiplexer_4 (
    .in0(JR_in), .in1(1'b0), .out(multiplexer_4_out), .sel(CLR));
  Multiplexer #(.select(1), .width(1), .disabled("Z"), .enable("false")) multiplexer_5 (
    .in0(SignedExt_in), .in1(1'b0), .out(multiplexer_5_out), .sel(CLR));
  Multiplexer #(.select(1), .width(1), .disabled("Z"), .enable("false")) multiplexer_6 (
    .in0(SLLV_in), .in1(1'b0), .out(multiplexer_6_out), .sel(CLR));
  Multiplexer #(.select(1), .width(1), .disabled("Z"), .enable("false")) multiplexer_7 (
    .in0(SRAV_in), .in1(1'b0), .out(multiplexer_7_out), .sel(CLR));
  Multiplexer #(.select(1), .width(1), .disabled("Z"), .enable("false")) multiplexer_8 (
    .in0(LBU_in), .in1(1'b0), .out(multiplexer_8_out), .sel(CLR));
  Multiplexer #(.select(1), .width(1), .disabled("Z"), .enable("false")) multiplexer_9 (
    .in0(BGEZ_in), .in1(1'b0), .out(multiplexer_9_out), .sel(CLR));
  Register #(.width(1), .trigger("rising"), .Select("low")) register_1 (
    .D(multiplexer_1_out), .en(pull_resistor_2_node), .Q(RegDst_out), .clk(CLK));  // open: clr
  Register #(.width(1), .trigger("rising"), .Select("low")) register_2 (
    .D(multiplexer_2_out), .en(pull_resistor_2_node), .Q(Syscall_out), .clk(CLK));  // open: clr
  Register #(.width(1), .trigger("rising"), .Select("low")) register_3 (
    .D(multiplexer_3_out), .en(pull_resistor_2_node), .Q(JMP_out), .clk(CLK));  // open: clr
  Register #(.width(1), .trigger("rising"), .Select("low")) register_4 (
    .D(multiplexer_4_out), .en(pull_resistor_2_node), .Q(JR_out), .clk(CLK));  // open: clr
  Register #(.width(1), .trigger("rising"), .Select("low")) register_5 (
    .D(multiplexer_5_out), .en(pull_resistor_2_node), .Q(SignedExt_out), .clk(CLK));  // open: clr
  Register #(.width(1), .trigger("rising"), .Select("low")) register_6 (
    .D(multiplexer_6_out), .en(pull_resistor_2_node), .Q(SLLV_out), .clk(CLK));  // open: clr
  Register #(.width(1), .trigger("rising"), .Select("low")) register_7 (
    .D(multiplexer_7_out), .en(pull_resistor_2_node), .Q(SRAV_out), .clk(CLK));  // open: clr
  Register #(.width(1), .trigger("rising"), .Select("low")) register_8 (
    .D(multiplexer_8_out), .en(pull_resistor_2_node), .Q(LBU_out), .clk(CLK));  // open: clr
  Register #(.width(1), .trigger("rising"), .Select("low")) register_9 (
    .D(multiplexer_9_out), .en(pull_resistor_2_node), .Q(BGEZ_out), .clk(CLK));  // open: clr
  Pull_Resistor #(.pull(0)) pull_resistor_2 (.node(pull_resistor_2_node));
  not not_1 (pull_resistor_2_node, Stall);
  Multiplexer #(.select(1), .width(1), .disabled("Z"), .enable("false")) multiplexer_10 (
    .in0(Beq_in), .in1(1'b0), .out(multiplexer_10_out), .sel(CLR));
  Multiplexer #(.select(1), .width(1), .disabled("Z"), .enable("false")) multiplexer_11 (
    .in0(Bne_in), .in1(1'b0), .out(multiplexer_11_out), .sel(CLR));
  Multiplexer #(.select(1), .width(1), .disabled("Z"), .enable("false")) multiplexer_12 (
    .in0(MemToReg_in), .in1(1'b0), .out(multiplexer_12_out), .sel(CLR));
  Multiplexer #(.select(1), .width(32), .disabled("Z"), .enable("false")) multiplexer_13 (
    .in0(ALU), .in1({32{1'b0}}), .out(multiplexer_13_out), .sel(CLR));
  Multiplexer #(.select(1), .width(1), .disabled("Z"), .enable("false")) multiplexer_14 (
    .in0(AluSrcB_in), .in1(1'b0), .out(multiplexer_14_out), .sel(CLR));
  Multiplexer #(.select(1), .width(1), .disabled("Z"), .enable("false")) multiplexer_15 (
    .in0(RegWrite_in), .in1(1'b0), .out(multiplexer_15_out), .sel(CLR));
  Multiplexer #(.select(1), .width(1), .disabled("Z"), .enable("false")) multiplexer_16 (
    .in0(JAL_in), .in1(1'b0), .out(multiplexer_16_out), .sel(CLR));
  Multiplexer #(.select(1), .width(1), .disabled("Z"), .enable("false")) multiplexer_17 (
    .in0(MemWrite), .in1(1'b0), .out(multiplexer_17_out), .sel(CLR));
  Register #(.width(1), .trigger("rising"), .Select("low")) register_10 (
    .D(multiplexer_10_out), .en(pull_resistor_2_node), .Q(Beq_out), .clk(CLK));  // open: clr
  Register #(.width(1), .trigger("rising"), .Select("low")) register_11 (
    .D(multiplexer_11_out), .en(pull_resistor_2_node), .Q(Bne_out), .clk(CLK));  // open: clr
  Register #(.width(1), .trigger("rising"), .Select("low")) register_12 (
    .D(multiplexer_12_out), .en(pull_resistor_2_node), .Q(MemToReg_out), .clk(CLK));  // open: clr
  Register #(.width(32), .trigger("rising"), .Select("low")) register_13 (
    .D(multiplexer_13_out), .en(pull_resistor_2_node), .Q(ALU_2), .clk(CLK));  // open: clr
  Register #(.width(1), .trigger("rising"), .Select("low")) register_14 (
    .D(multiplexer_14_out), .en(pull_resistor_2_node), .Q(AluSrcB_out), .clk(CLK));  // open: clr
  Register #(.width(1), .trigger("rising"), .Select("low")) register_15 (
    .D(multiplexer_15_out), .en(pull_resistor_2_node), .Q(RegWrite_out), .clk(CLK));  // open: clr
  Register #(.width(1), .trigger("rising"), .Select("low")) register_16 (
    .D(multiplexer_16_out), .en(pull_resistor_2_node), .Q(JAL_out), .clk(CLK));  // open: clr
  Register #(.width(1), .trigger("rising"), .Select("low")) register_17 (
    .D(multiplexer_17_out), .en(pull_resistor_2_node), .Q(MemWrite_2), .clk(CLK));  // open: clr
  Multiplexer #(.select(1), .width(32), .disabled("Z"), .enable("false")) multiplexer_18 (
    .in0(IR_in), .in1({32{1'b0}}), .out(multiplexer_18_out), .sel(CLR));
  Multiplexer #(.select(1), .width(32), .disabled("Z"), .enable("false")) multiplexer_19 (
    .in0(PC_in), .in1({32{1'b0}}), .out(multiplexer_19_out), .sel(CLR));
  Multiplexer #(.select(1), .width(32), .disabled("Z"), .enable("false")) multiplexer_20 (
    .in0(A_in), .in1({32{1'b0}}), .out(multiplexer_20_out), .sel(CLR));
  Multiplexer #(.select(1), .width(32), .disabled("Z"), .enable("false")) multiplexer_21 (
    .in0(B_in), .in1({32{1'b0}}), .out(multiplexer_21_out), .sel(CLR));
  Multiplexer #(.select(1), .width(32), .disabled("Z"), .enable("false")) multiplexer_22 (
    .in0(Imm_in), .in1({32{1'b0}}), .out(multiplexer_22_out), .sel(CLR));
  Multiplexer #(.select(1), .width(32), .disabled("Z"), .enable("false")) multiplexer_23 (
    .in0(MD), .in1({32{1'b0}}), .out(multiplexer_23_out), .sel(CLR));
  Register #(.width(32), .trigger("rising"), .Select("low")) register_18 (
    .D(multiplexer_18_out), .en(pull_resistor_2_node), .Q(IR_out), .clk(CLK));  // open: clr
  Register #(.width(32), .trigger("rising"), .Select("low")) register_19 (
    .D(multiplexer_19_out), .en(pull_resistor_2_node), .Q(PC_out), .clk(CLK));  // open: clr
  Register #(.width(32), .trigger("rising"), .Select("low")) register_20 (
    .D(multiplexer_20_out), .en(pull_resistor_2_node), .Q(A_out), .clk(CLK));  // open: clr
  Register #(.width(32), .trigger("rising"), .Select("low")) register_21 (
    .D(multiplexer_21_out), .en(pull_resistor_2_node), .Q(B_out), .clk(CLK));  // open: clr
  Register #(.width(32), .trigger("rising"), .Select("low")) register_22 (
    .D(multiplexer_22_out), .en(pull_resistor_2_node), .Q(Imm_out), .clk(CLK));  // open: clr
  Register #(.width(32), .trigger("rising"), .Select("low")) register_23 (
    .D(multiplexer_23_out), .en(pull_resistor_2_node), .Q(MD_2), .clk(CLK));  // open: clr
endmodule

module \理想IF_ID  (
  input  RegDst_in,
  input  Beq_in,
  input  [31:0] IR_in,
  input  Syscall_in,
  input  Bne_in,
  input  [31:0] PC_in,
  input  JMP_in,
  input  MemToReg_in,
  input  [31:0] A_in,
  input  JR_in,
  input  [3:0] AluOP_in,
  input  SignedExt_in,
  input  AluSrcB_in,
  input  [31:0] B_in,
  input  SLLV_in,
  input  RegWrite_in,
  input  [31:0] Imm_in,
  input  SRAV_in,
  input  JAL_in,
  input  LBU_in,
  input  [4:0] Shamt,
  input  MemWrite,
  input  BGEZ_in,
  input  CLK,
  input  CLR,
  input  Stall,
  output RegDst_out,
  output Beq_out,
  output [31:0] IR_out,
  output Syscall_out,
  output Bne_out,
  output [31:0] PC_out,
  output JMP_out,
  output MemToReg_out,
  output [31:0] A_out,
  output JR_out,
  output [3:0] AluOP_out,
  output SignedExt_out,
  output AluSrcB_out,
  output [31:0] B_out,
  output SLLV_out,
  output RegWrite_out,
  output [31:0] Imm_out,
  output SRAV_out,
  output JAL_out,
  output LBU_out,
  output [4:0] Shamt_2,
  output MemWrite_2,
  output BGEZ_out
);

  wire multiplexer_1_out, multiplexer_2_out, multiplexer_3_out, multiplexer_4_out, multiplexer_5_out,
       multiplexer_6_out, multiplexer_7_out, multiplexer_8_out, multiplexer_9_out, multiplexer_10_out,
       multiplexer_11_out, multiplexer_12_out, multiplexer_14_out, multiplexer_15_out, multiplexer_16_out,
       multiplexer_17_out, pull_resistor_2_node;
  wire [3:0] multiplexer_13_out;
  wire [4:0] multiplexer_23_out;
  wire [31:0] multiplexer_18_out, multiplexer_19_out, multiplexer_20_out, multiplexer_21_out,
       multiplexer_22_out;

  Pull_Resistor #(.pull(0)) pull_resistor_1 (.node(CLR));
  Multiplexer #(.select(1), .width(1), .disabled("Z"), .enable("false")) multiplexer_1 (
    .in0(RegDst_in), .in1(1'b0), .out(multiplexer_1_out), .sel(CLR));
  Multiplexer #(.select(1), .width(1), .disabled("Z"), .enable("false")) multiplexer_2 (
    .in0(Syscall_in), .in1(1'b0), .out(multiplexer_2_out), .sel(CLR));
  Multiplexer #(.select(1), .width(1), .disabled("Z"), .enable("false")) multiplexer_3 (
    .in0(JMP_in), .in1(1'b0), .out(multiplexer_3_out), .sel(CLR));
  Multiplexer #(.select(1), .width(1), .disabled("Z"), .enable("false")) multiplexer_4 (
    .in0(JR_in), .in1(1'b0), .out(multiplexer_4_out), .sel(CLR));
  Multiplexer #(.select(1), .width(1), .disabled("Z"), .enable("false")) multiplexer_5 (
    .in0(SignedExt_in), .in1(1'b0), .out(multiplexer_5_out), .sel(CLR));
  Multiplexer #(.select(1), .width(1), .disabled("Z"), .enable("false")) multiplexer_6 (
    .in0(SLLV_in), .in1(1'b0), .out(multiplexer_6_out), .sel(CLR));
  Multiplexer #(.select(1), .width(1), .disabled("Z"), .enable("false")) multiplexer_7 (
    .in0(SRAV_in), .in1(1'b0), .out(multiplexer_7_out), .sel(CLR));
  Multiplexer #(.select(1), .width(1), .disabled("Z"), .enable("false")) multiplexer_8 (
    .in0(LBU_in), .in1(1'b0), .out(multiplexer_8_out), .sel(CLR));
  Multiplexer #(.select(1), .width(1), .disabled("Z"), .enable("false")) multiplexer_9 (
    .in0(BGEZ_in), .in1(1'b0), .out(multiplexer_9_out), .sel(CLR));
  Register #(.width(1), .trigger("rising"), .Select("low")) register_1 (
    .D(multiplexer_1_out), .en(pull_resistor_2_node), .Q(RegDst_out), .clk(CLK));  // open: clr
  Register #(.width(1), .trigger("rising"), .Select("low")) register_2 (
    .D(multiplexer_2_out), .en(pull_resistor_2_node), .Q(Syscall_out), .clk(CLK));  // open: clr
  Register #(.width(1), .trigger("rising"), .Select("low")) register_3 (
    .D(multiplexer_3_out), .en(pull_resistor_2_node), .Q(JMP_out), .clk(CLK));  // open: clr
  Register #(.width(1), .trigger("rising"), .Select("low")) register_4 (
    .D(multiplexer_4_out), .en(pull_resistor_2_node), .Q(JR_out), .clk(CLK));  // open: clr
  Register #(.width(1), .trigger("rising"), .Select("low")) register_5 (
    .D(multiplexer_5_out), .en(pull_resistor_2_node), .Q(SignedExt_out), .clk(CLK));  // open: clr
  Register #(.width(1), .trigger("rising"), .Select("low")) register_6 (
    .D(multiplexer_6_out), .en(pull_resistor_2_node), .Q(SLLV_out), .clk(CLK));  // open: clr
  Register #(.width(1), .trigger("rising"), .Select("low")) register_7 (
    .D(multiplexer_7_out), .en(pull_resistor_2_node), .Q(SRAV_out), .clk(CLK));  // open: clr
  Register #(.width(1), .trigger("rising"), .Select("low")) register_8 (
    .D(multiplexer_8_out), .en(pull_resistor_2_node), .Q(LBU_out), .clk(CLK));  // open: clr
  Register #(.width(1), .trigger("rising"), .Select("low")) register_9 (
    .D(multiplexer_9_out), .en(pull_resistor_2_node), .Q(BGEZ_out), .clk(CLK));  // open: clr
  Pull_Resistor #(.pull(0)) pull_resistor_2 (.node(pull_resistor_2_node));
  not not_1 (pull_resistor_2_node, Stall);
  Multiplexer #(.select(1), .width(1), .disabled("Z"), .enable("false")) multiplexer_10 (
    .in0(Beq_in), .in1(1'b0), .out(multiplexer_10_out), .sel(CLR));
  Multiplexer #(.select(1), .width(1), .disabled("Z"), .enable("false")) multiplexer_11 (
    .in0(Bne_in), .in1(1'b0), .out(multiplexer_11_out), .sel(CLR));
  Multiplexer #(.select(1), .width(1), .disabled("Z"), .enable("false")) multiplexer_12 (
    .in0(MemToReg_in), .in1(1'b0), .out(multiplexer_12_out), .sel(CLR));
  Multiplexer #(.select(1), .width(4), .disabled("Z"), .enable("false")) multiplexer_13 (
    .in0(AluOP_in), .in1(4'b0000), .out(multiplexer_13_out), .sel(CLR));
  Multiplexer #(.select(1), .width(1), .disabled("Z"), .enable("false")) multiplexer_14 (
    .in0(AluSrcB_in), .in1(1'b0), .out(multiplexer_14_out), .sel(CLR));
  Multiplexer #(.select(1), .width(1), .disabled("Z"), .enable("false")) multiplexer_15 (
    .in0(RegWrite_in), .in1(1'b0), .out(multiplexer_15_out), .sel(CLR));
  Multiplexer #(.select(1), .width(1), .disabled("Z"), .enable("false")) multiplexer_16 (
    .in0(JAL_in), .in1(1'b0), .out(multiplexer_16_out), .sel(CLR));
  Multiplexer #(.select(1), .width(1), .disabled("Z"), .enable("false")) multiplexer_17 (
    .in0(MemWrite), .in1(1'b0), .out(multiplexer_17_out), .sel(CLR));
  Register #(.width(1), .trigger("rising"), .Select("low")) register_10 (
    .D(multiplexer_10_out), .en(pull_resistor_2_node), .Q(Beq_out), .clk(CLK));  // open: clr
  Register #(.width(1), .trigger("rising"), .Select("low")) register_11 (
    .D(multiplexer_11_out), .en(pull_resistor_2_node), .Q(Bne_out), .clk(CLK));  // open: clr
  Register #(.width(1), .trigger("rising"), .Select("low")) register_12 (
    .D(multiplexer_12_out), .en(pull_resistor_2_node), .Q(MemToReg_out), .clk(CLK));  // open: clr
  Register #(.width(4), .trigger("rising"), .Select("low")) register_13 (
    .D(multiplexer_13_out), .en(pull_resistor_2_node), .Q(AluOP_out), .clk(CLK));  // open: clr
  Register #(.width(1), .trigger("rising"), .Select("low")) register_14 (
    .D(multiplexer_14_out), .en(pull_resistor_2_node), .Q(AluSrcB_out), .clk(CLK));  // open: clr
  Register #(.width(1), .trigger("rising"), .Select("low")) register_15 (
    .D(multiplexer_15_out), .en(pull_resistor_2_node), .Q(RegWrite_out), .clk(CLK));  // open: clr
  Register #(.width(1), .trigger("rising"), .Select("low")) register_16 (
    .D(multiplexer_16_out), .en(pull_resistor_2_node), .Q(JAL_out), .clk(CLK));  // open: clr
  Register #(.width(1), .trigger("rising"), .Select("low")) register_17 (
    .D(multiplexer_17_out), .en(pull_resistor_2_node), .Q(MemWrite_2), .clk(CLK));  // open: clr
  Multiplexer #(.select(1), .width(32), .disabled("Z"), .enable("false")) multiplexer_18 (
    .in0(IR_in), .in1({32{1'b0}}), .out(multiplexer_18_out), .sel(CLR));
  Multiplexer #(.select(1), .width(32), .disabled("Z"), .enable("false")) multiplexer_19 (
    .in0(PC_in), .in1({32{1'b0}}), .out(multiplexer_19_out), .sel(CLR));
  Multiplexer #(.select(1), .width(32), .disabled("Z"), .enable("false")) multiplexer_20 (
    .in0(A_in), .in1({32{1'b0}}), .out(multiplexer_20_out), .sel(CLR));
  Multiplexer #(.select(1), .width(32), .disabled("Z"), .enable("false")) multiplexer_21 (
    .in0(B_in), .in1({32{1'b0}}), .out(multiplexer_21_out), .sel(CLR));
  Multiplexer #(.select(1), .width(32), .disabled("Z"), .enable("false")) multiplexer_22 (
    .in0(Imm_in), .in1({32{1'b0}}), .out(multiplexer_22_out), .sel(CLR));
  Multiplexer #(.select(1), .width(5), .disabled("Z"), .enable("false")) multiplexer_23 (
    .in0(Shamt), .in1({5{1'b0}}), .out(multiplexer_23_out), .sel(CLR));
  Register #(.width(32), .trigger("rising"), .Select("low")) register_18 (
    .D(multiplexer_18_out), .en(pull_resistor_2_node), .Q(IR_out), .clk(CLK));  // open: clr
  Register #(.width(32), .trigger("rising"), .Select("low")) register_19 (
    .D(multiplexer_19_out), .en(pull_resistor_2_node), .Q(PC_out), .clk(CLK));  // open: clr
  Register #(.width(32), .trigger("rising"), .Select("low")) register_20 (
    .D(multiplexer_20_out), .en(pull_resistor_2_node), .Q(A_out), .clk(CLK));  // open: clr
  Register #(.width(32), .trigger("rising"), .Select("low")) register_21 (
    .D(multiplexer_21_out), .en(pull_resistor_2_node), .Q(B_out), .clk(CLK));  // open: clr
  Register #(.width(32), .trigger("rising"), .Select("low")) register_22 (
    .D(multiplexer_22_out), .en(pull_resistor_2_node), .Q(Imm_out), .clk(CLK));  // open: clr
  Register #(.width(5), .trigger("rising"), .Select("low")) register_23 (
    .D(multiplexer_23_out), .en(pull_resistor_2_node), .Q(Shamt_2), .clk(CLK));  // open: clr
endmodule
module \源寄存器使用情况  (
  input  [5:0] OP,
  input  [5:0] Funct,
  output R1_Used,
  output R2_Used
);

  wire and_1_out, and_2_out, and_3_out, and_4_out, and_5_out, and_6_out, and_7_out, and_8_out, and_9_out,
       and_10_out, and_11_out, and_12_out, and_13_out, and_14_out, and_15_out, and_16_out, and_17_out,
       and_18_out, and_19_out, and_20_out, and_21_out, and_22_out, and_23_out, and_24_out, and_25_out,
       and_26_out, and_27_out, and_28_out, and_29_out, and_30_out, and_31_out, and_32_out, and_33_out,
       and_34_out, and_35_out, and_36_out, and_37_out, and_38_out, and_39_out, and_40_out, not_1_out,
       not_2_out, not_3_out, not_4_out, not_5_out, not_6_out, not_7_out, not_8_out, not_9_out, not_10_out,
       not_11_out, not_12_out, not_13_out, not_14_out, not_15_out, not_16_out, not_17_out, not_18_out,
       not_19_out, not_20_out, not_21_out, not_22_out, not_23_out, not_24_out, not_25_out, not_26_out,
       not_27_out, not_28_out, not_29_out, not_30_out, not_31_out, not_32_out, not_33_out, not_34_out,
       not_35_out, not_36_out, not_37_out, not_38_out, not_39_out, not_40_out, not_41_out, not_42_out,
       not_43_out, not_44_out, not_45_out, not_46_out, not_47_out, not_48_out, not_49_out, not_50_out,
       not_51_out, not_52_out, not_53_out, not_54_out, not_55_out, not_56_out, not_57_out, not_58_out,
       not_59_out, not_60_out, not_61_out, not_62_out, not_63_out, not_64_out, not_65_out, not_66_out,
       not_67_out, not_68_out, not_69_out, not_70_out, not_71_out, not_72_out, not_73_out, not_74_out,
       not_75_out, not_76_out, not_77_out, not_78_out, not_79_out, not_80_out, not_81_out, not_82_out,
       not_83_out, not_84_out, not_85_out, not_86_out, not_87_out, not_88_out, not_89_out, not_90_out,
       not_91_out, not_92_out, not_93_out, not_94_out, not_95_out, not_96_out, not_97_out, not_98_out,
       not_99_out, not_100_out, not_101_out, not_102_out, not_103_out, not_104_out, not_105_out, not_106_out,
       not_107_out, not_108_out, not_109_out, not_110_out, not_111_out, not_112_out, not_113_out,
       not_114_out, not_115_out, not_116_out, not_117_out, not_118_out, not_119_out, not_120_out,
       not_121_out, not_122_out, not_123_out, not_124_out, not_125_out, not_126_out, not_127_out,
       not_128_out, not_129_out, not_130_out, not_131_out, not_132_out, not_133_out, not_134_out,
       not_135_out, not_136_out, not_137_out, not_138_out, not_139_out, not_140_out, not_141_out,
       not_142_out, not_143_out, not_144_out, not_145_out, not_146_out, not_147_out, not_148_out,
       not_149_out, not_150_out, not_151_out, not_152_out, not_153_out, not_154_out, not_155_out,
       not_156_out, not_157_out, not_158_out, not_159_out, not_160_out, not_161_out, not_162_out,
       not_163_out, not_164_out, not_165_out, not_166_out, not_167_out, not_168_out, not_169_out,
       not_170_out, not_171_out, not_172_out, not_173_out, not_174_out, not_175_out, not_176_out,
       not_177_out, not_178_out, not_179_out, not_180_out, not_181_out, not_182_out, not_183_out,
       not_184_out, not_185_out, not_186_out, not_187_out, not_188_out, not_189_out, not_190_out,
       not_191_out, not_192_out, not_193_out, not_194_out, not_195_out, not_196_out, not_197_out,
       not_198_out, not_199_out, not_200_out, not_201_out, not_202_out, not_203_out, not_204_out,
       not_205_out, not_206_out, not_207_out, not_208_out, not_209_out, not_210_out, not_211_out,
       not_212_out, not_213_out, not_214_out, not_215_out, not_216_out, not_217_out, not_218_out,
       not_219_out, not_220_out, not_221_out, not_222_out, not_223_out, not_224_out, not_225_out,
       not_226_out, not_227_out, not_228_out, not_229_out, not_230_out, not_231_out, not_232_out,
       not_233_out, not_234_out, not_235_out, not_236_out, not_237_out, not_238_out, not_239_out,
       not_240_out, not_241_out, not_242_out, not_243_out, not_244_out, not_245_out, not_246_out,
       not_247_out, not_248_out, not_249_out, not_250_out, not_251_out, not_252_out, not_253_out,
       not_254_out, not_255_out, not_256_out, not_257_out, not_258_out, not_259_out, not_260_out,
       not_261_out, not_262_out, not_263_out, not_264_out, not_265_out, not_266_out, not_267_out,
       not_268_out, not_269_out, not_270_out, not_271_out, not_272_out, not_273_out, not_274_out,
       not_275_out, not_276_out, not_277_out, not_278_out, not_279_out, not_280_out, not_281_out,
       not_282_out, not_283_out, not_284_out, not_285_out, not_286_out, not_287_out, not_288_out,
       not_289_out, not_290_out, not_291_out, not_292_out, not_293_out, not_294_out, not_295_out,
       not_296_out, not_297_out, not_298_out, not_299_out, not_300_out, not_301_out, not_302_out,
       not_303_out, not_304_out, not_305_out, not_306_out, not_307_out, not_308_out;

  not not_1 (not_1_out, OP[5]);
  not not_2 (not_2_out, OP[4]);
  not not_3 (not_3_out, OP[3]);
  not not_4 (not_4_out, OP[2]);
  not not_5 (not_5_out, OP[1]);
  not not_6 (not_6_out, OP[0]);
  not not_7 (not_7_out, Funct[4]);
  not not_8 (not_8_out, Funct[3]);
  not not_9 (not_9_out, Funct[2]);
  not not_10 (not_10_out, Funct[1]);
  not not_11 (not_11_out, Funct[0]);
  not not_12 (not_12_out, OP[5]);
  not not_13 (not_13_out, OP[4]);
  not not_14 (not_14_out, OP[3]);
  not not_15 (not_15_out, OP[2]);
  not not_16 (not_16_out, OP[1]);
  not not_17 (not_17_out, OP[0]);
  not not_18 (not_18_out, Funct[4]);
  not not_19 (not_19_out, Funct[3]);
  not not_20 (not_20_out, Funct[2]);
  not not_21 (not_21_out, Funct[1]);
  not not_22 (not_22_out, OP[5]);
  not not_23 (not_23_out, OP[4]);
  not not_24 (not_24_out, OP[3]);
  not not_25 (not_25_out, OP[2]);
  not not_26 (not_26_out, OP[1]);
  not not_27 (not_27_out, OP[0]);
  not not_28 (not_28_out, Funct[4]);
  not not_29 (not_29_out, Funct[3]);
  not not_30 (not_30_out, Funct[2]);
  not not_31 (not_31_out, Funct[0]);
  not not_32 (not_32_out, OP[5]);
  not not_33 (not_33_out, OP[4]);
  not not_34 (not_34_out, OP[3]);
  not not_35 (not_35_out, OP[2]);
  not not_36 (not_36_out, OP[1]);
  not not_37 (not_37_out, OP[0]);
  not not_38 (not_38_out, Funct[4]);
  not not_39 (not_39_out, Funct[3]);
  not not_40 (not_40_out, Funct[1]);
  not not_41 (not_41_out, Funct[0]);
  not not_42 (not_42_out, OP[5]);
  not not_43 (not_43_out, OP[4]);
  not not_44 (not_44_out, OP[3]);
  not not_45 (not_45_out, OP[2]);
  not not_46 (not_46_out, OP[1]);
  not not_47 (not_47_out, OP[0]);
  not not_48 (not_48_out, Funct[4]);
  not not_49 (not_49_out, Funct[3]);
  not not_50 (not_50_out, Funct[1]);
  not not_51 (not_51_out, OP[5]);
  not not_52 (not_52_out, OP[4]);
  not not_53 (not_53_out, OP[3]);
  not not_54 (not_54_out, OP[2]);
  not not_55 (not_55_out, OP[1]);
  not not_56 (not_56_out, OP[0]);
  not not_57 (not_57_out, Funct[4]);
  not not_58 (not_58_out, Funct[3]);
  not not_59 (not_59_out, OP[5]);
  not not_60 (not_60_out, OP[4]);
  not not_61 (not_61_out, OP[3]);
  not not_62 (not_62_out, OP[2]);
  not not_63 (not_63_out, OP[1]);
  not not_64 (not_64_out, OP[0]);
  not not_65 (not_65_out, Funct[4]);
  not not_66 (not_66_out, Funct[2]);
  not not_67 (not_67_out, Funct[0]);
  not not_68 (not_68_out, OP[5]);
  not not_69 (not_69_out, OP[4]);
  not not_70 (not_70_out, OP[3]);
  not not_71 (not_71_out, OP[2]);
  not not_72 (not_72_out, OP[1]);
  not not_73 (not_73_out, OP[0]);
  not not_74 (not_74_out, Funct[4]);
  not not_75 (not_75_out, Funct[2]);
  not not_76 (not_76_out, OP[5]);
  not not_77 (not_77_out, OP[4]);
  not not_78 (not_78_out, OP[3]);
  not not_79 (not_79_out, OP[2]);
  not not_80 (not_80_out, OP[1]);
  not not_81 (not_81_out, OP[0]);
  not not_82 (not_82_out, Funct[5]);
  not not_83 (not_83_out, Funct[4]);
  not not_84 (not_84_out, Funct[2]);
  not not_85 (not_85_out, Funct[1]);
  not not_86 (not_86_out, Funct[0]);
  not not_87 (not_87_out, OP[5]);
  not not_88 (not_88_out, OP[4]);
  not not_89 (not_89_out, OP[3]);
  not not_90 (not_90_out, OP[2]);
  not not_91 (not_91_out, OP[1]);
  not not_92 (not_92_out, OP[0]);
  not not_93 (not_93_out, Funct[5]);
  not not_94 (not_94_out, Funct[4]);
  not not_95 (not_95_out, Funct[1]);
  not not_96 (not_96_out, Funct[0]);
  not not_97 (not_97_out, OP[5]);
  not not_98 (not_98_out, OP[4]);
  not not_99 (not_99_out, OP[3]);
  not not_100 (not_100_out, OP[1]);
  not not_101 (not_101_out, OP[0]);
  not not_102 (not_102_out, OP[5]);
  not not_103 (not_103_out, OP[4]);
  not not_104 (not_104_out, OP[3]);
  not not_105 (not_105_out, OP[1]);
  not not_106 (not_106_out, OP[5]);
  not not_107 (not_107_out, OP[4]);
  not not_108 (not_108_out, OP[2]);
  not not_109 (not_109_out, OP[1]);
  not not_110 (not_110_out, OP[0]);
  not not_111 (not_111_out, OP[5]);
  not not_112 (not_112_out, OP[4]);
  not not_113 (not_113_out, OP[1]);
  not not_114 (not_114_out, OP[0]);
  not not_115 (not_115_out, OP[5]);
  not not_116 (not_116_out, OP[4]);
  not not_117 (not_117_out, OP[2]);
  not not_118 (not_118_out, OP[1]);
  not not_119 (not_119_out, OP[5]);
  not not_120 (not_120_out, OP[4]);
  not not_121 (not_121_out, OP[2]);
  not not_122 (not_122_out, OP[0]);
  not not_123 (not_123_out, OP[5]);
  not not_124 (not_124_out, OP[4]);
  not not_125 (not_125_out, OP[1]);
  not not_126 (not_126_out, OP[4]);
  not not_127 (not_127_out, OP[3]);
  not not_128 (not_128_out, OP[2]);
  not not_129 (not_129_out, OP[4]);
  not not_130 (not_130_out, OP[2]);
  not not_131 (not_131_out, OP[5]);
  not not_132 (not_132_out, OP[4]);
  not not_133 (not_133_out, OP[3]);
  not not_134 (not_134_out, OP[2]);
  not not_135 (not_135_out, OP[1]);
  not not_136 (not_136_out, OP[0]);
  not not_137 (not_137_out, Funct[5]);
  not not_138 (not_138_out, Funct[4]);
  not not_139 (not_139_out, Funct[3]);
  not not_140 (not_140_out, Funct[1]);
  not not_141 (not_141_out, Funct[0]);
  not not_142 (not_142_out, OP[5]);
  not not_143 (not_143_out, OP[4]);
  not not_144 (not_144_out, OP[3]);
  not not_145 (not_145_out, OP[2]);
  not not_146 (not_146_out, OP[1]);
  not not_147 (not_147_out, OP[0]);
  not not_148 (not_148_out, Funct[5]);
  not not_149 (not_149_out, Funct[4]);
  not not_150 (not_150_out, Funct[3]);
  not not_151 (not_151_out, OP[4]);
  not not_152 (not_152_out, OP[3]);
  not not_153 (not_153_out, OP[1]);
  not not_154 (not_154_out, OP[0]);
  not not_155 (not_155_out, OP[5]);
  not not_156 (not_156_out, OP[4]);
  not not_157 (not_157_out, OP[3]);
  not not_158 (not_158_out, OP[2]);
  not not_159 (not_159_out, OP[1]);
  not not_160 (not_160_out, OP[5]);
  not not_161 (not_161_out, OP[4]);
  not not_162 (not_162_out, OP[3]);
  not not_163 (not_163_out, OP[2]);
  not not_164 (not_164_out, OP[1]);
  not not_165 (not_165_out, OP[0]);
  not not_166 (not_166_out, Funct[5]);
  not not_167 (not_167_out, Funct[4]);
  not not_168 (not_168_out, Funct[3]);
  not not_169 (not_169_out, Funct[2]);
  not not_170 (not_170_out, Funct[1]);
  not not_171 (not_171_out, Funct[0]);
  not not_172 (not_172_out, OP[5]);
  not not_173 (not_173_out, OP[4]);
  not not_174 (not_174_out, OP[3]);
  not not_175 (not_175_out, OP[2]);
  not not_176 (not_176_out, OP[1]);
  not not_177 (not_177_out, OP[0]);
  not not_178 (not_178_out, Funct[5]);
  not not_179 (not_179_out, Funct[4]);
  not not_180 (not_180_out, Funct[3]);
  not not_181 (not_181_out, Funct[2]);
  not not_182 (not_182_out, OP[5]);
  not not_183 (not_183_out, OP[4]);
  not not_184 (not_184_out, OP[3]);
  not not_185 (not_185_out, OP[2]);
  not not_186 (not_186_out, OP[1]);
  not not_187 (not_187_out, OP[0]);
  not not_188 (not_188_out, Funct[5]);
  not not_189 (not_189_out, Funct[4]);
  not not_190 (not_190_out, Funct[3]);
  not not_191 (not_191_out, Funct[2]);
  not not_192 (not_192_out, Funct[0]);
  not not_193 (not_193_out, OP[5]);
  not not_194 (not_194_out, OP[4]);
  not not_195 (not_195_out, OP[3]);
  not not_196 (not_196_out, OP[2]);
  not not_197 (not_197_out, OP[1]);
  not not_198 (not_198_out, OP[0]);
  not not_199 (not_199_out, Funct[4]);
  not not_200 (not_200_out, Funct[3]);
  not not_201 (not_201_out, Funct[2]);
  not not_202 (not_202_out, Funct[1]);
  not not_203 (not_203_out, Funct[0]);
  not not_204 (not_204_out, OP[5]);
  not not_205 (not_205_out, OP[4]);
  not not_206 (not_206_out, OP[3]);
  not not_207 (not_207_out, OP[2]);
  not not_208 (not_208_out, OP[1]);
  not not_209 (not_209_out, OP[0]);
  not not_210 (not_210_out, Funct[4]);
  not not_211 (not_211_out, Funct[3]);
  not not_212 (not_212_out, Funct[2]);
  not not_213 (not_213_out, Funct[1]);
  not not_214 (not_214_out, OP[5]);
  not not_215 (not_215_out, OP[4]);
  not not_216 (not_216_out, OP[3]);
  not not_217 (not_217_out, OP[2]);
  not not_218 (not_218_out, OP[1]);
  not not_219 (not_219_out, OP[0]);
  not not_220 (not_220_out, Funct[4]);
  not not_221 (not_221_out, Funct[3]);
  not not_222 (not_222_out, Funct[2]);
  not not_223 (not_223_out, Funct[0]);
  not not_224 (not_224_out, OP[5]);
  not not_225 (not_225_out, OP[4]);
  not not_226 (not_226_out, OP[3]);
  not not_227 (not_227_out, OP[2]);
  not not_228 (not_228_out, OP[1]);
  not not_229 (not_229_out, OP[0]);
  not not_230 (not_230_out, Funct[4]);
  not not_231 (not_231_out, Funct[3]);
  not not_232 (not_232_out, Funct[1]);
  not not_233 (not_233_out, Funct[0]);
  not not_234 (not_234_out, OP[5]);
  not not_235 (not_235_out, OP[4]);
  not not_236 (not_236_out, OP[3]);
  not not_237 (not_237_out, OP[2]);
  not not_238 (not_238_out, OP[1]);
  not not_239 (not_239_out, OP[0]);
  not not_240 (not_240_out, Funct[4]);
  not not_241 (not_241_out, Funct[3]);
  not not_242 (not_242_out, Funct[1]);
  not not_243 (not_243_out, OP[5]);
  not not_244 (not_244_out, OP[4]);
  not not_245 (not_245_out, OP[3]);
  not not_246 (not_246_out, OP[2]);
  not not_247 (not_247_out, OP[1]);
  not not_248 (not_248_out, OP[0]);
  not not_249 (not_249_out, Funct[4]);
  not not_250 (not_250_out, Funct[3]);
  not not_251 (not_251_out, OP[5]);
  not not_252 (not_252_out, OP[4]);
  not not_253 (not_253_out, OP[3]);
  not not_254 (not_254_out, OP[2]);
  not not_255 (not_255_out, OP[1]);
  not not_256 (not_256_out, OP[0]);
  not not_257 (not_257_out, Funct[4]);
  not not_258 (not_258_out, Funct[2]);
  not not_259 (not_259_out, Funct[0]);
  not not_260 (not_260_out, OP[5]);
  not not_261 (not_261_out, OP[4]);
  not not_262 (not_262_out, OP[3]);
  not not_263 (not_263_out, OP[2]);
  not not_264 (not_264_out, OP[1]);
  not not_265 (not_265_out, OP[0]);
  not not_266 (not_266_out, Funct[4]);
  not not_267 (not_267_out, Funct[2]);
  not not_268 (not_268_out, OP[5]);
  not not_269 (not_269_out, OP[4]);
  not not_270 (not_270_out, OP[3]);
  not not_271 (not_271_out, OP[2]);
  not not_272 (not_272_out, OP[1]);
  not not_273 (not_273_out, OP[0]);
  not not_274 (not_274_out, Funct[5]);
  not not_275 (not_275_out, Funct[4]);
  not not_276 (not_276_out, Funct[1]);
  not not_277 (not_277_out, Funct[0]);
  not not_278 (not_278_out, OP[5]);
  not not_279 (not_279_out, OP[4]);
  not not_280 (not_280_out, OP[3]);
  not not_281 (not_281_out, OP[1]);
  not not_282 (not_282_out, OP[0]);
  not not_283 (not_283_out, OP[5]);
  not not_284 (not_284_out, OP[4]);
  not not_285 (not_285_out, OP[3]);
  not not_286 (not_286_out, OP[1]);
  not not_287 (not_287_out, OP[4]);
  not not_288 (not_288_out, OP[2]);
  not not_289 (not_289_out, OP[5]);
  not not_290 (not_290_out, OP[4]);
  not not_291 (not_291_out, OP[3]);
  not not_292 (not_292_out, OP[2]);
  not not_293 (not_293_out, OP[1]);
  not not_294 (not_294_out, OP[0]);
  not not_295 (not_295_out, Funct[5]);
  not not_296 (not_296_out, Funct[4]);
  not not_297 (not_297_out, Funct[3]);
  not not_298 (not_298_out, Funct[1]);
  not not_299 (not_299_out, Funct[0]);
  not not_300 (not_300_out, OP[5]);
  not not_301 (not_301_out, OP[4]);
  not not_302 (not_302_out, OP[3]);
  not not_303 (not_303_out, OP[2]);
  not not_304 (not_304_out, OP[1]);
  not not_305 (not_305_out, OP[0]);
  not not_306 (not_306_out, Funct[5]);
  not not_307 (not_307_out, Funct[4]);
  not not_308 (not_308_out, Funct[3]);
  and and_1 (and_1_out, not_1_out, not_2_out, not_3_out, not_4_out, not_5_out, not_6_out, Funct[5], not_7_out, not_8_out, not_9_out, not_10_out, not_11_out);
  and and_2 (and_2_out, not_12_out, not_13_out, not_14_out, not_15_out, not_16_out, not_17_out, Funct[5], not_18_out, not_19_out, not_20_out, not_21_out, Funct[0]);
  and and_3 (and_3_out, not_22_out, not_23_out, not_24_out, not_25_out, not_26_out, not_27_out, Funct[5], not_28_out, not_29_out, not_30_out, Funct[1], not_31_out);
  and and_4 (and_4_out, not_32_out, not_33_out, not_34_out, not_35_out, not_36_out, not_37_out, Funct[5], not_38_out, not_39_out, Funct[2], not_40_out, not_41_out);
  and and_5 (and_5_out, not_42_out, not_43_out, not_44_out, not_45_out, not_46_out, not_47_out, Funct[5], not_48_out, not_49_out, Funct[2], not_50_out, Funct[0]);
  and and_6 (and_6_out, not_51_out, not_52_out, not_53_out, not_54_out, not_55_out, not_56_out, Funct[5], not_57_out, not_58_out, Funct[2], Funct[1], Funct[0]);
  and and_7 (and_7_out, not_59_out, not_60_out, not_61_out, not_62_out, not_63_out, not_64_out, Funct[5], not_65_out, Funct[3], not_66_out, Funct[1], not_67_out);
  and and_8 (and_8_out, not_68_out, not_69_out, not_70_out, not_71_out, not_72_out, not_73_out, Funct[5], not_74_out, Funct[3], not_75_out, Funct[1], Funct[0]);
  and and_9 (and_9_out, not_76_out, not_77_out, not_78_out, not_79_out, not_80_out, not_81_out, not_82_out, not_83_out, Funct[3], not_84_out, not_85_out, not_86_out);
  and and_10 (and_10_out, not_87_out, not_88_out, not_89_out, not_90_out, not_91_out, not_92_out, not_93_out, not_94_out, Funct[3], Funct[2], not_95_out, not_96_out);
  and and_11 (and_11_out, not_97_out, not_98_out, not_99_out, OP[2], not_100_out, not_101_out);
  and and_12 (and_12_out, not_102_out, not_103_out, not_104_out, OP[2], not_105_out, OP[0]);
  and and_13 (and_13_out, not_106_out, not_107_out, OP[3], not_108_out, not_109_out, not_110_out);
  and and_14 (and_14_out, not_111_out, not_112_out, OP[3], OP[2], not_113_out, not_114_out);
  and and_15 (and_15_out, not_115_out, not_116_out, OP[3], not_117_out, not_118_out, OP[0]);
  and and_16 (and_16_out, not_119_out, not_120_out, OP[3], not_121_out, OP[1], not_122_out);
  and and_17 (and_17_out, not_123_out, not_124_out, OP[3], OP[2], not_125_out, OP[0]);
  and and_18 (and_18_out, OP[5], not_126_out, not_127_out, not_128_out, OP[1], OP[0]);
  and and_19 (and_19_out, OP[5], not_129_out, OP[3], not_130_out, OP[1], OP[0]);
  and and_20 (and_20_out, not_131_out, not_132_out, not_133_out, not_134_out, not_135_out, not_136_out, not_137_out, not_138_out, not_139_out, Funct[2], not_140_out, not_141_out);
  and and_21 (and_21_out, not_142_out, not_143_out, not_144_out, not_145_out, not_146_out, not_147_out, not_148_out, not_149_out, not_150_out, Funct[2], Funct[1], Funct[0]);
  and and_22 (and_22_out, OP[5], not_151_out, not_152_out, OP[2], not_153_out, not_154_out);
  and and_23 (and_23_out, not_155_out, not_156_out, not_157_out, not_158_out, not_159_out, OP[0]);
  and and_24 (and_24_out, not_160_out, not_161_out, not_162_out, not_163_out, not_164_out, not_165_out, not_166_out, not_167_out, not_168_out, not_169_out, not_170_out, not_171_out);
  and and_25 (and_25_out, not_172_out, not_173_out, not_174_out, not_175_out, not_176_out, not_177_out, not_178_out, not_179_out, not_180_out, not_181_out, Funct[1], Funct[0]);
  and and_26 (and_26_out, not_182_out, not_183_out, not_184_out, not_185_out, not_186_out, not_187_out, not_188_out, not_189_out, not_190_out, not_191_out, Funct[1], not_192_out);
  and and_27 (and_27_out, not_193_out, not_194_out, not_195_out, not_196_out, not_197_out, not_198_out, Funct[5], not_199_out, not_200_out, not_201_out, not_202_out, not_203_out);
  and and_28 (and_28_out, not_204_out, not_205_out, not_206_out, not_207_out, not_208_out, not_209_out, Funct[5], not_210_out, not_211_out, not_212_out, not_213_out, Funct[0]);
  and and_29 (and_29_out, not_214_out, not_215_out, not_216_out, not_217_out, not_218_out, not_219_out, Funct[5], not_220_out, not_221_out, not_222_out, Funct[1], not_223_out);
  and and_30 (and_30_out, not_224_out, not_225_out, not_226_out, not_227_out, not_228_out, not_229_out, Funct[5], not_230_out, not_231_out, Funct[2], not_232_out, not_233_out);
  and and_31 (and_31_out, not_234_out, not_235_out, not_236_out, not_237_out, not_238_out, not_239_out, Funct[5], not_240_out, not_241_out, Funct[2], not_242_out, Funct[0]);
  and and_32 (and_32_out, not_243_out, not_244_out, not_245_out, not_246_out, not_247_out, not_248_out, Funct[5], not_249_out, not_250_out, Funct[2], Funct[1], Funct[0]);
  and and_33 (and_33_out, not_251_out, not_252_out, not_253_out, not_254_out, not_255_out, not_256_out, Funct[5], not_257_out, Funct[3], not_258_out, Funct[1], not_259_out);
  and and_34 (and_34_out, not_260_out, not_261_out, not_262_out, not_263_out, not_264_out, not_265_out, Funct[5], not_266_out, Funct[3], not_267_out, Funct[1], Funct[0]);
  and and_35 (and_35_out, not_268_out, not_269_out, not_270_out, not_271_out, not_272_out, not_273_out, not_274_out, not_275_out, Funct[3], Funct[2], not_276_out, not_277_out);
  and and_36 (and_36_out, not_278_out, not_279_out, not_280_out, OP[2], not_281_out, not_282_out);
  and and_37 (and_37_out, not_283_out, not_284_out, not_285_out, OP[2], not_286_out, OP[0]);
  and and_38 (and_38_out, OP[5], not_287_out, OP[3], not_288_out, OP[1], OP[0]);
  and and_39 (and_39_out, not_289_out, not_290_out, not_291_out, not_292_out, not_293_out, not_294_out, not_295_out, not_296_out, not_297_out, Funct[2], not_298_out, not_299_out);
  and and_40 (and_40_out, not_300_out, not_301_out, not_302_out, not_303_out, not_304_out, not_305_out, not_306_out, not_307_out, not_308_out, Funct[2], Funct[1], Funct[0]);
  or or_1 (R2_Used, and_24_out, and_25_out, and_26_out, and_27_out, and_28_out, and_29_out, and_30_out, and_31_out, and_32_out, and_33_out, and_34_out, and_35_out, and_36_out, and_37_out, and_38_out, and_39_out, and_40_out);
  or or_2 (R1_Used, and_1_out, and_2_out, and_3_out, and_4_out, and_5_out, and_6_out, and_7_out, and_8_out, and_9_out, and_10_out, and_11_out, and_12_out, and_13_out, and_14_out, and_15_out, and_16_out, and_17_out, and_18_out, and_19_out, and_20_out, and_21_out, and_22_out, and_23_out);
endmodule

module \数据相关检测  (
  input  [4:0] R1_num,
  input  [4:0] MEM_WriteReg_num,
  input  MEM_RegWrite,
  input  [4:0] EX_WriteReg_num,
  input  EX_RegWrite,
  input  R1_Used,
  input  [4:0] R2_num,
  input  R2_Used,
  output Correlated
);

  wire and_1_out, and_2_out, and_3_out, and_4_out, and_5_out, and_6_out, comparator_1_eq, comparator_2_eq,
       comparator_3_eq, comparator_4_eq, comparator_5_eq, comparator_6_eq, or_1_out, or_2_out;

  Comparator #(.width(5), .mode("twosComplement")) comparator_1 (
    .a(R1_num), .b(MEM_WriteReg_num), .eq(comparator_1_eq));  // open: gt, lt
  Comparator #(.width(5), .mode("twosComplement")) comparator_2 (
    .a(R1_num), .b(EX_WriteReg_num), .eq(comparator_2_eq));  // open: gt, lt
  Comparator #(.width(5), .mode("twosComplement")) comparator_3 (
    .a(R1_num), .b({5{1'b0}}), .eq(comparator_3_eq));  // open: gt, lt
  Comparator #(.width(5), .mode("twosComplement")) comparator_4 (
    .a(R2_num), .b(MEM_WriteReg_num), .eq(comparator_4_eq));  // open: gt, lt
  Comparator #(.width(5), .mode("twosComplement")) comparator_5 (
    .a(R2_num), .b(EX_WriteReg_num), .eq(comparator_5_eq));  // open: gt, lt
  Comparator #(.width(5), .mode("twosComplement")) comparator_6 (
    .a(R2_num), .b({5{1'b0}}), .eq(comparator_6_eq));  // open: gt, lt
  and and_1 (and_1_out, comparator_1_eq, MEM_RegWrite);
  or or_1 (or_1_out, and_1_out, and_2_out);
  and and_2 (and_2_out, comparator_2_eq, EX_RegWrite);
  and and_3 (and_3_out, comparator_4_eq, MEM_RegWrite);
  or or_2 (or_2_out, and_3_out, and_4_out);
  and and_4 (and_4_out, comparator_5_eq, EX_RegWrite);
  and and_5 (and_5_out, or_1_out, ~comparator_3_eq, R1_Used);  // AND_Gate
  and and_6 (and_6_out, or_2_out, ~comparator_6_eq, R2_Used);  // AND_Gate
  or or_3 (Correlated, and_5_out, and_6_out);
endmodule

module \重定向数据相关检测  (
  input  [4:0] R1_num,
  input  [4:0] MEM_WriteReg_num,
  input  MEM_RegWrite,
  input  R1_Used,
  input  [4:0] EX_WriteReg_num,
  input  EX_RegWrite,
  input  Load_Use,
  input  [4:0] R2_num,
  input  R2_Used,
  output [1:0] R1,
  output LoadUse,
  output [1:0] R2
);

  wire and_1_out, and_2_out, and_3_out, and_4_out, comparator_1_eq, comparator_2_eq, comparator_3_eq,
       comparator_4_eq, comparator_5_eq, comparator_6_eq, comparator_7_eq, comparator_8_eq, or_1_out;
  wire [1:0] and_6_out, and_8_out;

  Comparator #(.width(5), .mode("twosComplement")) comparator_1 (
    .a(R1_num), .b(MEM_WriteReg_num), .eq(comparator_1_eq));  // open: gt, lt
  Comparator #(.width(5), .mode("twosComplement")) comparator_2 (
    .a(R1_num), .b({5{1'b0}}), .eq(comparator_2_eq));  // open: gt, lt
  Comparator #(.width(5), .mode("twosComplement")) comparator_3 (
    .a(R1_num), .b(EX_WriteReg_num), .eq(comparator_3_eq));  // open: gt, lt
  Comparator #(.width(5), .mode("twosComplement")) comparator_4 (
    .a(R1_num), .b({5{1'b0}}), .eq(comparator_4_eq));  // open: gt, lt
  Comparator #(.width(5), .mode("twosComplement")) comparator_5 (
    .a(R2_num), .b(MEM_WriteReg_num), .eq(comparator_5_eq));  // open: gt, lt
  Comparator #(.width(5), .mode("twosComplement")) comparator_6 (
    .a(R2_num), .b({5{1'b0}}), .eq(comparator_6_eq));  // open: gt, lt
  Comparator #(.width(5), .mode("twosComplement")) comparator_7 (
    .a(R2_num), .b(EX_WriteReg_num), .eq(comparator_7_eq));  // open: gt, lt
  Comparator #(.width(5), .mode("twosComplement")) comparator_8 (
    .a(R2_num), .b({5{1'b0}}), .eq(comparator_8_eq));  // open: gt, lt
  and and_1 (and_1_out, comparator_1_eq, MEM_RegWrite);
  and and_2 (and_2_out, comparator_3_eq, EX_RegWrite);
  and and_3 (and_3_out, comparator_5_eq, MEM_RegWrite);
  and and_4 (and_4_out, comparator_7_eq, EX_RegWrite);
  and and_5 (and_6_out[1], and_1_out, ~comparator_2_eq, R1_Used);  // AND_Gate
  and and_6 (and_6_out[0], and_2_out, ~comparator_4_eq, R1_Used);  // AND_Gate
  and and_7 (and_8_out[1], and_3_out, ~comparator_6_eq, R2_Used);  // AND_Gate
  and and_8 (and_8_out[0], and_4_out, ~comparator_8_eq, R2_Used);  // AND_Gate
  Multiplexer #(.select(1), .width(2), .disabled("Z"), .enable("false")) multiplexer_1 (
    .in0(and_6_out), .in1(2'b00), .out(R1), .sel(LoadUse));
  Multiplexer #(.select(1), .width(2), .disabled("Z"), .enable("false")) multiplexer_2 (
    .in0(and_8_out), .in1(2'b00), .out(R2), .sel(LoadUse));
  or or_1 (or_1_out, and_6_out[0], and_8_out[0]);
  and and_9 (LoadUse, or_1_out, Load_Use);
endmodule
