// Logisim project 电路图.circ as structural Verilog: 22 circuits, main circuit ◆单周期硬布线控制器
module \单周期MIPS  (
  input  IR1,
  input  IR2,
  input  IR3,
  input  in_4,
  input  in_5,
  input  in_6,
  input  in_7,
  input  in_8,
  input  in_9,
  input  in_10,
  input  in_11,
  input  in_12,
  input  in_13,
  input  in_14,
  input  in_15,
  input  in_16,
  input  in_17,
  input  in_18,
  input  in_19,
  input  in_20,
  input  in_21,
  input  in_22,
  input  in_23,
  input  in_24,
  input  in_25,
  input  in_26,
  input  in_27,
  input  in_28,
  input  in_29,
  input  in_30,
  input  in_31,
  input  in_32,
  input  in_33,
  input  in_34,
  input  in_35,
  input  in_36,
  input  in_37,
  input  in_38,
  input  in_39,
  input  in_40,
  input  in_41,
  input  in_42,
  input  in_43,
  input  in_44,
  input  in_45,
  input  in_46,
  input  in_47,
  input  in_48,
  input  in_49,
  input  in_50,
  input  in_51,
  input  in_52,
  input  in_53,
  input  in_54,
  input  in_55,
  input  in_56,
  input  in_57,
  input  in_58,
  input  in_59,
  input  in_60,
  input  in_61,
  input  in_62,
  input  in_63,
  input  in_64,
  input  in_65,
  input  in_66,
  input  in_67,
  input  in_68,
  input  in_69,
  input  in_70,
  input  in_71,
  input  in_72,
  input  in_73,
  input  in_74,
  input  in_75,
  input  in_76,
  input  in_77,
  input  in_78,
  input  in_79,
  input  in_80,
  input  in_81,
  input  in_82,
  input  in_83,
  input  in_84,
  input  in_85,
  input  in_86,
  input  in_87,
  input  in_88,
  input  in_89,
  input  in_90,
  input  in_91,
  input  in_92,
  input  in_93,
  input  in_94,
  input  in_95,
  input  in_96,
  input  in_97,
  input  in_98,
  input  in_99,
  input  in_100,
  input  in_101,
  input  in_102,
  input  in_103,
  input  in_104,
  input  in_105,
  input  in_106,
  input  in_107,
  input  in_108,
  input  in_109,
  input  in_110,
  input  in_111,
  input  in_112,
  input  in_113,
  input  in_114,
  input  in_115,
  input  in_116,
  input  in_117,
  input  in_118,
  input  in_119,
  input  in_120,
  input  in_121,
  input  in_122,
  input  in_123,
  input  in_124,
  input  in_125,
  input  in_126,
  input  in_127,
  input  in_128,
  input  in_129,
  input  in_130,
  input  in_131,
  input  in_132,
  input  in_133,
  input  in_134,
  input  in_135,
  input  in_136,
  input  in_137,
  input  in_138,
  input  in_139,
  input  in_140,
  input  in_141,
  input  in_142,
  input  in_143,
  input  in_144,
  input  in_145,
  input  in_146,
  input  in_147,
  input  in_148,
  input  in_149,
  input  in_150,
  input  in_151,
  input  in_152,
  input  in_153,
  input  in_154,
  input  in_155,
  input  in_156,
  input  in_157,
  input  in_158,
  input  in_159,
  input  in_160,
  input  in_161,
  input  in_162,
  input  in_163,
  input  in_164,
  input  in_165,
  input  in_166,
  input  in_167,
  input  in_168,
  input  in_169,
  input  in_170,
  input  in_171,
  input  in_172,
  input  in_173,
  input  in_174,
  input  in_175,
  input  in_176,
  input  in_177,
  input  in_178,
  input  in_179,
  input  in_180,
  input  in_181,
  input  in_182,
  input  in_183,
  input  in_184,
  input  in_185,
  input  in_186,
  input  in_187,
  input  in_188,
  input  in_189,
  input  in_190,
  input  in_191,
  input  in_192,
  input  in_193,
  input  in_194,
  input  in_195,
  input  in_196,
  input  in_197,
  input  in_198,
  input  in_199,
  input  in_200,
  input  in_201,
  input  in_202,
  input  in_203,
  input  in_204,
  input  in_205,
  input  in_206,
  input  in_207,
  input  in_208,
  input  in_209,
  input  in_210,
  input  in_211,
  input  in_212,
  input  in_213,
  input  in_214,
  input  in_215,
  input  in_216,
  input  in_217,
  input  in_218,
  input  in_219,
  input  in_220,
  input  in_221,
  input  in_222,
  input  in_223,
  input  in_224,
  input  in_225,
  input  in_226,
  input  in_227,
  input  in_228,
  input  in_229,
  input  in_230,
  input  in_231,
  input  in_232,
  input  in_233,
  input  in_234,
  input  in_235,
  input  in_236,
  input  in_237,
  input  in_238,
  input  in_239,
  input  in_240,
  input  in_241,
  input  in_242,
  input  in_243,
  input  in_244,
  input  in_245,
  input  in_246,
  input  in_247,
  input  in_248,
  input  in_249,
  input  in_250,
  input  in_251,
  input  in_252,
  input  in_253,
  input  in_254,
  input  in_255,
  input  in_256,
  input  in_257,
  input  in_258,
  input  in_259,
  input  in_260,
  input  in_261,
  input  in_262,
  input  in_263,
  input  in_264,
  input  in_265,
  input  in_266,
  input  in_267,
  input  in_268,
  input  in_269,
  input  in_270,
  input  in_271,
  input  in_272,
  input  in_273,
  input  in_274,
  input  in_275,
  input  in_276,
  input  in_277,
  input  in_278,
  input  in_279,
  input  in_280,
  input  in_281,
  input  in_282,
  input  in_283,
  input  in_284,
  input  in_285,
  input  in_286,
  input  in_287,
  input  in_288,
  input  in_289,
  input  in_290,
  input  in_291,
  input  in_292,
  input  in_293,
  input  in_294,
  input  in_295,
  input  in_296,
  input  in_297,
  input  in_298,
  input  in_299,
  input  in_300,
  input  in_301,
  input  in_302,
  input  in_303,
  input  in_304,
  input  in_305,
  input  in_306,
  input  in_307,
  input  in_308,
  input  in_309,
  input  in_310,
  input  in_311,
  input  in_312,
  input  in_313,
  input  in_314,
  input  in_315,
  input  in_316,
  input  in_317,
  input  in_318,
  input  in_319,
  input  in_320,
  input  in_321,
  input  in_322,
  input  in_323,
  input  in_324,
  input  in_325,
  input  in_326,
  input  in_327,
  input  in_328,
  input  in_329,
  input  in_330,
  input  in_331,
  input  in_332,
  input  in_333,
  input  in_334,
  input  in_335,
  input  in_336,
  input  in_337,
  input  in_338,
  input  in_339,
  input  in_340,
  input  in_341,
  input  in_342,
  input  in_343,
  input  in_344,
  input  in_345,
  input  in_346,
  input  in_347,
  input  in_348,
  input  in_349,
  input  in_350,
  input  in_351,
  input  in_352,
  input  in_353,
  input  in_354,
  input  in_355,
  input  in_356,
  input  in_357,
  input  in_358,
  input  in_359,
  input  in_360,
  input  in_361,
  input  in_362,
  input  in_363,
  input  in_364,
  input  in_365,
  input  in_366,
  input  in_367,
  input  \开始计算 ,
  input  in_369,
  input  in_370,
  input  in_371,
  input  in_372,
  input  in_373,
  input  in_374,
  input  in_375,
  input  in_376,
  input  in_377,
  input  in_378,
  input  in_379,
  input  in_380,
  input  in_381,
  input  in_382,
  input  in_383,
  input  in_384,
  input  in_385,
  input  in_386,
  input  in_387,
  input  in_388,
  input  in_389,
  input  in_390,
  input  in_391,
  input  in_392,
  input  in_393,
  input  in_394,
  input  in_395,
  input  in_396,
  input  in_397,
  input  in_398,
  input  in_399,
  input  in_400,
  input  in_401,
  input  in_402,
  input  in_403,
  input  in_404,
  input  in_405,
  input  in_406,
  input  in_407,
  input  in_408,
  input  in_409,
  input  in_410,
  input  in_411,
  input  in_412,
  input  in_413,
  input  in_414,
  input  in_415,
  input  in_416,
  input  in_417,
  input  in_418,
  input  in_419,
  input  in_420,
  input  in_421,
  input  in_422,
  input  in_423,
  input  in_424,
  input  in_425,
  input  in_426,
  input  in_427,
  input  in_428,
  input  in_429,
  input  in_430,
  input  in_431,
  input  in_432,
  input  in_433,
  input  in_434,
  input  in_435,
  input  in_436,
  input  in_437,
  input  in_438,
  input  in_439,
  input  in_440,
  input  in_441,
  input  in_442,
  input  in_443,
  input  in_444,
  input  in_445,
  input  in_446,
  input  in_447,
  input  in_448,
  input  in_449,
  input  in_450,
  input  in_451,
  input  in_452,
  input  in_453,
  input  in_454,
  input  in_455,
  input  in_456,
  input  in_457,
  input  in_458,
  input  in_459,
  input  in_460,
  input  in_461,
  input  in_462,
  input  in_463,
  input  in_464,
  input  in_465,
  input  in_466,
  input  in_467,
  input  in_468,
  input  in_469,
  input  in_470,
  input  in_471,
  input  in_472,
  input  in_473,
  input  in_474,
  input  in_475,
  input  in_476,
  input  in_477,
  input  in_478,
  input  in_479,
  input  in_480,
  input  in_481,
  input  in_482,
  input  in_483,
  input  in_484,
  input  in_485,
  input  in_486,
  input  in_487,
  input  in_488,
  input  in_489,
  input  in_490,
  input  in_491,
  input  in_492,
  input  in_493,
  input  in_494,
  input  in_495,
  input  in_496,
  input  in_497,
  input  in_498,
  input  in_499,
  input  in_500,
  input  in_501,
  input  in_502,
  input  in_503,
  input  in_504,
  input  in_505,
  input  in_506,
  input  in_507,
  input  in_508,
  input  in_509,
  input  in_510,
  input  in_511,
  input  in_512,
  input  in_513,
  input  in_514,
  input  in_515,
  input  in_516,
  input  in_517,
  input  in_518,
  input  in_519,
  input  in_520,
  input  in_521,
  input  in_522,
  input  in_523,
  input  in_524,
  input  in_525,
  input  in_526,
  input  in_527,
  input  in_528,
  input  in_529,
  input  in_530,
  input  in_531,
  input  in_532,
  input  in_533,
  input  in_534,
  input  in_535,
  input  in_536,
  input  in_537,
  input  in_538,
  input  in_539,
  input  in_540,
  input  in_541,
  input  in_542,
  input  in_543,
  input  in_544,
  input  in_545,
  input  in_546,
  input  in_547,
  input  in_548,
  input  in_549,
  input  in_550,
  input  in_551,
  input  in_552,
  input  in_553,
  input  in_554,
  input  in_555,
  input  in_556,
  input  in_557,
  input  in_558,
  input  in_559,
  input  in_560,
  input  in_561,
  input  in_562,
  input  in_563,
  input  in_564,
  input  in_565,
  input  in_566,
  input  in_567,
  input  in_568,
  input  in_569,
  input  in_570,
  input  in_571,
  input  in_572,
  input  in_573,
  input  in_574,
  input  in_575,
  input  in_576,
  input  in_577,
  input  in_578,
  input  in_579,
  input  in_580,
  input  in_581,
  input  in_582,
  input  in_583,
  input  in_584,
  input  in_585,
  input  in_586,
  input  in_587,
  input  in_588,
  input  in_589,
  input  in_590,
  input  in_591,
  input  in_592,
  input  in_593,
  input  in_594,
  input  in_595,
  input  in_596,
  input  in_597,
  input  in_598,
  input  in_599,
  input  in_600,
  input  in_601,
  input  in_602,
  input  in_603,
  input  in_604,
  input  in_605,
  input  in_606,
  input  in_607,
  input  in_608,
  input  in_609,
  input  in_610,
  input  in_611,
  input  in_612,
  input  in_613,
  input  in_614,
  input  in_615,
  input  in_616,
  input  in_617,
  input  in_618,
  input  in_619,
  input  in_620,
  input  in_621,
  input  in_622,
  input  in_623,
  input  in_624,
  input  in_625,
  input  in_626,
  input  in_627,
  input  in_628,
  input  in_629,
  input  in_630,
  input  in_631,
  input  in_632,
  input  in_633,
  input  in_634,
  input  in_635,
  input  in_636,
  input  in_637,
  input  in_638,
  input  in_639,
  input  in_640,
  input  in_641,
  input  in_642,
  input  in_643,
  input  in_644,
  input  in_645,
  input  in_646,
  input  in_647,
  input  in_648,
  input  in_649,
  input  in_650,
  input  in_651,
  input  in_652,
  input  in_653,
  input  in_654,
  input  in_655,
  input  in_656,
  input  in_657,
  input  in_658,
  input  in_659,
  input  in_660,
  input  in_661,
  input  in_662,
  input  in_663,
  input  in_664,
  input  in_665,
  input  in_666,
  input  in_667,
  input  in_668,
  input  in_669,
  input  in_670,
  input  in_671,
  input  in_672,
  input  in_673,
  input  in_674,
  input  in_675,
  input  in_676,
  input  in_677,
  input  in_678,
  input  in_679,
  input  in_680,
  input  in_681,
  input  in_682,
  input  in_683,
  input  in_684,
  input  in_685,
  input  in_686,
  input  in_687,
  input  in_688,
  input  in_689,
  input  in_690,
  input  in_691,
  input  in_692,
  input  in_693,
  input  in_694,
  input  in_695,
  input  in_696,
  input  in_697,
  input  in_698,
  input  in_699,
  input  in_700,
  input  in_701,
  input  in_702,
  input  in_703,
  input  in_704,
  input  in_705,
  input  in_706,
  input  in_707,
  input  in_708,
  input  in_709,
  input  in_710,
  input  in_711,
  input  in_712,
  input  in_713,
  input  in_714,
  input  in_715,
  input  in_716,
  input  in_717,
  input  in_718,
  input  in_719,
  input  in_720,
  input  in_721,
  input  in_722,
  input  in_723,
  input  in_724,
  input  in_725,
  input  in_726,
  input  in_727,
  input  in_728,
  input  in_729,
  input  in_730,
  input  in_731,
  input  in_732,
  input  in_733,
  input  in_734,
  input  in_735,
  input  in_736,
  input  in_737,
  input  in_738,
  input  in_739,
  input  in_740,
  input  in_741,
  input  in_742,
  input  in_743,
  input  in_744,
  input  in_745,
  input  in_746,
  input  in_747,
  input  in_748,
  input  in_749,
  input  in_750,
  input  in_751,
  input  in_752,
  input  in_753,
  input  in_754,
  input  in_755,
  input  in_756,
  input  in_757,
  input  in_758,
  input  in_759,
  input  in_760,
  input  in_761,
  input  in_762,
  input  in_763,
  input  in_764,
  input  in_765,
  input  in_766,
  input  in_767,
  input  in_768,
  input  in_769,
  input  in_770,
  input  in_771,
  input  in_772,
  input  in_773,
  input  in_774,
  input  in_775,
  input  in_776,
  input  in_777,
  input  in_778,
  input  in_779,
  input  in_780,
  input  in_781,
  input  in_782,
  input  in_783,
  input  in_784,
  input  in_785,
  input  in_786,
  input  in_787,
  input  in_788,
  output RegWrite,
  output MemWrite,
  output [31:0] PC,
  output [31:0] IR,
  output [31:0] RDin,
  output [31:0] MDin,
  output [31:0] LedData
);

  wire and_1_out, and_2_out, and_3_out, and_4_out, and_5_out, and_6_out, and_7_out, BGEZ, Branch, CLK,
       clock_2_out, comparator_1_eq, comparator_1_lt, comparator_2_eq, CPU_On, CPUCLK, d_ff_1_q, Go, Halt,
       InputStop, IR1_t, IR2_t, IR3_t, IRA, IRB, IRC, JAL, JMP, JR, LBU, mips_alu_1_equal,
       multiplexer_16_out, nand_1_out, nor_1_out, not_1_out, not_2_out, not_3_out, not_4_out, not_5_out,
       not_6_out, not_7_out, not_8_out, or_5_out, or_7_out, SignedExt, SLLV, SRAV, Syscall, W1, W2, W3,
       \单周期硬布线控制器_1_alu_src , \单周期硬布线控制器_1_beq , \单周期硬布线控制器_1_bne , \单周期硬布线控制器_1_memtoreg ,
       \单周期硬布线控制器_1_regdst ;
  wire [3:0] controlled_buffer_6_out, controlled_buffer_7_out, \单周期硬布线控制器_1_alu_op ;
  wire [4:0] multiplexer_2_out, multiplexer_3_out, multiplexer_4_out, multiplexer_5_out, multiplexer_10_out;
  wire [9:0] adder_4_out, divider_1_out, divider_1_rem, PC_3_q;
  wire [12:0] CNT_num;
  wire [15:0] \总周期数 ;
  wire [23:0] multiplexer_11_out;
  wire [27:0] multiplexer_15_out, n222_1_out_29, n222_2_out_29, n222_3_out_29, n222_4_out_29, n222_5_out_29,
       n222_6_out_29, n222_7_out_29, n222_8_out_29, n222_9_out_29, n222_10_out_29, n222_11_out_29,
       n222_12_out_29, n222_13_out_29, n222_14_out_29, n222_15_out_29, n222_16_out_29, n222_17_out_29,
       n222_18_out_29, n222_19_out_29, n222_20_out_29, n222_21_out_29, n222_22_out_29, n222_23_out_29,
       n222_24_out_29, n222_25_out_29, n222_26_out_29, n222_27_out_29, n222_28_out_29;
  wire [31:0] adder_1_out, adder_2_out, adder_3_out, bit_extender_1_out, bit_extender_2_out,
       bit_extender_3_out, controlled_buffer_1_out, mips_alu_1_result, multiplexer_7_out, multiplexer_8_out,
       multiplexer_9_out, multiplexer_12_out, multiplexer_13_out, multiplexer_14_out, PC_2_q, ram_1_data,
       shifter_1_out, UserData, v0;

  Clock #(.highDuration(1), .lowDuration(1)) clock_1 ();  // open: out
  Button _1 (.out(IRA));
  Button _2 (.out(IRB));
  Button _3 (.out(IRC));
  Button \u_继续运行  (.out(Go));
  LED #(.active("true")) led_1 (.in(W1));
  LED #(.active("true")) led_2 (.in(W2));
  LED #(.active("true")) led_3 (.in(W3));
  or or_1 (CPU_On, InputStop, \开始计算 );
  Multiplexer #(.select(1), .width(1), .disabled("Z"), .enable("false")) multiplexer_1 (
    .in0(1'b0), .in1(CLK), .out(CPUCLK), .sel(\开始计算 ));
  Hex_Digit_Display hex_digit_display_1 (.value(LedData[31:28]));  // open: dp
  and and_1 (and_1_out, JMP, ~JR);  // AND_Gate
  nor nor_1 (nor_1_out, Branch, JMP);
  Hex_Digit_Display hex_digit_display_2 (.value(LedData[27:24]));  // open: dp
  Hex_Digit_Display hex_digit_display_3 (.value(LedData[23:20]));  // open: dp
  assign controlled_buffer_1_out = JR ? v0 : 32'bz;  // Controlled_Buffer controlled_buffer_1
  assign controlled_buffer_1_out = and_1_out ? {PC[31:28], IR[25:0], 2'b00} : 32'bz;  // Controlled_Buffer controlled_buffer_2
  assign controlled_buffer_1_out = Branch ? adder_2_out : 32'bz;  // Controlled_Buffer controlled_buffer_3
  assign controlled_buffer_1_out = nor_1_out ? adder_1_out : 32'bz;  // Controlled_Buffer controlled_buffer_4
  not not_1 (not_1_out, Halt);
  Hex_Digit_Display hex_digit_display_4 (.value(LedData[19:16]));  // open: dp
  Hex_Digit_Display hex_digit_display_5 (.value(LedData[15:12]));  // open: dp
  Register #(.width(32), .trigger("rising"), .Select("low")) u_PC (
    .D(controlled_buffer_1_out), .en(not_1_out), .Q(PC), .clk(CPUCLK));  // open: clr
  Hex_Digit_Display hex_digit_display_6 (.value(LedData[7:4]));  // open: dp
  Hex_Digit_Display hex_digit_display_7 (.value(LedData[11:8]));  // open: dp
  // Probe on \总周期数 
  Counter #(.width(16), .max('hffff), .ongoal("wrap"), .trigger("rising"), .behavior("new")) counter_1 (
    .Q(\总周期数 ), .clk(and_2_out));  // open: load, D, count, carry, clr, preset, down
  and and_2 (and_2_out, ~Halt, CPUCLK);  // AND_Gate
  Hex_Digit_Display hex_digit_display_8 (.value(LedData[3:0]));  // open: dp
  Adder #(.width(32)) adder_1 (.a(PC), .b(32'h4), .out(adder_1_out));  // open: cin, cout
  // Mips_Probe mips_probe_1: pin names not known; wires that end beside it: IR
  ROM #(.addrWidth(10), .dataWidth(32), .Select("high")) rom_1 (.addr(PC[11:2]), .data(IR));
  or or_2 (IR1_t, IR1, IRA);
  or or_3 (IR2_t, IR2, IRB);
  \单周期硬布线控制器  \u_单周期硬布线控制器_1  (
    .Func(IR[5:0]), .OP(IR[31:26]), .ALU_OP(\单周期硬布线控制器_1_alu_op ), .MemToReg(\单周期硬布线控制器_1_memtoreg ),
    .MemWrite(MemWrite), .ALU_SRC(\单周期硬布线控制器_1_alu_src ), .RegWrite(RegWrite), .SysCALL(Syscall),
    .SignedExt(SignedExt), .RegDst(\单周期硬布线控制器_1_regdst ), .JR(JR), .JMP(JMP), .Beq(\单周期硬布线控制器_1_beq ),
    .JAL(JAL), .Bne(\单周期硬布线控制器_1_bne ), .SLLV(SLLV), .SRAV(SRAV), .BGEZ(BGEZ), .LBU(LBU));
  Multiplexer #(.select(1), .width(5), .disabled("Z"), .enable("false")) multiplexer_2 (
    .in0(IR[20:16]), .in1(IR[15:11]), .out(multiplexer_2_out), .sel(\单周期硬布线控制器_1_regdst ));
  assign bit_extender_1_out = {{16{1'b0}}, IR[15:0]};  // Bit_Extender bit_extender_1
  assign bit_extender_2_out = {{16{IR[15]}}, IR[15:0]};  // Bit_Extender bit_extender_2
  Multiplexer #(.select(1), .width(5), .disabled("Z"), .enable("false")) multiplexer_3 (
    .in0(multiplexer_2_out), .in1({5{1'b1}}), .out(multiplexer_3_out), .sel(JAL));
  not not_2 (not_2_out, JAL);
  or or_4 (IR3_t, IR3, IRC);
  Multiplexer #(.select(1), .width(5), .disabled("Z"), .enable("false")) multiplexer_4 (
    .in0(IR[25:21]), .in1(5'b00010), .out(multiplexer_4_out), .sel(Syscall));
  Multiplexer #(.select(1), .width(5), .disabled("Z"), .enable("false")) multiplexer_5 (
    .in0(IR[20:16]), .in1(5'b00100), .out(multiplexer_5_out), .sel(Syscall));
  Multiplexer #(.select(1), .width(32), .disabled("Z"), .enable("false")) multiplexer_6 (
    .in0(adder_1_out), .in1(multiplexer_13_out), .out(RDin), .sel(not_2_out));
  MIPS_Regifile mips_regifile_1 (
    .Din(RDin), .Clk(CPUCLK), .R1(v0), .R2(MDin), .WE(RegWrite), .W_num(multiplexer_3_out),
    .R1_num(multiplexer_4_out), .R2_num(multiplexer_5_out));
  Multiplexer #(.select(1), .width(32), .disabled("Z"), .enable("false")) multiplexer_7 (
    .in0(bit_extender_1_out), .in1(bit_extender_2_out), .out(multiplexer_7_out), .sel(SignedExt));
  Multiplexer #(.select(1), .width(32), .disabled("Z"), .enable("false")) multiplexer_8 (
    .in0(MDin), .in1(multiplexer_7_out), .out(multiplexer_8_out), .sel(\单周期硬布线控制器_1_alu_src ));
  Multiplexer #(.select(1), .width(32), .disabled("Z"), .enable("false")) multiplexer_9 (
    .in0(multiplexer_8_out), .in1({32{1'b0}}), .out(multiplexer_9_out), .sel(BGEZ));
  Shifter #(.width(32), .shift("ll")) shifter_1 (.in(multiplexer_7_out), .\dist (5'b00010), .out(shifter_1_out));
  MIPS_ALU mips_alu_1 (
    .X(v0), .Y(multiplexer_9_out), .AluOP(\单周期硬布线控制器_1_alu_op ), .Equal(mips_alu_1_equal),
    .Result(mips_alu_1_result), .shamt(multiplexer_10_out));  // open: Result_2
  Multiplexer #(.select(1), .width(5), .disabled("Z"), .enable("false")) multiplexer_10 (
    .in0(IR[10:6]), .in1(v0[4:0]), .out(multiplexer_10_out), .sel(or_5_out));
  Adder #(.width(32)) adder_2 (.a(shifter_1_out), .b(adder_1_out), .out(adder_2_out));  // open: cin, cout
  and and_3 (and_3_out, BGEZ, ~mips_alu_1_result[0]);  // AND_Gate
  and and_4 (and_4_out, mips_alu_1_equal, \单周期硬布线控制器_1_beq );
  and and_5 (and_5_out, ~mips_alu_1_equal, \单周期硬布线控制器_1_bne );  // AND_Gate
  or or_5 (or_5_out, SRAV, SLLV);
  not not_3 (not_3_out, InputStop);
  or or_6 (Branch, and_3_out, and_4_out, and_5_out);
  Register #(.width(32), .trigger("rising"), .Select("low")) PC_2 (
    .D(adder_3_out), .en(not_3_out), .Q(PC_2_q), .clk(CLK));  // open: clr
  Multiplexer #(.select(1), .width(24), .disabled("Z"), .enable("false")) multiplexer_11 (
    .in0(PC_2_q[25:2]), .in1(mips_alu_1_result[25:2]), .out(multiplexer_11_out), .sel(CPU_On));
  Multiplexer #(.select(1), .width(32), .disabled("Z"), .enable("false")) multiplexer_12 (
    .in0(UserData), .in1(MDin), .out(multiplexer_12_out), .sel(CPU_On));
  not not_4 (not_4_out, CPU_On);
  D_Flip_Flop #(.trigger("high"), .Pre_Clr_Positions("LEGACY"), .NegatePresetClear("false"), .enable("true"), .NewFFLayout("false")) d_ff_1 (.Q(d_ff_1_q));  // open: clk, D, Qn, preset, en, reset
  // Probe on 13'ha
  not not_5 (not_5_out, Halt);
  or or_7 (or_7_out, MemWrite, not_4_out);
  Adder #(.width(32)) adder_3 (.a(PC_2_q), .b(32'h4), .out(adder_3_out));  // open: cin, cout
  Comparator #(.width(13), .mode("twosComplement")) comparator_1 (
    .a(CNT_num), .b(13'ha), .eq(comparator_1_eq), .lt(comparator_1_lt));  // open: gt
  Clock #(.highDuration(1), .lowDuration(1)) clock_2 (.out(clock_2_out));
  RAM #(.addrWidth(24), .dataWidth(32), .bus("separate"), .Select("high")) ram_1 (
    .addr(multiplexer_11_out), .din(multiplexer_12_out), .data(ram_1_data), .str(or_7_out), .sel(not_5_out),
    .clk(CLK));  // open: ld, clr
  Multiplexer #(.select(1), .width(32), .disabled("Z"), .enable("false")) multiplexer_13 (
    .in0(multiplexer_14_out), .in1(bit_extender_3_out), .out(multiplexer_13_out), .sel(LBU));
  _222 u_222_1 (
    .out_29(n222_1_out_29), .in_1(in_4), .in_2(in_5), .in_3(in_6), .in_4(in_7), .in_5(in_8), .in_6(in_9),
    .in_7(in_10), .in_8(in_11), .in_9(in_12), .in_10(in_13), .in_11(in_14), .in_12(in_15), .in_13(in_16),
    .in_14(in_17), .in_15(in_18), .in_16(in_19), .in_17(in_20), .in_18(in_21), .in_19(in_22), .in_20(in_23),
    .in_21(in_24), .in_22(in_25), .in_23(in_26), .in_24(in_27), .in_25(in_28), .in_26(in_29), .in_27(in_30),
    .in_28(in_31));
  _222 u_222_2 (
    .out_29(n222_2_out_29), .in_1(in_32), .in_2(in_33), .in_3(in_34), .in_4(in_35), .in_5(in_36),
    .in_6(in_37), .in_7(in_38), .in_8(in_39), .in_9(in_40), .in_10(in_41), .in_11(in_42), .in_12(in_43),
    .in_13(in_44), .in_14(in_45), .in_15(in_46), .in_16(in_47), .in_17(in_48), .in_18(in_49), .in_19(in_50),
    .in_20(in_51), .in_21(in_52), .in_22(in_53), .in_23(in_54), .in_24(in_55), .in_25(in_56), .in_26(in_57),
    .in_27(in_58), .in_28(in_59));
  _222 u_222_3 (
    .out_29(n222_3_out_29), .in_1(in_60), .in_2(in_61), .in_3(in_62), .in_4(in_63), .in_5(in_64),
    .in_6(in_65), .in_7(in_66), .in_8(in_67), .in_9(in_68), .in_10(in_69), .in_11(in_70), .in_12(in_71),
    .in_13(in_72), .in_14(in_73), .in_15(in_74), .in_16(in_75), .in_17(in_76), .in_18(in_77), .in_19(in_78),
    .in_20(in_79), .in_21(in_80), .in_22(in_81), .in_23(in_82), .in_24(in_83), .in_25(in_84), .in_26(in_85),
    .in_27(in_86), .in_28(in_87));
  _222 u_222_4 (
    .out_29(n222_4_out_29), .in_1(in_88), .in_2(in_89), .in_3(in_90), .in_4(in_91), .in_5(in_92),
    .in_6(in_93), .in_7(in_94), .in_8(in_95), .in_9(in_96), .in_10(in_97), .in_11(in_98), .in_12(in_99),
    .in_13(in_100), .in_14(in_101), .in_15(in_102), .in_16(in_103), .in_17(in_104), .in_18(in_105),
    .in_19(in_106), .in_20(in_107), .in_21(in_108), .in_22(in_109), .in_23(in_110), .in_24(in_111),
    .in_25(in_112), .in_26(in_113), .in_27(in_114), .in_28(in_115));
  _222 u_222_5 (
    .out_29(n222_5_out_29), .in_1(in_116), .in_2(in_117), .in_3(in_118), .in_4(in_119), .in_5(in_120),
    .in_6(in_121), .in_7(in_122), .in_8(in_123), .in_9(in_124), .in_10(in_125), .in_11(in_126),
    .in_12(in_127), .in_13(in_128), .in_14(in_129), .in_15(in_130), .in_16(in_131), .in_17(in_132),
    .in_18(in_133), .in_19(in_134), .in_20(in_135), .in_21(in_136), .in_22(in_137), .in_23(in_138),
    .in_24(in_139), .in_25(in_140), .in_26(in_141), .in_27(in_142), .in_28(in_143));
  _222 u_222_6 (
    .out_29(n222_6_out_29), .in_1(in_144), .in_2(in_145), .in_3(in_146), .in_4(in_147), .in_5(in_148),
    .in_6(in_149), .in_7(in_150), .in_8(in_151), .in_9(in_152), .in_10(in_153), .in_11(in_154),
    .in_12(in_155), .in_13(in_156), .in_14(in_157), .in_15(in_158), .in_16(in_159), .in_17(in_160),
    .in_18(in_161), .in_19(in_162), .in_20(in_163), .in_21(in_164), .in_22(in_165), .in_23(in_166),
    .in_24(in_167), .in_25(in_168), .in_26(in_169), .in_27(in_170), .in_28(in_171));
  _222 u_222_7 (
    .out_29(n222_7_out_29), .in_1(in_172), .in_2(in_173), .in_3(in_174), .in_4(in_175), .in_5(in_176),
    .in_6(in_177), .in_7(in_178), .in_8(in_179), .in_9(in_180), .in_10(in_181), .in_11(in_182),
    .in_12(in_183), .in_13(in_184), .in_14(in_185), .in_15(in_186), .in_16(in_187), .in_17(in_188),
    .in_18(in_189), .in_19(in_190), .in_20(in_191), .in_21(in_192), .in_22(in_193), .in_23(in_194),
    .in_24(in_195), .in_25(in_196), .in_26(in_197), .in_27(in_198), .in_28(in_199));
  _222 u_222_8 (
    .out_29(n222_8_out_29), .in_1(in_200), .in_2(in_201), .in_3(in_202), .in_4(in_203), .in_5(in_204),
    .in_6(in_205), .in_7(in_206), .in_8(in_207), .in_9(in_208), .in_10(in_209), .in_11(in_210),
    .in_12(in_211), .in_13(in_212), .in_14(in_213), .in_15(in_214), .in_16(in_215), .in_17(in_216),
    .in_18(in_217), .in_19(in_218), .in_20(in_219), .in_21(in_220), .in_22(in_221), .in_23(in_222),
    .in_24(in_223), .in_25(in_224), .in_26(in_225), .in_27(in_226), .in_28(in_227));
  _222 u_222_9 (
    .out_29(n222_9_out_29), .in_1(in_228), .in_2(in_229), .in_3(in_230), .in_4(in_231), .in_5(in_232),
    .in_6(in_233), .in_7(in_234), .in_8(in_235), .in_9(in_236), .in_10(in_237), .in_11(in_238),
    .in_12(in_239), .in_13(in_240), .in_14(in_241), .in_15(in_242), .in_16(in_243), .in_17(in_244),
    .in_18(in_245), .in_19(in_246), .in_20(in_247), .in_21(in_248), .in_22(in_249), .in_23(in_250),
    .in_24(in_251), .in_25(in_252), .in_26(in_253), .in_27(in_254), .in_28(in_255));
  _222 u_222_10 (
    .out_29(n222_10_out_29), .in_1(in_256), .in_2(in_257), .in_3(in_258), .in_4(in_259), .in_5(in_260),
    .in_6(in_261), .in_7(in_262), .in_8(in_263), .in_9(in_264), .in_10(in_265), .in_11(in_266),
    .in_12(in_267), .in_13(in_268), .in_14(in_269), .in_15(in_270), .in_16(in_271), .in_17(in_272),
    .in_18(in_273), .in_19(in_274), .in_20(in_275), .in_21(in_276), .in_22(in_277), .in_23(in_278),
    .in_24(in_279), .in_25(in_280), .in_26(in_281), .in_27(in_282), .in_28(in_283));
  _222 u_222_11 (
    .out_29(n222_11_out_29), .in_1(in_284), .in_2(in_285), .in_3(in_286), .in_4(in_287), .in_5(in_288),
    .in_6(in_289), .in_7(in_290), .in_8(in_291), .in_9(in_292), .in_10(in_293), .in_11(in_294),
    .in_12(in_295), .in_13(in_296), .in_14(in_297), .in_15(in_298), .in_16(in_299), .in_17(in_300),
    .in_18(in_301), .in_19(in_302), .in_20(in_303), .in_21(in_304), .in_22(in_305), .in_23(in_306),
    .in_24(in_307), .in_25(in_308), .in_26(in_309), .in_27(in_310), .in_28(in_311));
  _222 u_222_12 (
    .out_29(n222_12_out_29), .in_1(in_312), .in_2(in_313), .in_3(in_314), .in_4(in_315), .in_5(in_316),
    .in_6(in_317), .in_7(in_318), .in_8(in_319), .in_9(in_320), .in_10(in_321), .in_11(in_322),
    .in_12(in_323), .in_13(in_324), .in_14(in_325), .in_15(in_326), .in_16(in_327), .in_17(in_328),
    .in_18(in_329), .in_19(in_330), .in_20(in_331), .in_21(in_332), .in_22(in_333), .in_23(in_334),
    .in_24(in_335), .in_25(in_336), .in_26(in_337), .in_27(in_338), .in_28(in_339));
  _222 u_222_13 (
    .out_29(n222_13_out_29), .in_1(in_340), .in_2(in_341), .in_3(in_342), .in_4(in_343), .in_5(in_344),
    .in_6(in_345), .in_7(in_346), .in_8(in_347), .in_9(in_348), .in_10(in_349), .in_11(in_350),
    .in_12(in_351), .in_13(in_352), .in_14(in_353), .in_15(in_354), .in_16(in_355), .in_17(in_356),
    .in_18(in_357), .in_19(in_358), .in_20(in_359), .in_21(in_360), .in_22(in_361), .in_23(in_362),
    .in_24(in_363), .in_25(in_364), .in_26(in_365), .in_27(in_366), .in_28(in_367));
  _222 u_222_14 (
    .out_29(n222_14_out_29), .in_1(in_369), .in_2(in_370), .in_3(in_371), .in_4(in_372), .in_5(in_373),
    .in_6(in_374), .in_7(in_375), .in_8(in_376), .in_9(in_377), .in_10(in_378), .in_11(in_379),
    .in_12(in_380), .in_13(in_381), .in_14(in_382), .in_15(in_383), .in_16(in_384), .in_17(in_385),
    .in_18(in_386), .in_19(in_387), .in_20(in_388), .in_21(in_389), .in_22(in_390), .in_23(in_391),
    .in_24(in_392), .in_25(in_393), .in_26(in_394), .in_27(in_395), .in_28(in_396));
  _222 u_222_15 (
    .out_29(n222_15_out_29), .in_1(in_397), .in_2(in_398), .in_3(in_399), .in_4(in_400), .in_5(in_401),
    .in_6(in_402), .in_7(in_403), .in_8(in_404), .in_9(in_405), .in_10(in_406), .in_11(in_407),
    .in_12(in_408), .in_13(in_409), .in_14(in_410), .in_15(in_411), .in_16(in_412), .in_17(in_413),
    .in_18(in_414), .in_19(in_415), .in_20(in_416), .in_21(in_417), .in_22(in_418), .in_23(in_419),
    .in_24(in_420), .in_25(in_421), .in_26(in_422), .in_27(in_423), .in_28(in_424));
  _222 u_222_16 (
    .out_29(n222_16_out_29), .in_1(in_425), .in_2(in_426), .in_3(in_427), .in_4(in_428), .in_5(in_429),
    .in_6(in_430), .in_7(in_431), .in_8(in_432), .in_9(in_433), .in_10(in_434), .in_11(in_435),
    .in_12(in_436), .in_13(in_437), .in_14(in_438), .in_15(in_439), .in_16(in_440), .in_17(in_441),
    .in_18(in_442), .in_19(in_443), .in_20(in_444), .in_21(in_445), .in_22(in_446), .in_23(in_447),
    .in_24(in_448), .in_25(in_449), .in_26(in_450), .in_27(in_451), .in_28(in_452));
  _222 u_222_17 (
    .out_29(n222_17_out_29), .in_1(in_453), .in_2(in_454), .in_3(in_455), .in_4(in_456), .in_5(in_457),
    .in_6(in_458), .in_7(in_459), .in_8(in_460), .in_9(in_461), .in_10(in_462), .in_11(in_463),
    .in_12(in_464), .in_13(in_465), .in_14(in_466), .in_15(in_467), .in_16(in_468), .in_17(in_469),
    .in_18(in_470), .in_19(in_471), .in_20(in_472), .in_21(in_473), .in_22(in_474), .in_23(in_475),
    .in_24(in_476), .in_25(in_477), .in_26(in_478), .in_27(in_479), .in_28(in_480));
  _222 u_222_18 (
    .out_29(n222_18_out_29), .in_1(in_481), .in_2(in_482), .in_3(in_483), .in_4(in_484), .in_5(in_485),
    .in_6(in_486), .in_7(in_487), .in_8(in_488), .in_9(in_489), .in_10(in_490), .in_11(in_491),
    .in_12(in_492), .in_13(in_493), .in_14(in_494), .in_15(in_495), .in_16(in_496), .in_17(in_497),
    .in_18(in_498), .in_19(in_499), .in_20(in_500), .in_21(in_501), .in_22(in_502), .in_23(in_503),
    .in_24(in_504), .in_25(in_505), .in_26(in_506), .in_27(in_507), .in_28(in_508));
  _222 u_222_19 (
    .out_29(n222_19_out_29), .in_1(in_509), .in_2(in_510), .in_3(in_511), .in_4(in_512), .in_5(in_513),
    .in_6(in_514), .in_7(in_515), .in_8(in_516), .in_9(in_517), .in_10(in_518), .in_11(in_519),
    .in_12(in_520), .in_13(in_521), .in_14(in_522), .in_15(in_523), .in_16(in_524), .in_17(in_525),
    .in_18(in_526), .in_19(in_527), .in_20(in_528), .in_21(in_529), .in_22(in_530), .in_23(in_531),
    .in_24(in_532), .in_25(in_533), .in_26(in_534), .in_27(in_535), .in_28(in_536));
  _222 u_222_20 (
    .out_29(n222_20_out_29), .in_1(in_537), .in_2(in_538), .in_3(in_539), .in_4(in_540), .in_5(in_541),
    .in_6(in_542), .in_7(in_543), .in_8(in_544), .in_9(in_545), .in_10(in_546), .in_11(in_547),
    .in_12(in_548), .in_13(in_549), .in_14(in_550), .in_15(in_551), .in_16(in_552), .in_17(in_553),
    .in_18(in_554), .in_19(in_555), .in_20(in_556), .in_21(in_557), .in_22(in_558), .in_23(in_559),
    .in_24(in_560), .in_25(in_561), .in_26(in_562), .in_27(in_563), .in_28(in_564));
  _222 u_222_21 (
    .out_29(n222_21_out_29), .in_1(in_565), .in_2(in_566), .in_3(in_567), .in_4(in_568), .in_5(in_569),
    .in_6(in_570), .in_7(in_571), .in_8(in_572), .in_9(in_573), .in_10(in_574), .in_11(in_575),
    .in_12(in_576), .in_13(in_577), .in_14(in_578), .in_15(in_579), .in_16(in_580), .in_17(in_581),
    .in_18(in_582), .in_19(in_583), .in_20(in_584), .in_21(in_585), .in_22(in_586), .in_23(in_587),
    .in_24(in_588), .in_25(in_589), .in_26(in_590), .in_27(in_591), .in_28(in_592));
  _222 u_222_22 (
    .out_29(n222_22_out_29), .in_1(in_593), .in_2(in_594), .in_3(in_595), .in_4(in_596), .in_5(in_597),
    .in_6(in_598), .in_7(in_599), .in_8(in_600), .in_9(in_601), .in_10(in_602), .in_11(in_603),
    .in_12(in_604), .in_13(in_605), .in_14(in_606), .in_15(in_607), .in_16(in_608), .in_17(in_609),
    .in_18(in_610), .in_19(in_611), .in_20(in_612), .in_21(in_613), .in_22(in_614), .in_23(in_615),
    .in_24(in_616), .in_25(in_617), .in_26(in_618), .in_27(in_619), .in_28(in_620));
  _222 u_222_23 (
    .out_29(n222_23_out_29), .in_1(in_621), .in_2(in_622), .in_3(in_623), .in_4(in_624), .in_5(in_625),
    .in_6(in_626), .in_7(in_627), .in_8(in_628), .in_9(in_629), .in_10(in_630), .in_11(in_631),
    .in_12(in_632), .in_13(in_633), .in_14(in_634), .in_15(in_635), .in_16(in_636), .in_17(in_637),
    .in_18(in_638), .in_19(in_639), .in_20(in_640), .in_21(in_641), .in_22(in_642), .in_23(in_643),
    .in_24(in_644), .in_25(in_645), .in_26(in_646), .in_27(in_647), .in_28(in_648));
  _222 u_222_24 (
    .out_29(n222_24_out_29), .in_1(in_649), .in_2(in_650), .in_3(in_651), .in_4(in_652), .in_5(in_653),
    .in_6(in_654), .in_7(in_655), .in_8(in_656), .in_9(in_657), .in_10(in_658), .in_11(in_659),
    .in_12(in_660), .in_13(in_661), .in_14(in_662), .in_15(in_663), .in_16(in_664), .in_17(in_665),
    .in_18(in_666), .in_19(in_667), .in_20(in_668), .in_21(in_669), .in_22(in_670), .in_23(in_671),
    .in_24(in_672), .in_25(in_673), .in_26(in_674), .in_27(in_675), .in_28(in_676));
  _222 u_222_25 (
    .out_29(n222_25_out_29), .in_1(in_677), .in_2(in_678), .in_3(in_679), .in_4(in_680), .in_5(in_681),
    .in_6(in_682), .in_7(in_683), .in_8(in_684), .in_9(in_685), .in_10(in_686), .in_11(in_687),
    .in_12(in_688), .in_13(in_689), .in_14(in_690), .in_15(in_691), .in_16(in_692), .in_17(in_693),
    .in_18(in_694), .in_19(in_695), .in_20(in_696), .in_21(in_697), .in_22(in_698), .in_23(in_699),
    .in_24(in_700), .in_25(in_701), .in_26(in_702), .in_27(in_703), .in_28(in_704));
  _222 u_222_26 (
    .out_29(n222_26_out_29), .in_1(in_705), .in_2(in_706), .in_3(in_707), .in_4(in_708), .in_5(in_709),
    .in_6(in_710), .in_7(in_711), .in_8(in_712), .in_9(in_713), .in_10(in_714), .in_11(in_715),
    .in_12(in_716), .in_13(in_717), .in_14(in_718), .in_15(in_719), .in_16(in_720), .in_17(in_721),
    .in_18(in_722), .in_19(in_723), .in_20(in_724), .in_21(in_725), .in_22(in_726), .in_23(in_727),
    .in_24(in_728), .in_25(in_729), .in_26(in_730), .in_27(in_731), .in_28(in_732));
  _222 u_222_27 (
    .out_29(n222_27_out_29), .in_1(in_733), .in_2(in_734), .in_3(in_735), .in_4(in_736), .in_5(in_737),
    .in_6(in_738), .in_7(in_739), .in_8(in_740), .in_9(in_741), .in_10(in_742), .in_11(in_743),
    .in_12(in_744), .in_13(in_745), .in_14(in_746), .in_15(in_747), .in_16(in_748), .in_17(in_749),
    .in_18(in_750), .in_19(in_751), .in_20(in_752), .in_21(in_753), .in_22(in_754), .in_23(in_755),
    .in_24(in_756), .in_25(in_757), .in_26(in_758), .in_27(in_759), .in_28(in_760));
  _222 u_222_28 (
    .out_29(n222_28_out_29), .in_1(in_761), .in_2(in_762), .in_3(in_763), .in_4(in_764), .in_5(in_765),
    .in_6(in_766), .in_7(in_767), .in_8(in_768), .in_9(in_769), .in_10(in_770), .in_11(in_771),
    .in_12(in_772), .in_13(in_773), .in_14(in_774), .in_15(in_775), .in_16(in_776), .in_17(in_777),
    .in_18(in_778), .in_19(in_779), .in_20(in_780), .in_21(in_781), .in_22(in_782), .in_23(in_783),
    .in_24(in_784), .in_25(in_785), .in_26(in_786), .in_27(in_787), .in_28(in_788));
  nand nand_1 (nand_1_out, d_ff_1_q, comparator_1_eq);
  Counter #(.width(13), .max('h1fff), .ongoal("stay"), .trigger("rising"), .behavior("old")) counter_2 (
    .count(comparator_1_lt), .Q(CNT_num), .clk(clock_2_out));  // open: load, D, carry, clr, preset
  Multiplexer #(.select(1), .width(32), .disabled("Z"), .enable("false")) multiplexer_14 (
    .in0(mips_alu_1_result), .in1(ram_1_data), .out(multiplexer_14_out), .sel(\单周期硬布线控制器_1_memtoreg ));
  Comparator #(.width(32), .mode("twosComplement")) comparator_2 (
    .a(v0), .b(32'h22), .eq(comparator_2_eq));  // open: gt, lt
  not not_6 (not_6_out, comparator_2_eq);
  and and_6 (and_6_out, comparator_2_eq, Syscall);
  and and_7 (and_7_out, Syscall, not_6_out);
  assign CLK = nand_1_out ? clock_2_out : 1'bz;  // Controlled_Buffer controlled_buffer_5
  Pull_Resistor #(.pull(1)) pull_resistor_1 (.node(CLK));
  assign bit_extender_3_out = {{24{1'b0}}, multiplexer_14_out[7:0]};  // Bit_Extender bit_extender_3
  Register #(.width(32), .trigger("falling"), .Select("low")) register_1 (
    .D(MDin), .Q(LedData), .clk(and_6_out));  // open: en, clr
  Register #(.width(1), .trigger("rising"), .Select("low")) register_2 (
    .D(and_7_out), .en(and_7_out), .Q(Halt), .clk(CLK), .clr(Go));
  Register #(.width(10), .trigger("rising"), .Select("low")) PC_3 (
    .D(adder_4_out), .en(not_7_out), .Q(PC_3_q), .clk(CLK));  // open: clr
  not not_7 (not_7_out, InputStop);
  DotMatrix #(.inputtype("row"), .matrixcols(28), .matrixrows(28), .persist(0), .dotshape("square")) dotmatrix_1 (
    .row0(n222_1_out_29), .row1(n222_2_out_29), .row2(n222_3_out_29), .row3(n222_4_out_29),
    .row4(n222_5_out_29), .row5(n222_6_out_29), .row6(n222_7_out_29), .row7(n222_8_out_29),
    .row8(n222_9_out_29), .row9(n222_10_out_29), .row10(n222_11_out_29), .row11(n222_12_out_29),
    .row12(n222_13_out_29), .row13(n222_14_out_29), .row14(n222_15_out_29), .row15(n222_16_out_29),
    .row16(n222_17_out_29), .row17(n222_18_out_29), .row18(n222_19_out_29), .row19(n222_20_out_29),
    .row20(n222_21_out_29), .row21(n222_22_out_29), .row22(n222_23_out_29), .row23(n222_24_out_29),
    .row24(n222_25_out_29), .row25(n222_26_out_29), .row26(n222_27_out_29), .row27(n222_28_out_29));
  Adder #(.width(10)) adder_4 (.a(PC_3_q), .b(10'h1), .out(adder_4_out));  // open: cin, cout
  Comparator #(.width(10), .mode("twosComplement")) comparator_3 (
    .a(PC_3_q), .b(10'h310), .eq(InputStop));  // open: gt, lt
  Divider #(.width(10)) divider_1 (.a(PC_3_q), .b(10'h1c), .out(divider_1_out), .rem(divider_1_rem));  // open: upper
  Hex_Digit_Display hex_digit_display_9 (.value(controlled_buffer_6_out));  // open: dp
  assign controlled_buffer_6_out = Halt ? LedData[3:0] : 4'bz;  // Controlled_Buffer controlled_buffer_6
  Multiplexer #(.select(5), .width(28), .disabled("Z"), .enable("false")) multiplexer_15 (
    .in0(n222_1_out_29), .in1(n222_2_out_29), .in2(n222_3_out_29), .in3(n222_4_out_29), .in4(n222_5_out_29),
    .in5(n222_6_out_29), .in6(n222_7_out_29), .in7(n222_8_out_29), .in8(n222_9_out_29), .in9(n222_10_out_29),
    .in10(n222_11_out_29), .in11(n222_12_out_29), .in12(n222_13_out_29), .in13(n222_14_out_29),
    .in14(n222_15_out_29), .in15(n222_16_out_29), .in16(n222_17_out_29), .in17(n222_18_out_29),
    .in18(n222_19_out_29), .in19(n222_20_out_29), .in20(n222_21_out_29), .in21(n222_22_out_29),
    .in22(n222_23_out_29), .in23(n222_24_out_29), .in24(n222_25_out_29), .in25(n222_26_out_29),
    .in26(n222_27_out_29), .in27(n222_28_out_29), .out(multiplexer_15_out), .sel(divider_1_out[4:0]));  // open: in28, in29, in30, in31
  Multiplexer #(.select(5), .width(1), .disabled("Z"), .enable("false")) multiplexer_16 (
    .in0(multiplexer_15_out[27]), .in1(multiplexer_15_out[26]), .in2(multiplexer_15_out[25]),
    .in3(multiplexer_15_out[24]), .in4(multiplexer_15_out[23]), .in5(multiplexer_15_out[22]),
    .in6(multiplexer_15_out[21]), .in7(multiplexer_15_out[20]), .in8(multiplexer_15_out[19]),
    .in9(multiplexer_15_out[18]), .in10(multiplexer_15_out[17]), .in11(multiplexer_15_out[16]),
    .in12(multiplexer_15_out[15]), .in13(multiplexer_15_out[14]), .in14(multiplexer_15_out[13]),
    .in15(multiplexer_15_out[12]), .in16(multiplexer_15_out[11]), .in17(multiplexer_15_out[10]),
    .in18(multiplexer_15_out[9]), .in19(multiplexer_15_out[8]), .in20(multiplexer_15_out[7]),
    .in21(multiplexer_15_out[6]), .in22(multiplexer_15_out[5]), .in23(multiplexer_15_out[4]),
    .in24(multiplexer_15_out[3]), .in25(multiplexer_15_out[2]), .in26(multiplexer_15_out[1]),
    .in27(multiplexer_15_out[0]), .out(multiplexer_16_out), .sel(divider_1_rem[4:0]));  // open: in28, in29, in30, in31
  Hex_Digit_Display hex_digit_display_10 (.value(controlled_buffer_7_out));  // open: dp
  assign controlled_buffer_7_out = not_8_out ? LedData[3:0] : 4'bz;  // Controlled_Buffer controlled_buffer_7
  not not_8 (not_8_out, Halt);
  assign UserData = {{31{1'b0}}, multiplexer_16_out};  // Bit_Extender bit_extender_4
  LED #(.active("true")) led_4 (.in(InputStop));

  // Other names for the same wires on the sheet: a0[31:0] = MDin; StartCalc = \开始计算 

  // Notes on the sheet:
  //   中断源
  //   中断等待指示
  //   总复位信号应将除ROM以外所有存储组件全部清零
  //   数码管输出
  //   数码管输出应该用寄存器锁存，否则显示数据只能一闪而过
  //   指令存储器
  //   指令字
  //   contents of rom_1 (hex, n*v repeats v):
  //   20100000 2011b1e0 20120000 20130000 20140000 20160000 20170000 200b0000 20090c40 1209820 8ef60000
  //   8e680000 12c00001 2489020 22f70004 22730004 16e9fff9 251502a 15400002 2408820 2808020 20120000
  //   22940001 200c000a 20170000 142020 20020022 c 168cffed 102020 20020022 c 20020032 c
  //   JMP
  //   JR
  //   OP
  //   OP
  //   Func
  //   Func
  //   rs
  //   rt
  //   rd
  //   Beq
  //   Bne
  //   MemToReg
  //   MemWrite
  //   AluOP
  //   AluSrcB
  //   RegWrite
  //   JAL
  //   RegDst
  //   Syscall
  //   为方便自动评测，需要输出PC，IR，寄存器堆写如数据RDin
  //   RAM写使能MemWrite、RAM写入数据MDin等信号
  //   控制位
  //   暂停节拍，不能为0
  //   戳工具置1进入计数暂停模式，ctrl+k时钟自动运行到对应节拍暂停
  //   ctrl+k关闭时钟连续运行，将控制位置零，进入单步调试模式调试
  //   用这个时钟源需要去掉电路中的其他时钟源
  //   可计数暂停的时钟源
  //   预测结果:
  //   使用方法:
  //   提示:
  //   正在计算:
  //   2. 用户点击左侧输入，绘制需要判断的数字图像
  //   3. Ctrl/Command + k 开始导入点阵数据数据，等待下方提示导入完成
  //   1. 点击CPU中右侧的数据存储器，加载本地名为raw_data.txt的数据文件
  //   5. Ctrl/Command + r 重置数据，需要从(1)开始，重复上述步骤，即可进行下一次预测
  //   导入完成
  //   4. 点击开始计算，CPU将会开始预测，计算过程中进度会在'正在计算'中显示，最终的预测结果会在'预测结果显示'
  //   由于性能原因，计算的速度可能很慢，载入点阵数据的过程可以通过切到其他的应用来加速，预测过程可以通过双击进入Regfile来加速
endmodule

// 单周期硬布线控制器
module \单周期硬布线控制器  (
  input  [5:0] OP,
  input  [5:0] Func,
  output [3:0] ALU_OP,
  output MemToReg,
  output LBU,
  output MemWrite,
  output SLLV,
  output SRAV,
  output BGEZ,
  output ALU_SRC,
  output RegWrite,
  output SysCALL,
  output SignedExt,
  output RegDst,
  output Beq,
  output Bne,
  output JR,
  output JMP,
  output JAL
);

  \运算控制器自动生成  \u_运算控制器自动生成_1  (
    .OP0(OP[0]), .OP1(OP[1]), .OP2(OP[2]), .OP3(OP[3]), .OP4(OP[4]), .OP5(OP[5]), .F0(Func[0]), .F1(Func[1]),
    .F2(Func[2]), .F3(Func[3]), .F4(Func[4]), .F5(Func[5]), .S0(ALU_OP[0]), .S1(ALU_OP[1]), .S2(ALU_OP[2]),
    .S3(ALU_OP[3]));
  \控制信号自动生成  \u_控制信号自动生成_1  (
    .OP0(OP[0]), .OP1(OP[1]), .OP2(OP[2]), .OP3(OP[3]), .OP4(OP[4]), .OP5(OP[5]), .F0(Func[0]), .F1(Func[1]),
    .F2(Func[2]), .F3(Func[3]), .F4(Func[4]), .F5(Func[5]), .MemToReg(MemToReg), .LBU(LBU),
    .MemWrite(MemWrite), .SLLV(SLLV), .SRAV(SRAV), .BGEZ(BGEZ), .ALU_SRC(ALU_SRC), .RegWrite(RegWrite),
    .SysCALL(SysCALL), .SignedExt(SignedExt), .RegDst(RegDst), .BEQ(Beq), .BNE(Bne), .JR(JR), .JUMP(JMP),
    .JAL(JAL));

  // Other names for the same wires on the sheet: OP_CODE[5:0] = OP

  // Notes on the sheet:
  //   运算器控制器，根据指令生成运算器功能选择信号
  //   控制信号生成，产生数据通路需要的其他控制信号
endmodule

// 运算器控制器
module \运算控制器自动生成  (
  input  OP0,
  input  OP1,
  input  OP2,
  input  OP3,
  input  OP4,
  input  OP5,
  input  F0,
  input  F1,
  input  F2,
  input  F3,
  input  F4,
  input  F5,
  output S0,
  output S1,
  output S2,
  output S3
);

  wire and_1_out, and_2_out, and_3_out, and_4_out, and_5_out, and_6_out, and_7_out, and_8_out, and_9_out,
       and_10_out, and_11_out, and_12_out, and_13_out, and_14_out, and_15_out, and_16_out, and_17_out,
       and_18_out, and_19_out, and_20_out, and_21_out, and_22_out, and_23_out, and_24_out, and_25_out,
       and_26_out, and_27_out, and_28_out, and_29_out, and_30_out, and_31_out, and_32_out, and_33_out,
       and_34_out, and_35_out, and_36_out, and_37_out, and_38_out, and_39_out, and_40_out, not_1_out,
       not_2_out, not_3_out, not_4_out, not_5_out, not_6_out, not_7_out, not_8_out, not_9_out, not_10_out,
       not_11_out, not_12_out, not_13_out, not_14_out, not_15_out, not_16_out, not_17_out, not_18_out,
       not_19_out, not_20_out, not_21_out, not_22_out, not_23_out, not_24_out, not_25_out, not_26_out,
       not_27_out, not_28_out, not_29_out, not_30_out, not_31_out, not_32_out, not_33_out, not_34_out,
       not_35_out, not_36_out, not_37_out, not_38_out, not_39_out, not_40_out, not_41_out, not_42_out,
       not_43_out, not_44_out, not_45_out, not_46_out, not_47_out, not_48_out, not_49_out, not_50_out,
       not_51_out, not_52_out, not_53_out, not_54_out, not_55_out, not_56_out, not_57_out, not_58_out,
       not_59_out, not_60_out, not_61_out, not_62_out, not_63_out, not_64_out, not_65_out, not_66_out,
       not_67_out, not_68_out, not_69_out, not_70_out, not_71_out, not_72_out, not_73_out, not_74_out,
       not_75_out, not_76_out, not_77_out, not_78_out, not_79_out, not_80_out, not_81_out, not_82_out,
       not_83_out, not_84_out, not_85_out, not_86_out, not_87_out, not_88_out, not_89_out, not_90_out,
       not_91_out, not_92_out, not_93_out, not_94_out, not_95_out, not_96_out, not_97_out, not_98_out,
       not_99_out, not_100_out, not_101_out, not_102_out, not_103_out, not_104_out, not_105_out, not_106_out,
       not_107_out, not_108_out, not_109_out, not_110_out, not_111_out, not_112_out, not_113_out,
       not_114_out, not_115_out, not_116_out, not_117_out, not_118_out, not_119_out, not_120_out,
       not_121_out, not_122_out, not_123_out, not_124_out, not_125_out, not_126_out, not_127_out,
       not_128_out, not_129_out, not_130_out, not_131_out, not_132_out, not_133_out, not_134_out,
       not_135_out, not_136_out, not_137_out, not_138_out, not_139_out, not_140_out, not_141_out,
       not_142_out, not_143_out, not_144_out, not_145_out, not_146_out, not_147_out, not_148_out,
       not_149_out, not_150_out, not_151_out, not_152_out, not_153_out, not_154_out, not_155_out,
       not_156_out, not_157_out, not_158_out, not_159_out, not_160_out, not_161_out, not_162_out,
       not_163_out, not_164_out, not_165_out, not_166_out, not_167_out, not_168_out, not_169_out,
       not_170_out, not_171_out, not_172_out, not_173_out, not_174_out, not_175_out, not_176_out,
       not_177_out, not_178_out, not_179_out, not_180_out, not_181_out, not_182_out, not_183_out,
       not_184_out, not_185_out, not_186_out, not_187_out, not_188_out, not_189_out, not_190_out,
       not_191_out, not_192_out, not_193_out, not_194_out, not_195_out, not_196_out, not_197_out,
       not_198_out, not_199_out, not_200_out, not_201_out, not_202_out, not_203_out, not_204_out,
       not_205_out, not_206_out, not_207_out, not_208_out, not_209_out, not_210_out, not_211_out,
       not_212_out, not_213_out, not_214_out, not_215_out, not_216_out, not_217_out, not_218_out,
       not_219_out, not_220_out, not_221_out, not_222_out, not_223_out, not_224_out, not_225_out,
       not_226_out, not_227_out, not_228_out, not_229_out, not_230_out, not_231_out, not_232_out,
       not_233_out, not_234_out, not_235_out, not_236_out, not_237_out, not_238_out, not_239_out,
       not_240_out, not_241_out, not_242_out, not_243_out, not_244_out, not_245_out, not_246_out,
       not_247_out, not_248_out, not_249_out, not_250_out, not_251_out, not_252_out, not_253_out,
       not_254_out, not_255_out, not_256_out, not_257_out, not_258_out, not_259_out, not_260_out,
       not_261_out, not_262_out, not_263_out, not_264_out, not_265_out, not_266_out, not_267_out, not_268_out;

  not not_1 (not_1_out, OP5);
  not not_2 (not_2_out, OP4);
  not not_3 (not_3_out, OP3);
  not not_4 (not_4_out, OP2);
  not not_5 (not_5_out, OP1);
  not not_6 (not_6_out, OP0);
  not not_7 (not_7_out, F5);
  not not_8 (not_8_out, F4);
  not not_9 (not_9_out, F3);
  not not_10 (not_10_out, F2);
  not not_11 (not_11_out, OP5);
  not not_12 (not_12_out, OP4);
  not not_13 (not_13_out, OP3);
  not not_14 (not_14_out, OP2);
  not not_15 (not_15_out, OP1);
  not not_16 (not_16_out, OP0);
  not not_17 (not_17_out, F4);
  not not_18 (not_18_out, F3);
  not not_19 (not_19_out, F2);
  not not_20 (not_20_out, F1);
  not not_21 (not_21_out, F0);
  not not_22 (not_22_out, OP5);
  not not_23 (not_23_out, OP4);
  not not_24 (not_24_out, OP3);
  not not_25 (not_25_out, OP2);
  not not_26 (not_26_out, OP1);
  not not_27 (not_27_out, OP0);
  not not_28 (not_28_out, F4);
  not not_29 (not_29_out, F3);
  not not_30 (not_30_out, F2);
  not not_31 (not_31_out, F1);
  not not_32 (not_32_out, OP5);
  not not_33 (not_33_out, OP4);
  not not_34 (not_34_out, OP3);
  not not_35 (not_35_out, OP2);
  not not_36 (not_36_out, OP1);
  not not_37 (not_37_out, OP0);
  not not_38 (not_38_out, F4);
  not not_39 (not_39_out, F3);
  not not_40 (not_40_out, F1);
  not not_41 (not_41_out, F0);
  not not_42 (not_42_out, OP5);
  not not_43 (not_43_out, OP4);
  not not_44 (not_44_out, OP3);
  not not_45 (not_45_out, OP2);
  not not_46 (not_46_out, OP1);
  not not_47 (not_47_out, OP0);
  not not_48 (not_48_out, F4);
  not not_49 (not_49_out, F2);
  not not_50 (not_50_out, F0);
  not not_51 (not_51_out, OP5);
  not not_52 (not_52_out, OP4);
  not not_53 (not_53_out, OP2);
  not not_54 (not_54_out, OP1);
  not not_55 (not_55_out, OP0);
  not not_56 (not_56_out, OP5);
  not not_57 (not_57_out, OP4);
  not not_58 (not_58_out, OP1);
  not not_59 (not_59_out, OP0);
  not not_60 (not_60_out, OP5);
  not not_61 (not_61_out, OP4);
  not not_62 (not_62_out, OP2);
  not not_63 (not_63_out, OP1);
  not not_64 (not_64_out, OP5);
  not not_65 (not_65_out, OP4);
  not not_66 (not_66_out, OP2);
  not not_67 (not_67_out, OP0);
  not not_68 (not_68_out, OP4);
  not not_69 (not_69_out, OP3);
  not not_70 (not_70_out, OP2);
  not not_71 (not_71_out, OP4);
  not not_72 (not_72_out, OP2);
  not not_73 (not_73_out, OP5);
  not not_74 (not_74_out, OP4);
  not not_75 (not_75_out, OP3);
  not not_76 (not_76_out, OP2);
  not not_77 (not_77_out, OP1);
  not not_78 (not_78_out, OP0);
  not not_79 (not_79_out, F5);
  not not_80 (not_80_out, F4);
  not not_81 (not_81_out, F3);
  not not_82 (not_82_out, OP4);
  not not_83 (not_83_out, OP3);
  not not_84 (not_84_out, OP1);
  not not_85 (not_85_out, OP0);
  not not_86 (not_86_out, OP5);
  not not_87 (not_87_out, OP4);
  not not_88 (not_88_out, OP3);
  not not_89 (not_89_out, OP2);
  not not_90 (not_90_out, OP1);
  not not_91 (not_91_out, OP5);
  not not_92 (not_92_out, OP4);
  not not_93 (not_93_out, OP3);
  not not_94 (not_94_out, OP2);
  not not_95 (not_95_out, OP1);
  not not_96 (not_96_out, OP0);
  not not_97 (not_97_out, F5);
  not not_98 (not_98_out, F4);
  not not_99 (not_99_out, F3);
  not not_100 (not_100_out, F2);
  not not_101 (not_101_out, F0);
  not not_102 (not_102_out, OP5);
  not not_103 (not_103_out, OP4);
  not not_104 (not_104_out, OP3);
  not not_105 (not_105_out, OP2);
  not not_106 (not_106_out, OP1);
  not not_107 (not_107_out, OP0);
  not not_108 (not_108_out, F4);
  not not_109 (not_109_out, F3);
  not not_110 (not_110_out, F2);
  not not_111 (not_111_out, F0);
  not not_112 (not_112_out, OP5);
  not not_113 (not_113_out, OP4);
  not not_114 (not_114_out, OP3);
  not not_115 (not_115_out, OP2);
  not not_116 (not_116_out, OP1);
  not not_117 (not_117_out, OP0);
  not not_118 (not_118_out, F4);
  not not_119 (not_119_out, F3);
  not not_120 (not_120_out, F1);
  not not_121 (not_121_out, F0);
  not not_122 (not_122_out, OP5);
  not not_123 (not_123_out, OP4);
  not not_124 (not_124_out, OP3);
  not not_125 (not_125_out, OP2);
  not not_126 (not_126_out, OP1);
  not not_127 (not_127_out, OP0);
  not not_128 (not_128_out, F4);
  not not_129 (not_129_out, F3);
  not not_130 (not_130_out, OP5);
  not not_131 (not_131_out, OP4);
  not not_132 (not_132_out, OP3);
  not not_133 (not_133_out, OP2);
  not not_134 (not_134_out, OP1);
  not not_135 (not_135_out, OP0);
  not not_136 (not_136_out, F4);
  not not_137 (not_137_out, F2);
  not not_138 (not_138_out, F0);
  not not_139 (not_139_out, OP5);
  not not_140 (not_140_out, OP4);
  not not_141 (not_141_out, OP1);
  not not_142 (not_142_out, OP0);
  not not_143 (not_143_out, OP5);
  not not_144 (not_144_out, OP4);
  not not_145 (not_145_out, OP2);
  not not_146 (not_146_out, OP0);
  not not_147 (not_147_out, OP5);
  not not_148 (not_148_out, OP4);
  not not_149 (not_149_out, OP3);
  not not_150 (not_150_out, OP2);
  not not_151 (not_151_out, OP1);
  not not_152 (not_152_out, OP5);
  not not_153 (not_153_out, OP4);
  not not_154 (not_154_out, OP3);
  not not_155 (not_155_out, OP2);
  not not_156 (not_156_out, OP1);
  not not_157 (not_157_out, OP0);
  not not_158 (not_158_out, F4);
  not not_159 (not_159_out, F3);
  not not_160 (not_160_out, F2);
  not not_161 (not_161_out, F1);
  not not_162 (not_162_out, F0);
  not not_163 (not_163_out, OP5);
  not not_164 (not_164_out, OP4);
  not not_165 (not_165_out, OP3);
  not not_166 (not_166_out, OP2);
  not not_167 (not_167_out, OP1);
  not not_168 (not_168_out, OP0);
  not not_169 (not_169_out, F4);
  not not_170 (not_170_out, F3);
  not not_171 (not_171_out, F2);
  not not_172 (not_172_out, F1);
  not not_173 (not_173_out, OP5);
  not not_174 (not_174_out, OP4);
  not not_175 (not_175_out, OP3);
  not not_176 (not_176_out, OP2);
  not not_177 (not_177_out, OP1);
  not not_178 (not_178_out, OP0);
  not not_179 (not_179_out, F4);
  not not_180 (not_180_out, F3);
  not not_181 (not_181_out, F2);
  not not_182 (not_182_out, F0);
  not not_183 (not_183_out, OP5);
  not not_184 (not_184_out, OP4);
  not not_185 (not_185_out, OP3);
  not not_186 (not_186_out, OP2);
  not not_187 (not_187_out, OP1);
  not not_188 (not_188_out, OP0);
  not not_189 (not_189_out, F4);
  not not_190 (not_190_out, F3);
  not not_191 (not_191_out, F1);
  not not_192 (not_192_out, F0);
  not not_193 (not_193_out, OP5);
  not not_194 (not_194_out, OP4);
  not not_195 (not_195_out, OP3);
  not not_196 (not_196_out, OP2);
  not not_197 (not_197_out, OP1);
  not not_198 (not_198_out, OP0);
  not not_199 (not_199_out, F4);
  not not_200 (not_200_out, F2);
  not not_201 (not_201_out, OP5);
  not not_202 (not_202_out, OP4);
  not not_203 (not_203_out, OP2);
  not not_204 (not_204_out, OP1);
  not not_205 (not_205_out, OP0);
  not not_206 (not_206_out, OP5);
  not not_207 (not_207_out, OP4);
  not not_208 (not_208_out, OP1);
  not not_209 (not_209_out, OP0);
  not not_210 (not_210_out, OP5);
  not not_211 (not_211_out, OP4);
  not not_212 (not_212_out, OP2);
  not not_213 (not_213_out, OP1);
  not not_214 (not_214_out, OP4);
  not not_215 (not_215_out, OP3);
  not not_216 (not_216_out, OP2);
  not not_217 (not_217_out, OP4);
  not not_218 (not_218_out, OP2);
  not not_219 (not_219_out, OP4);
  not not_220 (not_220_out, OP3);
  not not_221 (not_221_out, OP1);
  not not_222 (not_222_out, OP0);
  not not_223 (not_223_out, OP5);
  not not_224 (not_224_out, OP4);
  not not_225 (not_225_out, OP3);
  not not_226 (not_226_out, OP2);
  not not_227 (not_227_out, OP1);
  not not_228 (not_228_out, OP0);
  not not_229 (not_229_out, F4);
  not not_230 (not_230_out, F3);
  not not_231 (not_231_out, F1);
  not not_232 (not_232_out, OP5);
  not not_233 (not_233_out, OP4);
  not not_234 (not_234_out, OP3);
  not not_235 (not_235_out, OP2);
  not not_236 (not_236_out, OP1);
  not not_237 (not_237_out, OP0);
  not not_238 (not_238_out, F4);
  not not_239 (not_239_out, F3);
  not not_240 (not_240_out, OP5);
  not not_241 (not_241_out, OP4);
  not not_242 (not_242_out, OP3);
  not not_243 (not_243_out, OP2);
  not not_244 (not_244_out, OP1);
  not not_245 (not_245_out, OP0);
  not not_246 (not_246_out, F4);
  not not_247 (not_247_out, F2);
  not not_248 (not_248_out, F0);
  not not_249 (not_249_out, OP5);
  not not_250 (not_250_out, OP4);
  not not_251 (not_251_out, OP3);
  not not_252 (not_252_out, OP2);
  not not_253 (not_253_out, OP1);
  not not_254 (not_254_out, OP0);
  not not_255 (not_255_out, F4);
  not not_256 (not_256_out, F2);
  not not_257 (not_257_out, OP5);
  not not_258 (not_258_out, OP4);
  not not_259 (not_259_out, OP2);
  not not_260 (not_260_out, OP0);
  not not_261 (not_261_out, OP5);
  not not_262 (not_262_out, OP4);
  not not_263 (not_263_out, OP1);
  not not_264 (not_264_out, OP5);
  not not_265 (not_265_out, OP4);
  not not_266 (not_266_out, OP3);
  not not_267 (not_267_out, OP2);
  not not_268 (not_268_out, OP1);
  and and_1 (and_1_out, not_1_out, not_2_out, not_3_out, not_4_out, not_5_out, not_6_out, not_7_out, not_8_out, not_9_out, not_10_out, F1, F0);
  and and_2 (and_2_out, not_11_out, not_12_out, not_13_out, not_14_out, not_15_out, not_16_out, F5, not_17_out, not_18_out, not_19_out, not_20_out, not_21_out);
  and and_3 (and_3_out, not_22_out, not_23_out, not_24_out, not_25_out, not_26_out, not_27_out, F5, not_28_out, not_29_out, not_30_out, not_31_out, F0);
  and and_4 (and_4_out, not_32_out, not_33_out, not_34_out, not_35_out, not_36_out, not_37_out, F5, not_38_out, not_39_out, F2, not_40_out, not_41_out);
  and and_5 (and_5_out, not_42_out, not_43_out, not_44_out, not_45_out, not_46_out, not_47_out, F5, not_48_out, F3, not_49_out, F1, not_50_out);
  and and_6 (and_6_out, not_51_out, not_52_out, OP3, not_53_out, not_54_out, not_55_out);
  and and_7 (and_7_out, not_56_out, not_57_out, OP3, OP2, not_58_out, not_59_out);
  and and_8 (and_8_out, not_60_out, not_61_out, OP3, not_62_out, not_63_out, OP0);
  and and_9 (and_9_out, not_64_out, not_65_out, OP3, not_66_out, OP1, not_67_out);
  and and_10 (and_10_out, OP5, not_68_out, not_69_out, not_70_out, OP1, OP0);
  and and_11 (and_11_out, OP5, not_71_out, OP3, not_72_out, OP1, OP0);
  and and_12 (and_12_out, not_73_out, not_74_out, not_75_out, not_76_out, not_77_out, not_78_out, not_79_out, not_80_out, not_81_out, F2, F1, F0);
  and and_13 (and_13_out, OP5, not_82_out, not_83_out, OP2, not_84_out, not_85_out);
  and and_14 (and_14_out, not_86_out, not_87_out, not_88_out, not_89_out, not_90_out, OP0);
  and and_15 (and_15_out, not_91_out, not_92_out, not_93_out, not_94_out, not_95_out, not_96_out, not_97_out, not_98_out, not_99_out, not_100_out, F1, not_101_out);
  and and_16 (and_16_out, not_102_out, not_103_out, not_104_out, not_105_out, not_106_out, not_107_out, F5, not_108_out, not_109_out, not_110_out, F1, not_111_out);
  and and_17 (and_17_out, not_112_out, not_113_out, not_114_out, not_115_out, not_116_out, not_117_out, F5, not_118_out, not_119_out, F2, not_120_out, not_121_out);
  and and_18 (and_18_out, not_122_out, not_123_out, not_124_out, not_125_out, not_126_out, not_127_out, F5, not_128_out, not_129_out, F2, F1, F0);
  and and_19 (and_19_out, not_130_out, not_131_out, not_132_out, not_133_out, not_134_out, not_135_out, F5, not_136_out, F3, not_137_out, F1, not_138_out);
  and and_20 (and_20_out, not_139_out, not_140_out, OP3, OP2, not_141_out, not_142_out);
  and and_21 (and_21_out, not_143_out, not_144_out, OP3, not_145_out, OP1, not_146_out);
  and and_22 (and_22_out, not_147_out, not_148_out, not_149_out, not_150_out, not_151_out, OP0);
  and and_23 (and_23_out, not_152_out, not_153_out, not_154_out, not_155_out, not_156_out, not_157_out, F5, not_158_out, not_159_out, not_160_out, not_161_out, not_162_out);
  and and_24 (and_24_out, not_163_out, not_164_out, not_165_out, not_166_out, not_167_out, not_168_out, F5, not_169_out, not_170_out, not_171_out, not_172_out, F0);
  and and_25 (and_25_out, not_173_out, not_174_out, not_175_out, not_176_out, not_177_out, not_178_out, F5, not_179_out, not_180_out, not_181_out, F1, not_182_out);
  and and_26 (and_26_out, not_183_out, not_184_out, not_185_out, not_186_out, not_187_out, not_188_out, F5, not_189_out, not_190_out, F2, not_191_out, not_192_out);
  and and_27 (and_27_out, not_193_out, not_194_out, not_195_out, not_196_out, not_197_out, not_198_out, F5, not_199_out, F3, not_200_out, F1, F0);
  and and_28 (and_28_out, not_201_out, not_202_out, OP3, not_203_out, not_204_out, not_205_out);
  and and_29 (and_29_out, not_206_out, not_207_out, OP3, OP2, not_208_out, not_209_out);
  and and_30 (and_30_out, not_210_out, not_211_out, OP3, not_212_out, not_213_out, OP0);
  and and_31 (and_31_out, OP5, not_214_out, not_215_out, not_216_out, OP1, OP0);
  and and_32 (and_32_out, OP5, not_217_out, OP3, not_218_out, OP1, OP0);
  and and_33 (and_33_out, OP5, not_219_out, not_220_out, OP2, not_221_out, not_222_out);
  and and_34 (and_34_out, not_223_out, not_224_out, not_225_out, not_226_out, not_227_out, not_228_out, F5, not_229_out, not_230_out, F2, not_231_out, F0);
  and and_35 (and_35_out, not_232_out, not_233_out, not_234_out, not_235_out, not_236_out, not_237_out, F5, not_238_out, not_239_out, F2, F1, F0);
  and and_36 (and_36_out, not_240_out, not_241_out, not_242_out, not_243_out, not_244_out, not_245_out, F5, not_246_out, F3, not_247_out, F1, not_248_out);
  and and_37 (and_37_out, not_249_out, not_250_out, not_251_out, not_252_out, not_253_out, not_254_out, F5, not_255_out, F3, not_256_out, F1, F0);
  and and_38 (and_38_out, not_257_out, not_258_out, OP3, not_259_out, OP1, not_260_out);
  and and_39 (and_39_out, not_261_out, not_262_out, OP3, OP2, not_263_out, OP0);
  and and_40 (and_40_out, not_264_out, not_265_out, not_266_out, not_267_out, not_268_out, OP0);
  or or_1 (S1, and_15_out, and_16_out, and_17_out, and_18_out, and_19_out, and_20_out, and_21_out, and_22_out);
  or or_2 (S2, and_23_out, and_24_out, and_25_out, and_26_out, and_27_out, and_28_out, and_29_out, and_30_out, and_31_out, and_32_out, and_33_out);
  or or_3 (S3, and_34_out, and_35_out, and_36_out, and_37_out, and_38_out, and_39_out, and_40_out);
  or or_4 (S0, and_1_out, and_2_out, and_3_out, and_4_out, and_5_out, and_6_out, and_7_out, and_8_out, and_9_out, and_10_out, and_11_out, and_12_out, and_13_out, and_14_out);
endmodule

// 控制信号生成
module \控制信号自动生成  (
  input  OP0,
  input  OP1,
  input  OP2,
  input  OP3,
  input  OP4,
  input  OP5,
  input  F0,
  input  F1,
  input  F2,
  input  F3,
  input  F4,
  input  F5,
  output MemToReg,
  output LBU,
  output MemWrite,
  output SLLV,
  output SRAV,
  output BGEZ,
  output ALU_SRC,
  output RegWrite,
  output SysCALL,
  output SignedExt,
  output RegDst,
  output BEQ,
  output BNE,
  output JR,
  output JUMP,
  output JAL
);

  wire and_1_out, and_2_out, and_8_out, and_9_out, and_10_out, and_11_out, and_12_out, and_13_out,
       and_14_out, and_15_out, and_16_out, and_17_out, and_18_out, and_19_out, and_20_out, and_21_out,
       and_22_out, and_23_out, and_24_out, and_25_out, and_26_out, and_27_out, and_28_out, and_29_out,
       and_30_out, and_31_out, and_32_out, and_33_out, and_34_out, and_35_out, and_36_out, and_38_out,
       and_39_out, and_40_out, and_41_out, and_42_out, and_43_out, and_44_out, and_45_out, and_46_out,
       and_47_out, and_48_out, and_49_out, and_50_out, and_51_out, and_52_out, and_53_out, and_54_out,
       and_55_out, and_56_out, and_57_out, and_58_out, and_59_out, and_63_out, and_64_out, and_65_out,
       not_1_out, not_2_out, not_3_out, not_4_out, not_5_out, not_6_out, not_7_out, not_8_out, not_9_out,
       not_10_out, not_11_out, not_12_out, not_13_out, not_14_out, not_15_out, not_16_out, not_17_out,
       not_18_out, not_19_out, not_20_out, not_21_out, not_22_out, not_23_out, not_24_out, not_25_out,
       not_26_out, not_27_out, not_28_out, not_29_out, not_30_out, not_31_out, not_32_out, not_33_out,
       not_34_out, not_35_out, not_36_out, not_37_out, not_38_out, not_39_out, not_40_out, not_41_out,
       not_42_out, not_43_out, not_44_out, not_45_out, not_46_out, not_47_out, not_48_out, not_49_out,
       not_50_out, not_51_out, not_52_out, not_53_out, not_54_out, not_55_out, not_56_out, not_57_out,
       not_58_out, not_59_out, not_60_out, not_61_out, not_62_out, not_63_out, not_64_out, not_65_out,
       not_66_out, not_67_out, not_68_out, not_69_out, not_70_out, not_71_out, not_72_out, not_73_out,
       not_74_out, not_75_out, not_76_out, not_77_out, not_78_out, not_79_out, not_80_out, not_81_out,
       not_82_out, not_83_out, not_84_out, not_85_out, not_86_out, not_87_out, not_88_out, not_89_out,
       not_90_out, not_91_out, not_92_out, not_93_out, not_94_out, not_95_out, not_96_out, not_97_out,
       not_98_out, not_99_out, not_100_out, not_101_out, not_102_out, not_103_out, not_104_out, not_105_out,
       not_106_out, not_107_out, not_108_out, not_109_out, not_110_out, not_111_out, not_112_out,
       not_113_out, not_114_out, not_115_out, not_116_out, not_117_out, not_118_out, not_119_out,
       not_120_out, not_121_out, not_122_out, not_123_out, not_124_out, not_125_out, not_126_out,
       not_127_out, not_128_out, not_129_out, not_130_out, not_131_out, not_132_out, not_133_out,
       not_134_out, not_135_out, not_136_out, not_137_out, not_138_out, not_139_out, not_140_out,
       not_141_out, not_142_out, not_143_out, not_144_out, not_145_out, not_146_out, not_147_out,
       not_148_out, not_149_out, not_150_out, not_151_out, not_152_out, not_153_out, not_154_out,
       not_155_out, not_156_out, not_157_out, not_158_out, not_159_out, not_160_out, not_161_out,
       not_162_out, not_163_out, not_164_out, not_165_out, not_166_out, not_167_out, not_168_out,
       not_169_out, not_170_out, not_171_out, not_172_out, not_173_out, not_174_out, not_175_out,
       not_176_out, not_177_out, not_178_out, not_179_out, not_180_out, not_181_out, not_182_out,
       not_183_out, not_184_out, not_185_out, not_186_out, not_187_out, not_188_out, not_189_out,
       not_190_out, not_191_out, not_192_out, not_193_out, not_194_out, not_195_out, not_196_out,
       not_197_out, not_198_out, not_199_out, not_200_out, not_201_out, not_202_out, not_203_out,
       not_204_out, not_205_out, not_206_out, not_207_out, not_208_out, not_209_out, not_210_out,
       not_211_out, not_212_out, not_213_out, not_214_out, not_215_out, not_216_out, not_217_out,
       not_218_out, not_219_out, not_220_out, not_221_out, not_222_out, not_223_out, not_224_out,
       not_225_out, not_226_out, not_227_out, not_228_out, not_229_out, not_230_out, not_231_out,
       not_232_out, not_233_out, not_234_out, not_235_out, not_236_out, not_237_out, not_238_out,
       not_239_out, not_240_out, not_241_out, not_242_out, not_243_out, not_244_out, not_245_out,
       not_246_out, not_247_out, not_248_out, not_249_out, not_250_out, not_251_out, not_252_out,
       not_253_out, not_254_out, not_255_out, not_256_out, not_257_out, not_258_out, not_259_out,
       not_260_out, not_261_out, not_262_out, not_263_out, not_264_out, not_265_out, not_266_out,
       not_267_out, not_268_out, not_269_out, not_270_out, not_271_out, not_272_out, not_273_out,
       not_274_out, not_275_out, not_276_out, not_277_out, not_278_out, not_279_out, not_280_out,
       not_281_out, not_282_out, not_283_out, not_284_out, not_285_out, not_286_out, not_287_out,
       not_288_out, not_289_out, not_290_out, not_291_out, not_292_out, not_293_out, not_294_out,
       not_295_out, not_296_out, not_297_out, not_298_out, not_299_out, not_300_out, not_301_out,
       not_302_out, not_303_out, not_304_out, not_305_out, not_306_out, not_307_out, not_308_out,
       not_309_out, not_310_out, not_311_out, not_312_out, not_313_out, not_314_out, not_315_out,
       not_316_out, not_317_out, not_318_out, not_319_out, not_320_out, not_321_out, not_322_out,
       not_323_out, not_324_out, not_325_out, not_326_out, not_327_out, not_328_out, not_329_out,
       not_330_out, not_331_out, not_332_out, not_333_out, not_334_out, not_335_out, not_336_out,
       not_337_out, not_338_out, not_339_out, not_340_out, not_341_out, not_342_out, not_343_out,
       not_344_out, not_345_out, not_346_out, not_347_out, not_348_out, not_349_out, not_350_out,
       not_351_out, not_352_out, not_353_out, not_354_out, not_355_out, not_356_out, not_357_out,
       not_358_out, not_359_out, not_360_out, not_361_out, not_362_out, not_363_out, not_364_out,
       not_365_out, not_366_out, not_367_out, not_368_out, not_369_out, not_370_out, not_371_out,
       not_372_out, not_373_out, not_374_out, not_375_out, not_376_out, not_377_out, not_378_out,
       not_379_out, not_380_out, not_381_out, not_382_out, not_383_out, not_384_out, not_385_out,
       not_386_out, not_387_out, not_388_out, not_389_out, not_390_out, not_391_out, not_392_out,
       not_393_out, not_394_out, not_395_out, not_396_out, not_397_out, not_398_out, not_399_out,
       not_400_out, not_401_out, not_402_out, not_403_out, not_404_out, not_405_out, not_406_out,
       not_407_out, not_408_out, not_409_out, not_410_out, not_411_out, not_412_out, not_413_out,
       not_414_out, not_415_out, not_416_out, not_417_out, not_418_out, not_419_out, not_420_out,
       not_421_out, not_422_out, not_423_out, not_424_out, not_425_out, not_426_out, not_427_out,
       not_428_out, not_429_out, not_430_out, not_431_out, not_432_out, not_433_out, not_434_out,
       not_435_out, not_436_out, not_437_out, not_438_out, not_439_out, not_440_out, not_441_out,
       not_442_out, not_443_out, not_444_out;

  not not_1 (not_1_out, OP4);
  not not_2 (not_2_out, OP3);
  not not_3 (not_3_out, OP2);
  not not_4 (not_4_out, OP4);
  not not_5 (not_5_out, OP3);
  not not_6 (not_6_out, OP1);
  not not_7 (not_7_out, OP0);
  not not_8 (not_8_out, OP4);
  not not_9 (not_9_out, OP3);
  not not_10 (not_10_out, OP1);
  not not_11 (not_11_out, OP0);
  not not_12 (not_12_out, OP4);
  not not_13 (not_13_out, OP2);
  not not_14 (not_14_out, OP5);
  not not_15 (not_15_out, OP4);
  not not_16 (not_16_out, OP3);
  not not_17 (not_17_out, OP2);
  not not_18 (not_18_out, OP1);
  not not_19 (not_19_out, OP0);
  not not_20 (not_20_out, F5);
  not not_21 (not_21_out, F4);
  not not_22 (not_22_out, F3);
  not not_23 (not_23_out, F1);
  not not_24 (not_24_out, F0);
  not not_25 (not_25_out, OP5);
  not not_26 (not_26_out, OP4);
  not not_27 (not_27_out, OP3);
  not not_28 (not_28_out, OP2);
  not not_29 (not_29_out, OP1);
  not not_30 (not_30_out, OP0);
  not not_31 (not_31_out, F5);
  not not_32 (not_32_out, F4);
  not not_33 (not_33_out, F3);
  not not_34 (not_34_out, OP5);
  not not_35 (not_35_out, OP4);
  not not_36 (not_36_out, OP3);
  not not_37 (not_37_out, OP2);
  not not_38 (not_38_out, OP1);
  not not_39 (not_39_out, OP5);
  not not_40 (not_40_out, OP4);
  not not_41 (not_41_out, OP2);
  not not_42 (not_42_out, OP1);
  not not_43 (not_43_out, OP0);
  not not_44 (not_44_out, OP5);
  not not_45 (not_45_out, OP4);
  not not_46 (not_46_out, OP1);
  not not_47 (not_47_out, OP0);
  not not_48 (not_48_out, OP5);
  not not_49 (not_49_out, OP4);
  not not_50 (not_50_out, OP2);
  not not_51 (not_51_out, OP1);
  not not_52 (not_52_out, OP5);
  not not_53 (not_53_out, OP4);
  not not_54 (not_54_out, OP2);
  not not_55 (not_55_out, OP0);
  not not_56 (not_56_out, OP5);
  not not_57 (not_57_out, OP4);
  not not_58 (not_58_out, OP1);
  not not_59 (not_59_out, OP4);
  not not_60 (not_60_out, OP3);
  not not_61 (not_61_out, OP2);
  not not_62 (not_62_out, OP4);
  not not_63 (not_63_out, OP2);
  not not_64 (not_64_out, OP4);
  not not_65 (not_65_out, OP3);
  not not_66 (not_66_out, OP1);
  not not_67 (not_67_out, OP0);
  not not_68 (not_68_out, OP5);
  not not_69 (not_69_out, OP4);
  not not_70 (not_70_out, OP3);
  not not_71 (not_71_out, OP2);
  not not_72 (not_72_out, OP1);
  not not_73 (not_73_out, OP0);
  not not_74 (not_74_out, F5);
  not not_75 (not_75_out, F4);
  not not_76 (not_76_out, F3);
  not not_77 (not_77_out, F2);
  not not_78 (not_78_out, F1);
  not not_79 (not_79_out, F0);
  not not_80 (not_80_out, OP5);
  not not_81 (not_81_out, OP4);
  not not_82 (not_82_out, OP3);
  not not_83 (not_83_out, OP2);
  not not_84 (not_84_out, OP1);
  not not_85 (not_85_out, OP0);
  not not_86 (not_86_out, F5);
  not not_87 (not_87_out, F4);
  not not_88 (not_88_out, F3);
  not not_89 (not_89_out, F2);
  not not_90 (not_90_out, OP5);
  not not_91 (not_91_out, OP4);
  not not_92 (not_92_out, OP3);
  not not_93 (not_93_out, OP2);
  not not_94 (not_94_out, OP1);
  not not_95 (not_95_out, OP0);
  not not_96 (not_96_out, F5);
  not not_97 (not_97_out, F4);
  not not_98 (not_98_out, F3);
  not not_99 (not_99_out, F2);
  not not_100 (not_100_out, F0);
  not not_101 (not_101_out, OP5);
  not not_102 (not_102_out, OP4);
  not not_103 (not_103_out, OP3);
  not not_104 (not_104_out, OP2);
  not not_105 (not_105_out, OP1);
  not not_106 (not_106_out, OP0);
  not not_107 (not_107_out, F4);
  not not_108 (not_108_out, F3);
  not not_109 (not_109_out, F2);
  not not_110 (not_110_out, F1);
  not not_111 (not_111_out, F0);
  not not_112 (not_112_out, OP5);
  not not_113 (not_113_out, OP4);
  not not_114 (not_114_out, OP3);
  not not_115 (not_115_out, OP2);
  not not_116 (not_116_out, OP1);
  not not_117 (not_117_out, OP0);
  not not_118 (not_118_out, F4);
  not not_119 (not_119_out, F3);
  not not_120 (not_120_out, F2);
  not not_121 (not_121_out, F1);
  not not_122 (not_122_out, OP5);
  not not_123 (not_123_out, OP4);
  not not_124 (not_124_out, OP3);
  not not_125 (not_125_out, OP2);
  not not_126 (not_126_out, OP1);
  not not_127 (not_127_out, OP0);
  not not_128 (not_128_out, F4);
  not not_129 (not_129_out, F3);
  not not_130 (not_130_out, F2);
  not not_131 (not_131_out, F0);
  not not_132 (not_132_out, OP5);
  not not_133 (not_133_out, OP4);
  not not_134 (not_134_out, OP3);
  not not_135 (not_135_out, OP2);
  not not_136 (not_136_out, OP1);
  not not_137 (not_137_out, OP0);
  not not_138 (not_138_out, F4);
  not not_139 (not_139_out, F3);
  not not_140 (not_140_out, F1);
  not not_141 (not_141_out, F0);
  not not_142 (not_142_out, OP5);
  not not_143 (not_143_out, OP4);
  not not_144 (not_144_out, OP3);
  not not_145 (not_145_out, OP2);
  not not_146 (not_146_out, OP1);
  not not_147 (not_147_out, OP0);
  not not_148 (not_148_out, F4);
  not not_149 (not_149_out, F3);
  not not_150 (not_150_out, F1);
  not not_151 (not_151_out, OP5);
  not not_152 (not_152_out, OP4);
  not not_153 (not_153_out, OP3);
  not not_154 (not_154_out, OP2);
  not not_155 (not_155_out, OP1);
  not not_156 (not_156_out, OP0);
  not not_157 (not_157_out, F4);
  not not_158 (not_158_out, F3);
  not not_159 (not_159_out, OP5);
  not not_160 (not_160_out, OP4);
  not not_161 (not_161_out, OP3);
  not not_162 (not_162_out, OP2);
  not not_163 (not_163_out, OP1);
  not not_164 (not_164_out, OP0);
  not not_165 (not_165_out, F4);
  not not_166 (not_166_out, F2);
  not not_167 (not_167_out, F0);
  not not_168 (not_168_out, OP5);
  not not_169 (not_169_out, OP4);
  not not_170 (not_170_out, OP3);
  not not_171 (not_171_out, OP2);
  not not_172 (not_172_out, OP1);
  not not_173 (not_173_out, OP0);
  not not_174 (not_174_out, F4);
  not not_175 (not_175_out, F2);
  not not_176 (not_176_out, OP5);
  not not_177 (not_177_out, OP4);
  not not_178 (not_178_out, OP3);
  not not_179 (not_179_out, OP2);
  not not_180 (not_180_out, OP5);
  not not_181 (not_181_out, OP4);
  not not_182 (not_182_out, OP2);
  not not_183 (not_183_out, OP1);
  not not_184 (not_184_out, OP0);
  not not_185 (not_185_out, OP5);
  not not_186 (not_186_out, OP4);
  not not_187 (not_187_out, OP1);
  not not_188 (not_188_out, OP0);
  not not_189 (not_189_out, OP5);
  not not_190 (not_190_out, OP4);
  not not_191 (not_191_out, OP2);
  not not_192 (not_192_out, OP1);
  not not_193 (not_193_out, OP5);
  not not_194 (not_194_out, OP4);
  not not_195 (not_195_out, OP2);
  not not_196 (not_196_out, OP0);
  not not_197 (not_197_out, OP5);
  not not_198 (not_198_out, OP4);
  not not_199 (not_199_out, OP1);
  not not_200 (not_200_out, OP4);
  not not_201 (not_201_out, OP3);
  not not_202 (not_202_out, OP2);
  not not_203 (not_203_out, OP5);
  not not_204 (not_204_out, OP4);
  not not_205 (not_205_out, OP3);
  not not_206 (not_206_out, OP2);
  not not_207 (not_207_out, OP1);
  not not_208 (not_208_out, OP0);
  not not_209 (not_209_out, F5);
  not not_210 (not_210_out, F4);
  not not_211 (not_211_out, F3);
  not not_212 (not_212_out, F1);
  not not_213 (not_213_out, F0);
  not not_214 (not_214_out, OP5);
  not not_215 (not_215_out, OP4);
  not not_216 (not_216_out, OP3);
  not not_217 (not_217_out, OP2);
  not not_218 (not_218_out, OP1);
  not not_219 (not_219_out, OP0);
  not not_220 (not_220_out, F5);
  not not_221 (not_221_out, F4);
  not not_222 (not_222_out, F3);
  not not_223 (not_223_out, OP4);
  not not_224 (not_224_out, OP3);
  not not_225 (not_225_out, OP1);
  not not_226 (not_226_out, OP0);
  not not_227 (not_227_out, OP5);
  not not_228 (not_228_out, OP4);
  not not_229 (not_229_out, OP3);
  not not_230 (not_230_out, OP2);
  not not_231 (not_231_out, OP1);
  not not_232 (not_232_out, OP0);
  not not_233 (not_233_out, F5);
  not not_234 (not_234_out, F4);
  not not_235 (not_235_out, F1);
  not not_236 (not_236_out, F0);
  not not_237 (not_237_out, OP5);
  not not_238 (not_238_out, OP4);
  not not_239 (not_239_out, OP3);
  not not_240 (not_240_out, OP1);
  not not_241 (not_241_out, OP0);
  not not_242 (not_242_out, OP5);
  not not_243 (not_243_out, OP4);
  not not_244 (not_244_out, OP3);
  not not_245 (not_245_out, OP1);
  not not_246 (not_246_out, OP5);
  not not_247 (not_247_out, OP4);
  not not_248 (not_248_out, OP2);
  not not_249 (not_249_out, OP1);
  not not_250 (not_250_out, OP0);
  not not_251 (not_251_out, OP5);
  not not_252 (not_252_out, OP4);
  not not_253 (not_253_out, OP2);
  not not_254 (not_254_out, OP1);
  not not_255 (not_255_out, OP5);
  not not_256 (not_256_out, OP4);
  not not_257 (not_257_out, OP2);
  not not_258 (not_258_out, OP0);
  not not_259 (not_259_out, OP4);
  not not_260 (not_260_out, OP3);
  not not_261 (not_261_out, OP2);
  not not_262 (not_262_out, OP4);
  not not_263 (not_263_out, OP2);
  not not_264 (not_264_out, OP4);
  not not_265 (not_265_out, OP3);
  not not_266 (not_266_out, OP1);
  not not_267 (not_267_out, OP0);
  not not_268 (not_268_out, OP5);
  not not_269 (not_269_out, OP4);
  not not_270 (not_270_out, OP3);
  not not_271 (not_271_out, OP2);
  not not_272 (not_272_out, OP1);
  not not_273 (not_273_out, OP5);
  not not_274 (not_274_out, OP4);
  not not_275 (not_275_out, OP3);
  not not_276 (not_276_out, OP2);
  not not_277 (not_277_out, OP1);
  not not_278 (not_278_out, OP0);
  not not_279 (not_279_out, F5);
  not not_280 (not_280_out, F4);
  not not_281 (not_281_out, F3);
  not not_282 (not_282_out, F2);
  not not_283 (not_283_out, F1);
  not not_284 (not_284_out, F0);
  not not_285 (not_285_out, OP5);
  not not_286 (not_286_out, OP4);
  not not_287 (not_287_out, OP3);
  not not_288 (not_288_out, OP2);
  not not_289 (not_289_out, OP1);
  not not_290 (not_290_out, OP0);
  not not_291 (not_291_out, F5);
  not not_292 (not_292_out, F4);
  not not_293 (not_293_out, F3);
  not not_294 (not_294_out, F2);
  not not_295 (not_295_out, OP5);
  not not_296 (not_296_out, OP4);
  not not_297 (not_297_out, OP3);
  not not_298 (not_298_out, OP2);
  not not_299 (not_299_out, OP1);
  not not_300 (not_300_out, OP0);
  not not_301 (not_301_out, F5);
  not not_302 (not_302_out, F4);
  not not_303 (not_303_out, F3);
  not not_304 (not_304_out, F2);
  not not_305 (not_305_out, F0);
  not not_306 (not_306_out, OP5);
  not not_307 (not_307_out, OP4);
  not not_308 (not_308_out, OP3);
  not not_309 (not_309_out, OP2);
  not not_310 (not_310_out, OP1);
  not not_311 (not_311_out, OP0);
  not not_312 (not_312_out, F4);
  not not_313 (not_313_out, F3);
  not not_314 (not_314_out, F2);
  not not_315 (not_315_out, F1);
  not not_316 (not_316_out, F0);
  not not_317 (not_317_out, OP5);
  not not_318 (not_318_out, OP4);
  not not_319 (not_319_out, OP3);
  not not_320 (not_320_out, OP2);
  not not_321 (not_321_out, OP1);
  not not_322 (not_322_out, OP0);
  not not_323 (not_323_out, F4);
  not not_324 (not_324_out, F3);
  not not_325 (not_325_out, F2);
  not not_326 (not_326_out, F1);
  not not_327 (not_327_out, OP5);
  not not_328 (not_328_out, OP4);
  not not_329 (not_329_out, OP3);
  not not_330 (not_330_out, OP2);
  not not_331 (not_331_out, OP1);
  not not_332 (not_332_out, OP0);
  not not_333 (not_333_out, F4);
  not not_334 (not_334_out, F3);
  not not_335 (not_335_out, F2);
  not not_336 (not_336_out, F0);
  not not_337 (not_337_out, OP5);
  not not_338 (not_338_out, OP4);
  not not_339 (not_339_out, OP3);
  not not_340 (not_340_out, OP2);
  not not_341 (not_341_out, OP1);
  not not_342 (not_342_out, OP0);
  not not_343 (not_343_out, F4);
  not not_344 (not_344_out, F3);
  not not_345 (not_345_out, F1);
  not not_346 (not_346_out, F0);
  not not_347 (not_347_out, OP5);
  not not_348 (not_348_out, OP4);
  not not_349 (not_349_out, OP3);
  not not_350 (not_350_out, OP2);
  not not_351 (not_351_out, OP1);
  not not_352 (not_352_out, OP0);
  not not_353 (not_353_out, F4);
  not not_354 (not_354_out, F3);
  not not_355 (not_355_out, F1);
  not not_356 (not_356_out, OP5);
  not not_357 (not_357_out, OP4);
  not not_358 (not_358_out, OP3);
  not not_359 (not_359_out, OP2);
  not not_360 (not_360_out, OP1);
  not not_361 (not_361_out, OP0);
  not not_362 (not_362_out, F4);
  not not_363 (not_363_out, F3);
  not not_364 (not_364_out, OP5);
  not not_365 (not_365_out, OP4);
  not not_366 (not_366_out, OP3);
  not not_367 (not_367_out, OP2);
  not not_368 (not_368_out, OP1);
  not not_369 (not_369_out, OP0);
  not not_370 (not_370_out, F4);
  not not_371 (not_371_out, F2);
  not not_372 (not_372_out, F0);
  not not_373 (not_373_out, OP5);
  not not_374 (not_374_out, OP4);
  not not_375 (not_375_out, OP3);
  not not_376 (not_376_out, OP2);
  not not_377 (not_377_out, OP1);
  not not_378 (not_378_out, OP0);
  not not_379 (not_379_out, F4);
  not not_380 (not_380_out, F2);
  not not_381 (not_381_out, OP5);
  not not_382 (not_382_out, OP4);
  not not_383 (not_383_out, OP3);
  not not_384 (not_384_out, OP2);
  not not_385 (not_385_out, OP1);
  not not_386 (not_386_out, OP0);
  not not_387 (not_387_out, F5);
  not not_388 (not_388_out, F4);
  not not_389 (not_389_out, F3);
  not not_390 (not_390_out, F1);
  not not_391 (not_391_out, F0);
  not not_392 (not_392_out, OP5);
  not not_393 (not_393_out, OP4);
  not not_394 (not_394_out, OP3);
  not not_395 (not_395_out, OP2);
  not not_396 (not_396_out, OP1);
  not not_397 (not_397_out, OP0);
  not not_398 (not_398_out, F5);
  not not_399 (not_399_out, F4);
  not not_400 (not_400_out, F3);
  not not_401 (not_401_out, OP5);
  not not_402 (not_402_out, OP4);
  not not_403 (not_403_out, OP3);
  not not_404 (not_404_out, OP1);
  not not_405 (not_405_out, OP0);
  not not_406 (not_406_out, OP5);
  not not_407 (not_407_out, OP4);
  not not_408 (not_408_out, OP3);
  not not_409 (not_409_out, OP1);
  not not_410 (not_410_out, OP5);
  not not_411 (not_411_out, OP4);
  not not_412 (not_412_out, OP3);
  not not_413 (not_413_out, OP2);
  not not_414 (not_414_out, OP1);
  not not_415 (not_415_out, OP0);
  not not_416 (not_416_out, F5);
  not not_417 (not_417_out, F4);
  not not_418 (not_418_out, F2);
  not not_419 (not_419_out, F1);
  not not_420 (not_420_out, F0);
  not not_421 (not_421_out, OP5);
  not not_422 (not_422_out, OP4);
  not not_423 (not_423_out, OP3);
  not not_424 (not_424_out, OP2);
  not not_425 (not_425_out, OP1);
  not not_426 (not_426_out, OP0);
  not not_427 (not_427_out, F5);
  not not_428 (not_428_out, F4);
  not not_429 (not_429_out, F2);
  not not_430 (not_430_out, F1);
  not not_431 (not_431_out, F0);
  not not_432 (not_432_out, OP5);
  not not_433 (not_433_out, OP4);
  not not_434 (not_434_out, OP3);
  not not_435 (not_435_out, OP2);
  not not_436 (not_436_out, OP0);
  not not_437 (not_437_out, OP5);
  not not_438 (not_438_out, OP4);
  not not_439 (not_439_out, OP3);
  not not_440 (not_440_out, OP2);
  not not_441 (not_441_out, OP5);
  not not_442 (not_442_out, OP4);
  not not_443 (not_443_out, OP3);
  not not_444 (not_444_out, OP2);
  and and_1 (and_1_out, OP5, not_1_out, not_2_out, not_3_out, OP1, OP0);
  and and_2 (and_2_out, OP5, not_4_out, not_5_out, OP2, not_6_out, not_7_out);
  and and_3 (LBU, OP5, not_8_out, not_9_out, OP2, not_10_out, not_11_out);
  and and_4 (MemWrite, OP5, not_12_out, OP3, not_13_out, OP1, OP0);
  and and_5 (SLLV, not_14_out, not_15_out, not_16_out, not_17_out, not_18_out, not_19_out, not_20_out, not_21_out, not_22_out, F2, not_23_out, not_24_out);
  and and_6 (SRAV, not_25_out, not_26_out, not_27_out, not_28_out, not_29_out, not_30_out, not_31_out, not_32_out, not_33_out, F2, F1, F0);
  and and_7 (BGEZ, not_34_out, not_35_out, not_36_out, not_37_out, not_38_out, OP0);
  and and_8 (and_8_out, not_39_out, not_40_out, OP3, not_41_out, not_42_out, not_43_out);
  and and_9 (and_9_out, not_44_out, not_45_out, OP3, OP2, not_46_out, not_47_out);
  and and_10 (and_10_out, not_48_out, not_49_out, OP3, not_50_out, not_51_out, OP0);
  and and_11 (and_11_out, not_52_out, not_53_out, OP3, not_54_out, OP1, not_55_out);
  and and_12 (and_12_out, not_56_out, not_57_out, OP3, OP2, not_58_out, OP0);
  and and_13 (and_13_out, OP5, not_59_out, not_60_out, not_61_out, OP1, OP0);
  and and_14 (and_14_out, OP5, not_62_out, OP3, not_63_out, OP1, OP0);
  and and_15 (and_15_out, OP5, not_64_out, not_65_out, OP2, not_66_out, not_67_out);
  and and_16 (and_16_out, not_68_out, not_69_out, not_70_out, not_71_out, not_72_out, not_73_out, not_74_out, not_75_out, not_76_out, not_77_out, not_78_out, not_79_out);
  and and_17 (and_17_out, not_80_out, not_81_out, not_82_out, not_83_out, not_84_out, not_85_out, not_86_out, not_87_out, not_88_out, not_89_out, F1, F0);
  and and_18 (and_18_out, not_90_out, not_91_out, not_92_out, not_93_out, not_94_out, not_95_out, not_96_out, not_97_out, not_98_out, not_99_out, F1, not_100_out);
  and and_19 (and_19_out, not_101_out, not_102_out, not_103_out, not_104_out, not_105_out, not_106_out, F5, not_107_out, not_108_out, not_109_out, not_110_out, not_111_out);
  and and_20 (and_20_out, not_112_out, not_113_out, not_114_out, not_115_out, not_116_out, not_117_out, F5, not_118_out, not_119_out, not_120_out, not_121_out, F0);
  and and_21 (and_21_out, not_122_out, not_123_out, not_124_out, not_125_out, not_126_out, not_127_out, F5, not_128_out, not_129_out, not_130_out, F1, not_131_out);
  and and_22 (and_22_out, not_132_out, not_133_out, not_134_out, not_135_out, not_136_out, not_137_out, F5, not_138_out, not_139_out, F2, not_140_out, not_141_out);
  and and_23 (and_23_out, not_142_out, not_143_out, not_144_out, not_145_out, not_146_out, not_147_out, F5, not_148_out, not_149_out, F2, not_150_out, F0);
  and and_24 (and_24_out, not_151_out, not_152_out, not_153_out, not_154_out, not_155_out, not_156_out, F5, not_157_out, not_158_out, F2, F1, F0);
  and and_25 (and_25_out, not_159_out, not_160_out, not_161_out, not_162_out, not_163_out, not_164_out, F5, not_165_out, F3, not_166_out, F1, not_167_out);
  and and_26 (and_26_out, not_168_out, not_169_out, not_170_out, not_171_out, not_172_out, not_173_out, F5, not_174_out, F3, not_175_out, F1, F0);
  and and_27 (and_27_out, not_176_out, not_177_out, not_178_out, not_179_out, OP1, OP0);
  and and_28 (and_28_out, not_180_out, not_181_out, OP3, not_182_out, not_183_out, not_184_out);
  and and_29 (and_29_out, not_185_out, not_186_out, OP3, OP2, not_187_out, not_188_out);
  and and_30 (and_30_out, not_189_out, not_190_out, OP3, not_191_out, not_192_out, OP0);
  and and_31 (and_31_out, not_193_out, not_194_out, OP3, not_195_out, OP1, not_196_out);
  and and_32 (and_32_out, not_197_out, not_198_out, OP3, OP2, not_199_out, OP0);
  and and_33 (and_33_out, OP5, not_200_out, not_201_out, not_202_out, OP1, OP0);
  and and_34 (and_34_out, not_203_out, not_204_out, not_205_out, not_206_out, not_207_out, not_208_out, not_209_out, not_210_out, not_211_out, F2, not_212_out, not_213_out);
  and and_35 (and_35_out, not_214_out, not_215_out, not_216_out, not_217_out, not_218_out, not_219_out, not_220_out, not_221_out, not_222_out, F2, F1, F0);
  and and_36 (and_36_out, OP5, not_223_out, not_224_out, OP2, not_225_out, not_226_out);
  and and_37 (SysCALL, not_227_out, not_228_out, not_229_out, not_230_out, not_231_out, not_232_out, not_233_out, not_234_out, F3, F2, not_235_out, not_236_out);
  and and_38 (and_38_out, not_237_out, not_238_out, not_239_out, OP2, not_240_out, not_241_out);
  and and_39 (and_39_out, not_242_out, not_243_out, not_244_out, OP2, not_245_out, OP0);
  and and_40 (and_40_out, not_246_out, not_247_out, OP3, not_248_out, not_249_out, not_250_out);
  and and_41 (and_41_out, not_251_out, not_252_out, OP3, not_253_out, not_254_out, OP0);
  and and_42 (and_42_out, not_255_out, not_256_out, OP3, not_257_out, OP1, not_258_out);
  and and_43 (and_43_out, OP5, not_259_out, not_260_out, not_261_out, OP1, OP0);
  and and_44 (and_44_out, OP5, not_262_out, OP3, not_263_out, OP1, OP0);
  and and_45 (and_45_out, OP5, not_264_out, not_265_out, OP2, not_266_out, not_267_out);
  and and_46 (and_46_out, not_268_out, not_269_out, not_270_out, not_271_out, not_272_out, OP0);
  and and_47 (and_47_out, not_273_out, not_274_out, not_275_out, not_276_out, not_277_out, not_278_out, not_279_out, not_280_out, not_281_out, not_282_out, not_283_out, not_284_out);
  and and_48 (and_48_out, not_285_out, not_286_out, not_287_out, not_288_out, not_289_out, not_290_out, not_291_out, not_292_out, not_293_out, not_294_out, F1, F0);
  and and_49 (and_49_out, not_295_out, not_296_out, not_297_out, not_298_out, not_299_out, not_300_out, not_301_out, not_302_out, not_303_out, not_304_out, F1, not_305_out);
  and and_50 (and_50_out, not_306_out, not_307_out, not_308_out, not_309_out, not_310_out, not_311_out, F5, not_312_out, not_313_out, not_314_out, not_315_out, not_316_out);
  and and_51 (and_51_out, not_317_out, not_318_out, not_319_out, not_320_out, not_321_out, not_322_out, F5, not_323_out, not_324_out, not_325_out, not_326_out, F0);
  and and_52 (and_52_out, not_327_out, not_328_out, not_329_out, not_330_out, not_331_out, not_332_out, F5, not_333_out, not_334_out, not_335_out, F1, not_336_out);
  and and_53 (and_53_out, not_337_out, not_338_out, not_339_out, not_340_out, not_341_out, not_342_out, F5, not_343_out, not_344_out, F2, not_345_out, not_346_out);
  and and_54 (and_54_out, not_347_out, not_348_out, not_349_out, not_350_out, not_351_out, not_352_out, F5, not_353_out, not_354_out, F2, not_355_out, F0);
  and and_55 (and_55_out, not_356_out, not_357_out, not_358_out, not_359_out, not_360_out, not_361_out, F5, not_362_out, not_363_out, F2, F1, F0);
  and and_56 (and_56_out, not_364_out, not_365_out, not_366_out, not_367_out, not_368_out, not_369_out, F5, not_370_out, F3, not_371_out, F1, not_372_out);
  and and_57 (and_57_out, not_373_out, not_374_out, not_375_out, not_376_out, not_377_out, not_378_out, F5, not_379_out, F3, not_380_out, F1, F0);
  and and_58 (and_58_out, not_381_out, not_382_out, not_383_out, not_384_out, not_385_out, not_386_out, not_387_out, not_388_out, not_389_out, F2, not_390_out, not_391_out);
  and and_59 (and_59_out, not_392_out, not_393_out, not_394_out, not_395_out, not_396_out, not_397_out, not_398_out, not_399_out, not_400_out, F2, F1, F0);
  and and_60 (BEQ, not_401_out, not_402_out, not_403_out, OP2, not_404_out, not_405_out);
  and and_61 (BNE, not_406_out, not_407_out, not_408_out, OP2, not_409_out, OP0);
  and and_62 (JR, not_410_out, not_411_out, not_412_out, not_413_out, not_414_out, not_415_out, not_416_out, not_417_out, F3, not_418_out, not_419_out, not_420_out);
  and and_63 (and_63_out, not_421_out, not_422_out, not_423_out, not_424_out, not_425_out, not_426_out, not_427_out, not_428_out, F3, not_429_out, not_430_out, not_431_out);
  and and_64 (and_64_out, not_432_out, not_433_out, not_434_out, not_435_out, OP1, not_436_out);
  and and_65 (and_65_out, not_437_out, not_438_out, not_439_out, not_440_out, OP1, OP0);
  and and_66 (JAL, not_441_out, not_442_out, not_443_out, not_444_out, OP1, OP0);
  or or_1 (MemToReg, and_1_out, and_2_out);
  or or_2 (ALU_SRC, and_8_out, and_9_out, and_10_out, and_11_out, and_12_out, and_13_out, and_14_out, and_15_out);
  or or_3 (SignedExt, and_38_out, and_39_out, and_40_out, and_41_out, and_42_out, and_43_out, and_44_out, and_45_out, and_46_out);
  or or_4 (JUMP, and_63_out, and_64_out, and_65_out);
  or or_5 (RegWrite, and_16_out, and_17_out, and_18_out, and_19_out, and_20_out, and_21_out, and_22_out, and_23_out, and_24_out, and_25_out, and_26_out, and_27_out, and_28_out, and_29_out, and_30_out, and_31_out, and_32_out, and_33_out, and_34_out, and_35_out, and_36_out);
  or or_6 (RegDst, and_47_out, and_48_out, and_49_out, and_50_out, and_51_out, and_52_out, and_53_out, and_54_out, and_55_out, and_56_out, and_57_out, and_58_out, and_59_out);
endmodule

// ALU
module MIPS_ALU (
  input  [4:0] shamt,
  input  [31:0] X,
  input  [31:0] Y,
  input  [3:0] AluOP,
  output Equal,
  output [31:0] Result,
  output [31:0] Result_2
);

  wire [0:0] comparator_1_lt, comparator_2_lt;
  wire [31:0] adder_1_out, AND_out, divider_1_out, divider_1_rem, multiplier_1_cout, multiplier_1_out,
       NOR_out, OR_out, shifter_1_out, shifter_2_out, shifter_3_out, subtractor_1_out, XOR_out;

  assign AND_out = X & Y;  // AND_Gate AND, 32 bits wide
  assign OR_out = X | Y;  // OR_Gate OR, 32 bits wide
  Shifter #(.width(32), .shift("ll")) shifter_1 (.in(Y), .\dist (shamt), .out(shifter_1_out));
  Shifter #(.width(32), .shift("ar")) shifter_2 (.in(Y), .\dist (shamt), .out(shifter_2_out));
  Shifter #(.width(32), .shift("lr")) shifter_3 (.in(Y), .\dist (shamt), .out(shifter_3_out));
  Multiplier #(.width(32)) multiplier_1 (.a(X), .b(Y), .out(multiplier_1_out), .cout(multiplier_1_cout));  // open: cin
  Divider #(.width(32)) divider_1 (.a(X), .b(Y), .out(divider_1_out), .rem(divider_1_rem));  // open: upper
  Adder #(.width(32)) adder_1 (.a(X), .b(Y), .out(adder_1_out));  // open: cin, cout
  Subtractor #(.width(32)) subtractor_1 (.a(X), .b(Y), .out(subtractor_1_out));  // open: bin, bout
  assign XOR_out = X ^ Y;  // XOR_Gate XOR, 32 bits wide
  assign NOR_out = ~(X | Y);  // NOR_Gate NOR, 32 bits wide
  Comparator #(.width(32), .mode("twosComplement")) comparator_1 (
    .a(X), .b(Y), .eq(Equal), .lt(comparator_1_lt[0]));  // open: gt
  Comparator #(.width(32), .mode("unsigned")) comparator_2 (.a(X), .b(Y), .lt(comparator_2_lt[0]));  // open: gt, eq
  Multiplexer #(.select(4), .width(32), .disabled("Z"), .enable("false")) multiplexer_1 (
    .in0(shifter_1_out), .in1(shifter_2_out), .in2(shifter_3_out), .in3(multiplier_1_out),
    .in4(divider_1_out), .in5(adder_1_out), .in6(subtractor_1_out), .in7(AND_out), .in8(OR_out),
    .in9(XOR_out), .in10(NOR_out), .in11({{31{1'b0}}, comparator_1_lt[0]}),
    .in12({{31{1'b0}}, comparator_2_lt[0]}), .in13({32{1'b0}}), .in14({32{1'b0}}), .in15({32{1'b0}}),
    .out(Result), .sel(AluOP));
  Multiplexer #(.select(4), .width(32), .disabled("Z"), .enable("false")) multiplexer_2 (
    .in0({32{1'b0}}), .in1({32{1'b0}}), .in2({32{1'b0}}), .in3(multiplier_1_cout), .in4(divider_1_rem),
    .in5({32{1'b0}}), .in6({32{1'b0}}), .in7({32{1'b0}}), .in8({32{1'b0}}), .in9({32{1'b0}}),
    .in10({32{1'b0}}), .in11({32{1'b0}}), .in12({32{1'b0}}), .in13({32{1'b0}}), .in14({32{1'b0}}),
    .in15({32{1'b0}}), .out(Result_2), .sel(AluOP));

  // Other names for the same wires on the sheet: Result2[31:0] = Result_2; S[3:0] = AluOP

  // Notes on the sheet:
  //   不要改变此引脚区域内容，也不要改变ALU封装形式
  //   输入引脚
  //   输出引脚
endmodule

module MIPS_Regifile (
  input  [31:0] Din,
  input  Clk,
  input  WE,
  input  [4:0] R1_num,
  input  [4:0] W_num,
  input  [4:0] R2_num,
  output [31:0] R1,
  output [31:0] R2
);

  // RegisterFile registerfile_1: pin names not known; wires that end beside it: Din, Clk, WE, W_num, R1_num, R2_num, R1, R2
endmodule
module \理想流水线  (
  output RegWrite,
  output MemWrite,
  output [31:0] IF_PC,
  output [31:0] ID_PC,
  output [31:0] EX_PC,
  output [31:0] M_PC,
  output [31:0] WB_PC,
  output [31:0] RDin,
  output [31:0] MDin,
  output [31:0] LedData
);

  wire and_1_out, and_2_out, and_3_out, CLK, clock_1_out, clock_2_out, comparator_1_eq, comparator_1_lt,
       comparator_2_eq, d_ff_1_q, Go, Halt, IR1, IR2, IR3, nand_1_out, not_1_out, not_2_out, not_3_out, RST,
       SignedExt, W1, W2, W3, \单周期硬布线控制器_1_alu_src , \单周期硬布线控制器_1_memtoreg , \单周期硬布线控制器_1_memwrite ,
       \单周期硬布线控制器_1_regdst , \单周期硬布线控制器_1_regwrite , \单周期硬布线控制器_1_syscall , \理想ex_mem_1_memtoreg_out ,
       \理想ex_mem_1_regdst_out , \理想ex_mem_1_regwrite_out , \理想ex_mem_1_syscall_out , \理想id_ex_1_alusrcb_out ,
       \理想id_ex_1_memtoreg_out , \理想id_ex_1_memwrite_2 , \理想id_ex_1_regdst_out , \理想id_ex_1_regwrite_out ,
       \理想id_ex_1_syscall_out , \理想mem_wb_1_memtoreg_out , \理想mem_wb_1_regdst_out , \理想mem_wb_1_syscall_out ;
  wire [3:0] \单周期硬布线控制器_1_alu_op , \理想id_ex_1_aluop_out ;
  wire [4:0] multiplexer_1_out, multiplexer_2_out, multiplexer_6_out, \理想id_ex_1_shamt_2 ;
  wire [12:0] CNT_num;
  wire [15:0] \LoadUse次数 , \总周期数 , \插入气泡数 , \无条件分支数 , \条件分支成功数 ;
  wire [31:0] adder_1_out, bit_extender_1_out, bit_extender_2_out, EX_IR, ID_IR, IF_IR, MEM_IR,
       mips_alu_1_result, mips_regifile_1_r1, mips_regifile_1_r2, multiplexer_3_out, multiplexer_4_out,
       ram_1_data, WB_IR, \理想ex_mem_1_a_in_2 , \理想ex_mem_1_alu_2 , \理想id_ex_1_a_out , \理想id_ex_1_b_out ,
       \理想id_ex_1_imm_out , \理想mem_wb_1_a_out , \理想mem_wb_1_alu_2 , \理想mem_wb_1_b_out , \理想mem_wb_1_md_2 ;

  Button \u_总复位  (.out(RST));
  Button _1 (.out(IR1));
  Button _2 (.out(IR2));
  Button _3 (.out(IR3));
  // Probe on \总周期数 
  // Probe on \总周期数 
  and and_1 (and_1_out, ~Halt, CLK);  // AND_Gate
  Button \u_继续运行  (.out(Go));
  LED #(.active("true")) led_1 (.in(W1));
  LED #(.active("true")) led_2 (.in(W2));
  LED #(.active("true")) led_3 (.in(W3));
  Counter #(.width(16), .max('hffff), .ongoal("wrap"), .trigger("rising"), .behavior("new")) counter_1 (
    .Q(\总周期数 ), .clk(and_1_out));  // open: load, D, count, carry, clr, preset, down
  Hex_Digit_Display hex_digit_display_1 (.value(LedData[31:28]));  // open: dp
  // Probe on IF_PC[19:0]
  // Mips_Probe mips_probe_1: pin names not known; wires that end beside it: IF_IR
  Register #(.width(32), .trigger("rising"), .Select("low")) PC (
    .D(adder_1_out), .en(not_1_out), .Q(IF_PC), .clk(CLK));  // open: clr
  not not_1 (not_1_out, Halt);
  Hex_Digit_Display hex_digit_display_2 (.value(LedData[27:24]));  // open: dp
  Hex_Digit_Display hex_digit_display_3 (.value(LedData[23:20]));  // open: dp
  // Probe on ID_PC[19:0]
  // Mips_Probe mips_probe_2: pin names not known; wires that end beside it: ID_IR
  Hex_Digit_Display hex_digit_display_4 (.value(LedData[19:16]));  // open: dp
  Hex_Digit_Display hex_digit_display_5 (.value(LedData[15:12]));  // open: dp
  Adder #(.width(32)) adder_1 (.a(IF_PC), .b(32'h4), .out(adder_1_out));  // open: cin, cout
  Hex_Digit_Display hex_digit_display_6 (.value(LedData[11:8]));  // open: dp
  Hex_Digit_Display hex_digit_display_7 (.value(LedData[7:4]));  // open: dp
  Clock #(.highDuration(1), .lowDuration(1)) clock_1 (.out(clock_1_out));
  // Probe on EX_PC[19:0]
  // Mips_Probe mips_probe_3: pin names not known; wires that end beside it: clock_1_out, EX_IR, CLK
  Hex_Digit_Display hex_digit_display_8 (.value(LedData[3:0]));  // open: dp
  ROM #(.addrWidth(10), .dataWidth(32), .Select("high")) rom_1 (.addr(IF_PC[11:2]), .data(IF_IR));
  // Probe on \总周期数 
  // Probe on M_PC[19:0]
  // Mips_Probe mips_probe_4: pin names not known; wires that end beside it: MEM_IR
  \理想IF_ID  \u_理想if_id_1  (
    .IR_in(IF_IR), .PC_in(IF_PC), .CLK(CLK), .IR_out(ID_IR), .PC_out(ID_PC), .CLR(RST));  // open: RegDst_in, Beq_in, Syscall_in, Bne_in, JMP_in, MemToReg_in, A_in, JR_in, AluOP_in, SignedExt_in, AluSrcB_in, B_in, SLLV_in, RegWrite_in, Imm_in, SRAV_in, JAL_in, LBU_in, Shamt, MemWrite, BGEZ_in, RegDst_out, Beq_out, Syscall_out, Bne_out, JMP_out, MemToReg_out, A_out, JR_out, AluOP_out, SignedExt_out, AluSrcB_out, B_out, SLLV_out, RegWrite_out, Imm_out, SRAV_out, JAL_out, LBU_out, Shamt_2, MemWrite_2, BGEZ_out, Stall
  // Probe on \总周期数 
  // Probe on \无条件分支数 
  // Probe on \条件分支成功数 
  // Probe on \插入气泡数 
  // Probe on \LoadUse次数 
  // Probe on IF_PC[11:0]
  // Probe on WB_PC[19:0]
  // Mips_Probe mips_probe_5: pin names not known; wires that end beside it: WB_IR
  // Probe on ID_PC[11:0]
  // Probe on EX_PC[11:0]
  \单周期硬布线控制器  \u_单周期硬布线控制器_1  (
    .Func(ID_IR[5:0]), .OP(ID_IR[31:26]), .ALU_OP(\单周期硬布线控制器_1_alu_op ), .MemToReg(\单周期硬布线控制器_1_memtoreg ),
    .MemWrite(\单周期硬布线控制器_1_memwrite ), .ALU_SRC(\单周期硬布线控制器_1_alu_src ), .RegWrite(\单周期硬布线控制器_1_regwrite ),
    .SysCALL(\单周期硬布线控制器_1_syscall ), .SignedExt(SignedExt), .RegDst(\单周期硬布线控制器_1_regdst ));  // open: JR, JMP, Beq, JAL, Bne, SLLV, SRAV, BGEZ, LBU
  assign bit_extender_1_out = {{16{1'b0}}, ID_IR[15:0]};  // Bit_Extender bit_extender_1
  assign bit_extender_2_out = {{16{ID_IR[15]}}, ID_IR[15:0]};  // Bit_Extender bit_extender_2
  // Probe on M_PC[11:0]
  D_Flip_Flop #(.trigger("high"), .Pre_Clr_Positions("LEGACY"), .NegatePresetClear("false"), .enable("true"), .NewFFLayout("false")) d_ff_1 (.Q(d_ff_1_q));  // open: clk, D, Qn, preset, en, reset
  // Probe on 13'hc
  // Probe on WB_PC[11:0]
  Comparator #(.width(13), .mode("twosComplement")) comparator_1 (
    .a(CNT_num), .b(13'hc), .eq(comparator_1_eq), .lt(comparator_1_lt));  // open: gt
  Clock #(.highDuration(1), .lowDuration(1)) clock_2 (.out(clock_2_out));
  Multiplexer #(.select(1), .width(5), .disabled("Z"), .enable("false")) multiplexer_1 (
    .in0(ID_IR[25:21]), .in1(5'b00010), .out(multiplexer_1_out), .sel(\单周期硬布线控制器_1_syscall ));
  Multiplexer #(.select(1), .width(5), .disabled("Z"), .enable("false")) multiplexer_2 (
    .in0(ID_IR[20:16]), .in1(5'b00100), .out(multiplexer_2_out), .sel(\单周期硬布线控制器_1_syscall ));
  nand nand_1 (nand_1_out, d_ff_1_q, comparator_1_eq);
  Counter #(.width(13), .max('h1fff), .ongoal("stay"), .trigger("rising"), .behavior("old")) counter_2 (
    .count(comparator_1_lt), .Q(CNT_num), .clk(clock_2_out));  // open: load, D, carry, clr, preset
  Multiplexer #(.select(1), .width(32), .disabled("Z"), .enable("false")) multiplexer_3 (
    .in0(bit_extender_1_out), .in1(bit_extender_2_out), .out(multiplexer_3_out), .sel(SignedExt));
  assign CLK = nand_1_out ? clock_2_out : 1'bz;  // Controlled_Buffer controlled_buffer_1
  MIPS_Regifile mips_regifile_1 (
    .Din(RDin), .Clk(CLK), .R1(mips_regifile_1_r1), .R2(mips_regifile_1_r2), .WE(RegWrite),
    .W_num(multiplexer_6_out), .R1_num(multiplexer_1_out), .R2_num(multiplexer_2_out));
  Pull_Resistor #(.pull(1)) pull_resistor_1 (.node(CLK));
  \理想ID_EX  \u_理想id_ex_1  (
    .RegDst_in(\单周期硬布线控制器_1_regdst ), .IR_in(ID_IR), .Syscall_in(\单周期硬布线控制器_1_syscall ), .PC_in(ID_PC),
    .MemToReg_in(\单周期硬布线控制器_1_memtoreg ), .A_in(mips_regifile_1_r1), .AluOP_in(\单周期硬布线控制器_1_alu_op ),
    .SignedExt_in(SignedExt), .AluSrcB_in(\单周期硬布线控制器_1_alu_src ), .B_in(mips_regifile_1_r2),
    .RegWrite_in(\单周期硬布线控制器_1_regwrite ), .Imm_in(multiplexer_3_out), .CLK(CLK),
    .RegDst_out(\理想id_ex_1_regdst_out ), .IR_out(EX_IR), .Syscall_out(\理想id_ex_1_syscall_out ),
    .PC_out(EX_PC), .MemToReg_out(\理想id_ex_1_memtoreg_out ), .A_out(\理想id_ex_1_a_out ),
    .AluOP_out(\理想id_ex_1_aluop_out ), .AluSrcB_out(\理想id_ex_1_alusrcb_out ), .B_out(\理想id_ex_1_b_out ),
    .RegWrite_out(\理想id_ex_1_regwrite_out ), .Imm_out(\理想id_ex_1_imm_out ), .CLR(RST), .Shamt(ID_IR[10:6]),
    .Shamt_2(\理想id_ex_1_shamt_2 ), .MemWrite(\单周期硬布线控制器_1_memwrite ), .MemWrite_2(\理想id_ex_1_memwrite_2 ));  // open: Beq_in, Bne_in, JMP_in, JR_in, SLLV_in, SRAV_in, JAL_in, LBU_in, BGEZ_in, Beq_out, Bne_out, JMP_out, JR_out, SignedExt_out, SLLV_out, SRAV_out, JAL_out, LBU_out, BGEZ_out, Stall
  Multiplexer #(.select(1), .width(32), .disabled("Z"), .enable("false")) multiplexer_4 (
    .in0(\理想id_ex_1_b_out ), .in1(\理想id_ex_1_imm_out ), .out(multiplexer_4_out), .sel(\理想id_ex_1_alusrcb_out ));
  MIPS_ALU mips_alu_1 (
    .X(\理想id_ex_1_a_out ), .Y(multiplexer_4_out), .AluOP(\理想id_ex_1_aluop_out ), .Result(mips_alu_1_result),
    .shamt(\理想id_ex_1_shamt_2 ));  // open: Equal, Result_2
  \理想EX_MEM  \u_理想ex_mem_1  (
    .RegDst_in(\理想id_ex_1_regdst_out ), .IR_in(EX_IR), .Syscall_in(\理想id_ex_1_syscall_out ), .PC_in(EX_PC),
    .MemToReg_in(\理想id_ex_1_memtoreg_out ), .A_in(\理想id_ex_1_a_out ), .B_in(\理想id_ex_1_b_out ),
    .RegWrite_in(\理想id_ex_1_regwrite_out ), .CLK(CLK), .RegDst_out(\理想ex_mem_1_regdst_out ), .IR_out(MEM_IR),
    .Syscall_out(\理想ex_mem_1_syscall_out ), .PC_out(M_PC), .MemToReg_out(\理想ex_mem_1_memtoreg_out ),
    .A_in_2(\理想ex_mem_1_a_in_2 ), .B_out(MDin), .RegWrite_out(\理想ex_mem_1_regwrite_out ), .CLR(RST),
    .MemWrite(\理想id_ex_1_memwrite_2 ), .MemWrite_2(MemWrite), .ALU(mips_alu_1_result),
    .ALU_2(\理想ex_mem_1_alu_2 ));  // open: Beq_in, Bne_in, JMP_in, JR_in, SignedExt_in, AluSrcB_in, SLLV_in, Imm_in, SRAV_in, JAL_in, LBU_in, Shamt, BGEZ_in, Beq_out, Bne_out, JMP_out, JR_out, SignedExt_out, AluSrcB_out, SLLV_out, Imm_out, SRAV_out, JAL_out, LBU_out, Shamt_2, BGEZ_out, Stall
  not not_2 (not_2_out, Halt);
  RAM #(.addrWidth(10), .dataWidth(32), .bus("separate"), .Select("high")) ram_1 (
    .addr(\理想ex_mem_1_alu_2 [11:2]), .din(MDin), .data(ram_1_data), .str(MemWrite), .sel(not_2_out), .clk(CLK));  // open: ld, clr
  \理想MEM_WB  \u_理想mem_wb_1  (
    .RegDst_in(\理想ex_mem_1_regdst_out ), .RegDst_out(\理想mem_wb_1_regdst_out ), .IR_in(MEM_IR),
    .IR_out(WB_IR), .Syscall_in(\理想ex_mem_1_syscall_out ), .Syscall_out(\理想mem_wb_1_syscall_out ),
    .PC_in(M_PC), .PC_out(WB_PC), .MemToReg_in(\理想ex_mem_1_memtoreg_out ),
    .MemToReg_out(\理想mem_wb_1_memtoreg_out ), .A_in(\理想ex_mem_1_a_in_2 ), .A_out(\理想mem_wb_1_a_out ),
    .ALU(\理想ex_mem_1_alu_2 ), .ALU_2(\理想mem_wb_1_alu_2 ), .B_in(MDin), .B_out(\理想mem_wb_1_b_out ),
    .RegWrite_in(\理想ex_mem_1_regwrite_out ), .RegWrite_out(RegWrite), .MD(ram_1_data),
    .MD_2(\理想mem_wb_1_md_2 ), .CLK(CLK), .CLR(RST));  // open: Beq_in, Beq_out, Bne_in, Bne_out, JMP_in, JMP_out, JR_in, JR_out, SignedExt_in, SignedExt_out, AluSrcB_in, AluSrcB_out, SLLV_in, SLLV_out, Imm_in, Imm_out, SRAV_in, SRAV_out, JAL_in, JAL_out, LBU_in, LBU_out, BGEZ_in, BGEZ_out, Stall, MemWrite, MemWrite_2
  Multiplexer #(.select(1), .width(32), .disabled("Z"), .enable("false")) multiplexer_5 (
    .in0(\理想mem_wb_1_alu_2 ), .in1(\理想mem_wb_1_md_2 ), .out(RDin), .sel(\理想mem_wb_1_memtoreg_out ));
  Comparator #(.width(32), .mode("twosComplement")) comparator_2 (
    .a(\理想mem_wb_1_a_out ), .b(32'h22), .eq(comparator_2_eq));  // open: gt, lt
  not not_3 (not_3_out, comparator_2_eq);
  Register #(.width(32), .trigger("falling"), .Select("low")) register_1 (
    .D(\理想mem_wb_1_b_out ), .Q(LedData), .clk(and_2_out));  // open: en, clr
  and and_2 (and_2_out, comparator_2_eq, \理想mem_wb_1_syscall_out );
  and and_3 (and_3_out, \理想mem_wb_1_syscall_out , not_3_out);
  Register #(.width(1), .trigger("rising"), .Select("low")) register_2 (
    .D(and_3_out), .en(and_3_out), .Q(Halt), .clk(CLK), .clr(Go));
  Multiplexer #(.select(1), .width(5), .disabled("Z"), .enable("false")) multiplexer_6 (
    .in0(WB_IR[20:16]), .in1(WB_IR[15:11]), .out(multiplexer_6_out), .sel(\理想mem_wb_1_regdst_out ));

  // Other names for the same wires on the sheet: MEM_PC[31:0] = M_PC

  // Notes on the sheet:
  //   中断源
  //   时空图监测，可删除
  //   中断等待指示
  //   数码管输出
  //   contents of rom_1 (hex, n*v repeats v):
  //   20100000 20110000 20120000 20130000 36100000 36310001 36520002 36730003 ae100000 ae110004 ae120008
  //   ae13000c 2002000a 20110000 20120000 20130000 c
  //   指令字
  //   JMP
  //   JR
  //   OP
  //   OP
  //   Func
  //   rs
  //   rt
  //   rd
  //   控制位
  //   Beq
  //   Bne
  //   AluOP
  //   AluSrcB
  //   RegWrite
  //   JAL
  //   RegDst
  //   Syscall
  //   流水调试日志用
  //   暂停节拍，不能为0
  //   MemToReg
  //   MemWrite
  //   戳工具置1进入计数暂停模式，ctrl+k时钟自动运行到对应节拍暂停
  //   ctrl+k关闭时钟连续运行，将控制位置零，进入单步调试模式调试
  //   用这个时钟源需要去掉电路中的其他时钟源
  //   可计数暂停的时钟源
  //   Reg_dst
  //   beq
  //   IR
  //   Syscall
  //   Beq
  //   PC
  //   JMP
  //   MemToReg
  //   JR
  //   AluOP
  //   RegWrite
  //   为方便自动评测，需要输出流水线各段保存的PC值，注意是PC不是PC+4，另外ID段寄存器写入信息，Mem段内存写入信息也要输出
  //   rt
  //   rd
endmodule

module \气泡流水线  (
  output RegWrite,
  output MemWrite,
  output [31:0] IF_PC,
  output [31:0] ID_PC,
  output [31:0] EX_PC,
  output [31:0] M_PC,
  output [31:0] WB_PC,
  output [31:0] RDin,
  output [31:0] MDin,
  output [31:0] LedData
);

  wire and_1_out, and_2_out, and_3_out, and_4_out, and_5_out, and_6_out, and_7_out, B_CLR, Branch, CLK,
       clock_1_out, clock_2_out, comparator_1_eq, comparator_1_lt, comparator_2_eq, Correlated, d_ff_1_q,
       EX_JAL, EX_JMP, EX_JR, EX_RegDst, EX_RegWrite, Go, Halt, IR1, IR2, IR3, MEM_JAL, MEM_RegDst,
       MEM_RegWrite, mips_alu_1_equal, nand_1_out, nor_1_out, not_1_out, not_2_out, not_3_out, or_1_out,
       or_2_out, or_3_out, RST, SignedExt, W1, W2, W3, \单周期硬布线控制器_1_alu_src , \单周期硬布线控制器_1_beq ,
       \单周期硬布线控制器_1_bgez , \单周期硬布线控制器_1_bne , \单周期硬布线控制器_1_jal , \单周期硬布线控制器_1_jmp , \单周期硬布线控制器_1_jr ,
       \单周期硬布线控制器_1_lbu , \单周期硬布线控制器_1_memtoreg , \单周期硬布线控制器_1_memwrite , \单周期硬布线控制器_1_regdst ,
       \单周期硬布线控制器_1_regwrite , \单周期硬布线控制器_1_sllv , \单周期硬布线控制器_1_srav , \单周期硬布线控制器_1_syscall ,
       \源寄存器使用情况_1_r1_used , \源寄存器使用情况_1_r2_used , \理想ex_mem_1_lbu_out , \理想ex_mem_1_memtoreg_out ,
       \理想ex_mem_1_syscall_out , \理想id_ex_1_alusrcb_out , \理想id_ex_1_beq_out , \理想id_ex_1_bgez_out ,
       \理想id_ex_1_bne_out , \理想id_ex_1_lbu_out , \理想id_ex_1_memtoreg_out , \理想id_ex_1_memwrite_2 ,
       \理想id_ex_1_sllv_out , \理想id_ex_1_srav_out , \理想id_ex_1_syscall_out , \理想mem_wb_1_jal_out ,
       \理想mem_wb_1_lbu_out , \理想mem_wb_1_memtoreg_out , \理想mem_wb_1_regdst_out , \理想mem_wb_1_syscall_out ;
  wire [3:0] \单周期硬布线控制器_1_alu_op , \理想id_ex_1_aluop_out ;
  wire [4:0] multiplexer_1_out, multiplexer_2_out, multiplexer_3_out, multiplexer_4_out, multiplexer_10_out,
       multiplexer_13_out, multiplexer_15_out, R1_num, R2_num, \理想id_ex_1_a_out , \理想id_ex_1_shamt_2 ;
  wire [5:0] Func;
  wire [12:0] CNT_num;
  wire [15:0] \LoadUse次数 , \总周期数 , \插入气泡数 , \无条件分支数 , \条件分支成功数 ;
  wire [31:0] adder_2_out, adder_3_out, adder_4_out, bit_extender_1_out, bit_extender_2_out,
       bit_extender_3_out, controlled_buffer_2_out, EX_IR, IF_IR, MEM_IR, mips_alu_1_result,
       mips_regifile_1_r1, mips_regifile_1_r2, multiplexer_7_out, multiplexer_8_out, multiplexer_9_out,
       multiplexer_11_out, multiplexer_12_out, PC_4, ram_1_data, shifter_1_out, WB_IR, \理想ex_mem_1_a_in_2 ,
       \理想ex_mem_1_alu_2 , \理想id_ex_1_b_out , \理想id_ex_1_imm_out , \理想mem_wb_1_a_out , \理想mem_wb_1_alu_2 ,
       \理想mem_wb_1_b_out , \理想mem_wb_1_md_2 ;
  wire [31:5] \理想id_ex_1_a_out_2 ;
  wire [31:6] ID_IR;

  Button \u_总复位  (.out(RST));
  Button _1 (.out(IR1));
  Button _2 (.out(IR2));
  Button _3 (.out(IR3));
  // Probe on \总周期数 
  // Probe on \总周期数 
  and and_1 (and_1_out, ~Halt, CLK);  // AND_Gate
  Button \u_继续运行  (.out(Go));
  LED #(.active("true")) led_1 (.in(W1));
  LED #(.active("true")) led_2 (.in(W2));
  LED #(.active("true")) led_3 (.in(W3));
  Counter #(.width(16), .max('hffff), .ongoal("wrap"), .trigger("rising"), .behavior("new")) counter_1 (
    .Q(\总周期数 ), .clk(and_1_out));  // open: load, D, count, carry, clr, preset, down
  Hex_Digit_Display hex_digit_display_1 (.value(LedData[31:28]));  // open: dp
  // Probe on IF_PC[19:0]
  // Mips_Probe mips_probe_1: pin names not known; wires that end beside it: IF_IR
  nor nor_1 (nor_1_out, Correlated, Halt);
  Hex_Digit_Display hex_digit_display_2 (.value(LedData[23:20]));  // open: dp
  Hex_Digit_Display hex_digit_display_3 (.value(LedData[27:24]));  // open: dp
  // Probe on ID_PC[19:0]
  // Mips_Probe mips_probe_2: pin names not known; wires that end beside it: {ID_IR, Func}
  Register #(.width(32), .trigger("rising"), .Select("low")) PC (
    .D(controlled_buffer_2_out), .en(nor_1_out), .Q(IF_PC), .clk(CLK));  // open: clr
  Hex_Digit_Display hex_digit_display_4 (.value(LedData[15:12]));  // open: dp
  Hex_Digit_Display hex_digit_display_5 (.value(LedData[19:16]));  // open: dp
  Hex_Digit_Display hex_digit_display_6 (.value(LedData[11:8]));  // open: dp
  Hex_Digit_Display hex_digit_display_7 (.value(LedData[7:4]));  // open: dp
  Clock #(.highDuration(1), .lowDuration(1)) clock_1 (.out(clock_1_out));
  // Probe on EX_PC[19:0]
  // Mips_Probe mips_probe_3: pin names not known; wires that end beside it: clock_1_out, EX_IR, CLK
  Adder #(.width(32)) adder_1 (.a(IF_PC), .b(32'h4), .out(PC_4));  // open: cin, cout
  Hex_Digit_Display hex_digit_display_8 (.value(LedData[3:0]));  // open: dp
  ROM #(.addrWidth(10), .dataWidth(32), .Select("high")) rom_1 (.addr(IF_PC[11:2]), .data(IF_IR));
  // Probe on \总周期数 
  // Probe on M_PC[19:0]
  // Mips_Probe mips_probe_4: pin names not known; wires that end beside it: MEM_IR
  \理想IF_ID  \u_理想if_id_1  (
    .IR_in(IF_IR), .PC_in(IF_PC), .CLK(CLK), .IR_out({ID_IR, Func}), .PC_out(ID_PC), .CLR(or_1_out),
    .Stall(Correlated));  // open: RegDst_in, Beq_in, Syscall_in, Bne_in, JMP_in, MemToReg_in, A_in, JR_in, AluOP_in, SignedExt_in, AluSrcB_in, B_in, SLLV_in, RegWrite_in, Imm_in, SRAV_in, JAL_in, LBU_in, Shamt, MemWrite, BGEZ_in, RegDst_out, Beq_out, Syscall_out, Bne_out, JMP_out, MemToReg_out, A_out, JR_out, AluOP_out, SignedExt_out, AluSrcB_out, B_out, SLLV_out, RegWrite_out, Imm_out, SRAV_out, JAL_out, LBU_out, Shamt_2, MemWrite_2, BGEZ_out
  or or_1 (or_1_out, B_CLR, RST);
  // Probe on \总周期数 
  // Probe on \无条件分支数 
  // Probe on \条件分支成功数 
  // Probe on \插入气泡数 
  // Probe on \LoadUse次数 
  // Probe on IF_PC[11:0]
  // Probe on WB_PC[19:0]
  // Mips_Probe mips_probe_5: pin names not known; wires that end beside it: WB_IR
  // Probe on EX_PC[11:0]
  // Probe on ID_PC[11:0]
  Multiplexer #(.select(1), .width(5), .disabled("Z"), .enable("false")) multiplexer_1 (
    .in0(MEM_IR[20:16]), .in1(MEM_IR[15:11]), .out(multiplexer_1_out), .sel(MEM_RegDst));
  Multiplexer #(.select(1), .width(5), .disabled("Z"), .enable("false")) multiplexer_2 (
    .in0(EX_IR[20:16]), .in1(EX_IR[15:11]), .out(multiplexer_2_out), .sel(EX_RegDst));
  // Probe on M_PC[11:0]
  D_Flip_Flop #(.trigger("high"), .Pre_Clr_Positions("LEGACY"), .NegatePresetClear("false"), .enable("true"), .NewFFLayout("false")) d_ff_1 (.Q(d_ff_1_q));  // open: clk, D, Qn, preset, en, reset
  // Probe on 13'h12
  \单周期硬布线控制器  \u_单周期硬布线控制器_1  (
    .Func(Func), .OP(ID_IR[31:26]), .ALU_OP(\单周期硬布线控制器_1_alu_op ), .MemToReg(\单周期硬布线控制器_1_memtoreg ),
    .MemWrite(\单周期硬布线控制器_1_memwrite ), .ALU_SRC(\单周期硬布线控制器_1_alu_src ), .RegWrite(\单周期硬布线控制器_1_regwrite ),
    .SysCALL(\单周期硬布线控制器_1_syscall ), .SignedExt(SignedExt), .RegDst(\单周期硬布线控制器_1_regdst ),
    .JR(\单周期硬布线控制器_1_jr ), .JMP(\单周期硬布线控制器_1_jmp ), .Beq(\单周期硬布线控制器_1_beq ), .JAL(\单周期硬布线控制器_1_jal ),
    .Bne(\单周期硬布线控制器_1_bne ), .SLLV(\单周期硬布线控制器_1_sllv ), .SRAV(\单周期硬布线控制器_1_srav ), .BGEZ(\单周期硬布线控制器_1_bgez ),
    .LBU(\单周期硬布线控制器_1_lbu ));
  assign bit_extender_1_out = {{16{1'b0}}, {ID_IR[15:6], Func}};  // Bit_Extender bit_extender_1
  assign bit_extender_2_out = {{16{ID_IR[15]}}, {ID_IR[15:6], Func}};  // Bit_Extender bit_extender_2
  Multiplexer #(.select(1), .width(5), .disabled("Z"), .enable("false")) multiplexer_3 (
    .in0(multiplexer_1_out), .in1({5{1'b1}}), .out(multiplexer_3_out), .sel(MEM_JAL));
  Multiplexer #(.select(1), .width(5), .disabled("Z"), .enable("false")) multiplexer_4 (
    .in0(multiplexer_2_out), .in1({5{1'b1}}), .out(multiplexer_4_out), .sel(EX_JAL));
  // Probe on WB_PC[11:0]
  Comparator #(.width(13), .mode("twosComplement")) comparator_1 (
    .a(CNT_num), .b(13'h12), .eq(comparator_1_eq), .lt(comparator_1_lt));  // open: gt
  Clock #(.highDuration(1), .lowDuration(1)) clock_2 (.out(clock_2_out));
  Multiplexer #(.select(1), .width(5), .disabled("Z"), .enable("false")) multiplexer_5 (
    .in0(ID_IR[25:21]), .in1(5'b00010), .out(R1_num), .sel(\单周期硬布线控制器_1_syscall ));
  Multiplexer #(.select(1), .width(5), .disabled("Z"), .enable("false")) multiplexer_6 (
    .in0(ID_IR[20:16]), .in1(5'b00100), .out(R2_num), .sel(\单周期硬布线控制器_1_syscall ));
  nand nand_1 (nand_1_out, d_ff_1_q, comparator_1_eq);
  Counter #(.width(13), .max('h1fff), .ongoal("stay"), .trigger("rising"), .behavior("old")) counter_2 (
    .count(comparator_1_lt), .Q(CNT_num), .clk(clock_2_out));  // open: load, D, carry, clr, preset
  Multiplexer #(.select(1), .width(32), .disabled("Z"), .enable("false")) multiplexer_7 (
    .in0(bit_extender_1_out), .in1(bit_extender_2_out), .out(multiplexer_7_out), .sel(SignedExt));
  \源寄存器使用情况  \u_源寄存器使用情况_1  (
    .OP(ID_IR[31:26]), .Funct(Func), .R1_Used(\源寄存器使用情况_1_r1_used ), .R2_Used(\源寄存器使用情况_1_r2_used ));
  assign CLK = nand_1_out ? clock_2_out : 1'bz;  // Controlled_Buffer controlled_buffer_1
  MIPS_Regifile mips_regifile_1 (
    .Din(RDin), .Clk(CLK), .R1(mips_regifile_1_r1), .R2(mips_regifile_1_r2), .WE(RegWrite),
    .W_num(multiplexer_15_out), .R1_num(R1_num), .R2_num(R2_num));
  \数据相关检测  \u_数据相关检测_1  (
    .R1_num(R1_num), .MEM_WriteReg_num(multiplexer_3_out), .MEM_RegWrite(MEM_RegWrite),
    .EX_WriteReg_num(multiplexer_4_out), .EX_RegWrite(EX_RegWrite), .R1_Used(\源寄存器使用情况_1_r1_used ),
    .R2_num(R2_num), .R2_Used(\源寄存器使用情况_1_r2_used ), .Correlated(Correlated));
  Pull_Resistor #(.pull(1)) pull_resistor_1 (.node(CLK));
  \理想ID_EX  \u_理想id_ex_1  (
    .RegDst_in(\单周期硬布线控制器_1_regdst ), .Beq_in(\单周期硬布线控制器_1_beq ), .IR_in({ID_IR, Func}),
    .Syscall_in(\单周期硬布线控制器_1_syscall ), .Bne_in(\单周期硬布线控制器_1_bne ), .PC_in(ID_PC),
    .JMP_in(\单周期硬布线控制器_1_jmp ), .MemToReg_in(\单周期硬布线控制器_1_memtoreg ), .A_in(mips_regifile_1_r1),
    .JR_in(\单周期硬布线控制器_1_jr ), .AluOP_in(\单周期硬布线控制器_1_alu_op ), .SignedExt_in(SignedExt),
    .AluSrcB_in(\单周期硬布线控制器_1_alu_src ), .B_in(mips_regifile_1_r2), .SLLV_in(\单周期硬布线控制器_1_sllv ),
    .RegWrite_in(\单周期硬布线控制器_1_regwrite ), .Imm_in(multiplexer_7_out), .SRAV_in(\单周期硬布线控制器_1_srav ),
    .JAL_in(\单周期硬布线控制器_1_jal ), .LBU_in(\单周期硬布线控制器_1_lbu ), .BGEZ_in(\单周期硬布线控制器_1_bgez ), .CLK(CLK),
    .RegDst_out(EX_RegDst), .Beq_out(\理想id_ex_1_beq_out ), .IR_out(EX_IR),
    .Syscall_out(\理想id_ex_1_syscall_out ), .Bne_out(\理想id_ex_1_bne_out ), .PC_out(EX_PC), .JMP_out(EX_JMP),
    .MemToReg_out(\理想id_ex_1_memtoreg_out ), .A_out({\理想id_ex_1_a_out_2 , \理想id_ex_1_a_out }),
    .JR_out(EX_JR), .AluOP_out(\理想id_ex_1_aluop_out ), .AluSrcB_out(\理想id_ex_1_alusrcb_out ),
    .B_out(\理想id_ex_1_b_out ), .SLLV_out(\理想id_ex_1_sllv_out ), .RegWrite_out(EX_RegWrite),
    .Imm_out(\理想id_ex_1_imm_out ), .SRAV_out(\理想id_ex_1_srav_out ), .JAL_out(EX_JAL),
    .LBU_out(\理想id_ex_1_lbu_out ), .BGEZ_out(\理想id_ex_1_bgez_out ), .CLR(or_2_out), .Shamt(ID_IR[10:6]),
    .Shamt_2(\理想id_ex_1_shamt_2 ), .MemWrite(\单周期硬布线控制器_1_memwrite ), .MemWrite_2(\理想id_ex_1_memwrite_2 ));  // open: SignedExt_out, Stall
  or or_2 (or_2_out, B_CLR, Correlated, RST);
  Multiplexer #(.select(1), .width(32), .disabled("Z"), .enable("false")) multiplexer_8 (
    .in0(\理想id_ex_1_b_out ), .in1(\理想id_ex_1_imm_out ), .out(multiplexer_8_out), .sel(\理想id_ex_1_alusrcb_out ));
  Multiplexer #(.select(1), .width(32), .disabled("Z"), .enable("false")) multiplexer_9 (
    .in0(multiplexer_8_out), .in1({32{1'b0}}), .out(multiplexer_9_out), .sel(\理想id_ex_1_bgez_out ));
  or or_3 (or_3_out, \理想id_ex_1_sllv_out , \理想id_ex_1_srav_out );
  Shifter #(.width(32), .shift("ll")) shifter_1 (.in(\理想id_ex_1_imm_out ), .\dist (5'b00010), .out(shifter_1_out));
  Adder #(.width(32)) adder_2 (.a(EX_PC), .b(32'h4), .out(adder_2_out));  // open: cin, cout
  or or_4 (B_CLR, Branch, EX_JMP);
  Multiplexer #(.select(1), .width(5), .disabled("Z"), .enable("false")) multiplexer_10 (
    .in0(\理想id_ex_1_shamt_2 ), .in1(\理想id_ex_1_a_out ), .out(multiplexer_10_out), .sel(or_3_out));
  Adder #(.width(32)) adder_3 (.a(shifter_1_out), .b(adder_2_out), .out(adder_3_out));  // open: cin, cout
  and and_2 (and_2_out, EX_JMP, ~EX_JR);  // AND_Gate
  not not_1 (not_1_out, B_CLR);
  MIPS_ALU mips_alu_1 (
    .X({\理想id_ex_1_a_out_2 , \理想id_ex_1_a_out }), .Y(multiplexer_9_out), .AluOP(\理想id_ex_1_aluop_out ),
    .Equal(mips_alu_1_equal), .Result(mips_alu_1_result), .shamt(multiplexer_10_out));  // open: Result_2
  assign controlled_buffer_2_out = EX_JR ? {\理想id_ex_1_a_out_2 , \理想id_ex_1_a_out } : 32'bz;  // Controlled_Buffer controlled_buffer_2
  assign controlled_buffer_2_out = Branch ? adder_3_out : 32'bz;  // Controlled_Buffer controlled_buffer_3
  assign controlled_buffer_2_out = and_2_out ? {EX_PC[31:28], EX_IR[25:0], 2'b00} : 32'bz;  // Controlled_Buffer controlled_buffer_4
  assign controlled_buffer_2_out = not_1_out ? PC_4 : 32'bz;  // Controlled_Buffer controlled_buffer_5
  and and_3 (and_3_out, \理想id_ex_1_bgez_out , ~mips_alu_1_result[0]);  // AND_Gate
  and and_4 (and_4_out, mips_alu_1_equal, \理想id_ex_1_beq_out );
  and and_5 (and_5_out, ~mips_alu_1_equal, \理想id_ex_1_bne_out );  // AND_Gate
  or or_5 (Branch, and_3_out, and_4_out, and_5_out);
  \理想EX_MEM  \u_理想ex_mem_1  (
    .RegDst_in(EX_RegDst), .IR_in(EX_IR), .Syscall_in(\理想id_ex_1_syscall_out ), .PC_in(EX_PC),
    .MemToReg_in(\理想id_ex_1_memtoreg_out ), .A_in({\理想id_ex_1_a_out_2 , \理想id_ex_1_a_out }),
    .B_in(\理想id_ex_1_b_out ), .RegWrite_in(EX_RegWrite), .JAL_in(EX_JAL), .LBU_in(\理想id_ex_1_lbu_out ),
    .CLK(CLK), .RegDst_out(MEM_RegDst), .IR_out(MEM_IR), .Syscall_out(\理想ex_mem_1_syscall_out ),
    .PC_out(M_PC), .MemToReg_out(\理想ex_mem_1_memtoreg_out ), .A_in_2(\理想ex_mem_1_a_in_2 ), .B_out(MDin),
    .RegWrite_out(MEM_RegWrite), .JAL_out(MEM_JAL), .LBU_out(\理想ex_mem_1_lbu_out ), .CLR(RST),
    .MemWrite(\理想id_ex_1_memwrite_2 ), .MemWrite_2(MemWrite), .ALU(mips_alu_1_result),
    .ALU_2(\理想ex_mem_1_alu_2 ));  // open: Beq_in, Bne_in, JMP_in, JR_in, SignedExt_in, AluSrcB_in, SLLV_in, Imm_in, SRAV_in, Shamt, BGEZ_in, Beq_out, Bne_out, JMP_out, JR_out, SignedExt_out, AluSrcB_out, SLLV_out, Imm_out, SRAV_out, Shamt_2, BGEZ_out, Stall
  not not_2 (not_2_out, Halt);
  RAM #(.addrWidth(10), .dataWidth(32), .bus("separate"), .Select("high")) ram_1 (
    .addr(\理想ex_mem_1_alu_2 [11:2]), .din(MDin), .data(ram_1_data), .str(MemWrite), .sel(not_2_out), .clk(CLK));  // open: ld, clr
  \理想MEM_WB  \u_理想mem_wb_1  (
    .RegDst_in(MEM_RegDst), .RegDst_out(\理想mem_wb_1_regdst_out ), .IR_in(MEM_IR), .IR_out(WB_IR),
    .Syscall_in(\理想ex_mem_1_syscall_out ), .Syscall_out(\理想mem_wb_1_syscall_out ), .PC_in(M_PC),
    .PC_out(WB_PC), .MemToReg_in(\理想ex_mem_1_memtoreg_out ), .MemToReg_out(\理想mem_wb_1_memtoreg_out ),
    .A_in(\理想ex_mem_1_a_in_2 ), .A_out(\理想mem_wb_1_a_out ), .ALU(\理想ex_mem_1_alu_2 ),
    .ALU_2(\理想mem_wb_1_alu_2 ), .B_in(MDin), .B_out(\理想mem_wb_1_b_out ), .RegWrite_in(MEM_RegWrite),
    .RegWrite_out(RegWrite), .JAL_in(MEM_JAL), .JAL_out(\理想mem_wb_1_jal_out ), .LBU_in(\理想ex_mem_1_lbu_out ),
    .MD(ram_1_data), .LBU_out(\理想mem_wb_1_lbu_out ), .MD_2(\理想mem_wb_1_md_2 ), .CLK(CLK), .CLR(RST));  // open: Beq_in, Beq_out, Bne_in, Bne_out, JMP_in, JMP_out, JR_in, JR_out, SignedExt_in, SignedExt_out, AluSrcB_in, AluSrcB_out, SLLV_in, SLLV_out, Imm_in, Imm_out, SRAV_in, SRAV_out, BGEZ_in, BGEZ_out, Stall, MemWrite, MemWrite_2
  Multiplexer #(.select(1), .width(32), .disabled("Z"), .enable("false")) multiplexer_11 (
    .in0(\理想mem_wb_1_alu_2 ), .in1(\理想mem_wb_1_md_2 ), .out(multiplexer_11_out),
    .sel(\理想mem_wb_1_memtoreg_out ));
  Comparator #(.width(32), .mode("twosComplement")) comparator_2 (
    .a(\理想mem_wb_1_a_out ), .b(32'h22), .eq(comparator_2_eq));  // open: gt, lt
  not not_3 (not_3_out, comparator_2_eq);
  assign bit_extender_3_out = {{24{1'b0}}, multiplexer_11_out[7:0]};  // Bit_Extender bit_extender_3
  Adder #(.width(32)) adder_4 (.a(WB_PC), .b(32'h4), .out(adder_4_out));  // open: cin, cout
  and and_6 (and_6_out, comparator_2_eq, \理想mem_wb_1_syscall_out );
  and and_7 (and_7_out, \理想mem_wb_1_syscall_out , not_3_out);
  Multiplexer #(.select(1), .width(32), .disabled("Z"), .enable("false")) multiplexer_12 (
    .in0(multiplexer_11_out), .in1(bit_extender_3_out), .out(multiplexer_12_out), .sel(\理想mem_wb_1_lbu_out ));
  Register #(.width(32), .trigger("rising"), .Select("low")) register_1 (
    .D(\理想mem_wb_1_b_out ), .Q(LedData), .clk(and_6_out));  // open: en, clr
  Register #(.width(1), .trigger("rising"), .Select("low")) register_2 (
    .D(and_7_out), .en(and_7_out), .Q(Halt), .clk(CLK), .clr(Go));
  Multiplexer #(.select(1), .width(5), .disabled("Z"), .enable("false")) multiplexer_13 (
    .in0(WB_IR[20:16]), .in1(WB_IR[15:11]), .out(multiplexer_13_out), .sel(\理想mem_wb_1_regdst_out ));
  Multiplexer #(.select(1), .width(32), .disabled("Z"), .enable("false")) multiplexer_14 (
    .in0(multiplexer_12_out), .in1(adder_4_out), .out(RDin), .sel(\理想mem_wb_1_jal_out ));
  Multiplexer #(.select(1), .width(5), .disabled("Z"), .enable("false")) multiplexer_15 (
    .in0(multiplexer_13_out), .in1({5{1'b1}}), .out(multiplexer_15_out), .sel(\理想mem_wb_1_jal_out ));

  // Other names for the same wires on the sheet: ID_IR[5:0] = Func; OP[5:0] = ID_IR[31:26]; MEM_PC[31:0] = M_PC

  // Notes on the sheet:
  //   中断源
  //   时空图监测，可删除
  //   中断等待指示
  //   数码管输出
  //   contents of rom_1 (hex, n*v repeats v):
  //   20110001 8000c05 20110001 20120002 20130003 8000c09 20110001 20120002 20130003 8000c0d 20110001
  //   20120002 20130003 8000c11 20110001 20120002 20130003 c000cb8 20100001 20110001 118fc0 112020
  //   20020022 c 118882 12200001 8000c15 112020 20020022 c 20110001 118880 112020 20020022 c 12200001
  //   8000c1f 20110001 118fc0 112020 20020022 c 1188c3 112020 20020022 c 118903 112020 20020022 c 118903
  //   112020 20020022 c 118903 112020 20020022 c 118903 112020 20020022 c 118903 112020 20020022 c 118903
  //   112020 20020022 c 118903 112020 20020022 c 20100001 109fc0 139fc3 8021 2012000c 24160003 26100001
  //   3210000f 20080008 20090001 139900 2709825 132020 20020022 c 1094022 1500fff9 22100001 2018000f
  //   2188024 108700 20080008 20090001 139902 2709825 132021 20020022 c 1094022 1500fff9 108702 2c9b022
  //   12c00001 8000c50 4020 1084027 84400 3508ffff 82021 20020022 c 2010ffff 20110000 ae300000 22100001
  //   22310004 ae300000 22100001 22310004 ae300000 22100001 22310004 ae300000 22100001 22310004 ae300000
  //   22100001 22310004 ae300000 22100001 22310004 ae300000 22100001 22310004 ae300000 22100001 22310004
  //   ae300000 22100001 22310004 ae300000 22100001 22310004 ae300000 22100001 22310004 ae300000 22100001
  //   22310004 ae300000 22100001 22310004 ae300000 22100001 22310004 ae300000 22100001 22310004 ae300000
  //   22100001 22310004 22100001 8020 2011003c 8e130000 8e340000 274402a 11000002 ae330000 ae140000
  //   2231fffc 1611fff8 102020 20020022 c 22100004 2011003c 1611fff2 20020032 c 20100000 22100001 102020
  //   20020022 c 22100002 102020 20020022 c 22100003 102020 20020022 c 22100004 102020 20020022 c 22100005
  //   102020 20020022 c 22100006 102020 20020022 c 22100007 102020 20020022 c 22100008 102020 20020022
  //   20020022 c 3e00008
  //   指令字
  //   rd
  //   rd
  //   控制位
  //   JMP
  //   JR
  //   OP
  //   OP
  //   Func
  //   rs
  //   rt
  //   rd
  //   流水调试日志用
  //   暂停节拍，不能为0
  //   Beq
  //   Bne
  //   MemToReg
  //   MemWrite
  //   AluOP
  //   AluSrcB
  //   RegWrite
  //   JAL
  //   RegDst
  //   Syscall
  //   戳工具置1进入计数暂停模式，ctrl+k时钟自动运行到对应节拍暂停
  //   ctrl+k关闭时钟连续运行，将控制位置零，进入单步调试模式调试
  //   用这个时钟源需要去掉电路中的其他时钟源
  //   可计数暂停的时钟源
  //   Reg_dst
  //   beq
  //   IR
  //   Syscall
  //   Bne
  //   PC
  //   JMP
  //   MemToReg
  //   JR
  //   AluOP
  //   RegWrite
  //   为方便自动评测，需要输出流水线各段保存的PC值，注意是PC不是PC+4，另外ID段寄存器写入信息，Mem段内存写入信息也要输出
  //   rt
  //   rd
endmodule

module \重定向流水线  (
  output RegWrite,
  output MemWrite,
  output [31:0] IF_PC,
  output [31:0] ID_PC,
  output [31:0] EX_PC,
  output [31:0] M_PC,
  output [31:0] WB_PC,
  output [31:0] RDin,
  output [31:0] MDin,
  output [31:0] LedData
);

  wire and_1_out, and_2_out, and_3_out, and_4_out, and_5_out, and_6_out, and_7_out, B_CLR, Branch, CLK,
       clock_1_out, clock_2_out, comparator_1_eq, comparator_2_eq, comparator_3_eq, comparator_3_lt,
       comparator_4_eq, d_ff_1_q, EX_JAL, EX_JMP, EX_JR, EX_RegDst, EX_RegWrite, Go, Halt, IR1, IR2, IR3,
       LoadUse, MEM_JAL, MEM_RegDst, MEM_RegWrite, mips_alu_1_equal, nand_1_out, nor_1_out, not_1_out,
       not_2_out, not_3_out, or_1_out, or_2_out, or_3_out, or_4_out, RST, SignedExt, W1, W2, W3,
       \单周期硬布线控制器_1_alu_src , \单周期硬布线控制器_1_beq , \单周期硬布线控制器_1_bgez , \单周期硬布线控制器_1_bne , \单周期硬布线控制器_1_jal ,
       \单周期硬布线控制器_1_jmp , \单周期硬布线控制器_1_jr , \单周期硬布线控制器_1_lbu , \单周期硬布线控制器_1_memtoreg ,
       \单周期硬布线控制器_1_memwrite , \单周期硬布线控制器_1_regdst , \单周期硬布线控制器_1_regwrite , \单周期硬布线控制器_1_sllv ,
       \单周期硬布线控制器_1_srav , \单周期硬布线控制器_1_syscall , \源寄存器使用情况_1_r1_used , \源寄存器使用情况_1_r2_used ,
       \理想ex_mem_1_lbu_out , \理想ex_mem_1_memtoreg_out , \理想ex_mem_1_syscall_out , \理想id_ex_1_alusrcb_out ,
       \理想id_ex_1_beq_out , \理想id_ex_1_bgez_out , \理想id_ex_1_bne_out , \理想id_ex_1_lbu_out ,
       \理想id_ex_1_memtoreg_out , \理想id_ex_1_memwrite_2 , \理想id_ex_1_sllv_out , \理想id_ex_1_srav_out ,
       \理想id_ex_1_syscall_out , \理想mem_wb_1_jal_out , \理想mem_wb_1_lbu_out , \理想mem_wb_1_memtoreg_out ,
       \理想mem_wb_1_regdst_out , \理想mem_wb_1_syscall_out ;
  wire [1:0] R1_Forward, R2_Forward, \重定向数据相关检测_1_r1 , \重定向数据相关检测_1_r2 ;
  wire [3:0] \单周期硬布线控制器_1_alu_op , \理想id_ex_1_aluop_out ;
  wire [4:0] multiplexer_1_out, multiplexer_2_out, multiplexer_3_out, multiplexer_4_out, multiplexer_12_out,
       multiplexer_15_out, multiplexer_17_out, R1_num, R2_num, \理想id_ex_1_shamt_2 ;
  wire [5:0] Func;
  wire [12:0] CNT_num;
  wire [15:0] \LoadUse次数 , \总周期数 , \插入气泡数 , \无条件分支数 , \条件分支成功数 ;
  wire [31:0] adder_2_out, adder_3_out, adder_4_out, bit_extender_1_out, bit_extender_2_out,
       bit_extender_3_out, controlled_buffer_2_out, EX_ALU, EX_IR, IF_IR, MEM_ALU, MEM_IR,
       mips_regifile_1_r1, mips_regifile_1_r2, multiplexer_7_out, multiplexer_8_out, multiplexer_9_out,
       multiplexer_10_out, multiplexer_11_out, multiplexer_13_out, multiplexer_14_out, PC_4, ram_1_data,
       shifter_1_out, WB_IR, \理想ex_mem_1_a_in_2 , \理想id_ex_1_a_out , \理想id_ex_1_b_out , \理想id_ex_1_imm_out ,
       \理想mem_wb_1_a_out , \理想mem_wb_1_alu_2 , \理想mem_wb_1_b_out , \理想mem_wb_1_md_2 ;
  wire [31:6] ID_IR;

  Button \u_总复位  (.out(RST));
  Button _1 (.out(IR1));
  Button _2 (.out(IR2));
  Button _3 (.out(IR3));
  // Probe on \总周期数 
  // Probe on \总周期数 
  Button \u_继续运行  (.out(Go));
  LED #(.active("true")) led_1 (.in(W1));
  LED #(.active("true")) led_2 (.in(W2));
  LED #(.active("true")) led_3 (.in(W3));
  Counter #(.width(16), .max('hffff), .ongoal("wrap"), .trigger("rising"), .behavior("new")) counter_1 (
    .Q(\总周期数 ), .clk(and_1_out));  // open: load, D, count, carry, clr, preset, down
  and and_1 (and_1_out, ~Halt, CLK);  // AND_Gate
  Hex_Digit_Display hex_digit_display_1 (.value(LedData[31:28]));  // open: dp
  // Probe on IF_PC[19:0]
  // Mips_Probe mips_probe_1: pin names not known; wires that end beside it: IF_IR
  nor nor_1 (nor_1_out, LoadUse, Halt);
  Hex_Digit_Display hex_digit_display_2 (.value(LedData[27:24]));  // open: dp
  Hex_Digit_Display hex_digit_display_3 (.value(LedData[23:20]));  // open: dp
  // Probe on ID_PC[19:0]
  // Mips_Probe mips_probe_2: pin names not known; wires that end beside it: {ID_IR, Func}
  Register #(.width(32), .trigger("rising"), .Select("low")) PC (
    .D(controlled_buffer_2_out), .en(nor_1_out), .Q(IF_PC), .clk(CLK));  // open: clr
  Hex_Digit_Display hex_digit_display_4 (.value(LedData[15:12]));  // open: dp
  Hex_Digit_Display hex_digit_display_5 (.value(LedData[19:16]));  // open: dp
  Hex_Digit_Display hex_digit_display_6 (.value(LedData[7:4]));  // open: dp
  Hex_Digit_Display hex_digit_display_7 (.value(LedData[11:8]));  // open: dp
  Clock #(.highDuration(1), .lowDuration(1)) clock_1 (.out(clock_1_out));
  // Probe on EX_PC[19:0]
  // Mips_Probe mips_probe_3: pin names not known; wires that end beside it: clock_1_out, EX_IR, CLK
  Adder #(.width(32)) adder_1 (.a(IF_PC), .b(32'h4), .out(PC_4));  // open: cin, cout
  Hex_Digit_Display hex_digit_display_8 (.value(LedData[3:0]));  // open: dp
  ROM #(.addrWidth(10), .dataWidth(32), .Select("high")) rom_1 (.addr(IF_PC[11:2]), .data(IF_IR));
  // Probe on \总周期数 
  // Probe on M_PC[19:0]
  // Mips_Probe mips_probe_4: pin names not known; wires that end beside it: MEM_IR
  \理想IF_ID  \u_理想if_id_1  (
    .IR_in(IF_IR), .PC_in(IF_PC), .CLK(CLK), .IR_out({ID_IR, Func}), .PC_out(ID_PC), .CLR(or_1_out),
    .Stall(LoadUse));  // open: RegDst_in, Beq_in, Syscall_in, Bne_in, JMP_in, MemToReg_in, A_in, JR_in, AluOP_in, SignedExt_in, AluSrcB_in, B_in, SLLV_in, RegWrite_in, Imm_in, SRAV_in, JAL_in, LBU_in, Shamt, MemWrite, BGEZ_in, RegDst_out, Beq_out, Syscall_out, Bne_out, JMP_out, MemToReg_out, A_out, JR_out, AluOP_out, SignedExt_out, AluSrcB_out, B_out, SLLV_out, RegWrite_out, Imm_out, SRAV_out, JAL_out, LBU_out, Shamt_2, MemWrite_2, BGEZ_out
  or or_1 (or_1_out, B_CLR, RST);
  // Probe on \总周期数 
  // Probe on \无条件分支数 
  // Probe on \条件分支成功数 
  // Probe on \插入气泡数 
  // Probe on \LoadUse次数 
  // Probe on IF_PC[11:0]
  // Probe on WB_PC[19:0]
  // Mips_Probe mips_probe_5: pin names not known; wires that end beside it: WB_IR
  Comparator #(.width(6), .mode("twosComplement")) comparator_1 (
    .a(EX_IR[31:26]), .b(6'b100011), .eq(comparator_1_eq));  // open: gt, lt
  Comparator #(.width(6), .mode("twosComplement")) comparator_2 (
    .a(EX_IR[31:26]), .b(6'b100100), .eq(comparator_2_eq));  // open: gt, lt
  // Probe on EX_PC[11:0]
  // Probe on ID_PC[11:0]
  or or_2 (or_2_out, comparator_1_eq, comparator_2_eq);
  Multiplexer #(.select(1), .width(5), .disabled("Z"), .enable("false")) multiplexer_1 (
    .in0(MEM_IR[20:16]), .in1(MEM_IR[15:11]), .out(multiplexer_1_out), .sel(MEM_RegDst));
  Multiplexer #(.select(1), .width(5), .disabled("Z"), .enable("false")) multiplexer_2 (
    .in0(EX_IR[20:16]), .in1(EX_IR[15:11]), .out(multiplexer_2_out), .sel(EX_RegDst));
  // Probe on M_PC[11:0]
  D_Flip_Flop #(.trigger("high"), .Pre_Clr_Positions("LEGACY"), .NegatePresetClear("false"), .enable("true"), .NewFFLayout("false")) d_ff_1 (.Q(d_ff_1_q));  // open: clk, D, Qn, preset, en, reset
  // Probe on 13'hc
  \单周期硬布线控制器  \u_单周期硬布线控制器_1  (
    .Func(Func), .OP(ID_IR[31:26]), .ALU_OP(\单周期硬布线控制器_1_alu_op ), .MemToReg(\单周期硬布线控制器_1_memtoreg ),
    .MemWrite(\单周期硬布线控制器_1_memwrite ), .ALU_SRC(\单周期硬布线控制器_1_alu_src ), .RegWrite(\单周期硬布线控制器_1_regwrite ),
    .SysCALL(\单周期硬布线控制器_1_syscall ), .SignedExt(SignedExt), .RegDst(\单周期硬布线控制器_1_regdst ),
    .JR(\单周期硬布线控制器_1_jr ), .JMP(\单周期硬布线控制器_1_jmp ), .Beq(\单周期硬布线控制器_1_beq ), .JAL(\单周期硬布线控制器_1_jal ),
    .Bne(\单周期硬布线控制器_1_bne ), .SLLV(\单周期硬布线控制器_1_sllv ), .SRAV(\单周期硬布线控制器_1_srav ), .BGEZ(\单周期硬布线控制器_1_bgez ),
    .LBU(\单周期硬布线控制器_1_lbu ));
  assign bit_extender_1_out = {{16{1'b0}}, {ID_IR[15:6], Func}};  // Bit_Extender bit_extender_1
  assign bit_extender_2_out = {{16{ID_IR[15]}}, {ID_IR[15:6], Func}};  // Bit_Extender bit_extender_2
  Multiplexer #(.select(1), .width(5), .disabled("Z"), .enable("false")) multiplexer_3 (
    .in0(multiplexer_1_out), .in1({5{1'b1}}), .out(multiplexer_3_out), .sel(MEM_JAL));
  Multiplexer #(.select(1), .width(5), .disabled("Z"), .enable("false")) multiplexer_4 (
    .in0(multiplexer_2_out), .in1({5{1'b1}}), .out(multiplexer_4_out), .sel(EX_JAL));
  // Probe on WB_PC[11:0]
  Comparator #(.width(13), .mode("twosComplement")) comparator_3 (
    .a(CNT_num), .b(13'hc), .eq(comparator_3_eq), .lt(comparator_3_lt));  // open: gt
  Clock #(.highDuration(1), .lowDuration(1)) clock_2 (.out(clock_2_out));
  Multiplexer #(.select(1), .width(5), .disabled("Z"), .enable("false")) multiplexer_5 (
    .in0(ID_IR[25:21]), .in1(5'b00010), .out(R1_num), .sel(\单周期硬布线控制器_1_syscall ));
  Multiplexer #(.select(1), .width(5), .disabled("Z"), .enable("false")) multiplexer_6 (
    .in0(ID_IR[20:16]), .in1(5'b00100), .out(R2_num), .sel(\单周期硬布线控制器_1_syscall ));
  nand nand_1 (nand_1_out, d_ff_1_q, comparator_3_eq);
  Counter #(.width(13), .max('h1fff), .ongoal("stay"), .trigger("rising"), .behavior("old")) counter_2 (
    .count(comparator_3_lt), .Q(CNT_num), .clk(clock_2_out));  // open: load, D, carry, clr, preset
  \源寄存器使用情况  \u_源寄存器使用情况_1  (
    .OP(ID_IR[31:26]), .Funct(Func), .R1_Used(\源寄存器使用情况_1_r1_used ), .R2_Used(\源寄存器使用情况_1_r2_used ));
  assign CLK = nand_1_out ? clock_2_out : 1'bz;  // Controlled_Buffer controlled_buffer_1
  MIPS_Regifile mips_regifile_1 (
    .Din(RDin), .Clk(CLK), .R1(mips_regifile_1_r1), .R2(mips_regifile_1_r2), .WE(RegWrite),
    .W_num(multiplexer_17_out), .R1_num(R1_num), .R2_num(R2_num));
  Multiplexer #(.select(1), .width(32), .disabled("Z"), .enable("false")) multiplexer_7 (
    .in0(bit_extender_1_out), .in1(bit_extender_2_out), .out(multiplexer_7_out), .sel(SignedExt));
  \重定向数据相关检测  \u_重定向数据相关检测_1  (
    .R1_num(R1_num), .MEM_WriteReg_num(multiplexer_3_out), .MEM_RegWrite(MEM_RegWrite),
    .R1_Used(\源寄存器使用情况_1_r1_used ), .EX_WriteReg_num(multiplexer_4_out), .EX_RegWrite(EX_RegWrite),
    .R2_num(R2_num), .R2_Used(\源寄存器使用情况_1_r2_used ), .R1(\重定向数据相关检测_1_r1 ), .R2(\重定向数据相关检测_1_r2 ),
    .Load_Use(or_2_out), .LoadUse(LoadUse));
  Pull_Resistor #(.pull(1)) pull_resistor_1 (.node(CLK));
  Register #(.width(2), .trigger("rising"), .Select("low")) register_1 (
    .D(\重定向数据相关检测_1_r1 ), .Q(R1_Forward), .clk(CLK));  // open: en, clr
  Register #(.width(2), .trigger("rising"), .Select("low")) register_2 (
    .D(\重定向数据相关检测_1_r2 ), .Q(R2_Forward), .clk(CLK));  // open: en, clr
  \理想ID_EX  \u_理想id_ex_1  (
    .RegDst_in(\单周期硬布线控制器_1_regdst ), .Beq_in(\单周期硬布线控制器_1_beq ), .IR_in({ID_IR, Func}),
    .Syscall_in(\单周期硬布线控制器_1_syscall ), .Bne_in(\单周期硬布线控制器_1_bne ), .PC_in(ID_PC),
    .JMP_in(\单周期硬布线控制器_1_jmp ), .MemToReg_in(\单周期硬布线控制器_1_memtoreg ), .A_in(mips_regifile_1_r1),
    .JR_in(\单周期硬布线控制器_1_jr ), .AluOP_in(\单周期硬布线控制器_1_alu_op ), .SignedExt_in(SignedExt),
    .AluSrcB_in(\单周期硬布线控制器_1_alu_src ), .B_in(mips_regifile_1_r2), .SLLV_in(\单周期硬布线控制器_1_sllv ),
    .RegWrite_in(\单周期硬布线控制器_1_regwrite ), .Imm_in(multiplexer_7_out), .SRAV_in(\单周期硬布线控制器_1_srav ),
    .JAL_in(\单周期硬布线控制器_1_jal ), .LBU_in(\单周期硬布线控制器_1_lbu ), .BGEZ_in(\单周期硬布线控制器_1_bgez ), .CLK(CLK),
    .RegDst_out(EX_RegDst), .Beq_out(\理想id_ex_1_beq_out ), .IR_out(EX_IR),
    .Syscall_out(\理想id_ex_1_syscall_out ), .Bne_out(\理想id_ex_1_bne_out ), .PC_out(EX_PC), .JMP_out(EX_JMP),
    .MemToReg_out(\理想id_ex_1_memtoreg_out ), .A_out(\理想id_ex_1_a_out ), .JR_out(EX_JR),
    .AluOP_out(\理想id_ex_1_aluop_out ), .AluSrcB_out(\理想id_ex_1_alusrcb_out ), .B_out(\理想id_ex_1_b_out ),
    .SLLV_out(\理想id_ex_1_sllv_out ), .RegWrite_out(EX_RegWrite), .Imm_out(\理想id_ex_1_imm_out ),
    .SRAV_out(\理想id_ex_1_srav_out ), .JAL_out(EX_JAL), .LBU_out(\理想id_ex_1_lbu_out ),
    .BGEZ_out(\理想id_ex_1_bgez_out ), .CLR(or_3_out), .Shamt(ID_IR[10:6]), .Shamt_2(\理想id_ex_1_shamt_2 ),
    .MemWrite(\单周期硬布线控制器_1_memwrite ), .MemWrite_2(\理想id_ex_1_memwrite_2 ));  // open: SignedExt_out, Stall
  or or_3 (or_3_out, B_CLR, LoadUse, RST);
  Multiplexer #(.select(1), .width(32), .disabled("Z"), .enable("false")) multiplexer_8 (
    .in0(multiplexer_9_out), .in1(\理想id_ex_1_imm_out ), .out(multiplexer_8_out), .sel(\理想id_ex_1_alusrcb_out ));
  Multiplexer #(.select(2), .width(32), .disabled("Z"), .enable("false")) multiplexer_9 (
    .in0(\理想id_ex_1_b_out ), .in1(MEM_ALU), .in2(RDin), .in3(MEM_ALU), .out(multiplexer_9_out),
    .sel(R2_Forward));
  Multiplexer #(.select(1), .width(32), .disabled("Z"), .enable("false")) multiplexer_10 (
    .in0(multiplexer_8_out), .in1({32{1'b0}}), .out(multiplexer_10_out), .sel(\理想id_ex_1_bgez_out ));
  or or_4 (or_4_out, \理想id_ex_1_sllv_out , \理想id_ex_1_srav_out );
  Multiplexer #(.select(2), .width(32), .disabled("Z"), .enable("false")) multiplexer_11 (
    .in0(\理想id_ex_1_a_out ), .in1(MEM_ALU), .in2(RDin), .in3(MEM_ALU), .out(multiplexer_11_out),
    .sel(R1_Forward));
  Multiplexer #(.select(1), .width(5), .disabled("Z"), .enable("false")) multiplexer_12 (
    .in0(\理想id_ex_1_shamt_2 ), .in1(multiplexer_11_out[4:0]), .out(multiplexer_12_out), .sel(or_4_out));
  MIPS_ALU mips_alu_1 (
    .X(multiplexer_11_out), .Y(multiplexer_10_out), .AluOP(\理想id_ex_1_aluop_out ), .Equal(mips_alu_1_equal),
    .Result(EX_ALU), .shamt(multiplexer_12_out));  // open: Result_2
  and and_2 (and_2_out, \理想id_ex_1_bgez_out , ~EX_ALU[0]);  // AND_Gate
  and and_3 (and_3_out, mips_alu_1_equal, \理想id_ex_1_beq_out );
  and and_4 (and_4_out, ~mips_alu_1_equal, \理想id_ex_1_bne_out );  // AND_Gate
  Shifter #(.width(32), .shift("ll")) shifter_1 (.in(\理想id_ex_1_imm_out ), .\dist (5'b00010), .out(shifter_1_out));
  Adder #(.width(32)) adder_2 (.a(EX_PC), .b(32'h4), .out(adder_2_out));  // open: cin, cout
  or or_5 (Branch, and_2_out, and_3_out, and_4_out);
  \理想EX_MEM  \u_理想ex_mem_1  (
    .RegDst_in(EX_RegDst), .IR_in(EX_IR), .Syscall_in(\理想id_ex_1_syscall_out ), .PC_in(EX_PC),
    .MemToReg_in(\理想id_ex_1_memtoreg_out ), .A_in(multiplexer_11_out), .B_in(multiplexer_9_out),
    .RegWrite_in(EX_RegWrite), .JAL_in(EX_JAL), .LBU_in(\理想id_ex_1_lbu_out ), .CLK(CLK),
    .RegDst_out(MEM_RegDst), .IR_out(MEM_IR), .Syscall_out(\理想ex_mem_1_syscall_out ), .PC_out(M_PC),
    .MemToReg_out(\理想ex_mem_1_memtoreg_out ), .A_in_2(\理想ex_mem_1_a_in_2 ), .B_out(MDin),
    .RegWrite_out(MEM_RegWrite), .JAL_out(MEM_JAL), .LBU_out(\理想ex_mem_1_lbu_out ), .CLR(RST),
    .MemWrite(\理想id_ex_1_memwrite_2 ), .MemWrite_2(MemWrite), .ALU(EX_ALU), .ALU_2(MEM_ALU));  // open: Beq_in, Bne_in, JMP_in, JR_in, SignedExt_in, AluSrcB_in, SLLV_in, Imm_in, SRAV_in, Shamt, BGEZ_in, Beq_out, Bne_out, JMP_out, JR_out, SignedExt_out, AluSrcB_out, SLLV_out, Imm_out, SRAV_out, Shamt_2, BGEZ_out, Stall
  Adder #(.width(32)) adder_3 (.a(shifter_1_out), .b(adder_2_out), .out(adder_3_out));  // open: cin, cout
  or or_6 (B_CLR, Branch, EX_JMP);
  not not_1 (not_1_out, B_CLR);
  assign controlled_buffer_2_out = EX_JR ? multiplexer_11_out : 32'bz;  // Controlled_Buffer controlled_buffer_2
  assign controlled_buffer_2_out = Branch ? adder_3_out : 32'bz;  // Controlled_Buffer controlled_buffer_3
  assign controlled_buffer_2_out = and_5_out ? {EX_PC[31:28], EX_IR[25:0], 2'b00} : 32'bz;  // Controlled_Buffer controlled_buffer_4
  and and_5 (and_5_out, EX_JMP, ~EX_JR);  // AND_Gate
  assign controlled_buffer_2_out = not_1_out ? PC_4 : 32'bz;  // Controlled_Buffer controlled_buffer_5
  not not_2 (not_2_out, Halt);
  RAM #(.addrWidth(10), .dataWidth(32), .bus("separate"), .Select("high")) ram_1 (
    .addr(MEM_ALU[11:2]), .din(MDin), .data(ram_1_data), .str(MemWrite), .sel(not_2_out), .clk(CLK));  // open: ld, clr
  \理想MEM_WB  \u_理想mem_wb_1  (
    .RegDst_in(MEM_RegDst), .RegDst_out(\理想mem_wb_1_regdst_out ), .IR_in(MEM_IR), .IR_out(WB_IR),
    .Syscall_in(\理想ex_mem_1_syscall_out ), .Syscall_out(\理想mem_wb_1_syscall_out ), .PC_in(M_PC),
    .PC_out(WB_PC), .MemToReg_in(\理想ex_mem_1_memtoreg_out ), .MemToReg_out(\理想mem_wb_1_memtoreg_out ),
    .A_in(\理想ex_mem_1_a_in_2 ), .A_out(\理想mem_wb_1_a_out ), .ALU(MEM_ALU), .ALU_2(\理想mem_wb_1_alu_2 ),
    .B_in(MDin), .B_out(\理想mem_wb_1_b_out ), .RegWrite_in(MEM_RegWrite), .RegWrite_out(RegWrite),
    .JAL_in(MEM_JAL), .JAL_out(\理想mem_wb_1_jal_out ), .LBU_in(\理想ex_mem_1_lbu_out ), .MD(ram_1_data),
    .LBU_out(\理想mem_wb_1_lbu_out ), .MD_2(\理想mem_wb_1_md_2 ), .CLK(CLK), .CLR(RST));  // open: Beq_in, Beq_out, Bne_in, Bne_out, JMP_in, JMP_out, JR_in, JR_out, SignedExt_in, SignedExt_out, AluSrcB_in, AluSrcB_out, SLLV_in, SLLV_out, Imm_in, Imm_out, SRAV_in, SRAV_out, BGEZ_in, BGEZ_out, Stall, MemWrite, MemWrite_2
  Multiplexer #(.select(1), .width(32), .disabled("Z"), .enable("false")) multiplexer_13 (
    .in0(\理想mem_wb_1_alu_2 ), .in1(\理想mem_wb_1_md_2 ), .out(multiplexer_13_out),
    .sel(\理想mem_wb_1_memtoreg_out ));
  Comparator #(.width(32), .mode("twosComplement")) comparator_4 (
    .a(\理想mem_wb_1_a_out ), .b(32'h22), .eq(comparator_4_eq));  // open: gt, lt
  not not_3 (not_3_out, comparator_4_eq);
  assign bit_extender_3_out = {{24{1'b0}}, multiplexer_13_out[7:0]};  // Bit_Extender bit_extender_3
  Adder #(.width(32)) adder_4 (.a(WB_PC), .b(32'h4), .out(adder_4_out));  // open: cin, cout
  and and_6 (and_6_out, comparator_4_eq, \理想mem_wb_1_syscall_out );
  and and_7 (and_7_out, \理想mem_wb_1_syscall_out , not_3_out);
  Multiplexer #(.select(1), .width(32), .disabled("Z"), .enable("false")) multiplexer_14 (
    .in0(multiplexer_13_out), .in1(bit_extender_3_out), .out(multiplexer_14_out), .sel(\理想mem_wb_1_lbu_out ));
  Register #(.width(32), .trigger("rising"), .Select("low")) register_3 (
    .D(\理想mem_wb_1_b_out ), .Q(LedData), .clk(and_6_out));  // open: en, clr
  Register #(.width(1), .trigger("rising"), .Select("low")) register_4 (
    .D(and_7_out), .en(and_7_out), .Q(Halt), .clk(CLK), .clr(Go));
  Multiplexer #(.select(1), .width(5), .disabled("Z"), .enable("false")) multiplexer_15 (
    .in0(WB_IR[20:16]), .in1(WB_IR[15:11]), .out(multiplexer_15_out), .sel(\理想mem_wb_1_regdst_out ));
  Multiplexer #(.select(1), .width(32), .disabled("Z"), .enable("false")) multiplexer_16 (
    .in0(multiplexer_14_out), .in1(adder_4_out), .out(RDin), .sel(\理想mem_wb_1_jal_out ));
  Multiplexer #(.select(1), .width(5), .disabled("Z"), .enable("false")) multiplexer_17 (
    .in0(multiplexer_15_out), .in1({5{1'b1}}), .out(multiplexer_17_out), .sel(\理想mem_wb_1_jal_out ));

  // Other names for the same wires on the sheet: ID_IR[5:0] = Func; OP[5:0] = ID_IR[31:26]; MEM_PC[31:0] = M_PC

  // Notes on the sheet:
  //   中断源
  //   时空图监测，可删除
  //   中断等待指示
  //   数码管输出
  //   contents of rom_1 (hex, n*v repeats v):
  //   20110001 8000c05 20110001 20120002 20130003 8000c09 20110001 20120002 20130003 8000c0d 20110001
  //   20120002 20130003 8000c11 20110001 20120002 20130003 c000cb8 20100001 20110001 118fc0 112020
  //   20020022 c 118882 12200001 8000c15 112020 20020022 c 20110001 118880 112020 20020022 c 12200001
  //   8000c1f 20110001 118fc0 112020 20020022 c 1188c3 112020 20020022 c 118903 112020 20020022 c 118903
  //   112020 20020022 c 118903 112020 20020022 c 118903 112020 20020022 c 118903 112020 20020022 c 118903
  //   112020 20020022 c 118903 112020 20020022 c 20100001 109fc0 139fc3 8021 2012000c 24160003 26100001
  //   3210000f 20080008 20090001 139900 2709825 132020 20020022 c 1094022 1500fff9 22100001 2018000f
  //   2188024 108700 20080008 20090001 139902 2709825 132021 20020022 c 1094022 1500fff9 108702 2c9b022
  //   12c00001 8000c50 4020 1084027 84400 3508ffff 82021 20020022 c 2010ffff 20110000 ae300000 22100001
  //   22310004 ae300000 22100001 22310004 ae300000 22100001 22310004 ae300000 22100001 22310004 ae300000
  //   22100001 22310004 ae300000 22100001 22310004 ae300000 22100001 22310004 ae300000 22100001 22310004
  //   ae300000 22100001 22310004 ae300000 22100001 22310004 ae300000 22100001 22310004 ae300000 22100001
  //   22310004 ae300000 22100001 22310004 ae300000 22100001 22310004 ae300000 22100001 22310004 ae300000
  //   22100001 22310004 22100001 8020 2011003c 8e130000 8e340000 274402a 11000002 ae330000 ae140000
  //   2231fffc 1611fff8 102020 20020022 c 22100004 2011003c 1611fff2 20020032 c 20100000 22100001 102020
  //   20020022 c 22100002 102020 20020022 c 22100003 102020 20020022 c 22100004 102020 20020022 c 22100005
  //   102020 20020022 c 22100006 102020 20020022 c 22100007 102020 20020022 c 22100008 102020 20020022
  //   20020022 c 3e00008
  //   指令字
  //   控制位
  //   JMP
  //   JR
  //   OP
  //   OP
  //   Func
  //   rs
  //   rt
  //   rd
  //   rd
  //   rd
  //   流水调试日志用
  //   暂停节拍，不能为0
  //   Beq
  //   Bne
  //   MemToReg
  //   MemWrite
  //   AluOP
  //   AluSrcB
  //   RegWrite
  //   JAL
  //   RegDst
  //   Syscall
  //   戳工具置1进入计数暂停模式，ctrl+k时钟自动运行到对应节拍暂停
  //   ctrl+k关闭时钟连续运行，将控制位置零，进入单步调试模式调试
  //   用这个时钟源需要去掉电路中的其他时钟源
  //   可计数暂停的时钟源
  //   IR
  //   Syscall
  //   MemToReg
  //   AluOP
  //   RegWrite
  //   Reg_dst
  //   beq
  //   Bne
  //   PC
  //   JMP
  //   JR
  //   为方便自动评测，需要输出流水线各段保存的PC值，注意是PC不是PC+4，另外ID段寄存器写入信息，Mem段内存写入信息也要输出
  //   rt
  //   rd
endmodule

module \中断按键参考电路  (
  input  \同步清零信号 ,
  output \与中断屏蔽位与 
);

  wire \_1号中断_out , and_1_out, clock_1_out, d_ff_1_q, or_1_out, or_2_out;

  Clock #(.highDuration(1), .lowDuration(1)) clock_1 (.out(clock_1_out));
  Button \_1号中断  (.out(\_1号中断_out ));
  or or_1 (or_1_out, \与中断屏蔽位与 , d_ff_1_q);
  LED #(.active("true")) \_1号中断等待指示灯  (.in(or_1_out));
  D_Flip_Flop #(.trigger("rising"), .Pre_Clr_Positions("LEGACY"), .NegatePresetClear("false"), .enable("true"), .NewFFLayout("false")) d_ff_1 (
    .clk(\_1号中断_out ), .D(1'b1), .Q(d_ff_1_q), .reset(\与中断屏蔽位与 ));  // open: Qn, preset, en
  or or_2 (or_2_out, d_ff_1_q, \与中断屏蔽位与 );
  and and_1 (and_1_out, or_2_out, ~\同步清零信号 );  // AND_Gate
  D_Flip_Flop #(.trigger("rising"), .Pre_Clr_Positions("LEGACY"), .NegatePresetClear("false"), .enable("true"), .NewFFLayout("false")) IR1 (
    .clk(clock_1_out), .D(and_1_out), .Q(\与中断屏蔽位与 ));  // open: Qn, preset, en, reset
  \单周期硬布线控制器  \u_单周期硬布线控制器_1  ();  // open: Func, OP, ALU_OP, MemToReg, MemWrite, ALU_SRC, RegWrite, SysCALL, SignedExt, RegDst, JR, JMP, Beq, JAL, Bne, SLLV, SRAV, BGEZ, LBU

  // Notes on the sheet:
  //   中断信号采样参考电路
  //   Reset 
endmodule

module \单周期MIPS_单级中断  (
  input  IR1,
  input  IR2,
  input  IR3,
  output RegWrite,
  output MemWrite,
  output [31:0] PC,
  output [31:0] IR,
  output [31:0] RDin,
  output [31:0] MDin,
  output [31:0] LedData
);

  wire CLK, comparator_1_eq, comparator_2_eq, comparator_3_eq, comparator_4_eq, Go, IR1_t, IR2_t, IR3_t, IRA,
       IRB, IRC, or_1_out, W1, W2, W3;
  wire [15:0] \总周期数 ;

  Clock #(.highDuration(1), .lowDuration(1)) clock_1 (.out(CLK));
  Button _1 ();  // open: out
  Button _2 ();  // open: out
  Button _3 ();  // open: out
  Button \u_继续运行  (.out(Go));
  LED #(.active("true")) led_1 (.in(W1));
  LED #(.active("true")) led_2 (.in(W2));
  LED #(.active("true")) led_3 (.in(W3));
  Hex_Digit_Display hex_digit_display_1 (.value(LedData[31:28]));  // open: dp
  Comparator #(.width(16), .mode("twosComplement")) comparator_1 (
    .a(16'h23b), .b(\总周期数 ), .eq(comparator_1_eq));  // open: gt, lt
  Comparator #(.width(16), .mode("twosComplement")) comparator_2 (
    .a(\总周期数 ), .b(16'h1), .eq(comparator_2_eq));  // open: gt, lt
  Comparator #(.width(16), .mode("twosComplement")) comparator_3 (
    .a(\总周期数 ), .b(16'h4), .eq(comparator_3_eq));  // open: gt, lt
  Comparator #(.width(16), .mode("twosComplement")) comparator_4 (
    .a(\总周期数 ), .b(16'h7), .eq(comparator_4_eq));  // open: gt, lt
  Hex_Digit_Display hex_digit_display_2 (.value(LedData[23:20]));  // open: dp
  Hex_Digit_Display hex_digit_display_3 (.value(LedData[27:24]));  // open: dp
  or or_1 (or_1_out, comparator_1_eq, comparator_2_eq);
  assign IRA = or_1_out ? ~CLK : 1'bz;  // Controlled_Inverter controlled_inverter_1
  assign IRB = comparator_3_eq ? ~CLK : 1'bz;  // Controlled_Inverter controlled_inverter_2
  assign IRC = comparator_4_eq ? ~CLK : 1'bz;  // Controlled_Inverter controlled_inverter_3
  Hex_Digit_Display hex_digit_display_4 (.value(LedData[19:16]));  // open: dp
  Hex_Digit_Display hex_digit_display_5 (.value(LedData[15:12]));  // open: dp
  Pull_Resistor #(.pull(0)) pull_resistor_1 (.node(IRA));
  Pull_Resistor #(.pull(0)) pull_resistor_2 (.node(IRB));
  Pull_Resistor #(.pull(0)) pull_resistor_3 (.node(IRC));
  Hex_Digit_Display hex_digit_display_6 (.value(LedData[7:4]));  // open: dp
  Hex_Digit_Display hex_digit_display_7 (.value(LedData[11:8]));  // open: dp
  // Probe on \总周期数 
  Hex_Digit_Display hex_digit_display_8 (.value(LedData[3:0]));  // open: dp
  or or_2 (IR1_t, IR1, IRA);
  or or_3 (IR2_t, IR2, IRB);
  or or_4 (IR3_t, IR3, IRC);

  // Notes on the sheet:
  //   中断源
  //   中断等待指示
  //   总复位信号应将除ROM以外所有存储组件全部清零
  //   单级中断测试信号模拟器
  //   数码管输出
  //   数码管输出应该用寄存器锁存，否则显示数据只能一闪而过
  //   为方便自动评测，需要输出PC，IR，寄存器堆写如数据RDin
  //   RAM写使能MemWrite、RAM写入数据MDin等信号
endmodule

module \单周期MIPS_多级中断  (
  input  IR1,
  input  IR2,
  input  IR3,
  output RegWrite,
  output MemWrite,
  output [31:0] PC,
  output [31:0] IR,
  output [31:0] RDin,
  output [31:0] MDin,
  output [31:0] LedData
);

  wire CLK, comparator_1_eq, comparator_2_eq, comparator_3_eq, comparator_4_eq, comparator_5_eq, Go, IR1_t,
       IR2_t, IR3_t, IRA, IRB, IRC, or_1_out, or_2_out, W1, W2, W3;
  wire [15:0] \总周期数 ;

  Clock #(.highDuration(1), .lowDuration(1)) clock_1 (.out(CLK));
  Button _1 ();  // open: out
  Button _2 ();  // open: out
  Button _3 ();  // open: out
  Button \u_继续运行  (.out(Go));
  LED #(.active("true")) led_1 (.in(W1));
  LED #(.active("true")) led_2 (.in(W2));
  LED #(.active("true")) led_3 (.in(W3));
  Hex_Digit_Display hex_digit_display_1 (.value(LedData[31:28]));  // open: dp
  Comparator #(.width(16), .mode("twosComplement")) comparator_1 (
    .a(\总周期数 ), .b(16'h7), .eq(comparator_1_eq));  // open: gt, lt
  Comparator #(.width(16), .mode("twosComplement")) comparator_2 (
    .a(\总周期数 ), .b(16'h241), .eq(comparator_2_eq));  // open: gt, lt
  Hex_Digit_Display hex_digit_display_2 (.value(LedData[27:24]));  // open: dp
  Hex_Digit_Display hex_digit_display_3 (.value(LedData[23:20]));  // open: dp
  Comparator #(.width(16), .mode("twosComplement")) comparator_3 (
    .a(16'h258), .b(\总周期数 ), .eq(comparator_3_eq));  // open: gt, lt
  or or_1 (or_1_out, comparator_3_eq, comparator_4_eq);
  Comparator #(.width(16), .mode("twosComplement")) comparator_4 (
    .a(\总周期数 ), .b(16'h1), .eq(comparator_4_eq));  // open: gt, lt
  Comparator #(.width(16), .mode("twosComplement")) comparator_5 (
    .a(\总周期数 ), .b(16'h4), .eq(comparator_5_eq));  // open: gt, lt
  or or_2 (or_2_out, comparator_1_eq, comparator_2_eq);
  Hex_Digit_Display hex_digit_display_4 (.value(LedData[15:12]));  // open: dp
  Hex_Digit_Display hex_digit_display_5 (.value(LedData[19:16]));  // open: dp
  Pull_Resistor #(.pull(0)) pull_resistor_1 (.node(IRA));
  assign IRA = or_1_out ? ~CLK : 1'bz;  // Controlled_Inverter controlled_inverter_1
  Pull_Resistor #(.pull(0)) pull_resistor_2 (.node(IRB));
  assign IRB = comparator_5_eq ? ~CLK : 1'bz;  // Controlled_Inverter controlled_inverter_2
  Pull_Resistor #(.pull(0)) pull_resistor_3 (.node(IRC));
  assign IRC = or_2_out ? ~CLK : 1'bz;  // Controlled_Inverter controlled_inverter_3
  Hex_Digit_Display hex_digit_display_6 (.value(LedData[7:4]));  // open: dp
  Hex_Digit_Display hex_digit_display_7 (.value(LedData[11:8]));  // open: dp
  // Probe on \总周期数 
  Hex_Digit_Display hex_digit_display_8 (.value(LedData[3:0]));  // open: dp
  or or_3 (IR1_t, IR1, IRA);
  or or_4 (IR2_t, IR2, IRB);
  or or_5 (IR3_t, IR3, IRC);

  // Notes on the sheet:
  //   中断源
  //   中断等待指示
  //   总复位信号应将除ROM以外所有存储组件全部清零
  //   多级中断测试信号模拟器
  //   数码管输出
  //   数码管输出应该用寄存器锁存，否则显示数据只能一闪而过
  //   为方便自动评测，需要输出PC，IR，寄存器堆写如数据RDin
  //   RAM写使能MemWrite、RAM写入数据MDin等信号
endmodule

module \封装正确性测试  (
);

  wire IR1, IR2, IR3, MemW, RegW;
  wire [31:0] EX_PC, ID_PC, IF_PC, IR, LED, MDin, MDinr, MEM_PC, PC, RDin, RDinr, WB_PC;

  \单周期MIPS  \u_单周期mips_1  (
    .RegWrite(RegW), .MemWrite(MemW), .PC(PC), .IR(IR), .RDin(RDin), .MDin(MDin), .LedData(LED));  // open: IR1, IR2, IR3, in_4, in_5, in_6, in_7, in_8, in_9, in_10, in_11, in_12, in_13, in_14, in_15, in_16, in_17, in_18, in_19, in_20, in_21, in_22, in_23, in_24, in_25, in_26, in_27, in_28, in_29, in_30, in_31, in_32, in_33, in_34, in_35, in_36, in_37, in_38, in_39, in_40, in_41, in_42, in_43, in_44, in_45, in_46, in_47, in_48, in_49, in_50, in_51, in_52, in_53, in_54, in_55, in_56, in_57, in_58, in_59, in_60, in_61, in_62, in_63, in_64, in_65, in_66, in_67, in_68, in_69, in_70, in_71, in_72, in_73, in_74, in_75, in_76, in_77, in_78, in_79, in_80, in_81, in_82, in_83, in_84, in_85, in_86, in_87, in_88, in_89, in_90, in_91, in_92, in_93, in_94, in_95, in_96, in_97, in_98, in_99, in_100, in_101, in_102, in_103, in_104, in_105, in_106, in_107, in_108, in_109, in_110, in_111, in_112, in_113, in_114, in_115, in_116, in_117, in_118, in_119, in_120, in_121, in_122, in_123, in_124, in_125, in_126, in_127, in_128, in_129, in_130, in_131, in_132, in_133, in_134, in_135, in_136, in_137, in_138, in_139, in_140, in_141, in_142, in_143, in_144, in_145, in_146, in_147, in_148, in_149, in_150, in_151, in_152, in_153, in_154, in_155, in_156, in_157, in_158, in_159, in_160, in_161, in_162, in_163, in_164, in_165, in_166, in_167, in_168, in_169, in_170, in_171, in_172, in_173, in_174, in_175, in_176, in_177, in_178, in_179, in_180, in_181, in_182, in_183, in_184, in_185, in_186, in_187, in_188, in_189, in_190, in_191, in_192, in_193, in_194, in_195, in_196, in_197, in_198, in_199, in_200, in_201, in_202, in_203, in_204, in_205, in_206, in_207, in_208, in_209, in_210, in_211, in_212, in_213, in_214, in_215, in_216, in_217, in_218, in_219, in_220, in_221, in_222, in_223, in_224, in_225, in_226, in_227, in_228, in_229, in_230, in_231, in_232, in_233, in_234, in_235, in_236, in_237, in_238, in_239, in_240, in_241, in_242, in_243, in_244, in_245, in_246, in_247, in_248, in_249, in_250, in_251, in_252, in_253, in_254, in_255, in_256, in_257, in_258, in_259, in_260, in_261, in_262, in_263, in_264, in_265, in_266, in_267, in_268, in_269, in_270, in_271, in_272, in_273, in_274, in_275, in_276, in_277, in_278, in_279, in_280, in_281, in_282, in_283, in_284, in_285, in_286, in_287, in_288, in_289, in_290, in_291, in_292, in_293, in_294, in_295, in_296, in_297, in_298, in_299, in_300, in_301, in_302, in_303, in_304, in_305, in_306, in_307, in_308, in_309, in_310, in_311, in_312, in_313, in_314, in_315, in_316, in_317, in_318, in_319, in_320, in_321, in_322, in_323, in_324, in_325, in_326, in_327, in_328, in_329, in_330, in_331, in_332, in_333, in_334, in_335, in_336, in_337, in_338, in_339, in_340, in_341, in_342, in_343, in_344, in_345, in_346, in_347, in_348, in_349, in_350, in_351, in_352, in_353, in_354, in_355, in_356, in_357, in_358, in_359, in_360, in_361, in_362, in_363, in_364, in_365, in_366, in_367, 开始计算, in_369, in_370, in_371, in_372, in_373, in_374, in_375, in_376, in_377, in_378, in_379, in_380, in_381, in_382, in_383, in_384, in_385, in_386, in_387, in_388, in_389, in_390, in_391, in_392, in_393, in_394, in_395, in_396, in_397, in_398, in_399, in_400, in_401, in_402, in_403, in_404, in_405, in_406, in_407, in_408, in_409, in_410, in_411, in_412, in_413, in_414, in_415, in_416, in_417, in_418, in_419, in_420, in_421, in_422, in_423, in_424, in_425, in_426, in_427, in_428, in_429, in_430, in_431, in_432, in_433, in_434, in_435, in_436, in_437, in_438, in_439, in_440, in_441, in_442, in_443, in_444, in_445, in_446, in_447, in_448, in_449, in_450, in_451, in_452, in_453, in_454, in_455, in_456, in_457, in_458, in_459, in_460, in_461, in_462, in_463, in_464, in_465, in_466, in_467, in_468, in_469, in_470, in_471, in_472, in_473, in_474, in_475, in_476, in_477, in_478, in_479, in_480, in_481, in_482, in_483, in_484, in_485, in_486, in_487, in_488, in_489, in_490, in_491, in_492, in_493, in_494, in_495, in_496, in_497, in_498, in_499, in_500, in_501, in_502, in_503, in_504, in_505, in_506, in_507, in_508, in_509, in_510, in_511, in_512, in_513, in_514, in_515, in_516, in_517, in_518, in_519, in_520, in_521, in_522, in_523, in_524, in_525, in_526, in_527, in_528, in_529, in_530, in_531, in_532, in_533, in_534, in_535, in_536, in_537, in_538, in_539, in_540, in_541, in_542, in_543, in_544, in_545, in_546, in_547, in_548, in_549, in_550, in_551, in_552, in_553, in_554, in_555, in_556, in_557, in_558, in_559, in_560, in_561, in_562, in_563, in_564, in_565, in_566, in_567, in_568, in_569, in_570, in_571, in_572, in_573, in_574, in_575, in_576, in_577, in_578, in_579, in_580, in_581, in_582, in_583, in_584, in_585, in_586, in_587, in_588, in_589, in_590, in_591, in_592, in_593, in_594, in_595, in_596, in_597, in_598, in_599, in_600, in_601, in_602, in_603, in_604, in_605, in_606, in_607, in_608, in_609, in_610, in_611, in_612, in_613, in_614, in_615, in_616, in_617, in_618, in_619, in_620, in_621, in_622, in_623, in_624, in_625, in_626, in_627, in_628, in_629, in_630, in_631, in_632, in_633, in_634, in_635, in_636, in_637, in_638, in_639, in_640, in_641, in_642, in_643, in_644, in_645, in_646, in_647, in_648, in_649, in_650, in_651, in_652, in_653, in_654, in_655, in_656, in_657, in_658, in_659, in_660, in_661, in_662, in_663, in_664, in_665, in_666, in_667, in_668, in_669, in_670, in_671, in_672, in_673, in_674, in_675, in_676, in_677, in_678, in_679, in_680, in_681, in_682, in_683, in_684, in_685, in_686, in_687, in_688, in_689, in_690, in_691, in_692, in_693, in_694, in_695, in_696, in_697, in_698, in_699, in_700, in_701, in_702, in_703, in_704, in_705, in_706, in_707, in_708, in_709, in_710, in_711, in_712, in_713, in_714, in_715, in_716, in_717, in_718, in_719, in_720, in_721, in_722, in_723, in_724, in_725, in_726, in_727, in_728, in_729, in_730, in_731, in_732, in_733, in_734, in_735, in_736, in_737, in_738, in_739, in_740, in_741, in_742, in_743, in_744, in_745, in_746, in_747, in_748, in_749, in_750, in_751, in_752, in_753, in_754, in_755, in_756, in_757, in_758, in_759, in_760, in_761, in_762, in_763, in_764, in_765, in_766, in_767, in_768, in_769, in_770, in_771, in_772, in_773, in_774, in_775, in_776, in_777, in_778, in_779, in_780, in_781, in_782, in_783, in_784, in_785, in_786, in_787, in_788
  \气泡流水线  \u_气泡流水线_1  (
    .RegWrite(RegW), .MemWrite(MemW), .IF_PC(IF_PC), .ID_PC(ID_PC), .EX_PC(EX_PC), .M_PC(MEM_PC),
    .WB_PC(WB_PC), .RDin(RDinr), .MDin(MDinr), .LedData(LED));
  \单周期MIPS_单级中断  \u_单周期mips_单级中断_1  (
    .IR1(IR1), .IR2(IR2), .IR3(IR3), .RegWrite(RegW), .MemWrite(MemW), .PC(PC), .IR(IR), .RDin(RDin),
    .MDin(MDin), .LedData(LED));
  \理想流水线  \u_理想流水线_1  (
    .RegWrite(RegW), .MemWrite(MemW), .IF_PC(IF_PC), .ID_PC(ID_PC), .EX_PC(EX_PC), .M_PC(MEM_PC),
    .WB_PC(WB_PC), .RDin(RDinr), .MDin(MDinr), .LedData(LED));
  \重定向流水线  \u_重定向流水线_1  (
    .RegWrite(RegW), .MemWrite(MemW), .IF_PC(IF_PC), .ID_PC(ID_PC), .EX_PC(EX_PC), .M_PC(MEM_PC),
    .WB_PC(WB_PC), .RDin(RDinr), .MDin(MDinr), .LedData(LED));
  \单周期MIPS_多级中断  \u_单周期mips_多级中断_1  (
    .IR1(IR1), .IR2(IR2), .IR3(IR3), .RegWrite(RegW), .MemWrite(MemW), .PC(PC), .IR(IR), .RDin(RDin),
    .MDin(MDin), .LedData(LED));

  // Notes on the sheet:
  //   单周期封装测试
  //   气泡流水封装测试
  //   单周期+单级中断封装测试
  //   请检查上面封装有无位宽不匹配，引脚标签是否和连接的标签相对应，否则无法在educoder平台上正确测试
  //   理想流水封装测试
  //   重定向流水封装测试
  //   单周期+多级中断封装测试
endmodule

module \理想ID_EX  (
  input  RegDst_in,
  input  Beq_in,
  input  [31:0] IR_in,
  input  Syscall_in,
  input  Bne_in,
  input  [31:0] PC_in,
  input  JMP_in,
  input  MemToReg_in,
  input  [31:0] A_in,
  input  JR_in,
  input  [3:0] AluOP_in,
  input  SignedExt_in,
  input  AluSrcB_in,
  input  [31:0] B_in,
  input  SLLV_in,
  input  RegWrite_in,
  input  [31:0] Imm_in,
  input  SRAV_in,
  input  JAL_in,
  input  LBU_in,
  input  [4:0] Shamt,
  input  MemWrite,
  input  BGEZ_in,
  input  CLK,
  input  CLR,
  input  Stall,
  output RegDst_out,
  output Beq_out,
  output [31:0] IR_out,
  output Syscall_out,
  output Bne_out,
  output [31:0] PC_out,
  output JMP_out,
  output MemToReg_out,
  output [31:0] A_out,
  output JR_out,
  output [3:0] AluOP_out,
  output SignedExt_out,
  output AluSrcB_out,
  output [31:0] B_out,
  output SLLV_out,
  output RegWrite_out,
  output [31:0] Imm_out,
  output SRAV_out,
  output JAL_out,
  output LBU_out,
  output [4:0] Shamt_2,
  output MemWrite_2,
  output BGEZ_out
);

  wire multiplexer_1_out, multiplexer_2_out, multiplexer_3_out, multiplexer_4_out, multiplexer_5_out,
       multiplexer_6_out, multiplexer_7_out, multiplexer_8_out, multiplexer_9_out, multiplexer_10_out,
       multiplexer_11_out, multiplexer_12_out, multiplexer_14_out, multiplexer_15_out, multiplexer_16_out,
       multiplexer_17_out, pull_resistor_2_node;
  wire [3:0] multiplexer_13_out;
  wire [4:0] multiplexer_23_out;
  wire [31:0] multiplexer_18_out, multiplexer_19_out, multiplexer_20_out, multiplexer_21_out,
       multiplexer_22_out;

  Pull_Resistor #(.pull(0)) pull_resistor_1 (.node(CLR));
  Multiplexer #(.select(1), .width(1), .disabled("Z"), .enable("false")) multiplexer_1 (
    .in0(RegDst_in), .in1(1'b0), .out(multiplexer_1_out), .sel(CLR));
  Multiplexer #(.select(1), .width(1), .disabled("Z"), .enable("false")) multiplexer_2 (
    .in0(Syscall_in), .in1(1'b0), .out(multiplexer_2_out), .sel(CLR));
  Multiplexer #(.select(1), .width(1), .disabled("Z"), .enable("false")) multiplexer_3 (
    .in0(JMP_in), .in1(1'b0), .out(multiplexer_3_out), .sel(CLR));
  Multiplexer #(.select(1), .width(1), .disabled("Z"), .enable("false")) multiplexer_4 (
    .in0(JR_in), .in1(1'b0), .out(multiplexer_4_out), .sel(CLR));
  Multiplexer #(.select(1), .width(1), .disabled("Z"), .enable("false")) multiplexer_5 (
    .in0(SignedExt_in), .in1(1'b0), .out(multiplexer_5_out), .sel(CLR));
  Multiplexer #(.select(1), .width(1), .disabled("Z"), .enable("false")) multiplexer_6 (
    .in0(SLLV_in), .in1(1'b0), .out(multiplexer_6_out), .sel(CLR));
  Multiplexer #(.select(1), .width(1), .disabled("Z"), .enable("false")) multiplexer_7 (
    .in0(SRAV_in), .in1(1'b0), .out(multiplexer_7_out), .sel(CLR));
  Multiplexer #(.select(1), .width(1), .disabled("Z"), .enable("false")) multiplexer_8 (
    .in0(LBU_in), .in1(1'b0), .out(multiplexer_8_out), .sel(CLR));
  Multiplexer #(.select(1), .width(1), .disabled("Z"), .enable("false")) multiplexer_9 (
    .in0(BGEZ_in), .in1(1'b0), .out(multiplexer_9_out), .sel(CLR));
  Register #(.width(1), .trigger("rising"), .Select("low")) register_1 (
    .D(multiplexer_1_out), .en(pull_resistor_2_node), .Q(RegDst_out), .clk(CLK));  // open: clr
  Register #(.width(1), .trigger("rising"), .Select("low")) register_2 (
    .D(multiplexer_2_out), .en(pull_resistor_2_node), .Q(Syscall_out), .clk(CLK));  // open: clr
  Register #(.width(1), .trigger("rising"), .Select("low")) register_3 (
    .D(multiplexer_3_out), .en(pull_resistor_2_node), .Q(JMP_out), .clk(CLK));  // open: clr
  Register #(.width(1), .trigger("rising"), .Select("low")) register_4 (
    .D(multiplexer_4_out), .en(pull_resistor_2_node), .Q(JR_out), .clk(CLK));  // open: clr
  Register #(.width(1), .trigger("rising"), .Select("low")) register_5 (
    .D(multiplexer_5_out), .en(pull_resistor_2_node), .Q(SignedExt_out), .clk(CLK));  // open: clr
  Register #(.width(1), .trigger("rising"), .Select("low")) register_6 (
    .D(multiplexer_6_out), .en(pull_resistor_2_node), .Q(SLLV_out), .clk(CLK));  // open: clr
  Register #(.width(1), .trigger("rising"), .Select("low")) register_7 (
    .D(multiplexer_7_out), .en(pull_resistor_2_node), .Q(SRAV_out), .clk(CLK));  // open: clr
  Register #(.width(1), .trigger("rising"), .Select("low")) register_8 (
    .D(multiplexer_8_out), .en(pull_resistor_2_node), .Q(LBU_out), .clk(CLK));  // open: clr
  Register #(.width(1), .trigger("rising"), .Select("low")) register_9 (
    .D(multiplexer_9_out), .en(pull_resistor_2_node), .Q(BGEZ_out), .clk(CLK));  // open: clr
  Pull_Resistor #(.pull(0)) pull_resistor_2 (.node(pull_resistor_2_node));
  not not_1 (pull_resistor_2_node, Stall);
  Multiplexer #(.select(1), .width(1), .disabled("Z"), .enable("false")) multiplexer_10 (
    .in0(Beq_in), .in1(1'b0), .out(multiplexer_10_out), .sel(CLR));
  Multiplexer #(.select(1), .width(1), .disabled("Z"), .enable("false")) multiplexer_11 (
    .in0(Bne_in), .in1(1'b0), .out(multiplexer_11_out), .sel(CLR));
  Multiplexer #(.select(1), .width(1), .disabled("Z"), .enable("false")) multiplexer_12 (
    .in0(MemToReg_in), .in1(1'b0), .out(multiplexer_12_out), .sel(CLR));
  Multiplexer #(.select(1), .width(4), .disabled("Z"), .enable("false")) multiplexer_13 (
    .in0(AluOP_in), .in1(4'b0000), .out(multiplexer_13_out), .sel(CLR));
  Multiplexer #(.select(1), .width(1), .disabled("Z"), .enable("false")) multiplexer_14 (
    .in0(AluSrcB_in), .in1(1'b0), .out(multiplexer_14_out), .sel(CLR));
  Multiplexer #(.select(1), .width(1), .disabled("Z"), .enable("false")) multiplexer_15 (
    .in0(RegWrite_in), .in1(1'b0), .out(multiplexer_15_out), .sel(CLR));
  Multiplexer #(.select(1), .width(1), .disabled("Z"), .enable("false")) multiplexer_16 (
    .in0(JAL_in), .in1(1'b0), .out(multiplexer_16_out), .sel(CLR));
  Multiplexer #(.select(1), .width(1), .disabled("Z"), .enable("false")) multiplexer_17 (
    .in0(MemWrite), .in1(1'b0), .out(multiplexer_17_out), .sel(CLR));
  Register #(.width(1), .trigger("rising"), .Select("low")) register_10 (
    .D(multiplexer_10_out), .en(pull_resistor_2_node), .Q(Beq_out), .clk(CLK));  // open: clr
  Register #(.width(1), .trigger("rising"), .Select("low")) register_11 (
    .D(multiplexer_11_out), .en(pull_resistor_2_node), .Q(Bne_out), .clk(CLK));  // open: clr
  Register #(.width(1), .trigger("rising"), .Select("low")) register_12 (
    .D(multiplexer_12_out), .en(pull_resistor_2_node), .Q(MemToReg_out), .clk(CLK));  // open: clr
  Register #(.width(4), .trigger("rising"), .Select("low")) register_13 (
    .D(multiplexer_13_out), .en(pull_resistor_2_node), .Q(AluOP_out), .clk(CLK));  // open: clr
  Register #(.width(1), .trigger("rising"), .Select("low")) register_14 (
    .D(multiplexer_14_out), .en(pull_resistor_2_node), .Q(AluSrcB_out), .clk(CLK));  // open: clr
  Register #(.width(1), .trigger("rising"), .Select("low")) register_15 (
    .D(multiplexer_15_out), .en(pull_resistor_2_node), .Q(RegWrite_out), .clk(CLK));  // open: clr
  Register #(.width(1), .trigger("rising"), .Select("low")) register_16 (
    .D(multiplexer_16_out), .en(pull_resistor_2_node), .Q(JAL_out), .clk(CLK));  // open: clr
  Register #(.width(1), .trigger("rising"), .Select("low")) register_17 (
    .D(multiplexer_17_out), .en(pull_resistor_2_node), .Q(MemWrite_2), .clk(CLK));  // open: clr
  Multiplexer #(.select(1), .width(32), .disabled("Z"), .enable("false")) multiplexer_18 (
    .in0(IR_in), .in1({32{1'b0}}), .out(multiplexer_18_out), .sel(CLR));
  Multiplexer #(.select(1), .width(32), .disabled("Z"), .enable("false")) multiplexer_19 (
    .in0(PC_in), .in1({32{1'b0}}), .out(multiplexer_19_out), .sel(CLR));
  Multiplexer #(.select(1), .width(32), .disabled("Z"), .enable("false")) multiplexer_20 (
    .in0(A_in), .in1({32{1'b0}}), .out(multiplexer_20_out), .sel(CLR));
  Multiplexer #(.select(1), .width(32), .disabled("Z"), .enable("false")) multiplexer_21 (
    .in0(B_in), .in1({32{1'b0}}), .out(multiplexer_21_out), .sel(CLR));
  Multiplexer #(.select(1), .width(32), .disabled("Z"), .enable("false")) multiplexer_22 (
    .in0(Imm_in), .in1({32{1'b0}}), .out(multiplexer_22_out), .sel(CLR));
  Multiplexer #(.select(1), .width(5), .disabled("Z"), .enable("false")) multiplexer_23 (
    .in0(Shamt), .in1({5{1'b0}}), .out(multiplexer_23_out), .sel(CLR));
  Register #(.width(32), .trigger("rising"), .Select("low")) register_18 (
    .D(multiplexer_18_out), .en(pull_resistor_2_node), .Q(IR_out), .clk(CLK));  // open: clr
  Register #(.width(32), .trigger("rising"), .Select("low")) register_19 (
    .D(multiplexer_19_out), .en(pull_resistor_2_node), .Q(PC_out), .clk(CLK));  // open: clr
  Register #(.width(32), .trigger("rising"), .Select("low")) register_20 (
    .D(multiplexer_20_out), .en(pull_resistor_2_node), .Q(A_out), .clk(CLK));  // open: clr
  Register #(.width(32), .trigger("rising"), .Select("low")) register_21 (
    .D(multiplexer_21_out), .en(pull_resistor_2_node), .Q(B_out), .clk(CLK));  // open: clr
  Register #(.width(32), .trigger("rising"), .Select("low")) register_22 (
    .D(multiplexer_22_out), .en(pull_resistor_2_node), .Q(Imm_out), .clk(CLK));  // open: clr
  Register #(.width(5), .trigger("rising"), .Select("low")) register_23 (
    .D(multiplexer_23_out), .en(pull_resistor_2_node), .Q(Shamt_2), .clk(CLK));  // open: clr
endmodule

module \理想EX_MEM  (
  input  RegDst_in,
  input  Beq_in,
  input  [31:0] IR_in,
  input  Syscall_in,
  input  Bne_in,
  input  [31:0] PC_in,
  input  JMP_in,
  input  MemToReg_in,
  input  [31:0] A_in,
  input  JR_in,
  input  [31:0] ALU,
  input  SignedExt_in,
  input  AluSrcB_in,
  input  [31:0] B_in,
  input  SLLV_in,
  input  RegWrite_in,
  input  [31:0] Imm_in,
  input  SRAV_in,
  input  JAL_in,
  input  LBU_in,
  input  [4:0] Shamt,
  input  MemWrite,
  input  BGEZ_in,
  input  CLK,
  input  CLR,
  input  Stall,
  output RegDst_out,
  output Beq_out,
  output [31:0] IR_out,
  output Syscall_out,
  output Bne_out,
  output [31:0] PC_out,
  output JMP_out,
  output MemToReg_out,
  output [31:0] A_in_2,
  output JR_out,
  output [31:0] ALU_2,
  output SignedExt_out,
  output AluSrcB_out,
  output [31:0] B_out,
  output SLLV_out,
  output RegWrite_out,
  output [31:0] Imm_out,
  output SRAV_out,
  output JAL_out,
  output LBU_out,
  output [4:0] Shamt_2,
  output MemWrite_2,
  output BGEZ_out
);

  wire multiplexer_1_out, multiplexer_2_out, multiplexer_3_out, multiplexer_4_out, multiplexer_5_out,
       multiplexer_6_out, multiplexer_7_out, multiplexer_8_out, multiplexer_9_out, multiplexer_10_out,
       multiplexer_11_out, multiplexer_12_out, multiplexer_14_out, multiplexer_15_out, multiplexer_16_out,
       multiplexer_17_out, pull_resistor_2_node;
  wire [4:0] multiplexer_23_out;
  wire [31:0] multiplexer_13_out, multiplexer_18_out, multiplexer_19_out, multiplexer_20_out,
       multiplexer_21_out, multiplexer_22_out;

  Pull_Resistor #(.pull(0)) pull_resistor_1 (.node(CLR));
  Multiplexer #(.select(1), .width(1), .disabled("Z"), .enable("false")) multiplexer_1 (
    .in0(RegDst_in), .in1(1'b0), .out(multiplexer_1_out), .sel(CLR));
  Multiplexer #(.select(1), .width(1), .disabled("Z"), .enable("false")) multiplexer_2 (
    .in0(Syscall_in), .in1(1'b0), .out(multiplexer_2_out), .sel(CLR));
  Multiplexer #(.select(1), .width(1), .disabled("Z"), .enable("false")) multiplexer_3 (
    .in0(JMP_in), .in1(1'b0), .out(multiplexer_3_out), .sel(CLR));
  Multiplexer #(.select(1), .width(1), .disabled("Z"), .enable("false")) multiplexer_4 (
    .in0(JR_in), .in1(1'b0), .out(multiplexer_4_out), .sel(CLR));
  Multiplexer #(.select(1), .width(1), .disabled("Z"), .enable("false")) multiplexer_5 (
    .in0(SignedExt_in), .in1(1'b0), .out(multiplexer_5_out), .sel(CLR));
  Multiplexer #(.select(1), .width(1), .disabled("Z"), .enable("false")) multiplexer_6 (
    .in0(SLLV_in), .in1(1'b0), .out(multiplexer_6_out), .sel(CLR));
  Multiplexer #(.select(1), .width(1), .disabled("Z"), .enable("false")) multiplexer_7 (
    .in0(SRAV_in), .in1(1'b0), .out(multiplexer_7_out), .sel(CLR));
  Multiplexer #(.select(1), .width(1), .disabled("Z"), .enable("false")) multiplexer_8 (
    .in0(LBU_in), .in1(1'b0), .out(multiplexer_8_out), .sel(CLR));
  Multiplexer #(.select(1), .width(1), .disabled("Z"), .enable("false")) multiplexer_9 (
    .in0(BGEZ_in), .in1(1'b0), .out(multiplexer_9_out), .sel(CLR));
  Register #(.width(1), .trigger("rising"), .Select("low")) register_1 (
    .D(multiplexer_1_out), .en(pull_resistor_2_node), .Q(RegDst_out), .clk(CLK));  // open: clr
  Register #(.width(1), .trigger("rising"), .Select("low")) register_2 (
    .D(multiplexer_2_out), .en(pull_resistor_2_node), .Q(Syscall_out), .clk(CLK));  // open: clr
  Register #(.width(1), .trigger("rising"), .Select("low")) register_3 (
    .D(multiplexer_3_out), .en(pull_resistor_2_node), .Q(JMP_out), .clk(CLK));  // open: clr
  Register #(.width(1), .trigger("rising"), .Select("low")) register_4 (
    .D(multiplexer_4_out), .en(pull_resistor_2_node), .Q(JR_out), .clk(CLK));  // open: clr
  Register #(.width(1), .trigger("rising"), .Select("low")) register_5 (
    .D(multiplexer_5_out), .en(pull_resistor_2_node), .Q(SignedExt_out), .clk(CLK));  // open: clr
  Register #(.width(1), .trigger("rising"), .Select("low")) register_6 (
    .D(multiplexer_6_out), .en(pull_resistor_2_node), .Q(SLLV_out), .clk(CLK));  // open: clr
  Register #(.width(1), .trigger("rising"), .Select("low")) register_7 (
    .D(multiplexer_7_out), .en(pull_resistor_2_node), .Q(SRAV_out), .clk(CLK));  // open: clr
  Register #(.width(1), .trigger("rising"), .Select("low")) register_8 (
    .D(multiplexer_8_out), .en(pull_resistor_2_node), .Q(LBU_out), .clk(CLK));  // open: clr
  Register #(.width(1), .trigger("rising"), .Select("low")) register_9 (
    .D(multiplexer_9_out), .en(pull_resistor_2_node), .Q(BGEZ_out), .clk(CLK));  // open: clr
  Pull_Resistor #(.pull(0)) pull_resistor_2 (.node(pull_resistor_2_node));
  not not_1 (pull_resistor_2_node, Stall);
  Multiplexer #(.select(1), .width(1), .disabled("Z"), .enable("false")) multiplexer_10 (
    .in0(Beq_in), .in1(1'b0), .out(multiplexer_10_out), .sel(CLR));
  Multiplexer #(.select(1), .width(1), .disabled("Z"), .enable("false")) multiplexer_11 (
    .in0(Bne_in), .in1(1'b0), .out(multiplexer_11_out), .sel(CLR));
  Multiplexer #(.select(1), .width(1), .disabled("Z"), .enable("false")) multiplexer_12 (
    .in0(MemToReg_in), .in1(1'b0), .out(multiplexer_12_out), .sel(CLR));
  Multiplexer #(.select(1), .width(32), .disabled("Z"), .enable("false")) multiplexer_13 (
    .in0(ALU), .in1({32{1'b0}}), .out(multiplexer_13_out), .sel(CLR));
  Multiplexer #(.select(1), .width(1), .disabled("Z"), .enable("false")) multiplexer_14 (
    .in0(AluSrcB_in), .in1(1'b0), .out(multiplexer_14_out), .sel(CLR));
  Multiplexer #(.select(1), .width(1), .disabled("Z"), .enable("false")) multiplexer_15 (
    .in0(RegWrite_in), .in1(1'b0), .out(multiplexer_15_out), .sel(CLR));
  Multiplexer #(.select(1), .width(1), .disabled("Z"), .enable("false")) multiplexer_16 (
    .in0(JAL_in), .in1(1'b0), .out(multiplexer_16_out), .sel(CLR));
  Multiplexer #(.select(1), .width(1), .disabled("Z"), .enable("false")) multiplexer_17 (
    .in0(MemWrite), .in1(1'b0), .out(multiplexer_17_out), .sel(CLR));
  Register #(.width(1), .trigger("rising"), .Select("low")) register_10 (
    .D(multiplexer_10_out), .en(pull_resistor_2_node), .Q(Beq_out), .clk(CLK));  // open: clr
  Register #(.width(1), .trigger("rising"), .Select("low")) register_11 (
    .D(multiplexer_11_out), .en(pull_resistor_2_node), .Q(Bne_out), .clk(CLK));  // open: clr
  Register #(.width(1), .trigger("rising"), .Select("low")) register_12 (
    .D(multiplexer_12_out), .en(pull_resistor_2_node), .Q(MemToReg_out), .clk(CLK));  // open: clr
  Register #(.width(32), .trigger("rising"), .Select("low")) register_13 (
    .D(multiplexer_13_out), .en(pull_resistor_2_node), .Q(ALU_2), .clk(CLK));  // open: clr
  Register #(.width(1), .trigger("rising"), .Select("low")) register_14 (
    .D(multiplexer_14_out), .en(pull_resistor_2_node), .Q(AluSrcB_out), .clk(CLK));  // open: clr
  Register #(.width(1), .trigger("rising"), .Select("low")) register_15 (
    .D(multiplexer_15_out), .en(pull_resistor_2_node), .Q(RegWrite_out), .clk(CLK));  // open: clr
  Register #(.width(1), .trigger("rising"), .Select("low")) register_16 (
    .D(multiplexer_16_out), .en(pull_resistor_2_node), .Q(JAL_out), .clk(CLK));  // open: clr
  Register #(.width(1), .trigger("rising"), .Select("low")) register_17 (
    .D(multiplexer_17_out), .en(pull_resistor_2_node), .Q(MemWrite_2), .clk(CLK));  // open: clr
  Multiplexer #(.select(1), .width(32), .disabled("Z"), .enable("false")) multiplexer_18 (
    .in0(IR_in), .in1({32{1'b0}}), .out(multiplexer_18_out), .sel(CLR));
  Multiplexer #(.select(1), .width(32), .disabled("Z"), .enable("false")) multiplexer_19 (
    .in0(PC_in), .in1({32{1'b0}}), .out(multiplexer_19_out), .sel(CLR));
  Multiplexer #(.select(1), .width(32), .disabled("Z"), .enable("false")) multiplexer_20 (
    .in0(A_in), .in1({32{1'b0}}), .out(multiplexer_20_out), .sel(CLR));
  Multiplexer #(.select(1), .width(32), .disabled("Z"), .enable("false")) multiplexer_21 (
    .in0(B_in), .in1({32{1'b0}}), .out(multiplexer_21_out), .sel(CLR));
  Multiplexer #(.select(1), .width(32), .disabled("Z"), .enable("false")) multiplexer_22 (
    .in0(Imm_in), .in1({32{1'b0}}), .out(multiplexer_22_out), .sel(CLR));
  Multiplexer #(.select(1), .width(5), .disabled("Z"), .enable("false")) multiplexer_23 (
    .in0(Shamt), .in1({5{1'b0}}), .out(multiplexer_23_out), .sel(CLR));
  Register #(.width(32), .trigger("rising"), .Select("low")) register_18 (
    .D(multiplexer_18_out), .en(pull_resistor_2_node), .Q(IR_out), .clk(CLK));  // open: clr
  Register #(.width(32), .trigger("rising"), .Select("low")) register_19 (
    .D(multiplexer_19_out), .en(pull_resistor_2_node), .Q(PC_out), .clk(CLK));  // open: clr
  Register #(.width(32), .trigger("rising"), .Select("low")) register_20 (
    .D(multiplexer_20_out), .en(pull_resistor_2_node), .Q(A_in_2), .clk(CLK));  // open: clr
  Register #(.width(32), .trigger("rising"), .Select("low")) register_21 (
    .D(multiplexer_21_out), .en(pull_resistor_2_node), .Q(B_out), .clk(CLK));  // open: clr
  Register #(.width(32), .trigger("rising"), .Select("low")) register_22 (
    .D(multiplexer_22_out), .en(pull_resistor_2_node), .Q(Imm_out), .clk(CLK));  // open: clr
  Register #(.width(5), .trigger("rising"), .Select("low")) register_23 (
    .D(multiplexer_23_out), .en(pull_resistor_2_node), .Q(Shamt_2), .clk(CLK));  // open: clr
endmodule

module \理想MEM_WB  (
  input  RegDst_in,
  input  Beq_in,
  input  [31:0] IR_in,
  input  Syscall_in,
  input  Bne_in,
  input  [31:0] PC_in,
  input  JMP_in,
  input  MemToReg_in,
  input  [31:0] A_in,
  input  JR_in,
  input  [31:0] ALU,
  input  SignedExt_in,
  input  AluSrcB_in,
  input  [31:0] B_in,
  input  SLLV_in,
  input  RegWrite_in,
  input  [31:0] Imm_in,
  input  SRAV_in,
  input  JAL_in,
  input  LBU_in,
  input  [31:0] MD,
  input  MemWrite,
  input  BGEZ_in,
  input  CLK,
  input  CLR,
  input  Stall,
  output RegDst_out,
  output Beq_out,
  output [31:0] IR_out,
  output Syscall_out,
  output Bne_out,
  output [31:0] PC_out,
  output JMP_out,
  output MemToReg_out,
  output [31:0] A_out,
  output JR_out,
  output [31:0] ALU_2,
  output SignedExt_out,
  output AluSrcB_out,
  output [31:0] B_out,
  output SLLV_out,
  output RegWrite_out,
  output [31:0] Imm_out,
  output SRAV_out,
  output JAL_out,
  output LBU_out,
  output [31:0] MD_2,
  output MemWrite_2,
  output BGEZ_out
);

  wire multiplexer_1_out, multiplexer_2_out, multiplexer_3_out, multiplexer_4_out, multiplexer_5_out,
       multiplexer_6_out, multiplexer_7_out, multiplexer_8_out, multiplexer_9_out, multiplexer_10_out,
       multiplexer_11_out, multiplexer_12_out, multiplexer_14_out, multiplexer_15_out, multiplexer_16_out,
       multiplexer_17_out, pull_resistor_2_node;
  wire [31:0] multiplexer_13_out, multiplexer_18_out, multiplexer_19_out, multiplexer_20_out,
       multiplexer_21_out, multiplexer_22_out, multiplexer_23_out;

  Pull_Resistor #(.pull(0)) pull_resistor_1 (.node(CLR));
  Multiplexer #(.select(1), .width(1), .disabled("Z"), .enable("false")) multiplexer_1 (
    .in0(RegDst_in), .in1(1'b0), .out(multiplexer_1_out), .sel(CLR));
  Multiplexer #(.select(1), .width(1), .disabled("Z"), .enable("false")) multiplexer_2 (
    .in0(Syscall_in), .in1(1'b0), .out(multiplexer_2_out), .sel(CLR));
  Multiplexer #(.select(1), .width(1), .disabled("Z"), .enable("false")) multiplexer_3 (
    .in0(JMP_in), .in1(1'b0), .out(multiplexer_3_out), .sel(CLR));
  Multiplexer #(.select(1), .width(1), .disabled("Z"), .enable("false")) multiplexer_4 (
    .in0(JR_in), .in1(1'b0), .out(multiplexer_4_out), .sel(CLR));
  Multiplexer #(.select(1), .width(1), .disabled("Z"), .enable("false")) multiplexer_5 (
    .in0(SignedExt_in), .in1(1'b0), .out(multiplexer_5_out), .sel(CLR));
  Multiplexer #(.select(1), .width(1), .disabled("Z"), .enable("false")) multiplexer_6 (
    .in0(SLLV_in), .in1(1'b0), .out(multiplexer_6_out), .sel(CLR));
  Multiplexer #(.select(1), .width(1), .disabled("Z"), .enable("false")) multiplexer_7 (
    .in0(SRAV_in), .in1(1'b0), .out(multiplexer_7_out), .sel(CLR));
  Multiplexer #(.select(1), .width(1), .disabled("Z"), .enable("false")) multiplexer_8 (
    .in0(LBU_in), .in1(1'b0), .out(multiplexer_8_out), .sel(CLR));
  Multiplexer #(.select(1), .width(1), .disabled("Z"), .enable("false")) multiplexer_9 (
    .in0(BGEZ_in), .in1(1'b0), .out(multiplexer_9_out), .sel(CLR));
  Register #(.width(1), .trigger("rising"), .Select("low")) register_1 (
    .D(multiplexer_1_out), .en(pull_resistor_2_node), .Q(RegDst_out), .clk(CLK));  // open: clr
  Register #(.width(1), .trigger("rising"), .Select("low")) register_2 (
    .D(multiplexer_2_out), .en(pull_resistor_2_node), .Q(Syscall_out), .clk(CLK));  // open: clr
  Register #(.width(1), .trigger("rising"), .Select("low")) register_3 (
    .D(multiplexer_3_out), .en(pull_resistor_2_node), .Q(JMP_out), .clk(CLK));  // open: clr
  Register #(.width(1), .trigger("rising"), .Select("low")) register_4 (
    .D(multiplexer_4_out), .en(pull_resistor_2_node), .Q(JR_out), .clk(CLK));  // open: clr
  Register #(.width(1), .trigger("rising"), .Select("low")) register_5 (
    .D(multiplexer_5_out), .en(pull_resistor_2_node), .Q(SignedExt_out), .clk(CLK));  // open: clr
  Register #(.width(1), .trigger("rising"), .Select("low")) register_6 (
    .D(multiplexer_6_out), .en(pull_resistor_2_node), .Q(SLLV_out), .clk(CLK));  // open: clr
  Register #(.width(1), .trigger("rising"), .Select("low")) register_7 (
    .D(multiplexer_7_out), .en(pull_resistor_2_node), .Q(SRAV_out), .clk(CLK));  // open: clr
  Register #(.width(1), .trigger("rising"), .Select("low")) register_8 (
    .D(multiplexer_8_out), .en(pull_resistor_2_node), .Q(LBU_out), .clk(CLK));  // open: clr
  Register #(.width(1), .trigger("rising"), .Select("low")) register_9 (
    .D(multiplexer_9_out), .en(pull_resistor_2_node), .Q(BGEZ_out), .clk(CLK));  // open: clr
  Pull_Resistor #(.pull(0)) pull_resistor_2 (.node(pull_resistor_2_node));
  not not_1 (pull_resistor_2_node, Stall);
  Multiplexer #(.select(1), .width(1), .disabled("Z"), .enable("false")) multiplexer_10 (
    .in0(Beq_in), .in1(1'b0), .out(multiplexer_10_out), .sel(CLR));
  Multiplexer #(.select(1), .width(1), .disabled("Z"), .enable("false")) multiplexer_11 (
    .in0(Bne_in), .in1(1'b0), .out(multiplexer_11_out), .sel(CLR));
  Multiplexer #(.select(1), .width(1), .disabled("Z"), .enable("false")) multiplexer_12 (
    .in0(MemToReg_in), .in1(1'b0), .out(multiplexer_12_out), .sel(CLR));
  Multiplexer #(.select(1), .width(32), .disabled("Z"), .enable("false")) multiplexer_13 (
    .in0(ALU), .in1({32{1'b0}}), .out(multiplexer_13_out), .sel(CLR));
  Multiplexer #(.select(1), .width(1), .disabled("Z"), .enable("false")) multiplexer_14 (
    .in0(AluSrcB_in), .in1(1'b0), .out(multiplexer_14_out), .sel(CLR));
  Multiplexer #(.select(1), .width(1), .disabled("Z"), .enable("false")) multiplexer_15 (
    .in0(RegWrite_in), .in1(1'b0), .out(multiplexer_15_out), .sel(CLR));
  Multiplexer #(.select(1), .width(1), .disabled("Z"), .enable("false")) multiplexer_16 (
    .in0(JAL_in), .in1(1'b0), .out(multiplexer_16_out), .sel(CLR));
  Multiplexer #(.select(1), .width(1), .disabled("Z"), .enable("false")) multiplexer_17 (
    .in0(MemWrite), .in1(1'b0), .out(multiplexer_17_out), .sel(CLR));
  Register #(.width(1), .trigger("rising"), .Select("low")) register_10 (
    .D(multiplexer_10_out), .en(pull_resistor_2_node), .Q(Beq_out), .clk(CLK));  // open: clr
  Register #(.width(1), .trigger("rising"), .Select("low")) register_11 (
    .D(multiplexer_11_out), .en(pull_resistor_2_node), .Q(Bne_out), .clk(CLK));  // open: clr
  Register #(.width(1), .trigger("rising"), .Select("low")) register_12 (
    .D(multiplexer_12_out), .en(pull_resistor_2_node), .Q(MemToReg_out), .clk(CLK));  // open: clr
  Register #(.width(32), .trigger("rising"), .Select("low")) register_13 (
    .D(multiplexer_13_out), .en(pull_resistor_2_node), .Q(ALU_2), .clk(CLK));  // open: clr
  Register #(.width(1), .trigger("rising"), .Select("low")) register_14 (
    .D(multiplexer_14_out), .en(pull_resistor_2_node), .Q(AluSrcB_out), .clk(CLK));  // open: clr
  Register #(.width(1), .trigger("rising"), .Select("low")) register_15 (
    .D(multiplexer_15_out), .en(pull_resistor_2_node), .Q(RegWrite_out), .clk(CLK));  // open: clr
  Register #(.width(1), .trigger("rising"), .Select("low")) register_16 (
    .D(multiplexer_16_out), .en(pull_resistor_2_node), .Q(JAL_out), .clk(CLK));  // open: clr
  Register #(.width(1), .trigger("rising"), .Select("low")) register_17 (
    .D(multiplexer_17_out), .en(pull_resistor_2_node), .Q(MemWrite_2), .clk(CLK));  // open: clr
  Multiplexer #(.select(1), .width(32), .disabled("Z"), .enable("false")) multiplexer_18 (
    .in0(IR_in), .in1({32{1'b0}}), .out(multiplexer_18_out), .sel(CLR));
  Multiplexer #(.select(1), .width(32), .disabled("Z"), .enable("false")) multiplexer_19 (
    .in0(PC_in), .in1({32{1'b0}}), .out(multiplexer_19_out), .sel(CLR));
  Multiplexer #(.select(1), .width(32), .disabled("Z"), .enable("false")) multiplexer_20 (
    .in0(A_in), .in1({32{1'b0}}), .out(multiplexer_20_out), .sel(CLR));
  Multiplexer #(.select(1), .width(32), .disabled("Z"), .enable("false")) multiplexer_21 (
    .in0(B_in), .in1({32{1'b0}}), .out(multiplexer_21_out), .sel(CLR));
  Multiplexer #(.select(1), .width(32), .disabled("Z"), .enable("false")) multiplexer_22 (
    .in0(Imm_in), .in1({32{1'b0}}), .out(multiplexer_22_out), .sel(CLR));
  Multiplexer #(.select(1), .width(32), .disabled("Z"), .enable("false")) multiplexer_23 (
    .in0(MD), .in1({32{1'b0}}), .out(multiplexer_23_out), .sel(CLR));
  Register #(.width(32), .trigger("rising"), .Select("low")) register_18 (
    .D(multiplexer_18_out), .en(pull_resistor_2_node), .Q(IR_out), .clk(CLK));  // open: clr
  Register #(.width(32), .trigger("rising"), .Select("low")) register_19 (
    .D(multiplexer_19_out), .en(pull_resistor_2_node), .Q(PC_out), .clk(CLK));  // open: clr
  Register #(.width(32), .trigger("rising"), .Select("low")) register_20 (
    .D(multiplexer_20_out), .en(pull_resistor_2_node), .Q(A_out), .clk(CLK));  // open: clr
  Register #(.width(32), .trigger("rising"), .Select("low")) register_21 (
    .D(multiplexer_21_out), .en(pull_resistor_2_node), .Q(B_out), .clk(CLK));  // open: clr
  Register #(.width(32), .trigger("rising"), .Select("low")) register_22 (
    .D(multiplexer_22_out), .en(pull_resistor_2_node), .Q(Imm_out), .clk(CLK));  // open: clr
  Register #(.width(32), .trigger("rising"), .Select("low")) register_23 (
    .D(multiplexer_23_out), .en(pull_resistor_2_node), .Q(MD_2), .clk(CLK));  // open: clr
endmodule
module \理想IF_ID  (
  input  RegDst_in,
  input  Beq_in,
  input  [31:0] IR_in,
  input  Syscall_in,
  input  Bne_in,
  input  [31:0] PC_in,
  input  JMP_in,
  input  MemToReg_in,
  input  [31:0] A_in,
  input  JR_in,
  input  [3:0] AluOP_in,
  input  SignedExt_in,
  input  AluSrcB_in,
  input  [31:0] B_in,
  input  SLLV_in,
  input  RegWrite_in,
  input  [31:0] Imm_in,
  input  SRAV_in,
  input  JAL_in,
  input  LBU_in,
  input  [4:0] Shamt,
  input  MemWrite,
  input  BGEZ_in,
  input  CLK,
  input  CLR,
  input  Stall,
  output RegDst_out,
  output Beq_out,
  output [31:0] IR_out,
  output Syscall_out,
  output Bne_out,
  output [31:0] PC_out,
  output JMP_out,
  output MemToReg_out,
  output [31:0] A_out,
  output JR_out,
  output [3:0] AluOP_out,
  output SignedExt_out,
  output AluSrcB_out,
  output [31:0] B_out,
  output SLLV_out,
  output RegWrite_out,
  output [31:0] Imm_out,
  output SRAV_out,
  output JAL_out,
  output LBU_out,
  output [4:0] Shamt_2,
  output MemWrite_2,
  output BGEZ_out
);

  wire multiplexer_1_out, multiplexer_2_out, multiplexer_3_out, multiplexer_4_out, multiplexer_5_out,
       multiplexer_6_out, multiplexer_7_out, multiplexer_8_out, multiplexer_9_out, multiplexer_10_out,
       multiplexer_11_out, multiplexer_12_out, multiplexer_14_out, multiplexer_15_out, multiplexer_16_out,
       multiplexer_17_out, pull_resistor_2_node;
  wire [3:0] multiplexer_13_out;
  wire [4:0] multiplexer_23_out;
  wire [31:0] multiplexer_18_out, multiplexer_19_out, multiplexer_20_out, multiplexer_21_out,
       multiplexer_22_out;

  Pull_Resistor #(.pull(0)) pull_resistor_1 (.node(CLR));
  Multiplexer #(.select(1), .width(1), .disabled("Z"), .enable("false")) multiplexer_1 (
    .in0(RegDst_in), .in1(1'b0), .out(multiplexer_1_out), .sel(CLR));
  Multiplexer #(.select(1), .width(1), .disabled("Z"), .enable("false")) multiplexer_2 (
    .in0(Syscall_in), .in1(1'b0), .out(multiplexer_2_out), .sel(CLR));
  Multiplexer #(.select(1), .width(1), .disabled("Z"), .enable("false")) multiplexer_3 (
    .in0(JMP_in), .in1(1'b0), .out(multiplexer_3_out), .sel(CLR));
  Multiplexer #(.select(1), .width(1), .disabled("Z"), .enable("false")) multiplexer_4 (
    .in0(JR_in), .in1(1'b0), .out(multiplexer_4_out), .sel(CLR));
  Multiplexer #(.select(1), .width(1), .disabled("Z"), .enable("false")) multiplexer_5 (
    .in0(SignedExt_in), .in1(1'b0), .out(multiplexer_5_out), .sel(CLR));
  Multiplexer #(.select(1), .width(1), .disabled("Z"), .enable("false")) multiplexer_6 (
    .in0(SLLV_in), .in1(1'b0), .out(multiplexer_6_out), .sel(CLR));
  Multiplexer #(.select(1), .width(1), .disabled("Z"), .enable("false")) multiplexer_7 (
    .in0(SRAV_in), .in1(1'b0), .out(multiplexer_7_out), .sel(CLR));
  Multiplexer #(.select(1), .width(1), .disabled("Z"), .enable("false")) multiplexer_8 (
    .in0(LBU_in), .in1(1'b0), .out(multiplexer_8_out), .sel(CLR));
  Multiplexer #(.select(1), .width(1), .disabled("Z"), .enable("false")) multiplexer_9 (
    .in0(BGEZ_in), .in1(1'b0), .out(multiplexer_9_out), .sel(CLR));
  Register #(.width(1), .trigger("rising"), .Select("low")) register_1 (
    .D(multiplexer_1_out), .en(pull_resistor_2_node), .Q(RegDst_out), .clk(CLK));  // open: clr
  Register #(.width(1), .trigger("rising"), .Select("low")) register_2 (
    .D(multiplexer_2_out), .en(pull_resistor_2_node), .Q(Syscall_out), .clk(CLK));  // open: clr
  Register #(.width(1), .trigger("rising"), .Select("low")) register_3 (
    .D(multiplexer_3_out), .en(pull_resistor_2_node), .Q(JMP_out), .clk(CLK));  // open: clr
  Register #(.width(1), .trigger("rising"), .Select("low")) register_4 (
    .D(multiplexer_4_out), .en(pull_resistor_2_node), .Q(JR_out), .clk(CLK));  // open: clr
  Register #(.width(1), .trigger("rising"), .Select("low")) register_5 (
    .D(multiplexer_5_out), .en(pull_resistor_2_node), .Q(SignedExt_out), .clk(CLK));  // open: clr
  Register #(.width(1), .trigger("rising"), .Select("low")) register_6 (
    .D(multiplexer_6_out), .en(pull_resistor_2_node), .Q(SLLV_out), .clk(CLK));  // open: clr
  Register #(.width(1), .trigger("rising"), .Select("low")) register_7 (
    .D(multiplexer_7_out), .en(pull_resistor_2_node), .Q(SRAV_out), .clk(CLK));  // open: clr
  Register #(.width(1), .trigger("rising"), .Select("low")) register_8 (
    .D(multiplexer_8_out), .en(pull_resistor_2_node), .Q(LBU_out), .clk(CLK));  // open: clr
  Register #(.width(1), .trigger("rising"), .Select("low")) register_9 (
    .D(multiplexer_9_out), .en(pull_resistor_2_node), .Q(BGEZ_out), .clk(CLK));  // open: clr
  Pull_Resistor #(.pull(0)) pull_resistor_2 (.node(pull_resistor_2_node));
  not not_1 (pull_resistor_2_node, Stall);
  Multiplexer #(.select(1), .width(1), .disabled("Z"), .enable("false")) multiplexer_10 (
    .in0(Beq_in), .in1(1'b0), .out(multiplexer_10_out), .sel(CLR));
  Multiplexer #(.select(1), .width(1), .disabled("Z"), .enable("false")) multiplexer_11 (
    .in0(Bne_in), .in1(1'b0), .out(multiplexer_11_out), .sel(CLR));
  Multiplexer #(.select(1), .width(1), .disabled("Z"), .enable("false")) multiplexer_12 (
    .in0(MemToReg_in), .in1(1'b0), .out(multiplexer_12_out), .sel(CLR));
  Multiplexer #(.select(1), .width(4), .disabled("Z"), .enable("false")) multiplexer_13 (
    .in0(AluOP_in), .in1(4'b0000), .out(multiplexer_13_out), .sel(CLR));
  Multiplexer #(.select(1), .width(1), .disabled("Z"), .enable("false")) multiplexer_14 (
    .in0(AluSrcB_in), .in1(1'b0), .out(multiplexer_14_out), .sel(CLR));
  Multiplexer #(.select(1), .width(1), .disabled("Z"), .enable("false")) multiplexer_15 (
    .in0(RegWrite_in), .in1(1'b0), .out(multiplexer_15_out), .sel(CLR));
  Multiplexer #(.select(1), .width(1), .disabled("Z"), .enable("false")) multiplexer_16 (
    .in0(JAL_in), .in1(1'b0), .out(multiplexer_16_out), .sel(CLR));
  Multiplexer #(.select(1), .width(1), .disabled("Z"), .enable("false")) multiplexer_17 (
    .in0(MemWrite), .in1(1'b0), .out(multiplexer_17_out), .sel(CLR));
  Register #(.width(1), .trigger("rising"), .Select("low")) register_10 (
    .D(multiplexer_10_out), .en(pull_resistor_2_node), .Q(Beq_out), .clk(CLK));  // open: clr
  Register #(.width(1), .trigger("rising"), .Select("low")) register_11 (
    .D(multiplexer_11_out), .en(pull_resistor_2_node), .Q(Bne_out), .clk(CLK));  // open: clr
  Register #(.width(1), .trigger("rising"), .Select("low")) register_12 (
    .D(multiplexer_12_out), .en(pull_resistor_2_node), .Q(MemToReg_out), .clk(CLK));  // open: clr
  Register #(.width(4), .trigger("rising"), .Select("low")) register_13 (
    .D(multiplexer_13_out), .en(pull_resistor_2_node), .Q(AluOP_out), .clk(CLK));  // open: clr
  Register #(.width(1), .trigger("rising"), .Select("low")) register_14 (
    .D(multiplexer_14_out), .en(pull_resistor_2_node), .Q(AluSrcB_out), .clk(CLK));  // open: clr
  Register #(.width(1), .trigger("rising"), .Select("low")) register_15 (
    .D(multiplexer_15_out), .en(pull_resistor_2_node), .Q(RegWrite_out), .clk(CLK));  // open: clr
  Register #(.width(1), .trigger("rising"), .Select("low")) register_16 (
    .D(multiplexer_16_out), .en(pull_resistor_2_node), .Q(JAL_out), .clk(CLK));  // open: clr
  Register #(.width(1), .trigger("rising"), .Select("low")) register_17 (
    .D(multiplexer_17_out), .en(pull_resistor_2_node), .Q(MemWrite_2), .clk(CLK));  // open: clr
  Multiplexer #(.select(1), .width(32), .disabled("Z"), .enable("false")) multiplexer_18 (
    .in0(IR_in), .in1({32{1'b0}}), .out(multiplexer_18_out), .sel(CLR));
  Multiplexer #(.select(1), .width(32), .disabled("Z"), .enable("false")) multiplexer_19 (
    .in0(PC_in), .in1({32{1'b0}}), .out(multiplexer_19_out), .sel(CLR));
  Multiplexer #(.select(1), .width(32), .disabled("Z"), .enable("false")) multiplexer_20 (
    .in0(A_in), .in1({32{1'b0}}), .out(multiplexer_20_out), .sel(CLR));
  Multiplexer #(.select(1), .width(32), .disabled("Z"), .enable("false")) multiplexer_21 (
    .in0(B_in), .in1({32{1'b0}}), .out(multiplexer_21_out), .sel(CLR));
  Multiplexer #(.select(1), .width(32), .disabled("Z"), .enable("false")) multiplexer_22 (
    .in0(Imm_in), .in1({32{1'b0}}), .out(multiplexer_22_out), .sel(CLR));
  Multiplexer #(.select(1), .width(5), .disabled("Z"), .enable("false")) multiplexer_23 (
    .in0(Shamt), .in1({5{1'b0}}), .out(multiplexer_23_out), .sel(CLR));
  Register #(.width(32), .trigger("rising"), .Select("low")) register_18 (
    .D(multiplexer_18_out), .en(pull_resistor_2_node), .Q(IR_out), .clk(CLK));  // open: clr
  Register #(.width(32), .trigger("rising"), .Select("low")) register_19 (
    .D(multiplexer_19_out), .en(pull_resistor_2_node), .Q(PC_out), .clk(CLK));  // open: clr
  Register #(.width(32), .trigger("rising"), .Select("low")) register_20 (
    .D(multiplexer_20_out), .en(pull_resistor_2_node), .Q(A_out), .clk(CLK));  // open: clr
  Register #(.width(32), .trigger("rising"), .Select("low")) register_21 (
    .D(multiplexer_21_out), .en(pull_resistor_2_node), .Q(B_out), .clk(CLK));  // open: clr
  Register #(.width(32), .trigger("rising"), .Select("low")) register_22 (
    .D(multiplexer_22_out), .en(pull_resistor_2_node), .Q(Imm_out), .clk(CLK));  // open: clr
  Register #(.width(5), .trigger("rising"), .Select("low")) register_23 (
    .D(multiplexer_23_out), .en(pull_resistor_2_node), .Q(Shamt_2), .clk(CLK));  // open: clr
endmodule

module \源寄存器使用情况  (
  input  [5:0] OP,
  input  [5:0] Funct,
  output R1_Used,
  output R2_Used
);

  wire and_1_out, and_2_out, and_3_out, and_4_out, and_5_out, and_6_out, and_7_out, and_8_out, and_9_out,
       and_10_out, and_11_out, and_12_out, and_13_out, and_14_out, and_15_out, and_16_out, and_17_out,
       and_18_out, and_19_out, and_20_out, and_21_out, and_22_out, and_23_out, and_24_out, and_25_out,
       and_26_out, and_27_out, and_28_out, and_29_out, and_30_out, and_31_out, and_32_out, and_33_out,
       and_34_out, and_35_out, and_36_out, and_37_out, and_38_out, and_39_out, and_40_out, not_1_out,
       not_2_out, not_3_out, not_4_out, not_5_out, not_6_out, not_7_out, not_8_out, not_9_out, not_10_out,
       not_11_out, not_12_out, not_13_out, not_14_out, not_15_out, not_16_out, not_17_out, not_18_out,
       not_19_out, not_20_out, not_21_out, not_22_out, not_23_out, not_24_out, not_25_out, not_26_out,
       not_27_out, not_28_out, not_29_out, not_30_out, not_31_out, not_32_out, not_33_out, not_34_out,
       not_35_out, not_36_out, not_37_out, not_38_out, not_39_out, not_40_out, not_41_out, not_42_out,
       not_43_out, not_44_out, not_45_out, not_46_out, not_47_out, not_48_out, not_49_out, not_50_out,
       not_51_out, not_52_out, not_53_out, not_54_out, not_55_out, not_56_out, not_57_out, not_58_out,
       not_59_out, not_60_out, not_61_out, not_62_out, not_63_out, not_64_out, not_65_out, not_66_out,
       not_67_out, not_68_out, not_69_out, not_70_out, not_71_out, not_72_out, not_73_out, not_74_out,
       not_75_out, not_76_out, not_77_out, not_78_out, not_79_out, not_80_out, not_81_out, not_82_out,
       not_83_out, not_84_out, not_85_out, not_86_out, not_87_out, not_88_out, not_89_out, not_90_out,
       not_91_out, not_92_out, not_93_out, not_94_out, not_95_out, not_96_out, not_97_out, not_98_out,
       not_99_out, not_100_out, not_101_out, not_102_out, not_103_out, not_104_out, not_105_out, not_106_out,
       not_107_out, not_108_out, not_109_out, not_110_out, not_111_out, not_112_out, not_113_out,
       not_114_out, not_115_out, not_116_out, not_117_out, not_118_out, not_119_out, not_120_out,
       not_121_out, not_122_out, not_123_out, not_124_out, not_125_out, not_126_out, not_127_out,
       not_128_out, not_129_out, not_130_out, not_131_out, not_132_out, not_133_out, not_134_out,
       not_135_out, not_136_out, not_137_out, not_138_out, not_139_out, not_140_out, not_141_out,
       not_142_out, not_143_out, not_144_out, not_145_out, not_146_out, not_147_out, not_148_out,
       not_149_out, not_150_out, not_151_out, not_152_out, not_153_out, not_154_out, not_155_out,
       not_156_out, not_157_out, not_158_out, not_159_out, not_160_out, not_161_out, not_162_out,
       not_163_out, not_164_out, not_165_out, not_166_out, not_167_out, not_168_out, not_169_out,
       not_170_out, not_171_out, not_172_out, not_173_out, not_174_out, not_175_out, not_176_out,
       not_177_out, not_178_out, not_179_out, not_180_out, not_181_out, not_182_out, not_183_out,
       not_184_out, not_185_out, not_186_out, not_187_out, not_188_out, not_189_out, not_190_out,
       not_191_out, not_192_out, not_193_out, not_194_out, not_195_out, not_196_out, not_197_out,
       not_198_out, not_199_out, not_200_out, not_201_out, not_202_out, not_203_out, not_204_out,
       not_205_out, not_206_out, not_207_out, not_208_out, not_209_out, not_210_out, not_211_out,
       not_212_out, not_213_out, not_214_out, not_215_out, not_216_out, not_217_out, not_218_out,
       not_219_out, not_220_out, not_221_out, not_222_out, not_223_out, not_224_out, not_225_out,
       not_226_out, not_227_out, not_228_out, not_229_out, not_230_out, not_231_out, not_232_out,
       not_233_out, not_234_out, not_235_out, not_236_out, not_237_out, not_238_out, not_239_out,
       not_240_out, not_241_out, not_242_out, not_243_out, not_244_out, not_245_out, not_246_out,
       not_247_out, not_248_out, not_249_out, not_250_out, not_251_out, not_252_out, not_253_out,
       not_254_out, not_255_out, not_256_out, not_257_out, not_258_out, not_259_out, not_260_out,
       not_261_out, not_262_out, not_263_out, not_264_out, not_265_out, not_266_out, not_267_out,
       not_268_out, not_269_out, not_270_out, not_271_out, not_272_out, not_273_out, not_274_out,
       not_275_out, not_276_out, not_277_out, not_278_out, not_279_out, not_280_out, not_281_out,
       not_282_out, not_283_out, not_284_out, not_285_out, not_286_out, not_287_out, not_288_out,
       not_289_out, not_290_out, not_291_out, not_292_out, not_293_out, not_294_out, not_295_out,
       not_296_out, not_297_out, not_298_out, not_299_out, not_300_out, not_301_out, not_302_out,
       not_303_out, not_304_out, not_305_out, not_306_out, not_307_out, not_308_out;

  not not_1 (not_1_out, OP[5]);
  not not_2 (not_2_out, OP[4]);
  not not_3 (not_3_out, OP[3]);
  not not_4 (not_4_out, OP[2]);
  not not_5 (not_5_out, OP[1]);
  not not_6 (not_6_out, OP[0]);
  not not_7 (not_7_out, Funct[4]);
  not not_8 (not_8_out, Funct[3]);
  not not_9 (not_9_out, Funct[2]);
  not not_10 (not_10_out, Funct[1]);
  not not_11 (not_11_out, Funct[0]);
  not not_12 (not_12_out, OP[5]);
  not not_13 (not_13_out, OP[4]);
  not not_14 (not_14_out, OP[3]);
  not not_15 (not_15_out, OP[2]);
  not not_16 (not_16_out, OP[1]);
  not not_17 (not_17_out, OP[0]);
  not not_18 (not_18_out, Funct[4]);
  not not_19 (not_19_out, Funct[3]);
  not not_20 (not_20_out, Funct[2]);
  not not_21 (not_21_out, Funct[1]);
  not not_22 (not_22_out, OP[5]);
  not not_23 (not_23_out, OP[4]);
  not not_24 (not_24_out, OP[3]);
  not not_25 (not_25_out, OP[2]);
  not not_26 (not_26_out, OP[1]);
  not not_27 (not_27_out, OP[0]);
  not not_28 (not_28_out, Funct[4]);
  not not_29 (not_29_out, Funct[3]);
  not not_30 (not_30_out, Funct[2]);
  not not_31 (not_31_out, Funct[0]);
  not not_32 (not_32_out, OP[5]);
  not not_33 (not_33_out, OP[4]);
  not not_34 (not_34_out, OP[3]);
  not not_35 (not_35_out, OP[2]);
  not not_36 (not_36_out, OP[1]);
  not not_37 (not_37_out, OP[0]);
  not not_38 (not_38_out, Funct[4]);
  not not_39 (not_39_out, Funct[3]);
  not not_40 (not_40_out, Funct[1]);
  not not_41 (not_41_out, Funct[0]);
  not not_42 (not_42_out, OP[5]);
  not not_43 (not_43_out, OP[4]);
  not not_44 (not_44_out, OP[3]);
  not not_45 (not_45_out, OP[2]);
  not not_46 (not_46_out, OP[1]);
  not not_47 (not_47_out, OP[0]);
  not not_48 (not_48_out, Funct[4]);
  not not_49 (not_49_out, Funct[3]);
  not not_50 (not_50_out, Funct[1]);
  not not_51 (not_51_out, OP[5]);
  not not_52 (not_52_out, OP[4]);
  not not_53 (not_53_out, OP[3]);
  not not_54 (not_54_out, OP[2]);
  not not_55 (not_55_out, OP[1]);
  not not_56 (not_56_out, OP[0]);
  not not_57 (not_57_out, Funct[4]);
  not not_58 (not_58_out, Funct[3]);
  not not_59 (not_59_out, OP[5]);
  not not_60 (not_60_out, OP[4]);
  not not_61 (not_61_out, OP[3]);
  not not_62 (not_62_out, OP[2]);
  not not_63 (not_63_out, OP[1]);
  not not_64 (not_64_out, OP[0]);
  not not_65 (not_65_out, Funct[4]);
  not not_66 (not_66_out, Funct[2]);
  not not_67 (not_67_out, Funct[0]);
  not not_68 (not_68_out, OP[5]);
  not not_69 (not_69_out, OP[4]);
  not not_70 (not_70_out, OP[3]);
  not not_71 (not_71_out, OP[2]);
  not not_72 (not_72_out, OP[1]);
  not not_73 (not_73_out, OP[0]);
  not not_74 (not_74_out, Funct[4]);
  not not_75 (not_75_out, Funct[2]);
  not not_76 (not_76_out, OP[5]);
  not not_77 (not_77_out, OP[4]);
  not not_78 (not_78_out, OP[3]);
  not not_79 (not_79_out, OP[2]);
  not not_80 (not_80_out, OP[1]);
  not not_81 (not_81_out, OP[0]);
  not not_82 (not_82_out, Funct[5]);
  not not_83 (not_83_out, Funct[4]);
  not not_84 (not_84_out, Funct[2]);
  not not_85 (not_85_out, Funct[1]);
  not not_86 (not_86_out, Funct[0]);
  not not_87 (not_87_out, OP[5]);
  not not_88 (not_88_out, OP[4]);
  not not_89 (not_89_out, OP[3]);
  not not_90 (not_90_out, OP[2]);
  not not_91 (not_91_out, OP[1]);
  not not_92 (not_92_out, OP[0]);
  not not_93 (not_93_out, Funct[5]);
  not not_94 (not_94_out, Funct[4]);
  not not_95 (not_95_out, Funct[1]);
  not not_96 (not_96_out, Funct[0]);
  not not_97 (not_97_out, OP[5]);
  not not_98 (not_98_out, OP[4]);
  not not_99 (not_99_out, OP[3]);
  not not_100 (not_100_out, OP[1]);
  not not_101 (not_101_out, OP[0]);
  not not_102 (not_102_out, OP[5]);
  not not_103 (not_103_out, OP[4]);
  not not_104 (not_104_out, OP[3]);
  not not_105 (not_105_out, OP[1]);
  not not_106 (not_106_out, OP[5]);
  not not_107 (not_107_out, OP[4]);
  not not_108 (not_108_out, OP[2]);
  not not_109 (not_109_out, OP[1]);
  not not_110 (not_110_out, OP[0]);
  not not_111 (not_111_out, OP[5]);
  not not_112 (not_112_out, OP[4]);
  not not_113 (not_113_out, OP[1]);
  not not_114 (not_114_out, OP[0]);
  not not_115 (not_115_out, OP[5]);
  not not_116 (not_116_out, OP[4]);
  not not_117 (not_117_out, OP[2]);
  not not_118 (not_118_out, OP[1]);
  not not_119 (not_119_out, OP[5]);
  not not_120 (not_120_out, OP[4]);
  not not_121 (not_121_out, OP[2]);
  not not_122 (not_122_out, OP[0]);
  not not_123 (not_123_out, OP[5]);
  not not_124 (not_124_out, OP[4]);
  not not_125 (not_125_out, OP[1]);
  not not_126 (not_126_out, OP[4]);
  not not_127 (not_127_out, OP[3]);
  not not_128 (not_128_out, OP[2]);
  not not_129 (not_129_out, OP[4]);
  not not_130 (not_130_out, OP[2]);
  not not_131 (not_131_out, OP[5]);
  not not_132 (not_132_out, OP[4]);
  not not_133 (not_133_out, OP[3]);
  not not_134 (not_134_out, OP[2]);
  not not_135 (not_135_out, OP[1]);
  not not_136 (not_136_out, OP[0]);
  not not_137 (not_137_out, Funct[5]);
  not not_138 (not_138_out, Funct[4]);
  not not_139 (not_139_out, Funct[3]);
  not not_140 (not_140_out, Funct[1]);
  not not_141 (not_141_out, Funct[0]);
  not not_142 (not_142_out, OP[5]);
  not not_143 (not_143_out, OP[4]);
  not not_144 (not_144_out, OP[3]);
  not not_145 (not_145_out, OP[2]);
  not not_146 (not_146_out, OP[1]);
  not not_147 (not_147_out, OP[0]);
  not not_148 (not_148_out, Funct[5]);
  not not_149 (not_149_out, Funct[4]);
  not not_150 (not_150_out, Funct[3]);
  not not_151 (not_151_out, OP[4]);
  not not_152 (not_152_out, OP[3]);
  not not_153 (not_153_out, OP[1]);
  not not_154 (not_154_out, OP[0]);
  not not_155 (not_155_out, OP[5]);
  not not_156 (not_156_out, OP[4]);
  not not_157 (not_157_out, OP[3]);
  not not_158 (not_158_out, OP[2]);
  not not_159 (not_159_out, OP[1]);
  not not_160 (not_160_out, OP[5]);
  not not_161 (not_161_out, OP[4]);
  not not_162 (not_162_out, OP[3]);
  not not_163 (not_163_out, OP[2]);
  not not_164 (not_164_out, OP[1]);
  not not_165 (not_165_out, OP[0]);
  not not_166 (not_166_out, Funct[5]);
  not not_167 (not_167_out, Funct[4]);
  not not_168 (not_168_out, Funct[3]);
  not not_169 (not_169_out, Funct[2]);
  not not_170 (not_170_out, Funct[1]);
  not not_171 (not_171_out, Funct[0]);
  not not_172 (not_172_out, OP[5]);
  not not_173 (not_173_out, OP[4]);
  not not_174 (not_174_out, OP[3]);
  not not_175 (not_175_out, OP[2]);
  not not_176 (not_176_out, OP[1]);
  not not_177 (not_177_out, OP[0]);
  not not_178 (not_178_out, Funct[5]);
  not not_179 (not_179_out, Funct[4]);
  not not_180 (not_180_out, Funct[3]);
  not not_181 (not_181_out, Funct[2]);
  not not_182 (not_182_out, OP[5]);
  not not_183 (not_183_out, OP[4]);
  not not_184 (not_184_out, OP[3]);
  not not_185 (not_185_out, OP[2]);
  not not_186 (not_186_out, OP[1]);
  not not_187 (not_187_out, OP[0]);
  not not_188 (not_188_out, Funct[5]);
  not not_189 (not_189_out, Funct[4]);
  not not_190 (not_190_out, Funct[3]);
  not not_191 (not_191_out, Funct[2]);
  not not_192 (not_192_out, Funct[0]);
  not not_193 (not_193_out, OP[5]);
  not not_194 (not_194_out, OP[4]);
  not not_195 (not_195_out, OP[3]);
  not not_196 (not_196_out, OP[2]);
  not not_197 (not_197_out, OP[1]);
  not not_198 (not_198_out, OP[0]);
  not not_199 (not_199_out, Funct[4]);
  not not_200 (not_200_out, Funct[3]);
  not not_201 (not_201_out, Funct[2]);
  not not_202 (not_202_out, Funct[1]);
  not not_203 (not_203_out, Funct[0]);
  not not_204 (not_204_out, OP[5]);
  not not_205 (not_205_out, OP[4]);
  not not_206 (not_206_out, OP[3]);
  not not_207 (not_207_out, OP[2]);
  not not_208 (not_208_out, OP[1]);
  not not_209 (not_209_out, OP[0]);
  not not_210 (not_210_out, Funct[4]);
  not not_211 (not_211_out, Funct[3]);
  not not_212 (not_212_out, Funct[2]);
  not not_213 (not_213_out, Funct[1]);
  not not_214 (not_214_out, OP[5]);
  not not_215 (not_215_out, OP[4]);
  not not_216 (not_216_out, OP[3]);
  not not_217 (not_217_out, OP[2]);
  not not_218 (not_218_out, OP[1]);
  not not_219 (not_219_out, OP[0]);
  not not_220 (not_220_out, Funct[4]);
  not not_221 (not_221_out, Funct[3]);
  not not_222 (not_222_out, Funct[2]);
  not not_223 (not_223_out, Funct[0]);
  not not_224 (not_224_out, OP[5]);
  not not_225 (not_225_out, OP[4]);
  not not_226 (not_226_out, OP[3]);
  not not_227 (not_227_out, OP[2]);
  not not_228 (not_228_out, OP[1]);
  not not_229 (not_229_out, OP[0]);
  not not_230 (not_230_out, Funct[4]);
  not not_231 (not_231_out, Funct[3]);
  not not_232 (not_232_out, Funct[1]);
  not not_233 (not_233_out, Funct[0]);
  not not_234 (not_234_out, OP[5]);
  not not_235 (not_235_out, OP[4]);
  not not_236 (not_236_out, OP[3]);
  not not_237 (not_237_out, OP[2]);
  not not_238 (not_238_out, OP[1]);
  not not_239 (not_239_out, OP[0]);
  not not_240 (not_240_out, Funct[4]);
  not not_241 (not_241_out, Funct[3]);
  not not_242 (not_242_out, Funct[1]);
  not not_243 (not_243_out, OP[5]);
  not not_244 (not_244_out, OP[4]);
  not not_245 (not_245_out, OP[3]);
  not not_246 (not_246_out, OP[2]);
  not not_247 (not_247_out, OP[1]);
  not not_248 (not_248_out, OP[0]);
  not not_249 (not_249_out, Funct[4]);
  not not_250 (not_250_out, Funct[3]);
  not not_251 (not_251_out, OP[5]);
  not not_252 (not_252_out, OP[4]);
  not not_253 (not_253_out, OP[3]);
  not not_254 (not_254_out, OP[2]);
  not not_255 (not_255_out, OP[1]);
  not not_256 (not_256_out, OP[0]);
  not not_257 (not_257_out, Funct[4]);
  not not_258 (not_258_out, Funct[2]);
  not not_259 (not_259_out, Funct[0]);
  not not_260 (not_260_out, OP[5]);
  not not_261 (not_261_out, OP[4]);
  not not_262 (not_262_out, OP[3]);
  not not_263 (not_263_out, OP[2]);
  not not_264 (not_264_out, OP[1]);
  not not_265 (not_265_out, OP[0]);
  not not_266 (not_266_out, Funct[4]);
  not not_267 (not_267_out, Funct[2]);
  not not_268 (not_268_out, OP[5]);
  not not_269 (not_269_out, OP[4]);
  not not_270 (not_270_out, OP[3]);
  not not_271 (not_271_out, OP[2]);
  not not_272 (not_272_out, OP[1]);
  not not_273 (not_273_out, OP[0]);
  not not_274 (not_274_out, Funct[5]);
  not not_275 (not_275_out, Funct[4]);
  not not_276 (not_276_out, Funct[1]);
  not not_277 (not_277_out, Funct[0]);
  not not_278 (not_278_out, OP[5]);
  not not_279 (not_279_out, OP[4]);
  not not_280 (not_280_out, OP[3]);
  not not_281 (not_281_out, OP[1]);
  not not_282 (not_282_out, OP[0]);
  not not_283 (not_283_out, OP[5]);
  not not_284 (not_284_out, OP[4]);
  not not_285 (not_285_out, OP[3]);
  not not_286 (not_286_out, OP[1]);
  not not_287 (not_287_out, OP[4]);
  not not_288 (not_288_out, OP[2]);
  not not_289 (not_289_out, OP[5]);
  not not_290 (not_290_out, OP[4]);
  not not_291 (not_291_out, OP[3]);
  not not_292 (not_292_out, OP[2]);
  not not_293 (not_293_out, OP[1]);
  not not_294 (not_294_out, OP[0]);
  not not_295 (not_295_out, Funct[5]);
  not not_296 (not_296_out, Funct[4]);
  not not_297 (not_297_out, Funct[3]);
  not not_298 (not_298_out, Funct[1]);
  not not_299 (not_299_out, Funct[0]);
  not not_300 (not_300_out, OP[5]);
  not not_301 (not_301_out, OP[4]);
  not not_302 (not_302_out, OP[3]);
  not not_303 (not_303_out, OP[2]);
  not not_304 (not_304_out, OP[1]);
  not not_305 (not_305_out, OP[0]);
  not not_306 (not_306_out, Funct[5]);
  not not_307 (not_307_out, Funct[4]);
  not not_308 (not_308_out, Funct[3]);
  and and_1 (and_1_out, not_1_out, not_2_out, not_3_out, not_4_out, not_5_out, not_6_out, Funct[5], not_7_out, not_8_out, not_9_out, not_10_out, not_11_out);
  and and_2 (and_2_out, not_12_out, not_13_out, not_14_out, not_15_out, not_16_out, not_17_out, Funct[5], not_18_out, not_19_out, not_20_out, not_21_out, Funct[0]);
  and and_3 (and_3_out, not_22_out, not_23_out, not_24_out, not_25_out, not_26_out, not_27_out, Funct[5], not_28_out, not_29_out, not_30_out, Funct[1], not_31_out);
  and and_4 (and_4_out, not_32_out, not_33_out, not_34_out, not_35_out, not_36_out, not_37_out, Funct[5], not_38_out, not_39_out, Funct[2], not_40_out, not_41_out);
  and and_5 (and_5_out, not_42_out, not_43_out, not_44_out, not_45_out, not_46_out, not_47_out, Funct[5], not_48_out, not_49_out, Funct[2], not_50_out, Funct[0]);
  and and_6 (and_6_out, not_51_out, not_52_out, not_53_out, not_54_out, not_55_out, not_56_out, Funct[5], not_57_out, not_58_out, Funct[2], Funct[1], Funct[0]);
  and and_7 (and_7_out, not_59_out, not_60_out, not_61_out, not_62_out, not_63_out, not_64_out, Funct[5], not_65_out, Funct[3], not_66_out, Funct[1], not_67_out);
  and and_8 (and_8_out, not_68_out, not_69_out, not_70_out, not_71_out, not_72_out, not_73_out, Funct[5], not_74_out, Funct[3], not_75_out, Funct[1], Funct[0]);
  and and_9 (and_9_out, not_76_out, not_77_out, not_78_out, not_79_out, not_80_out, not_81_out, not_82_out, not_83_out, Funct[3], not_84_out, not_85_out, not_86_out);
  and and_10 (and_10_out, not_87_out, not_88_out, not_89_out, not_90_out, not_91_out, not_92_out, not_93_out, not_94_out, Funct[3], Funct[2], not_95_out, not_96_out);
  and and_11 (and_11_out, not_97_out, not_98_out, not_99_out, OP[2], not_100_out, not_101_out);
  and and_12 (and_12_out, not_102_out, not_103_out, not_104_out, OP[2], not_105_out, OP[0]);
  and and_13 (and_13_out, not_106_out, not_107_out, OP[3], not_108_out, not_109_out, not_110_out);
  and and_14 (and_14_out, not_111_out, not_112_out, OP[3], OP[2], not_113_out, not_114_out);
  and and_15 (and_15_out, not_115_out, not_116_out, OP[3], not_117_out, not_118_out, OP[0]);
  and and_16 (and_16_out, not_119_out, not_120_out, OP[3], not_121_out, OP[1], not_122_out);
  and and_17 (and_17_out, not_123_out, not_124_out, OP[3], OP[2], not_125_out, OP[0]);
  and and_18 (and_18_out, OP[5], not_126_out, not_127_out, not_128_out, OP[1], OP[0]);
  and and_19 (and_19_out, OP[5], not_129_out, OP[3], not_130_out, OP[1], OP[0]);
  and and_20 (and_20_out, not_131_out, not_132_out, not_133_out, not_134_out, not_135_out, not_136_out, not_137_out, not_138_out, not_139_out, Funct[2], not_140_out, not_141_out);
  and and_21 (and_21_out, not_142_out, not_143_out, not_144_out, not_145_out, not_146_out, not_147_out, not_148_out, not_149_out, not_150_out, Funct[2], Funct[1], Funct[0]);
  and and_22 (and_22_out, OP[5], not_151_out, not_152_out, OP[2], not_153_out, not_154_out);
  and and_23 (and_23_out, not_155_out, not_156_out, not_157_out, not_158_out, not_159_out, OP[0]);
  and and_24 (and_24_out, not_160_out, not_161_out, not_162_out, not_163_out, not_164_out, not_165_out, not_166_out, not_167_out, not_168_out, not_169_out, not_170_out, not_171_out);
  and and_25 (and_25_out, not_172_out, not_173_out, not_174_out, not_175_out, not_176_out, not_177_out, not_178_out, not_179_out, not_180_out, not_181_out, Funct[1], Funct[0]);
  and and_26 (and_26_out, not_182_out, not_183_out, not_184_out, not_185_out, not_186_out, not_187_out, not_188_out, not_189_out, not_190_out, not_191_out, Funct[1], not_192_out);
  and and_27 (and_27_out, not_193_out, not_194_out, not_195_out, not_196_out, not_197_out, not_198_out, Funct[5], not_199_out, not_200_out, not_201_out, not_202_out, not_203_out);
  and and_28 (and_28_out, not_204_out, not_205_out, not_206_out, not_207_out, not_208_out, not_209_out, Funct[5], not_210_out, not_211_out, not_212_out, not_213_out, Funct[0]);
  and and_29 (and_29_out, not_214_out, not_215_out, not_216_out, not_217_out, not_218_out, not_219_out, Funct[5], not_220_out, not_221_out, not_222_out, Funct[1], not_223_out);
  and and_30 (and_30_out, not_224_out, not_225_out, not_226_out, not_227_out, not_228_out, not_229_out, Funct[5], not_230_out, not_231_out, Funct[2], not_232_out, not_233_out);
  and and_31 (and_31_out, not_234_out, not_235_out, not_236_out, not_237_out, not_238_out, not_239_out, Funct[5], not_240_out, not_241_out, Funct[2], not_242_out, Funct[0]);
  and and_32 (and_32_out, not_243_out, not_244_out, not_245_out, not_246_out, not_247_out, not_248_out, Funct[5], not_249_out, not_250_out, Funct[2], Funct[1], Funct[0]);
  and and_33 (and_33_out, not_251_out, not_252_out, not_253_out, not_254_out, not_255_out, not_256_out, Funct[5], not_257_out, Funct[3], not_258_out, Funct[1], not_259_out);
  and and_34 (and_34_out, not_260_out, not_261_out, not_262_out, not_263_out, not_264_out, not_265_out, Funct[5], not_266_out, Funct[3], not_267_out, Funct[1], Funct[0]);
  and and_35 (and_35_out, not_268_out, not_269_out, not_270_out, not_271_out, not_272_out, not_273_out, not_274_out, not_275_out, Funct[3], Funct[2], not_276_out, not_277_out);
  and and_36 (and_36_out, not_278_out, not_279_out, not_280_out, OP[2], not_281_out, not_282_out);
  and and_37 (and_37_out, not_283_out, not_284_out, not_285_out, OP[2], not_286_out, OP[0]);
  and and_38 (and_38_out, OP[5], not_287_out, OP[3], not_288_out, OP[1], OP[0]);
  and and_39 (and_39_out, not_289_out, not_290_out, not_291_out, not_292_out, not_293_out, not_294_out, not_295_out, not_296_out, not_297_out, Funct[2], not_298_out, not_299_out);
  and and_40 (and_40_out, not_300_out, not_301_out, not_302_out, not_303_out, not_304_out, not_305_out, not_306_out, not_307_out, not_308_out, Funct[2], Funct[1], Funct[0]);
  or or_1 (R2_Used, and_24_out, and_25_out, and_26_out, and_27_out, and_28_out, and_29_out, and_30_out, and_31_out, and_32_out, and_33_out, and_34_out, and_35_out, and_36_out, and_37_out, and_38_out, and_39_out, and_40_out);
  or or_2 (R1_Used, and_1_out, and_2_out, and_3_out, and_4_out, and_5_out, and_6_out, and_7_out, and_8_out, and_9_out, and_10_out, and_11_out, and_12_out, and_13_out, and_14_out, and_15_out, and_16_out, and_17_out, and_18_out, and_19_out, and_20_out, and_21_out, and_22_out, and_23_out);
endmodule

module \数据相关检测  (
  input  [4:0] R1_num,
  input  [4:0] MEM_WriteReg_num,
  input  MEM_RegWrite,
  input  [4:0] EX_WriteReg_num,
  input  EX_RegWrite,
  input  R1_Used,
  input  [4:0] R2_num,
  input  R2_Used,
  output Correlated
);

  wire and_1_out, and_2_out, and_3_out, and_4_out, and_5_out, and_6_out, comparator_1_eq, comparator_2_eq,
       comparator_3_eq, comparator_4_eq, comparator_5_eq, comparator_6_eq, or_1_out, or_2_out;

  Comparator #(.width(5), .mode("twosComplement")) comparator_1 (
    .a(R1_num), .b(MEM_WriteReg_num), .eq(comparator_1_eq));  // open: gt, lt
  Comparator #(.width(5), .mode("twosComplement")) comparator_2 (
    .a(R1_num), .b(EX_WriteReg_num), .eq(comparator_2_eq));  // open: gt, lt
  Comparator #(.width(5), .mode("twosComplement")) comparator_3 (
    .a(R1_num), .b({5{1'b0}}), .eq(comparator_3_eq));  // open: gt, lt
  Comparator #(.width(5), .mode("twosComplement")) comparator_4 (
    .a(R2_num), .b(MEM_WriteReg_num), .eq(comparator_4_eq));  // open: gt, lt
  Comparator #(.width(5), .mode("twosComplement")) comparator_5 (
    .a(R2_num), .b(EX_WriteReg_num), .eq(comparator_5_eq));  // open: gt, lt
  Comparator #(.width(5), .mode("twosComplement")) comparator_6 (
    .a(R2_num), .b({5{1'b0}}), .eq(comparator_6_eq));  // open: gt, lt
  and and_1 (and_1_out, comparator_1_eq, MEM_RegWrite);
  or or_1 (or_1_out, and_1_out, and_2_out);
  and and_2 (and_2_out, comparator_2_eq, EX_RegWrite);
  and and_3 (and_3_out, comparator_4_eq, MEM_RegWrite);
  or or_2 (or_2_out, and_3_out, and_4_out);
  and and_4 (and_4_out, comparator_5_eq, EX_RegWrite);
  and and_5 (and_5_out, or_1_out, ~comparator_3_eq, R1_Used);  // AND_Gate
  and and_6 (and_6_out, or_2_out, ~comparator_6_eq, R2_Used);  // AND_Gate
  or or_3 (Correlated, and_5_out, and_6_out);
endmodule

module \重定向数据相关检测  (
  input  [4:0] R1_num,
  input  [4:0] MEM_WriteReg_num,
  input  MEM_RegWrite,
  input  R1_Used,
  input  [4:0] EX_WriteReg_num,
  input  EX_RegWrite,
  input  Load_Use,
  input  [4:0] R2_num,
  input  R2_Used,
  output [1:0] R1,
  output LoadUse,
  output [1:0] R2
);

  wire and_1_out, and_2_out, and_3_out, and_4_out, comparator_1_eq, comparator_2_eq, comparator_3_eq,
       comparator_4_eq, comparator_5_eq, comparator_6_eq, comparator_7_eq, comparator_8_eq, or_1_out;
  wire [1:0] and_6_out, and_8_out;

  Comparator #(.width(5), .mode("twosComplement")) comparator_1 (
    .a(R1_num), .b(MEM_WriteReg_num), .eq(comparator_1_eq));  // open: gt, lt
  Comparator #(.width(5), .mode("twosComplement")) comparator_2 (
    .a(R1_num), .b({5{1'b0}}), .eq(comparator_2_eq));  // open: gt, lt
  Comparator #(.width(5), .mode("twosComplement")) comparator_3 (
    .a(R1_num), .b(EX_WriteReg_num), .eq(comparator_3_eq));  // open: gt, lt
  Comparator #(.width(5), .mode("twosComplement")) comparator_4 (
    .a(R1_num), .b({5{1'b0}}), .eq(comparator_4_eq));  // open: gt, lt
  Comparator #(.width(5), .mode("twosComplement")) comparator_5 (
    .a(R2_num), .b(MEM_WriteReg_num), .eq(comparator_5_eq));  // open: gt, lt
  Comparator #(.width(5), .mode("twosComplement")) comparator_6 (
    .a(R2_num), .b({5{1'b0}}), .eq(comparator_6_eq));  // open: gt, lt
  Comparator #(.width(5), .mode("twosComplement")) comparator_7 (
    .a(R2_num), .b(EX_WriteReg_num), .eq(comparator_7_eq));  // open: gt, lt
  Comparator #(.width(5), .mode("twosComplement")) comparator_8 (
    .a(R2_num), .b({5{1'b0}}), .eq(comparator_8_eq));  // open: gt, lt
  and and_1 (and_1_out, comparator_1_eq, MEM_RegWrite);
  and and_2 (and_2_out, comparator_3_eq, EX_RegWrite);
  and and_3 (and_3_out, comparator_5_eq, MEM_RegWrite);
  and and_4 (and_4_out, comparator_7_eq, EX_RegWrite);
  and and_5 (and_6_out[1], and_1_out, ~comparator_2_eq, R1_Used);  // AND_Gate
  and and_6 (and_6_out[0], and_2_out, ~comparator_4_eq, R1_Used);  // AND_Gate
  and and_7 (and_8_out[1], and_3_out, ~comparator_6_eq, R2_Used);  // AND_Gate
  and and_8 (and_8_out[0], and_4_out, ~comparator_8_eq, R2_Used);  // AND_Gate
  Multiplexer #(.select(1), .width(2), .disabled("Z"), .enable("false")) multiplexer_1 (
    .in0(and_6_out), .in1(2'b00), .out(R1), .sel(LoadUse));
  Multiplexer #(.select(1), .width(2), .disabled("Z"), .enable("false")) multiplexer_2 (
    .in0(and_8_out), .in1(2'b00), .out(R2), .sel(LoadUse));
  or or_1 (or_1_out, and_6_out[0], and_8_out[0]);
  and and_9 (LoadUse, or_1_out, Load_Use);
endmodule

module \列输入转换  (
  input  [31:0] in_1,
  input  [31:0] in_2,
  input  [31:0] in_3,
  input  [31:0] in_4,
  input  [31:0] in_5,
  input  [31:0] in_6,
  input  [31:0] in_7,
  input  [31:0] in_8,
  input  [31:0] in_9,
  input  [31:0] in_10,
  input  [31:0] in_11,
  input  [31:0] in_12,
  input  [31:0] in_13,
  input  [31:0] in_14,
  input  [31:0] in_15,
  input  [31:0] in_16,
  input  [31:0] in_17,
  input  [31:0] in_18,
  input  [31:0] in_19,
  input  [31:0] in_20,
  input  [31:0] in_21,
  input  [31:0] in_22,
  input  [31:0] in_23,
  input  [31:0] in_24,
  input  [31:0] in_25,
  input  [31:0] in_26,
  input  [31:0] in_27,
  input  [31:0] in_28,
  output [27:0] _17,
  output [27:0] _1,
  output [27:0] _18,
  output [27:0] _2,
  output [27:0] _19,
  output [27:0] _3,
  output [27:0] _20,
  output [27:0] _4,
  output [27:0] _21,
  output [27:0] _5,
  output [27:0] _22,
  output [27:0] _6,
  output [27:0] _23,
  output [27:0] _7,
  output [27:0] _24,
  output [27:0] _8,
  output [27:0] _25,
  output [27:0] _9,
  output [27:0] _26,
  output [27:0] _10,
  output [27:0] _27,
  output [27:0] _11,
  output [27:0] _28,
  output [27:0] _12,
  output [27:0] _13,
  output [27:0] _14,
  output [27:0] _15,
  output [27:0] _16
);


  assign _1 = {in_5[31:24], in_6[31:24], in_7[31:24], in_8[31:28]};
  assign _2 = {in_5[23:16], in_6[23:16], in_7[23:16], in_8[23:20]};
  assign _3 = {in_5[15:8], in_6[15:8], in_7[15:8], in_8[15:12]};
  assign _4 = {in_5[7:0], in_6[7:0], in_7[7:0], in_8[7:4]};
  assign _5 = {in_13[31:24], in_14[31:24], in_15[31:24], in_16[31:28]};
  assign _6 = {in_13[23:16], in_14[23:16], in_15[23:16], in_16[23:20]};
  assign _7 = {in_13[15:8], in_14[15:8], in_15[15:8], in_16[15:12]};
  assign _8 = {in_13[7:0], in_14[7:0], in_15[7:0], in_16[7:4]};
  assign _9 = {in_21[31:24], in_22[31:24], in_23[31:24], in_24[31:28]};
  assign _10 = {in_21[23:16], in_22[23:16], in_23[23:16], in_24[23:20]};
  assign _11 = {in_21[15:8], in_22[15:8], in_23[15:8], in_24[15:12]};
  assign _12 = {in_21[7:0], in_22[7:0], in_23[7:0], in_24[7:4]};
  assign _13 = {in_25[31:24], in_26[31:24], in_27[31:24], in_28[31:28]};
  assign _14 = {in_25[23:16], in_26[23:16], in_27[23:16], in_28[23:20]};
  assign _15 = {in_25[15:8], in_26[15:8], in_27[15:8], in_28[15:12]};
  assign _16 = {in_25[7:0], in_26[7:0], in_27[7:0], in_28[7:4]};
  assign _17 = {in_1[31:24], in_2[31:24], in_3[31:24], in_4[31:28]};
  assign _18 = {in_1[23:16], in_2[23:16], in_3[23:16], in_4[23:20]};
  assign _19 = {in_1[15:8], in_2[15:8], in_3[15:8], in_4[15:12]};
  assign _20 = {in_1[7:0], in_2[7:0], in_3[7:0], in_4[7:4]};
  assign _21 = {in_9[31:24], in_10[31:24], in_11[31:24], in_12[31:28]};
  assign _22 = {in_9[23:16], in_10[23:16], in_11[23:16], in_12[23:20]};
  assign _23 = {in_9[15:8], in_10[15:8], in_11[15:8], in_12[15:12]};
  assign _24 = {in_9[7:0], in_10[7:0], in_11[7:0], in_12[7:4]};
  assign _25 = {in_17[31:24], in_18[31:24], in_19[31:24], in_20[31:28]};
  assign _26 = {in_17[23:16], in_18[23:16], in_19[23:16], in_20[23:20]};
  assign _27 = {in_17[15:8], in_18[15:8], in_19[15:8], in_20[15:12]};
  assign _28 = {in_17[7:0], in_18[7:0], in_19[7:0], in_20[7:4]};
endmodule

module _222 (
  input  in_1,
  input  in_2,
  input  in_3,
  input  in_4,
  input  in_5,
  input  in_6,
  input  in_7,
  input  in_8,
  input  in_9,
  input  in_10,
  input  in_11,
  input  in_12,
  input  in_13,
  input  in_14,
  input  in_15,
  input  in_16,
  input  in_17,
  input  in_18,
  input  in_19,
  input  in_20,
  input  in_21,
  input  in_22,
  input  in_23,
  input  in_24,
  input  in_25,
  input  in_26,
  input  in_27,
  input  in_28,
  output [27:0] out_29
);


  assign out_29 = {in_1, in_2, in_3, in_4, in_5, in_6, in_7, in_8, in_9, in_10, in_11, in_12, in_13, in_14, in_15, in_16, in_17, in_18, in_19, in_20, in_21, in_22, in_23, in_24, in_25, in_26, in_27, in_28};
endmodule
